// Logisim project NCPx8.circ as structural Verilog: 41 circuits, main circuit NAND_HA
module NAND_HA (
  input  A,
  input  B,
  output O,
  output Carry
);

  wire nand_1_out, nand_2_out, nand_4_out;

  nand nand_1 (nand_1_out, A, B);
  nand nand_2 (nand_2_out, A, nand_1_out);
  nand nand_3 (O, nand_2_out, nand_4_out);
  nand nand_4 (nand_4_out, nand_1_out, B);
  nand nand_5 (Carry, nand_1_out, nand_1_out);
endmodule

module NAND_FA (
  input  Carry_in,
  input  A,
  input  B,
  output O,
  output Carry
);

  wire nand_1_out, nand_2_out, nand_ha_1_carry, nand_ha_1_o, nand_ha_2_carry;

  NAND_HA nand_ha_1 (.A(A), .B(B), .O(nand_ha_1_o), .Carry(nand_ha_1_carry));
  NAND_HA nand_ha_2 (.A(Carry_in), .B(nand_ha_1_o), .O(O), .Carry(nand_ha_2_carry));
  nand nand_1 (nand_1_out, nand_ha_2_carry, nand_ha_2_carry);
  nand nand_2 (nand_2_out, nand_ha_1_carry, nand_ha_1_carry);
  nand nand_3 (Carry, nand_1_out, nand_2_out);
endmodule

module NAND_Adder_x8 (
  input  A0,
  input  A1,
  input  A2,
  input  A3,
  input  A4,
  input  A5,
  input  A6,
  input  A7,
  input  B0,
  input  B1,
  input  B2,
  input  B3,
  input  B4,
  input  B5,
  input  B6,
  input  B7,
  output O0,
  output O1,
  output O2,
  output O3,
  output O4,
  output O5,
  output O6,
  output O7,
  output OverCarry,
  output OverFlow
);

  wire nand_1_out, nand_2_out, nand_3_out, nand_fa_1_carry, nand_fa_2_carry, nand_fa_3_carry,
       nand_fa_4_carry, nand_fa_5_carry, nand_fa_6_carry, nand_fa_7_carry;

  NAND_FA nand_fa_1 (.Carry_in(1'b0), .A(A0), .B(B0), .O(O0), .Carry(nand_fa_1_carry));
  NAND_FA nand_fa_2 (.Carry_in(nand_fa_1_carry), .A(A1), .B(B1), .O(O1), .Carry(nand_fa_2_carry));
  NAND_FA nand_fa_3 (.Carry_in(nand_fa_2_carry), .A(A2), .B(B2), .O(O2), .Carry(nand_fa_3_carry));
  NAND_FA nand_fa_4 (.Carry_in(nand_fa_3_carry), .A(A3), .B(B3), .O(O3), .Carry(nand_fa_4_carry));
  NAND_FA nand_fa_5 (.Carry_in(nand_fa_4_carry), .A(A4), .B(B4), .O(O4), .Carry(nand_fa_5_carry));
  NAND_FA nand_fa_6 (.Carry_in(nand_fa_5_carry), .A(A5), .B(B5), .O(O5), .Carry(nand_fa_6_carry));
  NAND_FA nand_fa_7 (.Carry_in(nand_fa_6_carry), .A(A6), .B(B6), .O(O6), .Carry(nand_fa_7_carry));
  NAND_FA nand_fa_8 (.Carry_in(nand_fa_7_carry), .A(A7), .B(B7), .O(O7), .Carry(OverCarry));
  nand nand_1 (nand_1_out, nand_fa_7_carry, OverCarry);
  nand nand_2 (nand_2_out, nand_fa_7_carry, nand_1_out);
  nand nand_3 (nand_3_out, nand_1_out, OverCarry);
  nand nand_4 (OverFlow, nand_2_out, nand_3_out);
endmodule

module NAND_DFF (
  input  Din,
  input  Clk,
  input  Rst,
  output data
);

  wire nand_1_out, nand_2_out, nand_3_out, nand_4_out, nand_5_out, nand_6_out, nand_7_out, nand_8_out,
       nand_9_out, nand_10_out, nand_11_out, nand_12_out, nand_13_out, nand_14_out, nand_16_out;

  nand nand_1 (nand_1_out, Rst, Rst);
  nand nand_2 (nand_2_out, Din, nand_4_out);
  nand nand_3 (nand_3_out, nand_2_out, nand_4_out);
  nand nand_4 (nand_4_out, Clk, nand_1_out);
  nand nand_5 (nand_5_out, nand_4_out, nand_4_out);
  nand nand_6 (nand_6_out, nand_2_out, nand_7_out);
  nand nand_7 (nand_7_out, nand_6_out, nand_3_out);
  nand nand_8 (nand_8_out, nand_6_out, nand_10_out);
  nand nand_9 (nand_9_out, nand_5_out, nand_5_out);
  nand nand_10 (nand_10_out, Rst, Rst);
  nand nand_11 (nand_11_out, nand_8_out, nand_8_out);
  nand nand_12 (nand_12_out, nand_9_out, nand_10_out);
  nand nand_13 (nand_13_out, nand_11_out, nand_12_out);
  nand nand_14 (nand_14_out, nand_13_out, nand_12_out);
  nand nand_15 (data, nand_13_out, nand_16_out);
  nand nand_16 (nand_16_out, data, nand_14_out);
endmodule

module NAND_Reg_x8 (
  input  D0,
  input  D1,
  input  D2,
  input  D3,
  input  D4,
  input  D5,
  input  D6,
  input  D7,
  input  RST,
  input  CLK,
  output O0,
  output O1,
  output O2,
  output O3,
  output O4,
  output O5,
  output O6,
  output O7
);

  NAND_DFF nand_dff_1 (.Din(D0), .Clk(CLK), .Rst(RST), .data(O0));
  NAND_DFF nand_dff_2 (.Din(D1), .Clk(CLK), .Rst(RST), .data(O1));
  NAND_DFF nand_dff_3 (.Din(D2), .Clk(CLK), .Rst(RST), .data(O2));
  NAND_DFF nand_dff_4 (.Din(D3), .Clk(CLK), .Rst(RST), .data(O3));
  NAND_DFF nand_dff_5 (.Din(D4), .Clk(CLK), .Rst(RST), .data(O4));
  NAND_DFF nand_dff_6 (.Din(D5), .Clk(CLK), .Rst(RST), .data(O5));
  NAND_DFF nand_dff_7 (.Din(D6), .Clk(CLK), .Rst(RST), .data(O6));
  NAND_DFF nand_dff_8 (.Din(D7), .Clk(CLK), .Rst(RST), .data(O7));
endmodule

module NAND_SubGate (
  input  NotGate,
  input  GateCIn,
  input  D,
  output O,
  output GateCOut
);

  wire nand_1_out, nand_2_out, nand_3_out, nand_4_out, nand_5_out, nand_6_out, nand_8_out;

  nand nand_1 (nand_1_out, NotGate, D);
  nand nand_2 (nand_2_out, NotGate, nand_1_out);
  nand nand_3 (nand_3_out, nand_2_out, nand_4_out);
  nand nand_4 (nand_4_out, nand_1_out, D);
  nand nand_5 (nand_5_out, GateCIn, nand_3_out);
  nand nand_6 (nand_6_out, GateCIn, nand_5_out);
  nand nand_7 (O, nand_6_out, nand_8_out);
  nand nand_8 (nand_8_out, nand_5_out, nand_3_out);
  nand nand_9 (GateCOut, nand_5_out, nand_5_out);
endmodule

module NAND_SubGate_x8 (
  input  SubGateFlag,
  input  D0,
  input  D1,
  input  D2,
  input  D3,
  input  D4,
  input  D5,
  input  D6,
  input  D7,
  output O0,
  output O1,
  output O2,
  output O3,
  output O4,
  output O5,
  output O6,
  output O7
);

  wire nand_subgate_1_gatecout, nand_subgate_2_gatecout, nand_subgate_3_gatecout, nand_subgate_4_gatecout,
       nand_subgate_5_gatecout, nand_subgate_6_gatecout, nand_subgate_7_gatecout;

  NAND_SubGate nand_subgate_1 (
    .NotGate(SubGateFlag), .GateCIn(SubGateFlag), .D(D0), .O(O0), .GateCOut(nand_subgate_1_gatecout));
  NAND_SubGate nand_subgate_2 (
    .NotGate(SubGateFlag), .GateCIn(nand_subgate_1_gatecout), .D(D1), .O(O1),
    .GateCOut(nand_subgate_2_gatecout));
  NAND_SubGate nand_subgate_3 (
    .NotGate(SubGateFlag), .GateCIn(nand_subgate_2_gatecout), .D(D2), .O(O2),
    .GateCOut(nand_subgate_3_gatecout));
  NAND_SubGate nand_subgate_4 (
    .NotGate(SubGateFlag), .GateCIn(nand_subgate_3_gatecout), .D(D3), .O(O3),
    .GateCOut(nand_subgate_4_gatecout));
  NAND_SubGate nand_subgate_5 (
    .NotGate(SubGateFlag), .GateCIn(nand_subgate_4_gatecout), .D(D4), .O(O4),
    .GateCOut(nand_subgate_5_gatecout));
  NAND_SubGate nand_subgate_6 (
    .NotGate(SubGateFlag), .GateCIn(nand_subgate_5_gatecout), .D(D5), .O(O5),
    .GateCOut(nand_subgate_6_gatecout));
  NAND_SubGate nand_subgate_7 (
    .NotGate(SubGateFlag), .GateCIn(nand_subgate_6_gatecout), .D(D6), .O(O6),
    .GateCOut(nand_subgate_7_gatecout));
  NAND_SubGate nand_subgate_8 (
    .NotGate(SubGateFlag), .GateCIn(nand_subgate_7_gatecout), .D(D7), .O(O7));  // open: GateCOut
endmodule

module NAND_AND (
  input  A,
  input  B,
  output O
);

  wire nand_1_out;

  nand nand_1 (nand_1_out, A, B);
  nand nand_2 (O, nand_1_out, nand_1_out);
endmodule

module NAND_AND_x8 (
  input  A0,
  input  A1,
  input  A2,
  input  A3,
  input  A4,
  input  A5,
  input  A6,
  input  A7,
  input  B0,
  input  B1,
  input  B2,
  input  B3,
  input  B4,
  input  B5,
  input  B6,
  input  B7,
  output O0,
  output O1,
  output O2,
  output O3,
  output O4,
  output O5,
  output O6,
  output O7
);

  NAND_AND nand_and_1 (.A(A0), .B(B0), .O(O0));
  NAND_AND nand_and_2 (.A(A1), .B(B1), .O(O1));
  NAND_AND nand_and_3 (.A(A2), .B(B2), .O(O2));
  NAND_AND nand_and_4 (.A(A3), .B(B3), .O(O3));
  NAND_AND nand_and_5 (.A(A4), .B(B4), .O(O4));
  NAND_AND nand_and_6 (.A(A5), .B(B5), .O(O5));
  NAND_AND nand_and_7 (.A(A6), .B(B6), .O(O6));
  NAND_AND nand_and_8 (.A(A7), .B(B7), .O(O7));
endmodule

module NAND_OR (
  input  A,
  input  B,
  output lO
);

  wire nand_1_out, nand_2_out;

  nand nand_1 (nand_1_out, A, A);
  nand nand_2 (nand_2_out, B, B);
  nand nand_3 (lO, nand_1_out, nand_2_out);
endmodule

module NAND_OR_x8 (
  input  A0,
  input  A1,
  input  A2,
  input  A3,
  input  A4,
  input  A5,
  input  A6,
  input  A7,
  input  B0,
  input  B1,
  input  B2,
  input  B3,
  input  B4,
  input  B5,
  input  B6,
  input  B7,
  output O0,
  output O1,
  output O2,
  output O3,
  output O4,
  output O5,
  output O6,
  output O7
);

  NAND_OR nand_or_1 (.A(A0), .B(B0), .lO(O0));
  NAND_OR nand_or_2 (.A(A1), .B(B1), .lO(O1));
  NAND_OR nand_or_3 (.A(A2), .B(B2), .lO(O2));
  NAND_OR nand_or_4 (.A(A3), .B(B3), .lO(O3));
  NAND_OR nand_or_5 (.A(A4), .B(B4), .lO(O4));
  NAND_OR nand_or_6 (.A(A5), .B(B5), .lO(O5));
  NAND_OR nand_or_7 (.A(A6), .B(B6), .lO(O6));
  NAND_OR nand_or_8 (.A(A7), .B(B7), .lO(O7));
endmodule

module NAND_EXOR (
  input  A,
  input  B,
  output O
);

  wire nand_1_out, nand_2_out, nand_4_out;

  nand nand_1 (nand_1_out, A, B);
  nand nand_2 (nand_2_out, A, nand_1_out);
  nand nand_3 (O, nand_2_out, nand_4_out);
  nand nand_4 (nand_4_out, nand_1_out, B);
endmodule

module NAND_EXOR_x8 (
  input  A0,
  input  A1,
  input  A2,
  input  A3,
  input  A4,
  input  A5,
  input  A6,
  input  A7,
  input  B0,
  input  B1,
  input  B2,
  input  B3,
  input  B4,
  input  B5,
  input  B6,
  input  B7,
  output O0,
  output O1,
  output O2,
  output O3,
  output O4,
  output O5,
  output O6,
  output O7
);

  NAND_EXOR nand_exor_1 (.A(A0), .B(B0), .O(O0));
  NAND_EXOR nand_exor_2 (.A(A1), .B(B1), .O(O1));
  NAND_EXOR nand_exor_3 (.A(A2), .B(B2), .O(O2));
  NAND_EXOR nand_exor_4 (.A(A3), .B(B3), .O(O3));
  NAND_EXOR nand_exor_5 (.A(A4), .B(B4), .O(O4));
  NAND_EXOR nand_exor_6 (.A(A5), .B(B5), .O(O5));
  NAND_EXOR nand_exor_7 (.A(A6), .B(B6), .O(O6));
  NAND_EXOR nand_exor_8 (.A(A7), .B(B7), .O(O7));
endmodule

module BitShiftor_UP_x8 (
  input  A0,
  input  A1,
  input  A2,
  input  A3,
  input  A4,
  input  A5,
  input  A6,
  input  A7,
  output O0,
  output O1,
  output O2,
  output O3,
  output O4,
  output O5,
  output O6,
  output O7
);


  assign O0 = 1'b0;
  assign O1 = A0;
  assign O2 = A1;
  assign O3 = A2;
  assign O4 = A3;
  assign O5 = A4;
  assign O6 = A5;
  assign O7 = A6;
endmodule

module BitShiftor_DW_x8 (
  input  A0,
  input  A1,
  input  A2,
  input  A3,
  input  A4,
  input  A5,
  input  A6,
  input  A7,
  output O0,
  output O1,
  output O2,
  output O3,
  output O4,
  output O5,
  output O6,
  output O7
);


  assign O0 = A1;
  assign O1 = A2;
  assign O2 = A3;
  assign O3 = A4;
  assign O4 = A5;
  assign O5 = A6;
  assign O6 = A7;
  assign O7 = 1'b0;
endmodule

module NAND_GATE_x8 (
  input  Gate,
  input  D0,
  input  D1,
  input  D2,
  input  D3,
  input  D4,
  input  D5,
  input  D6,
  input  D7,
  output O0,
  output O1,
  output O2,
  output O3,
  output O4,
  output O5,
  output O6,
  output O7
);

  wire nand_1_out, nand_2_out, nand_3_out, nand_4_out, nand_5_out, nand_6_out, nand_7_out, nand_8_out;

  nand nand_1 (nand_1_out, D0, Gate);
  nand nand_2 (nand_2_out, D1, Gate);
  nand nand_3 (nand_3_out, D2, Gate);
  nand nand_4 (nand_4_out, D3, Gate);
  nand nand_5 (nand_5_out, D4, Gate);
  nand nand_6 (nand_6_out, D5, Gate);
  nand nand_7 (nand_7_out, D6, Gate);
  nand nand_8 (nand_8_out, D7, Gate);
  nand nand_9 (O0, nand_1_out, nand_1_out);
  nand nand_10 (O1, nand_2_out, nand_2_out);
  nand nand_11 (O2, nand_3_out, nand_3_out);
  nand nand_12 (O3, nand_4_out, nand_4_out);
  nand nand_13 (O4, nand_5_out, nand_5_out);
  nand nand_14 (O5, nand_6_out, nand_6_out);
  nand nand_15 (O6, nand_7_out, nand_7_out);
  nand nand_16 (O7, nand_8_out, nand_8_out);
endmodule

module NAND_MUX_x3_to_x7 (
  input  S0,
  input  S1,
  input  S2,
  output x1,
  output x2,
  output x3,
  output x4,
  output x5,
  output x6,
  output x7,
  output ModeSelected
);

  wire nand_1_out, nand_2_out, nand_3_out, nand_4_out, nand_5_out, nand_6_out, nand_7_out, nand_8_out,
       nand_9_out, nand_12_out, nand_13_out, nand_14_out, nand_16_out, nand_17_out, nand_18_out, nand_19_out,
       nand_20_out, nand_21_out, nand_24_out, nand_25_out, nand_26_out, nand_27_out, nand_28_out,
       nand_30_out, nand_31_out, nand_32_out;

  nand nand_1 (nand_1_out, S0, S0);
  nand nand_2 (nand_2_out, S1, S1);
  nand nand_3 (nand_3_out, S2, S2);
  nand nand_4 (nand_4_out, nand_3_out, nand_2_out);
  nand nand_5 (nand_5_out, nand_3_out, S1);
  nand nand_6 (nand_6_out, nand_4_out, nand_4_out);
  nand nand_7 (nand_7_out, nand_5_out, nand_5_out);
  nand nand_8 (nand_8_out, nand_6_out, S0);
  nand nand_9 (nand_9_out, nand_7_out, nand_1_out);
  nand nand_10 (x1, nand_8_out, nand_8_out);
  nand nand_11 (x2, nand_9_out, nand_9_out);
  nand nand_12 (nand_12_out, nand_3_out, S1);
  nand nand_13 (nand_13_out, nand_12_out, nand_12_out);
  nand nand_14 (nand_14_out, nand_13_out, S0);
  nand nand_15 (x3, nand_14_out, nand_14_out);
  nand nand_16 (nand_16_out, S2, nand_2_out);
  nand nand_17 (nand_17_out, S2, nand_2_out);
  nand nand_18 (nand_18_out, nand_16_out, nand_16_out);
  nand nand_19 (nand_19_out, nand_17_out, nand_17_out);
  nand nand_20 (nand_20_out, nand_18_out, nand_1_out);
  nand nand_21 (nand_21_out, nand_19_out, S0);
  nand nand_22 (x4, nand_20_out, nand_20_out);
  nand nand_23 (x5, nand_21_out, nand_21_out);
  nand nand_24 (nand_24_out, S2, S1);
  nand nand_25 (nand_25_out, S2, S1);
  nand nand_26 (nand_26_out, nand_24_out, nand_24_out);
  nand nand_27 (nand_27_out, nand_25_out, nand_25_out);
  nand nand_28 (nand_28_out, nand_26_out, nand_1_out);
  nand nand_29 (x6, nand_28_out, nand_28_out);
  nand nand_30 (nand_30_out, nand_3_out, nand_2_out);
  nand nand_31 (nand_31_out, nand_30_out, nand_30_out);
  nand nand_32 (nand_32_out, nand_27_out, S0);
  nand nand_33 (x7, nand_32_out, nand_32_out);
  nand nand_34 (ModeSelected, nand_31_out, nand_1_out);
endmodule

module ALU_x8 (
  input  RegCLK,
  input  [7:0] Data,
  input  [2:0] Mode,
  input  RegA_Load,
  input  RegA_Write,
  input  RegB_Write,
  input  CLR,
  output [7:0] Data_OUTPUT,
  output [3:0] Flag_OUTPUT,
  output [7:0] RegA,
  output [7:0] RegB
);

  wire bitshiftor_dw_x8_1_o0, bitshiftor_dw_x8_1_o1, bitshiftor_dw_x8_1_o2, bitshiftor_dw_x8_1_o3,
       bitshiftor_dw_x8_1_o4, bitshiftor_dw_x8_1_o5, bitshiftor_dw_x8_1_o6, bitshiftor_dw_x8_1_o7,
       bitshiftor_up_x8_1_o0, bitshiftor_up_x8_1_o1, bitshiftor_up_x8_1_o2, bitshiftor_up_x8_1_o3,
       bitshiftor_up_x8_1_o4, bitshiftor_up_x8_1_o5, bitshiftor_up_x8_1_o6, bitshiftor_up_x8_1_o7,
       nand_1_out, nand_2_out, nand_3_out, nand_4_out, nand_5_out, nand_6_out, nand_7_out, nand_8_out,
       nand_9_out, nand_10_out, nand_11_out, nand_12_out, nand_13_out, nand_14_out, nand_15_out, nand_16_out,
       nand_17_out, nand_18_out, nand_19_out, nand_20_out, nand_21_out, nand_22_out, nand_23_out,
       nand_adder_x8_1_o0, nand_adder_x8_1_o1, nand_adder_x8_1_o2, nand_adder_x8_1_o3, nand_adder_x8_1_o4,
       nand_adder_x8_1_o5, nand_adder_x8_1_o6, nand_adder_x8_1_o7, nand_and_x8_1_o0, nand_and_x8_1_o1,
       nand_and_x8_1_o2, nand_and_x8_1_o3, nand_and_x8_1_o4, nand_and_x8_1_o5, nand_and_x8_1_o6,
       nand_and_x8_1_o7, nand_exor_x8_1_o0, nand_exor_x8_1_o1, nand_exor_x8_1_o2, nand_exor_x8_1_o3,
       nand_exor_x8_1_o4, nand_exor_x8_1_o5, nand_exor_x8_1_o6, nand_exor_x8_1_o7,
       nand_mux_x3_to_x7_1_modeselected, nand_or_x8_1_o0, nand_or_x8_1_o1, nand_or_x8_1_o2, nand_or_x8_1_o3,
       nand_or_x8_1_o4, nand_or_x8_1_o5, nand_or_x8_1_o6, nand_or_x8_1_o7, nand_subgate_x8_1_o0,
       nand_subgate_x8_1_o1, nand_subgate_x8_1_o2, nand_subgate_x8_1_o3, nand_subgate_x8_1_o4,
       nand_subgate_x8_1_o5, nand_subgate_x8_1_o6, nand_subgate_x8_1_o7;
  wire [3:0] bus_flag_generator_1_zero;
  wire [6:0] nand_mux_x3_to_x7_1_x1;
  wire [7:0] bus_nand_mux_x8_2_1_o, bus_or_x6_1_out_7, nand_gate_x8_1_o0, nand_gate_x8_2_o0,
       nand_gate_x8_3_o0, nand_gate_x8_4_o0, nand_gate_x8_5_o0, nand_gate_x8_6_o0;

  nand nand_1 (nand_1_out, RegCLK, RegA_Write);
  nand nand_2 (nand_2_out, nand_1_out, nand_1_out);
  nand nand_3 (nand_3_out, RegCLK, RegB_Write);
  nand nand_4 (nand_4_out, nand_3_out, nand_3_out);
  BUS_NAND_MUX_x8_2 bus_nand_mux_x8_2_1 (
    .Selector(nand_mux_x3_to_x7_1_modeselected), .A(Data), .B(bus_or_x6_1_out_7), .O(bus_nand_mux_x8_2_1_o));
  NAND_MUX_x3_to_x7 nand_mux_x3_to_x7_1 (
    .S0(Mode[0]), .S1(Mode[1]), .S2(Mode[2]), .x1(nand_mux_x3_to_x7_1_x1[0]), .x2(nand_mux_x3_to_x7_1_x1[1]),
    .x3(nand_mux_x3_to_x7_1_x1[2]), .x4(nand_mux_x3_to_x7_1_x1[3]), .x5(nand_mux_x3_to_x7_1_x1[4]),
    .x6(nand_mux_x3_to_x7_1_x1[5]), .x7(nand_mux_x3_to_x7_1_x1[6]),
    .ModeSelected(nand_mux_x3_to_x7_1_modeselected));
  NAND_Reg_x8 nand_reg_x8_1 (
    .D0(bus_nand_mux_x8_2_1_o[0]), .D1(bus_nand_mux_x8_2_1_o[1]), .D2(bus_nand_mux_x8_2_1_o[2]),
    .D3(bus_nand_mux_x8_2_1_o[3]), .D4(bus_nand_mux_x8_2_1_o[4]), .D5(bus_nand_mux_x8_2_1_o[5]),
    .D6(bus_nand_mux_x8_2_1_o[6]), .D7(bus_nand_mux_x8_2_1_o[7]), .RST(CLR), .CLK(nand_2_out), .O0(RegA[0]),
    .O1(RegA[1]), .O2(RegA[2]), .O3(RegA[3]), .O4(RegA[4]), .O5(RegA[5]), .O6(RegA[6]), .O7(RegA[7]));
  NAND_Reg_x8 nand_reg_x8_2 (
    .D0(Data[0]), .D1(Data[1]), .D2(Data[2]), .D3(Data[3]), .D4(Data[4]), .D5(Data[5]), .D6(Data[6]),
    .D7(Data[7]), .RST(CLR), .CLK(nand_4_out), .O0(RegB[0]), .O1(RegB[1]), .O2(RegB[2]), .O3(RegB[3]),
    .O4(RegB[4]), .O5(RegB[5]), .O6(RegB[6]), .O7(RegB[7]));
  NAND_Reg_x4 nand_reg_x4_1 (
    .D0(bus_flag_generator_1_zero[0]), .D1(bus_flag_generator_1_zero[1]), .D2(bus_flag_generator_1_zero[2]),
    .D3(bus_flag_generator_1_zero[3]), .RST(CLR), .CLK(nand_2_out), .O0(Flag_OUTPUT[0]), .O1(Flag_OUTPUT[1]),
    .O2(Flag_OUTPUT[2]), .O3(Flag_OUTPUT[3]));
  nand nand_5 (nand_5_out, RegA_Load, RegA[0]);
  nand nand_6 (nand_6_out, RegA_Load, RegA[1]);
  nand nand_7 (nand_7_out, RegA_Load, RegA[2]);
  nand nand_8 (nand_8_out, RegA_Load, RegA[3]);
  nand nand_9 (nand_9_out, RegA_Load, RegA[4]);
  nand nand_10 (nand_10_out, RegA_Load, RegA[5]);
  nand nand_11 (nand_11_out, RegA_Load, RegA[6]);
  nand nand_12 (nand_12_out, RegA_Load, RegA[7]);
  nand nand_13 (nand_13_out, nand_5_out, nand_5_out);
  assign Data_OUTPUT[0] = nand_13_out ? nand_13_out : 1'bz;  // Controlled_Buffer controlled_buffer_1
  nand nand_14 (nand_14_out, nand_6_out, nand_6_out);
  assign Data_OUTPUT[1] = nand_14_out ? nand_14_out : 1'bz;  // Controlled_Buffer controlled_buffer_2
  nand nand_15 (nand_15_out, nand_7_out, nand_7_out);
  assign Data_OUTPUT[2] = nand_15_out ? nand_15_out : 1'bz;  // Controlled_Buffer controlled_buffer_3
  nand nand_16 (nand_16_out, nand_8_out, nand_8_out);
  assign Data_OUTPUT[3] = nand_16_out ? nand_16_out : 1'bz;  // Controlled_Buffer controlled_buffer_4
  nand nand_17 (nand_17_out, nand_9_out, nand_9_out);
  assign Data_OUTPUT[4] = nand_17_out ? nand_17_out : 1'bz;  // Controlled_Buffer controlled_buffer_5
  nand nand_18 (nand_18_out, nand_10_out, nand_10_out);
  assign Data_OUTPUT[5] = nand_18_out ? nand_18_out : 1'bz;  // Controlled_Buffer controlled_buffer_6
  nand nand_19 (nand_19_out, nand_11_out, nand_11_out);
  assign Data_OUTPUT[6] = nand_19_out ? nand_19_out : 1'bz;  // Controlled_Buffer controlled_buffer_7
  nand nand_20 (nand_20_out, nand_12_out, nand_12_out);
  assign Data_OUTPUT[7] = nand_20_out ? nand_20_out : 1'bz;  // Controlled_Buffer controlled_buffer_8
  NAND_SubGate_x8 nand_subgate_x8_1 (
    .SubGateFlag(nand_mux_x3_to_x7_1_x1[1]), .D0(RegB[0]), .D1(RegB[1]), .D2(RegB[2]), .D3(RegB[3]),
    .D4(RegB[4]), .D5(RegB[5]), .D6(RegB[6]), .D7(RegB[7]), .O0(nand_subgate_x8_1_o0),
    .O1(nand_subgate_x8_1_o1), .O2(nand_subgate_x8_1_o2), .O3(nand_subgate_x8_1_o3),
    .O4(nand_subgate_x8_1_o4), .O5(nand_subgate_x8_1_o5), .O6(nand_subgate_x8_1_o6), .O7(nand_subgate_x8_1_o7));
  NAND_Adder_x8 nand_adder_x8_1 (
    .A0(RegA[0]), .A1(RegA[1]), .A2(RegA[2]), .A3(RegA[3]), .A4(RegA[4]), .A5(RegA[5]), .A6(RegA[6]),
    .A7(RegA[7]), .B0(nand_subgate_x8_1_o0), .B1(nand_subgate_x8_1_o1), .B2(nand_subgate_x8_1_o2),
    .B3(nand_subgate_x8_1_o3), .B4(nand_subgate_x8_1_o4), .B5(nand_subgate_x8_1_o5),
    .B6(nand_subgate_x8_1_o6), .B7(nand_subgate_x8_1_o7), .O0(nand_adder_x8_1_o0), .O1(nand_adder_x8_1_o1),
    .O2(nand_adder_x8_1_o2), .O3(nand_adder_x8_1_o3), .O4(nand_adder_x8_1_o4), .O5(nand_adder_x8_1_o5),
    .O6(nand_adder_x8_1_o6), .O7(nand_adder_x8_1_o7), .OverCarry(bus_flag_generator_1_zero[2]),
    .OverFlow(bus_flag_generator_1_zero[3]));
  NAND_AND_x8 nand_and_x8_1 (
    .A0(RegA[0]), .A1(RegA[1]), .A2(RegA[2]), .A3(RegA[3]), .A4(RegA[4]), .A5(RegA[5]), .A6(RegA[6]),
    .A7(RegA[7]), .B0(RegB[0]), .B1(RegB[1]), .B2(RegB[2]), .B3(RegB[3]), .B4(RegB[4]), .B5(RegB[5]),
    .B6(RegB[6]), .B7(RegB[7]), .O0(nand_and_x8_1_o0), .O1(nand_and_x8_1_o1), .O2(nand_and_x8_1_o2),
    .O3(nand_and_x8_1_o3), .O4(nand_and_x8_1_o4), .O5(nand_and_x8_1_o5), .O6(nand_and_x8_1_o6),
    .O7(nand_and_x8_1_o7));
  NAND_OR_x8 nand_or_x8_1 (
    .A0(RegA[0]), .A1(RegA[1]), .A2(RegA[2]), .A3(RegA[3]), .A4(RegA[4]), .A5(RegA[5]), .A6(RegA[6]),
    .A7(RegA[7]), .B0(RegB[0]), .B1(RegB[1]), .B2(RegB[2]), .B3(RegB[3]), .B4(RegB[4]), .B5(RegB[5]),
    .B6(RegB[6]), .B7(RegB[7]), .O0(nand_or_x8_1_o0), .O1(nand_or_x8_1_o1), .O2(nand_or_x8_1_o2),
    .O3(nand_or_x8_1_o3), .O4(nand_or_x8_1_o4), .O5(nand_or_x8_1_o5), .O6(nand_or_x8_1_o6),
    .O7(nand_or_x8_1_o7));
  NAND_EXOR_x8 nand_exor_x8_1 (
    .A0(RegA[0]), .A1(RegA[1]), .A2(RegA[2]), .A3(RegA[3]), .A4(RegA[4]), .A5(RegA[5]), .A6(RegA[6]),
    .A7(RegA[7]), .B0(RegB[0]), .B1(RegB[1]), .B2(RegB[2]), .B3(RegB[3]), .B4(RegB[4]), .B5(RegB[5]),
    .B6(RegB[6]), .B7(RegB[7]), .O0(nand_exor_x8_1_o0), .O1(nand_exor_x8_1_o1), .O2(nand_exor_x8_1_o2),
    .O3(nand_exor_x8_1_o3), .O4(nand_exor_x8_1_o4), .O5(nand_exor_x8_1_o5), .O6(nand_exor_x8_1_o6),
    .O7(nand_exor_x8_1_o7));
  BitShiftor_UP_x8 bitshiftor_up_x8_1 (
    .A0(RegA[0]), .A1(RegA[1]), .A2(RegA[2]), .A3(RegA[3]), .A4(RegA[4]), .A5(RegA[5]), .A6(RegA[6]),
    .A7(RegA[7]), .O0(bitshiftor_up_x8_1_o0), .O1(bitshiftor_up_x8_1_o1), .O2(bitshiftor_up_x8_1_o2),
    .O3(bitshiftor_up_x8_1_o3), .O4(bitshiftor_up_x8_1_o4), .O5(bitshiftor_up_x8_1_o5),
    .O6(bitshiftor_up_x8_1_o6), .O7(bitshiftor_up_x8_1_o7));
  BitShiftor_DW_x8 bitshiftor_dw_x8_1 (
    .A0(RegA[0]), .A1(RegA[1]), .A2(RegA[2]), .A3(RegA[3]), .A4(RegA[4]), .A5(RegA[5]), .A6(RegA[6]),
    .A7(RegA[7]), .O0(bitshiftor_dw_x8_1_o0), .O1(bitshiftor_dw_x8_1_o1), .O2(bitshiftor_dw_x8_1_o2),
    .O3(bitshiftor_dw_x8_1_o3), .O4(bitshiftor_dw_x8_1_o4), .O5(bitshiftor_dw_x8_1_o5),
    .O6(bitshiftor_dw_x8_1_o6), .O7(bitshiftor_dw_x8_1_o7));
  nand nand_21 (nand_21_out, nand_mux_x3_to_x7_1_x1[0], nand_mux_x3_to_x7_1_x1[0]);
  nand nand_22 (nand_22_out, nand_mux_x3_to_x7_1_x1[1], nand_mux_x3_to_x7_1_x1[1]);
  nand nand_23 (nand_23_out, nand_21_out, nand_22_out);
  NAND_GATE_x8 nand_gate_x8_1 (
    .Gate(nand_23_out), .D0(nand_adder_x8_1_o0), .D1(nand_adder_x8_1_o1), .D2(nand_adder_x8_1_o2),
    .D3(nand_adder_x8_1_o3), .D4(nand_adder_x8_1_o4), .D5(nand_adder_x8_1_o5), .D6(nand_adder_x8_1_o6),
    .D7(nand_adder_x8_1_o7), .O0(nand_gate_x8_1_o0[0]), .O1(nand_gate_x8_1_o0[1]), .O2(nand_gate_x8_1_o0[2]),
    .O3(nand_gate_x8_1_o0[3]), .O4(nand_gate_x8_1_o0[4]), .O5(nand_gate_x8_1_o0[5]),
    .O6(nand_gate_x8_1_o0[6]), .O7(nand_gate_x8_1_o0[7]));
  NAND_GATE_x8 nand_gate_x8_2 (
    .Gate(nand_mux_x3_to_x7_1_x1[2]), .D0(nand_and_x8_1_o0), .D1(nand_and_x8_1_o1), .D2(nand_and_x8_1_o2),
    .D3(nand_and_x8_1_o3), .D4(nand_and_x8_1_o4), .D5(nand_and_x8_1_o5), .D6(nand_and_x8_1_o6),
    .D7(nand_and_x8_1_o7), .O0(nand_gate_x8_2_o0[0]), .O1(nand_gate_x8_2_o0[1]), .O2(nand_gate_x8_2_o0[2]),
    .O3(nand_gate_x8_2_o0[3]), .O4(nand_gate_x8_2_o0[4]), .O5(nand_gate_x8_2_o0[5]),
    .O6(nand_gate_x8_2_o0[6]), .O7(nand_gate_x8_2_o0[7]));
  NAND_GATE_x8 nand_gate_x8_3 (
    .Gate(nand_mux_x3_to_x7_1_x1[3]), .D0(nand_or_x8_1_o0), .D1(nand_or_x8_1_o1), .D2(nand_or_x8_1_o2),
    .D3(nand_or_x8_1_o3), .D4(nand_or_x8_1_o4), .D5(nand_or_x8_1_o5), .D6(nand_or_x8_1_o6),
    .D7(nand_or_x8_1_o7), .O0(nand_gate_x8_3_o0[0]), .O1(nand_gate_x8_3_o0[1]), .O2(nand_gate_x8_3_o0[2]),
    .O3(nand_gate_x8_3_o0[3]), .O4(nand_gate_x8_3_o0[4]), .O5(nand_gate_x8_3_o0[5]),
    .O6(nand_gate_x8_3_o0[6]), .O7(nand_gate_x8_3_o0[7]));
  NAND_GATE_x8 nand_gate_x8_4 (
    .Gate(nand_mux_x3_to_x7_1_x1[4]), .D0(nand_exor_x8_1_o0), .D1(nand_exor_x8_1_o1), .D2(nand_exor_x8_1_o2),
    .D3(nand_exor_x8_1_o3), .D4(nand_exor_x8_1_o4), .D5(nand_exor_x8_1_o5), .D6(nand_exor_x8_1_o6),
    .D7(nand_exor_x8_1_o7), .O0(nand_gate_x8_4_o0[0]), .O1(nand_gate_x8_4_o0[1]), .O2(nand_gate_x8_4_o0[2]),
    .O3(nand_gate_x8_4_o0[3]), .O4(nand_gate_x8_4_o0[4]), .O5(nand_gate_x8_4_o0[5]),
    .O6(nand_gate_x8_4_o0[6]), .O7(nand_gate_x8_4_o0[7]));
  NAND_GATE_x8 nand_gate_x8_5 (
    .Gate(nand_mux_x3_to_x7_1_x1[5]), .D0(bitshiftor_up_x8_1_o0), .D1(bitshiftor_up_x8_1_o1),
    .D2(bitshiftor_up_x8_1_o2), .D3(bitshiftor_up_x8_1_o3), .D4(bitshiftor_up_x8_1_o4),
    .D5(bitshiftor_up_x8_1_o5), .D6(bitshiftor_up_x8_1_o6), .D7(bitshiftor_up_x8_1_o7),
    .O0(nand_gate_x8_5_o0[0]), .O1(nand_gate_x8_5_o0[1]), .O2(nand_gate_x8_5_o0[2]),
    .O3(nand_gate_x8_5_o0[3]), .O4(nand_gate_x8_5_o0[4]), .O5(nand_gate_x8_5_o0[5]),
    .O6(nand_gate_x8_5_o0[6]), .O7(nand_gate_x8_5_o0[7]));
  NAND_GATE_x8 nand_gate_x8_6 (
    .Gate(nand_mux_x3_to_x7_1_x1[6]), .D0(bitshiftor_dw_x8_1_o0), .D1(bitshiftor_dw_x8_1_o1),
    .D2(bitshiftor_dw_x8_1_o2), .D3(bitshiftor_dw_x8_1_o3), .D4(bitshiftor_dw_x8_1_o4),
    .D5(bitshiftor_dw_x8_1_o5), .D6(bitshiftor_dw_x8_1_o6), .D7(bitshiftor_dw_x8_1_o7),
    .O0(nand_gate_x8_6_o0[0]), .O1(nand_gate_x8_6_o0[1]), .O2(nand_gate_x8_6_o0[2]),
    .O3(nand_gate_x8_6_o0[3]), .O4(nand_gate_x8_6_o0[4]), .O5(nand_gate_x8_6_o0[5]),
    .O6(nand_gate_x8_6_o0[6]), .O7(nand_gate_x8_6_o0[7]));
  BUS_OR_x6 bus_or_x6_1 (
    .in_1(nand_gate_x8_1_o0), .in_2(nand_gate_x8_2_o0), .in_3(nand_gate_x8_3_o0), .in_4(nand_gate_x8_4_o0),
    .in_5(nand_gate_x8_5_o0), .in_6(nand_gate_x8_6_o0), .out_7(bus_or_x6_1_out_7));
  BUS_FLAG_Generator bus_flag_generator_1 (
    .DATA(bus_or_x6_1_out_7), .ZERO(bus_flag_generator_1_zero[0]), .SIGN(bus_flag_generator_1_zero[1]));
endmodule

module BUS_OR_x6 (
  input  [7:0] in_1,
  input  [7:0] in_2,
  input  [7:0] in_3,
  input  [7:0] in_4,
  input  [7:0] in_5,
  input  [7:0] in_6,
  output [7:0] out_7
);

  wire [7:0] nand_or_x8_1_o0, nand_or_x8_2_o0, nand_or_x8_3_o0, nand_or_x8_4_o0;

  NAND_OR_x8 nand_or_x8_1 (
    .A0(in_1[0]), .A1(in_1[1]), .A2(in_1[2]), .A3(in_1[3]), .A4(in_1[4]), .A5(in_1[5]), .A6(in_1[6]),
    .A7(in_1[7]), .B0(in_2[0]), .B1(in_2[1]), .B2(in_2[2]), .B3(in_2[3]), .B4(in_2[4]), .B5(in_2[5]),
    .B6(in_2[6]), .B7(in_2[7]), .O0(nand_or_x8_1_o0[0]), .O1(nand_or_x8_1_o0[1]), .O2(nand_or_x8_1_o0[2]),
    .O3(nand_or_x8_1_o0[3]), .O4(nand_or_x8_1_o0[4]), .O5(nand_or_x8_1_o0[5]), .O6(nand_or_x8_1_o0[6]),
    .O7(nand_or_x8_1_o0[7]));
  NAND_OR_x8 nand_or_x8_2 (
    .A0(in_3[0]), .A1(in_3[1]), .A2(in_3[2]), .A3(in_3[3]), .A4(in_3[4]), .A5(in_3[5]), .A6(in_3[6]),
    .A7(in_3[7]), .B0(in_4[0]), .B1(in_4[1]), .B2(in_4[2]), .B3(in_4[3]), .B4(in_4[4]), .B5(in_4[5]),
    .B6(in_4[6]), .B7(in_4[7]), .O0(nand_or_x8_2_o0[0]), .O1(nand_or_x8_2_o0[1]), .O2(nand_or_x8_2_o0[2]),
    .O3(nand_or_x8_2_o0[3]), .O4(nand_or_x8_2_o0[4]), .O5(nand_or_x8_2_o0[5]), .O6(nand_or_x8_2_o0[6]),
    .O7(nand_or_x8_2_o0[7]));
  NAND_OR_x8 nand_or_x8_3 (
    .A0(in_5[0]), .A1(in_5[1]), .A2(in_5[2]), .A3(in_5[3]), .A4(in_5[4]), .A5(in_5[5]), .A6(in_5[6]),
    .A7(in_5[7]), .B0(in_6[0]), .B1(in_6[1]), .B2(in_6[2]), .B3(in_6[3]), .B4(in_6[4]), .B5(in_6[5]),
    .B6(in_6[6]), .B7(in_6[7]), .O0(nand_or_x8_3_o0[0]), .O1(nand_or_x8_3_o0[1]), .O2(nand_or_x8_3_o0[2]),
    .O3(nand_or_x8_3_o0[3]), .O4(nand_or_x8_3_o0[4]), .O5(nand_or_x8_3_o0[5]), .O6(nand_or_x8_3_o0[6]),
    .O7(nand_or_x8_3_o0[7]));
  NAND_OR_x8 nand_or_x8_4 (
    .A0(nand_or_x8_1_o0[0]), .A1(nand_or_x8_1_o0[1]), .A2(nand_or_x8_1_o0[2]), .A3(nand_or_x8_1_o0[3]),
    .A4(nand_or_x8_1_o0[4]), .A5(nand_or_x8_1_o0[5]), .A6(nand_or_x8_1_o0[6]), .A7(nand_or_x8_1_o0[7]),
    .B0(nand_or_x8_2_o0[0]), .B1(nand_or_x8_2_o0[1]), .B2(nand_or_x8_2_o0[2]), .B3(nand_or_x8_2_o0[3]),
    .B4(nand_or_x8_2_o0[4]), .B5(nand_or_x8_2_o0[5]), .B6(nand_or_x8_2_o0[6]), .B7(nand_or_x8_2_o0[7]),
    .O0(nand_or_x8_4_o0[0]), .O1(nand_or_x8_4_o0[1]), .O2(nand_or_x8_4_o0[2]), .O3(nand_or_x8_4_o0[3]),
    .O4(nand_or_x8_4_o0[4]), .O5(nand_or_x8_4_o0[5]), .O6(nand_or_x8_4_o0[6]), .O7(nand_or_x8_4_o0[7]));
  NAND_OR_x8 nand_or_x8_5 (
    .A0(nand_or_x8_4_o0[0]), .A1(nand_or_x8_4_o0[1]), .A2(nand_or_x8_4_o0[2]), .A3(nand_or_x8_4_o0[3]),
    .A4(nand_or_x8_4_o0[4]), .A5(nand_or_x8_4_o0[5]), .A6(nand_or_x8_4_o0[6]), .A7(nand_or_x8_4_o0[7]),
    .B0(nand_or_x8_3_o0[0]), .B1(nand_or_x8_3_o0[1]), .B2(nand_or_x8_3_o0[2]), .B3(nand_or_x8_3_o0[3]),
    .B4(nand_or_x8_3_o0[4]), .B5(nand_or_x8_3_o0[5]), .B6(nand_or_x8_3_o0[6]), .B7(nand_or_x8_3_o0[7]),
    .O0(out_7[0]), .O1(out_7[1]), .O2(out_7[2]), .O3(out_7[3]), .O4(out_7[4]), .O5(out_7[5]), .O6(out_7[6]),
    .O7(out_7[7]));
endmodule

module BUS_OR_x2 (
  input  [7:0] in_1,
  input  [7:0] in_2,
  output [7:0] out_3
);

  NAND_OR_x8 nand_or_x8_1 (
    .A0(in_1[0]), .A1(in_1[1]), .A2(in_1[2]), .A3(in_1[3]), .A4(in_1[4]), .A5(in_1[5]), .A6(in_1[6]),
    .A7(in_1[7]), .B0(in_2[0]), .B1(in_2[1]), .B2(in_2[2]), .B3(in_2[3]), .B4(in_2[4]), .B5(in_2[5]),
    .B6(in_2[6]), .B7(in_2[7]), .O0(out_3[0]), .O1(out_3[1]), .O2(out_3[2]), .O3(out_3[3]), .O4(out_3[4]),
    .O5(out_3[5]), .O6(out_3[6]), .O7(out_3[7]));
endmodule

module BUS_NAND_MUX_x8_2 (
  input  Selector,
  input  [7:0] A,
  input  [7:0] B,
  output [7:0] O
);

  wire nand_1_out, nand_2_out, nand_3_out, nand_4_out, nand_5_out, nand_6_out, nand_7_out, nand_8_out,
       nand_9_out, nand_10_out, nand_11_out, nand_12_out, nand_13_out, nand_14_out, nand_15_out, nand_16_out,
       nand_17_out;

  nand nand_1 (nand_1_out, Selector, Selector);
  nand nand_2 (nand_2_out, A[0], nand_1_out);
  nand nand_3 (nand_3_out, A[1], nand_1_out);
  nand nand_4 (nand_4_out, A[2], nand_1_out);
  nand nand_5 (nand_5_out, A[3], nand_1_out);
  nand nand_6 (nand_6_out, A[4], nand_1_out);
  nand nand_7 (nand_7_out, A[5], nand_1_out);
  nand nand_8 (nand_8_out, A[6], nand_1_out);
  nand nand_9 (nand_9_out, A[7], nand_1_out);
  nand nand_10 (nand_10_out, B[0], Selector);
  nand nand_11 (nand_11_out, B[1], Selector);
  nand nand_12 (nand_12_out, B[2], Selector);
  nand nand_13 (nand_13_out, B[3], Selector);
  nand nand_14 (nand_14_out, B[4], Selector);
  nand nand_15 (nand_15_out, B[5], Selector);
  nand nand_16 (nand_16_out, B[6], Selector);
  nand nand_17 (nand_17_out, B[7], Selector);
  nand nand_18 (O[0], nand_2_out, nand_10_out);
  nand nand_19 (O[1], nand_3_out, nand_11_out);
  nand nand_20 (O[2], nand_4_out, nand_12_out);
  nand nand_21 (O[3], nand_5_out, nand_13_out);
  nand nand_22 (O[4], nand_6_out, nand_14_out);
  nand nand_23 (O[5], nand_7_out, nand_15_out);
  nand nand_24 (O[6], nand_8_out, nand_16_out);
  nand nand_25 (O[7], nand_9_out, nand_17_out);
endmodule

module NAND_Reg_x4 (
  input  D0,
  input  D1,
  input  D2,
  input  D3,
  input  RST,
  input  CLK,
  output O0,
  output O1,
  output O2,
  output O3
);

  NAND_DFF nand_dff_1 (.Din(D0), .Clk(CLK), .Rst(RST), .data(O0));
  NAND_DFF nand_dff_2 (.Din(D1), .Clk(CLK), .Rst(RST), .data(O1));
  NAND_DFF nand_dff_3 (.Din(D2), .Clk(CLK), .Rst(RST), .data(O2));
  NAND_DFF nand_dff_4 (.Din(D3), .Clk(CLK), .Rst(RST), .data(O3));
endmodule

module BUS_FLAG_Generator (
  input  [7:0] DATA,
  output ZERO,
  output SIGN
);

  wire nand_1_out, nand_2_out, nand_3_out, nand_4_out, nand_5_out, nand_6_out, nand_7_out, nand_8_out,
       nand_9_out, nand_10_out, nand_11_out, nand_12_out, nand_13_out, nand_14_out, nand_15_out, nand_16_out,
       nand_17_out, nand_18_out, nand_19_out, nand_20_out, nand_21_out;

  nand nand_1 (nand_1_out, DATA[0], DATA[0]);
  nand nand_2 (nand_2_out, DATA[1], DATA[1]);
  nand nand_3 (nand_3_out, DATA[2], DATA[2]);
  nand nand_4 (nand_4_out, DATA[3], DATA[3]);
  nand nand_5 (nand_5_out, DATA[4], DATA[4]);
  nand nand_6 (nand_6_out, DATA[5], DATA[5]);
  nand nand_7 (nand_7_out, DATA[6], DATA[6]);
  nand nand_8 (nand_8_out, DATA[7], DATA[7]);
  nand nand_9 (nand_9_out, nand_1_out, nand_2_out);
  nand nand_10 (nand_10_out, nand_3_out, nand_4_out);
  nand nand_11 (nand_11_out, nand_5_out, nand_6_out);
  nand nand_12 (nand_12_out, nand_7_out, nand_8_out);
  nand nand_13 (nand_13_out, nand_9_out, nand_9_out);
  nand nand_14 (nand_14_out, nand_13_out, nand_15_out);
  nand nand_15 (nand_15_out, nand_10_out, nand_10_out);
  nand nand_16 (nand_16_out, nand_11_out, nand_11_out);
  nand nand_17 (nand_17_out, nand_16_out, nand_18_out);
  nand nand_18 (nand_18_out, nand_12_out, nand_12_out);
  nand nand_19 (nand_19_out, nand_14_out, nand_14_out);
  nand nand_20 (nand_20_out, nand_19_out, nand_21_out);
  nand nand_21 (nand_21_out, nand_17_out, nand_17_out);
  nand nand_22 (ZERO, nand_20_out, nand_20_out);

  assign SIGN = DATA[7];
endmodule

module M_ALL_CPU_M (
  input  [7:0] ROM_Data,
  input  RST,
  input  CLK,
  input  IDReset,
  input  [7:0] Port_Input_0,
  input  [7:0] Port_Input_1,
  input  [7:0] Port_Input_2,
  input  [7:0] Port_Input_3,
  input  [7:0] Port_Input_4,
  input  [7:0] Port_Input_5,
  input  [7:0] Port_Input_6,
  input  [7:0] Port_Input_7,
  output [7:0] Port_Output_0,
  output [7:0] Port_Output_1,
  output [7:0] Port_Output_2,
  output [7:0] Port_Output_3,
  output [7:0] Port_Output_4,
  output [7:0] Port_Output_5,
  output [7:0] Port_Output_6,
  output [7:0] Port_Output_7,
  output [15:0] ROM_Address
);

  wire button_1_out, id_1_clk, id_1_io_load, id_1_io_write, id_1_ram_load, id_1_ram_write, id_1_rega_load,
       id_1_rega_write, id_1_regb_write, id_1_regclk, id_1_rom_addr_select, id_1_rom_increment, nand_1_out,
       nand_2_out, nand_3_out;
  wire [2:0] id_1_alu_mode;
  wire [3:0] alu_x8_1_flag_output, bcd_x8_1_bcd_1, bcd_x8_1_bcd_10, bcd_x8_1_bcd_100, bcd_x8_2_bcd_1,
       bcd_x8_2_bcd_10, bcd_x8_2_bcd_100;
  wire [4:0] id_1_m_timing;
  wire [7:0] alu_x8_1_rega, alu_x8_1_regb, id_1_databus, id_1_io_addr, id_1_m_idr1, id_1_m_idr2, id_1_m_ir,
       id_1_ram_addr;
  wire [15:0] id_1_rom_addr;

  Button button_1 (.out(button_1_out));
  nand nand_1 (nand_1_out, RST, RST);
  nand nand_2 (nand_2_out, nand_1_out, nand_3_out);
  nand nand_3 (nand_3_out, button_1_out, button_1_out);
  ID id_1 (
    .Flag(alu_x8_1_flag_output), .ROM_INPUT(ROM_Data), .RST(nand_2_out), .CLK_Input(CLK),
    .TimingReset(IDReset), .CLK(id_1_clk), .RegCLK(id_1_regclk), .DATABUS(id_1_databus),
    .ALU_Mode(id_1_alu_mode), .RegA_Load(id_1_rega_load), .RegA_Write(id_1_rega_write),
    .RegB_Write(id_1_regb_write), .RAM_Addr(id_1_ram_addr), .RAM_Write(id_1_ram_write),
    .RAM_Load(id_1_ram_load), .IO_Addr(id_1_io_addr), .IO_Load(id_1_io_load), .IO_Write(id_1_io_write),
    .ROM_Addr_Select(id_1_rom_addr_select), .ROM_Addr(id_1_rom_addr), .ROM_Increment(id_1_rom_increment),
    .M_IR(id_1_m_ir), .M_IDR1(id_1_m_idr1), .M_IDR2(id_1_m_idr2), .M_Timing(id_1_m_timing));
  PC pc_1 (
    .SelectAddr(id_1_rom_addr_select), .Addr_In(id_1_rom_addr), .Addr_Change(id_1_rom_increment),
    .RST(nand_2_out), .CLK(id_1_clk), .Addr_OUTPUT(ROM_Address));
  LedBar #(.matrixcols(16)) ledbar_1 (
    .led0(ROM_Address[15]), .led1(ROM_Address[14]), .led2(ROM_Address[13]), .led3(ROM_Address[12]),
    .led4(ROM_Address[11]), .led5(ROM_Address[10]), .led6(ROM_Address[9]), .led7(ROM_Address[8]),
    .led8(ROM_Address[7]), .led9(ROM_Address[6]), .led10(ROM_Address[5]), .led11(ROM_Address[4]),
    .led12(ROM_Address[3]), .led13(ROM_Address[2]), .led14(ROM_Address[1]), .led15(ROM_Address[0]));
  Hex_Digit_Display hex_digit_display_1 (.value(ROM_Address[15:12]));  // open: dp
  Hex_Digit_Display hex_digit_display_2 (.value(ROM_Address[11:8]));  // open: dp
  Hex_Digit_Display hex_digit_display_3 (.value(ROM_Address[7:4]));  // open: dp
  Hex_Digit_Display hex_digit_display_4 (.value(ROM_Address[3:0]));  // open: dp
  Pull_Resistor pull_resistor_1 (.node(id_1_databus));
  LedBar #(.matrixcols(4)) ledbar_2 (
    .led0(alu_x8_1_flag_output[3]), .led1(alu_x8_1_flag_output[2]), .led2(alu_x8_1_flag_output[1]),
    .led3(alu_x8_1_flag_output[0]));
  ALU_x8 alu_x8_1 (
    .RegCLK(id_1_regclk), .Data(id_1_databus), .Mode(id_1_alu_mode), .RegA_Load(id_1_rega_load),
    .RegA_Write(id_1_rega_write), .RegB_Write(id_1_regb_write), .CLR(nand_2_out), .Data_OUTPUT(id_1_databus),
    .Flag_OUTPUT(alu_x8_1_flag_output), .RegA(alu_x8_1_rega), .RegB(alu_x8_1_regb));
  LedBar ledbar_3 (
    .led0(id_1_databus[7]), .led1(id_1_databus[6]), .led2(id_1_databus[5]), .led3(id_1_databus[4]),
    .led4(id_1_databus[3]), .led5(id_1_databus[2]), .led6(id_1_databus[1]), .led7(id_1_databus[0]));
  RAM_Module ram_module_1 (
    .Addr(id_1_ram_addr), .DATA_INPUT(id_1_databus), .RegCLK(id_1_regclk), .Write(id_1_ram_write),
    .Load(id_1_ram_load), .OUTPUT_BUS(id_1_databus));
  LedBar ledbar_4 (
    .led0(id_1_m_ir[7]), .led1(id_1_m_ir[6]), .led2(id_1_m_ir[5]), .led3(id_1_m_ir[4]), .led4(id_1_m_ir[3]),
    .led5(id_1_m_ir[2]), .led6(id_1_m_ir[1]), .led7(id_1_m_ir[0]));
  LedBar ledbar_5 (
    .led0(alu_x8_1_rega[7]), .led1(alu_x8_1_rega[6]), .led2(alu_x8_1_rega[5]), .led3(alu_x8_1_rega[4]),
    .led4(alu_x8_1_rega[3]), .led5(alu_x8_1_rega[2]), .led6(alu_x8_1_rega[1]), .led7(alu_x8_1_rega[0]));
  LedBar ledbar_6 (
    .led0(id_1_m_idr1[7]), .led1(id_1_m_idr1[6]), .led2(id_1_m_idr1[5]), .led3(id_1_m_idr1[4]),
    .led4(id_1_m_idr1[3]), .led5(id_1_m_idr1[2]), .led6(id_1_m_idr1[1]), .led7(id_1_m_idr1[0]));
  PORT_Input_x8 port_input_x8_1 (
    .Address_x8(id_1_io_addr), .Load(id_1_io_load), .IP0(Port_Input_0), .IP1(Port_Input_1),
    .IP2(Port_Input_2), .IP3(Port_Input_3), .IP4(Port_Input_4), .IP5(Port_Input_5), .IP6(Port_Input_6),
    .IP7(Port_Input_7), .DATA_BUS(id_1_databus));
  LedBar ledbar_7 (
    .led0(alu_x8_1_regb[7]), .led1(alu_x8_1_regb[6]), .led2(alu_x8_1_regb[5]), .led3(alu_x8_1_regb[4]),
    .led4(alu_x8_1_regb[3]), .led5(alu_x8_1_regb[2]), .led6(alu_x8_1_regb[1]), .led7(alu_x8_1_regb[0]));
  LedBar ledbar_8 (
    .led0(id_1_m_idr2[7]), .led1(id_1_m_idr2[6]), .led2(id_1_m_idr2[5]), .led3(id_1_m_idr2[4]),
    .led4(id_1_m_idr2[3]), .led5(id_1_m_idr2[2]), .led6(id_1_m_idr2[1]), .led7(id_1_m_idr2[0]));
  Hex_Digit_Display hex_digit_display_5 (.value(bcd_x8_1_bcd_100));  // open: dp
  BCD_x8 bcd_x8_1 (
    .HEX_INPUT(alu_x8_1_rega), .BCD_1(bcd_x8_1_bcd_1), .BCD_10(bcd_x8_1_bcd_10), .BCD_100(bcd_x8_1_bcd_100));
  LedBar #(.matrixcols(5)) ledbar_9 (
    .led0(id_1_m_timing[4]), .led1(id_1_m_timing[3]), .led2(id_1_m_timing[2]), .led3(id_1_m_timing[1]),
    .led4(id_1_m_timing[0]));
  Hex_Digit_Display hex_digit_display_6 (.value(bcd_x8_1_bcd_10));  // open: dp
  Hex_Digit_Display hex_digit_display_7 (.value(bcd_x8_1_bcd_1));  // open: dp
  PORT_Output_x8 port_output_x8_1 (
    .DATA(id_1_databus), .Address_x8(id_1_io_addr), .Write(id_1_io_write), .RegCLK(id_1_regclk),
    .RST(nand_2_out), .OP0(Port_Output_0), .OP1(Port_Output_1), .OP2(Port_Output_2), .OP3(Port_Output_3),
    .OP4(Port_Output_4), .OP5(Port_Output_5), .OP6(Port_Output_6), .OP7(Port_Output_7));
  Hex_Digit_Display hex_digit_display_8 (.value(bcd_x8_2_bcd_100));  // open: dp
  BCD_x8 bcd_x8_2 (
    .HEX_INPUT(alu_x8_1_regb), .BCD_1(bcd_x8_2_bcd_1), .BCD_10(bcd_x8_2_bcd_10), .BCD_100(bcd_x8_2_bcd_100));
  Hex_Digit_Display hex_digit_display_9 (.value(bcd_x8_2_bcd_10));  // open: dp
  Hex_Digit_Display hex_digit_display_10 (.value(bcd_x8_2_bcd_1));  // open: dp
endmodule

module PC (
  input  SelectAddr,
  input  [15:0] Addr_In,
  input  Addr_Change,
  input  RST,
  input  CLK,
  output [15:0] Addr_OUTPUT
);

  wire nand_1_out, nand_2_out;
  wire [7:0] bus_nand_mux_x8_2_1_o, bus_nand_mux_x8_2_2_o;
  wire [15:0] nand_incrementer_x16_1_out_2;

  nand nand_1 (nand_1_out, CLK, Addr_Change);
  NAND_Incrementer_x16 nand_incrementer_x16_1 (.in_1(Addr_OUTPUT), .out_2(nand_incrementer_x16_1_out_2));
  nand nand_2 (nand_2_out, nand_1_out, nand_1_out);
  BUS_NAND_MUX_x8_2 bus_nand_mux_x8_2_1 (
    .Selector(SelectAddr), .A(nand_incrementer_x16_1_out_2[7:0]), .B(Addr_In[7:0]), .O(bus_nand_mux_x8_2_1_o));
  BUS_NAND_MUX_x8_2 bus_nand_mux_x8_2_2 (
    .Selector(SelectAddr), .A(nand_incrementer_x16_1_out_2[15:8]), .B(Addr_In[15:8]),
    .O(bus_nand_mux_x8_2_2_o));
  NAND_Reg_x8 nand_reg_x8_1 (
    .D0(bus_nand_mux_x8_2_1_o[0]), .D1(bus_nand_mux_x8_2_1_o[1]), .D2(bus_nand_mux_x8_2_1_o[2]),
    .D3(bus_nand_mux_x8_2_1_o[3]), .D4(bus_nand_mux_x8_2_1_o[4]), .D5(bus_nand_mux_x8_2_1_o[5]),
    .D6(bus_nand_mux_x8_2_1_o[6]), .D7(bus_nand_mux_x8_2_1_o[7]), .RST(RST), .CLK(nand_2_out),
    .O0(Addr_OUTPUT[0]), .O1(Addr_OUTPUT[1]), .O2(Addr_OUTPUT[2]), .O3(Addr_OUTPUT[3]), .O4(Addr_OUTPUT[4]),
    .O5(Addr_OUTPUT[5]), .O6(Addr_OUTPUT[6]), .O7(Addr_OUTPUT[7]));
  NAND_Reg_x8 nand_reg_x8_2 (
    .D0(bus_nand_mux_x8_2_2_o[0]), .D1(bus_nand_mux_x8_2_2_o[1]), .D2(bus_nand_mux_x8_2_2_o[2]),
    .D3(bus_nand_mux_x8_2_2_o[3]), .D4(bus_nand_mux_x8_2_2_o[4]), .D5(bus_nand_mux_x8_2_2_o[5]),
    .D6(bus_nand_mux_x8_2_2_o[6]), .D7(bus_nand_mux_x8_2_2_o[7]), .RST(RST), .CLK(nand_2_out),
    .O0(Addr_OUTPUT[8]), .O1(Addr_OUTPUT[9]), .O2(Addr_OUTPUT[10]), .O3(Addr_OUTPUT[11]),
    .O4(Addr_OUTPUT[12]), .O5(Addr_OUTPUT[13]), .O6(Addr_OUTPUT[14]), .O7(Addr_OUTPUT[15]));
endmodule

module NAND_Incrementer_x16 (
  input  [15:0] in_1,
  output [15:0] out_2
);

  wire nand_1_out, nand_2_out, nand_3_out, nand_4_out, nand_5_out, nand_6_out, nand_7_out, nand_8_out,
       nand_9_out, nand_10_out, nand_11_out, nand_12_out, nand_13_out, nand_14_out, nand_15_out, nand_16_out,
       nand_17_out, nand_18_out, nand_19_out, nand_20_out, nand_21_out, nand_22_out, nand_23_out,
       nand_24_out, nand_25_out, nand_26_out, nand_27_out, nand_28_out, nand_29_out, nand_30_out,
       nand_31_out, nand_32_out, nand_34_out, nand_35_out, nand_37_out, nand_38_out, nand_40_out,
       nand_41_out, nand_43_out, nand_44_out, nand_46_out, nand_47_out, nand_49_out, nand_50_out,
       nand_52_out, nand_53_out, nand_55_out, nand_56_out, nand_58_out, nand_59_out, nand_61_out,
       nand_62_out, nand_64_out, nand_65_out, nand_67_out, nand_68_out, nand_70_out, nand_71_out,
       nand_73_out, nand_74_out, nand_76_out, nand_77_out, nand_79_out;

  nand nand_1 (nand_1_out, 1'b1, in_1[0]);
  nand nand_2 (nand_2_out, nand_1_out, nand_1_out);
  nand nand_3 (nand_3_out, nand_2_out, in_1[1]);
  nand nand_4 (nand_4_out, nand_3_out, nand_3_out);
  nand nand_5 (nand_5_out, nand_4_out, in_1[2]);
  nand nand_6 (nand_6_out, nand_5_out, nand_5_out);
  nand nand_7 (nand_7_out, nand_6_out, in_1[3]);
  nand nand_8 (nand_8_out, nand_7_out, nand_7_out);
  nand nand_9 (nand_9_out, nand_8_out, in_1[4]);
  nand nand_10 (nand_10_out, nand_9_out, nand_9_out);
  nand nand_11 (nand_11_out, nand_10_out, in_1[5]);
  nand nand_12 (nand_12_out, nand_11_out, nand_11_out);
  nand nand_13 (nand_13_out, nand_12_out, in_1[6]);
  nand nand_14 (nand_14_out, nand_13_out, nand_13_out);
  nand nand_15 (nand_15_out, nand_14_out, in_1[7]);
  nand nand_16 (nand_16_out, nand_15_out, nand_15_out);
  nand nand_17 (nand_17_out, nand_16_out, in_1[8]);
  nand nand_18 (nand_18_out, nand_17_out, nand_17_out);
  nand nand_19 (nand_19_out, nand_18_out, in_1[9]);
  nand nand_20 (nand_20_out, nand_19_out, nand_19_out);
  nand nand_21 (nand_21_out, nand_20_out, in_1[10]);
  nand nand_22 (nand_22_out, nand_21_out, nand_21_out);
  nand nand_23 (nand_23_out, nand_22_out, in_1[11]);
  nand nand_24 (nand_24_out, nand_23_out, nand_23_out);
  nand nand_25 (nand_25_out, nand_24_out, in_1[12]);
  nand nand_26 (nand_26_out, nand_25_out, nand_25_out);
  nand nand_27 (nand_27_out, nand_26_out, in_1[13]);
  nand nand_28 (nand_28_out, nand_27_out, nand_27_out);
  nand nand_29 (nand_29_out, nand_28_out, in_1[14]);
  nand nand_30 (nand_30_out, nand_29_out, nand_29_out);
  nand nand_31 (nand_31_out, nand_30_out, in_1[15]);
  nand nand_32 (nand_32_out, 1'b1, nand_1_out);
  nand nand_33 (out_2[0], nand_32_out, nand_34_out);
  nand nand_34 (nand_34_out, nand_1_out, in_1[0]);
  nand nand_35 (nand_35_out, nand_2_out, nand_3_out);
  nand nand_36 (out_2[1], nand_35_out, nand_37_out);
  nand nand_37 (nand_37_out, nand_3_out, in_1[1]);
  nand nand_38 (nand_38_out, nand_4_out, nand_5_out);
  nand nand_39 (out_2[2], nand_38_out, nand_40_out);
  nand nand_40 (nand_40_out, nand_5_out, in_1[2]);
  nand nand_41 (nand_41_out, nand_6_out, nand_7_out);
  nand nand_42 (out_2[3], nand_41_out, nand_43_out);
  nand nand_43 (nand_43_out, nand_7_out, in_1[3]);
  nand nand_44 (nand_44_out, nand_8_out, nand_9_out);
  nand nand_45 (out_2[4], nand_44_out, nand_46_out);
  nand nand_46 (nand_46_out, nand_9_out, in_1[4]);
  nand nand_47 (nand_47_out, nand_10_out, nand_11_out);
  nand nand_48 (out_2[5], nand_47_out, nand_49_out);
  nand nand_49 (nand_49_out, nand_11_out, in_1[5]);
  nand nand_50 (nand_50_out, nand_12_out, nand_13_out);
  nand nand_51 (out_2[6], nand_50_out, nand_52_out);
  nand nand_52 (nand_52_out, nand_13_out, in_1[6]);
  nand nand_53 (nand_53_out, nand_14_out, nand_15_out);
  nand nand_54 (out_2[7], nand_53_out, nand_55_out);
  nand nand_55 (nand_55_out, nand_15_out, in_1[7]);
  nand nand_56 (nand_56_out, nand_16_out, nand_17_out);
  nand nand_57 (out_2[8], nand_56_out, nand_58_out);
  nand nand_58 (nand_58_out, nand_17_out, in_1[8]);
  nand nand_59 (nand_59_out, nand_18_out, nand_19_out);
  nand nand_60 (out_2[9], nand_59_out, nand_61_out);
  nand nand_61 (nand_61_out, nand_19_out, in_1[9]);
  nand nand_62 (nand_62_out, nand_20_out, nand_21_out);
  nand nand_63 (out_2[10], nand_62_out, nand_64_out);
  nand nand_64 (nand_64_out, nand_21_out, in_1[10]);
  nand nand_65 (nand_65_out, nand_22_out, nand_23_out);
  nand nand_66 (out_2[11], nand_65_out, nand_67_out);
  nand nand_67 (nand_67_out, nand_23_out, in_1[11]);
  nand nand_68 (nand_68_out, nand_24_out, nand_25_out);
  nand nand_69 (out_2[12], nand_68_out, nand_70_out);
  nand nand_70 (nand_70_out, nand_25_out, in_1[12]);
  nand nand_71 (nand_71_out, nand_26_out, nand_27_out);
  nand nand_72 (out_2[13], nand_71_out, nand_73_out);
  nand nand_73 (nand_73_out, nand_27_out, in_1[13]);
  nand nand_74 (nand_74_out, nand_28_out, nand_29_out);
  nand nand_75 (out_2[14], nand_74_out, nand_76_out);
  nand nand_76 (nand_76_out, nand_29_out, in_1[14]);
  nand nand_77 (nand_77_out, nand_30_out, nand_31_out);
  nand nand_78 (out_2[15], nand_77_out, nand_79_out);
  nand nand_79 (nand_79_out, nand_31_out, in_1[15]);
endmodule

module ID (
  input  [3:0] Flag,
  input  [7:0] ROM_INPUT,
  input  RST,
  input  CLK_Input,
  input  TimingReset,
  output CLK,
  output RegCLK,
  output [7:0] DATABUS,
  output [2:0] ALU_Mode,
  output RegA_Load,
  output RegA_Write,
  output RegB_Write,
  output [7:0] RAM_Addr,
  output RAM_Write,
  output RAM_Load,
  output [7:0] IO_Addr,
  output IO_Load,
  output IO_Write,
  output ROM_Addr_Select,
  output [15:0] ROM_Addr,
  output ROM_Increment,
  output [7:0] M_IR,
  output [7:0] M_IDR1,
  output [7:0] M_IDR2,
  output [4:0] M_Timing
);

  wire ALU_ADD, ALU_AND, ALU_DWSHIFT, ALU_EXOR, ALU_OR, ALU_SUB, ALU_UPSHIFT, BUS_Load_Reg1_Buf,
       BUS_Load_Reg2_Buf, id_mux_x3_1_alu, id_mux_x3_1_jump, id_mux_x3_1_mov, InstRegWrite, JNP_JA, JNP_JBE,
       JNP_JC, JNP_JE, JNP_JG, JNP_JGE, JNP_JL, JNP_JLE, JNP_JNP, JNP_JO, JNP_JS, MOV_AfIO, MOV_AfRAM,
       MOV_AfROM, MOV_BfA, MOV_BfIO, MOV_BfRAM, MOV_BfROM, MOV_IOfA, MOV_IOfRAM, MOV_IOfROM, MOV_RAMfA,
       MOV_RAMfIO, MOV_RAMfROM, nand_2_out, nand_3_out, nand_4_out, nand_5_out, nand_6_out, nand_7_out,
       nand_8_out, nand_9_out, nand_10_out, nand_11_out, nand_13_out, nand_15_out, nand_17_out, nand_19_out,
       nand_21_out, nand_22_out, nand_23_out, nand_24_out, nand_25_out, nand_26_out, nand_27_out,
       nand_28_out, nand_29_out, nand_30_out, nand_31_out, nand_32_out, nand_33_out, nand_34_out,
       nand_35_out, nand_36_out, nand_37_out, nand_38_out, nand_39_out, nand_40_out, nand_41_out,
       nand_42_out, nand_43_out, nand_44_out, nand_45_out, nand_46_out, nand_47_out, nand_48_out,
       nand_49_out, nand_50_out, nand_51_out, nand_52_out, nand_53_out, nand_54_out, nand_55_out,
       nand_56_out, nand_57_out, nand_58_out, nand_59_out, nand_60_out, nand_61_out, nand_62_out,
       nand_63_out, nand_64_out, nand_65_out, nand_66_out, nand_67_out, nand_68_out, nand_69_out,
       nand_70_out, nand_71_out, nand_72_out, nand_73_out, nand_74_out, nand_75_out, nand_76_out,
       nand_77_out, nand_78_out, nand_79_out, nand_80_out, nand_81_out, nand_82_out, nand_83_out,
       nand_84_out, nand_85_out, nand_86_out, nand_87_out, nand_88_out, nand_89_out, nand_90_out,
       nand_91_out, nand_92_out, nand_93_out, nand_94_out, nand_95_out, nand_96_out, nand_97_out,
       nand_98_out, nand_99_out, nand_100_out, nand_101_out, nand_102_out, nand_103_out, nand_104_out,
       nand_105_out, nand_106_out, nand_107_out, nand_108_out, nand_109_out, nand_110_out, nand_111_out,
       nand_112_out, nand_113_out, nand_114_out, nand_115_out, nand_116_out, nand_117_out, nand_118_out,
       nand_119_out, nand_120_out, nand_121_out, nand_122_out, nand_123_out, nand_124_out, nand_125_out,
       nand_126_out, nand_127_out, nand_128_out, nand_129_out, nand_130_out, nand_131_out, nand_132_out,
       nand_133_out, nand_134_out, nand_135_out, nand_136_out, nand_137_out, nand_138_out, nand_139_out,
       nand_140_out, nand_141_out, nand_142_out, nand_143_out, nand_144_out, nand_145_out, nand_146_out,
       nand_147_out, nand_148_out, nand_149_out, nand_150_out, nand_151_out, nand_152_out, nand_153_out,
       nand_154_out, nand_155_out, nand_156_out, nand_157_out, nand_158_out, nand_159_out, nand_160_out,
       nand_161_out, nand_162_out, nand_163_out, nand_169_out, nand_170_out, nand_171_out, nand_172_out,
       nand_173_out, nand_174_out, nand_175_out, nand_176_out, nand_177_out, nand_178_out, nand_179_out,
       nand_180_out, nand_181_out, nand_182_out, nand_183_out, nand_184_out, nand_185_out, nand_186_out,
       nand_187_out, nand_188_out, nand_189_out, nand_190_out, nand_191_out, nand_192_out, nand_193_out,
       nand_194_out, nand_195_out, nand_196_out, nand_197_out, nand_198_out, nand_199_out, nand_200_out,
       nand_201_out, nand_202_out, nand_203_out, nand_204_out, nand_205_out, nand_206_out, nand_207_out,
       nand_208_out, nand_209_out, nand_210_out, nand_211_out, nand_212_out, nand_213_out, nand_214_out,
       nand_215_out, nand_216_out, nand_217_out, nand_218_out, nand_219_out, nand_220_out, nand_221_out,
       nand_222_out, nand_223_out, nand_224_out, nand_225_out, nand_226_out, nand_227_out, nand_228_out,
       nand_229_out, nand_230_out, nand_231_out, nand_232_out, nand_233_out, nand_234_out, nand_235_out,
       nand_236_out, nand_237_out, nand_238_out, nand_239_out, nand_240_out, nand_241_out, nand_242_out,
       nand_243_out, nand_244_out, nand_245_out, nand_246_out, nand_247_out, nand_248_out, nand_249_out,
       nand_250_out, nand_251_out, nand_252_out, nand_253_out, nand_254_out, nand_255_out, nand_256_out,
       nand_257_out, nand_258_out, nand_259_out, nand_260_out, nand_261_out, nand_262_out, nand_263_out,
       nand_264_out, nand_265_out, nand_266_out, nand_267_out, nand_268_out, nand_269_out, nand_270_out,
       nand_271_out, nand_272_out, nand_273_out, nand_274_out, nand_275_out, nand_276_out, nand_277_out,
       nand_278_out, nand_279_out, nand_280_out, nand_281_out, nand_282_out, nand_283_out, nand_284_out,
       nand_285_out, nand_286_out, nand_287_out, nand_288_out, nand_289_out, nand_290_out, nand_291_out,
       nand_292_out, nand_293_out, nand_294_out, nand_295_out, nand_296_out, nand_297_out, nand_298_out,
       nand_299_out, nand_300_out, nand_301_out, nand_302_out, nand_303_out, nand_304_out, nand_305_out,
       nand_306_out, nand_307_out, nand_308_out, nand_309_out, nand_310_out, Reg1_W_Buf, Reg2_W_Buf,
       ROM_Addr_Select_Buf, ROM_Increment_Buf, Start, t0, t1, t2, t3, t4, TimingReset_Buf, undriven;
  wire [4:0] id_mux_x3_1_dw_x5;
  wire [31:7] id_mux_x5_2_output_x32;
  wire [31:11] id_mux_x5_3_output_x32;
  wire [31:14] id_mux_x5_1_output_x32;

  Pull_Resistor pull_resistor_1 (.node(Reg1_W_Buf));
  Pull_Resistor pull_resistor_2 (.node(Reg2_W_Buf));
  Pull_Resistor pull_resistor_3 (.node(ROM_Increment_Buf));
  Pull_Resistor pull_resistor_4 (.node(ROM_Addr_Select_Buf));
  Pull_Resistor pull_resistor_5 (.node(TimingReset_Buf));
  nand nand_1 (RegCLK, CLK_Input, CLK_Input);
  nand nand_2 (nand_2_out, InstRegWrite, RegCLK);
  nand nand_3 (nand_3_out, Reg1_W_Buf, RegCLK);
  nand nand_4 (nand_4_out, Reg2_W_Buf, RegCLK);
  nand nand_5 (nand_5_out, TimingReset, TimingReset);
  nand nand_6 (nand_6_out, nand_5_out, nand_7_out);
  nand nand_7 (nand_7_out, TimingReset_Buf, TimingReset_Buf);
  assign DATABUS[7] = BUS_Load_Reg1_Buf ? M_IDR1[7] : 1'bz;  // Controlled_Buffer controlled_buffer_1
  assign DATABUS[6] = BUS_Load_Reg1_Buf ? M_IDR1[6] : 1'bz;  // Controlled_Buffer controlled_buffer_2
  assign DATABUS[7] = BUS_Load_Reg2_Buf ? IO_Addr[7] : 1'bz;  // Controlled_Buffer controlled_buffer_3
  assign DATABUS[6] = BUS_Load_Reg2_Buf ? IO_Addr[6] : 1'bz;  // Controlled_Buffer controlled_buffer_4
  nand nand_8 (nand_8_out, nand_2_out, nand_2_out);
  nand nand_9 (nand_9_out, nand_3_out, nand_3_out);
  nand nand_10 (nand_10_out, nand_4_out, nand_4_out);
  assign DATABUS[5] = BUS_Load_Reg1_Buf ? M_IDR1[5] : 1'bz;  // Controlled_Buffer controlled_buffer_5
  assign DATABUS[4] = BUS_Load_Reg1_Buf ? M_IDR1[4] : 1'bz;  // Controlled_Buffer controlled_buffer_6
  assign DATABUS[5] = BUS_Load_Reg2_Buf ? IO_Addr[5] : 1'bz;  // Controlled_Buffer controlled_buffer_7
  assign DATABUS[4] = BUS_Load_Reg2_Buf ? IO_Addr[4] : 1'bz;  // Controlled_Buffer controlled_buffer_8
  Pull_Resistor pull_resistor_6 (.node(ALU_Mode));
  Pull_Resistor pull_resistor_7 (.node(RegA_Load));
  Pull_Resistor pull_resistor_8 (.node(RegA_Write));
  Pull_Resistor pull_resistor_9 (.node(RegB_Write));
  Pull_Resistor pull_resistor_10 (.node(RAM_Write));
  Pull_Resistor pull_resistor_11 (.node(RAM_Load));
  Pull_Resistor pull_resistor_12 (.node(IO_Load));
  Pull_Resistor pull_resistor_13 (.node(IO_Write));
  Pull_Resistor pull_resistor_14 (.node(ROM_Addr_Select));
  nand nand_11 (nand_11_out, 1'b1, t0);
  nand nand_12 (M_Timing[0], nand_11_out, nand_11_out);
  nand nand_13 (nand_13_out, 1'b1, t1);
  nand nand_14 (M_Timing[1], nand_13_out, nand_13_out);
  nand nand_15 (nand_15_out, 1'b1, t2);
  nand nand_16 (M_Timing[2], nand_15_out, nand_15_out);
  nand nand_17 (nand_17_out, 1'b1, t3);
  nand nand_18 (M_Timing[3], nand_17_out, nand_17_out);
  nand nand_19 (nand_19_out, 1'b1, t4);
  nand nand_20 (M_Timing[4], nand_19_out, nand_19_out);
  assign DATABUS[3] = BUS_Load_Reg1_Buf ? M_IDR1[3] : 1'bz;  // Controlled_Buffer controlled_buffer_9
  assign DATABUS[2] = BUS_Load_Reg1_Buf ? M_IDR1[2] : 1'bz;  // Controlled_Buffer controlled_buffer_10
  assign DATABUS[3] = BUS_Load_Reg2_Buf ? IO_Addr[3] : 1'bz;  // Controlled_Buffer controlled_buffer_11
  assign DATABUS[2] = BUS_Load_Reg2_Buf ? IO_Addr[2] : 1'bz;  // Controlled_Buffer controlled_buffer_12
  assign DATABUS[1] = BUS_Load_Reg1_Buf ? M_IDR1[1] : 1'bz;  // Controlled_Buffer controlled_buffer_13
  assign DATABUS[0] = BUS_Load_Reg1_Buf ? M_IDR1[0] : 1'bz;  // Controlled_Buffer controlled_buffer_14
  assign DATABUS[1] = BUS_Load_Reg2_Buf ? IO_Addr[1] : 1'bz;  // Controlled_Buffer controlled_buffer_15
  assign DATABUS[0] = BUS_Load_Reg2_Buf ? IO_Addr[0] : 1'bz;  // Controlled_Buffer controlled_buffer_16
  ID_BUS_Reg_x8 id_bus_reg_x8_1 (.lINPUT_x8(ROM_INPUT), .RST(RST), .CLK(nand_8_out), .OUTPUT_x8(M_IR));
  ID_BUS_Reg_x8 id_bus_reg_x8_2 (.lINPUT_x8(ROM_INPUT), .RST(RST), .CLK(nand_9_out), .OUTPUT_x8(M_IDR1));
  ID_BUS_Reg_x8 id_bus_reg_x8_3 (.lINPUT_x8(ROM_INPUT), .RST(RST), .CLK(nand_10_out), .OUTPUT_x8(IO_Addr));
  NAND_DFF nand_dff_1 (.Din(ROM_Increment_Buf), .Clk(RegCLK), .Rst(RST), .data(ROM_Increment));
  NAND_DFF nand_dff_2 (.Din(ROM_Addr_Select_Buf), .Clk(RegCLK), .Rst(RST), .data(ROM_Addr_Select));
  ID_TimingController id_timingcontroller_1 (
    .ReSet(nand_6_out), .CLR(RST), .CLK(CLK_Input), .t0(InstRegWrite), .t1(t0), .t2(t1), .t3(t2), .t4(t3),
    .t5(t4));
  Pull_Resistor pull_resistor_15 (.node(BUS_Load_Reg1_Buf));
  Pull_Resistor pull_resistor_16 (.node(BUS_Load_Reg2_Buf));
  ID_MUX_x3 id_mux_x3_1 (
    .InstructionData(M_IR), .DW_x5(id_mux_x3_1_dw_x5), .MOV(id_mux_x3_1_mov), .ALU(id_mux_x3_1_alu),
    .JUMP(id_mux_x3_1_jump));
  LedBar #(.matrixcols(5)) ledbar_1 (
    .led0(id_mux_x3_1_dw_x5[4]), .led1(id_mux_x3_1_dw_x5[3]), .led2(id_mux_x3_1_dw_x5[2]),
    .led3(id_mux_x3_1_dw_x5[1]), .led4(id_mux_x3_1_dw_x5[0]));
  ID_MUX_x5 id_mux_x5_1 (
    .Gate(id_mux_x3_1_mov), .INPUT_x5(id_mux_x3_1_dw_x5),
    .OUTPUT_x32({id_mux_x5_1_output_x32, MOV_IOfROM, MOV_IOfRAM, MOV_IOfA, MOV_RAMfIO, MOV_BfIO, MOV_AfIO, MOV_RAMfA, MOV_RAMfROM, MOV_BfRAM, MOV_BfROM, MOV_BfA, MOV_AfRAM, MOV_AfROM, Start}));
  nand nand_21 (nand_21_out, Start, t1);
  nand nand_22 (nand_22_out, MOV_AfROM, t0);
  nand nand_23 (nand_23_out, MOV_AfROM, t1);
  nand nand_24 (nand_24_out, MOV_AfROM, t2);
  nand nand_25 (nand_25_out, MOV_AfROM, t3);
  nand nand_26 (nand_26_out, MOV_AfRAM, t0);
  nand nand_27 (nand_27_out, MOV_AfRAM, t1);
  nand nand_28 (nand_28_out, MOV_AfRAM, t2);
  nand nand_29 (nand_29_out, MOV_AfRAM, t3);
  nand nand_30 (nand_30_out, MOV_BfA, t1);
  nand nand_31 (nand_31_out, MOV_BfA, t2);
  nand nand_32 (nand_32_out, MOV_BfROM, t0);
  nand nand_33 (nand_33_out, MOV_BfROM, t1);
  nand nand_34 (nand_34_out, MOV_BfROM, t2);
  nand nand_35 (nand_35_out, MOV_BfROM, t3);
  nand nand_36 (nand_36_out, MOV_BfRAM, t0);
  nand nand_37 (nand_37_out, MOV_BfRAM, t1);
  nand nand_38 (nand_38_out, MOV_BfRAM, t2);
  nand nand_39 (nand_39_out, MOV_BfRAM, t3);
  nand nand_40 (nand_40_out, MOV_RAMfROM, t0);
  nand nand_41 (nand_41_out, MOV_RAMfROM, t1);
  nand nand_42 (nand_42_out, MOV_RAMfROM, t2);
  nand nand_43 (nand_43_out, MOV_RAMfROM, t3);
  nand nand_44 (nand_44_out, MOV_RAMfROM, t4);
  nand nand_45 (nand_45_out, MOV_RAMfA, t0);
  nand nand_46 (nand_46_out, MOV_RAMfA, t1);
  nand nand_47 (nand_47_out, MOV_RAMfA, t2);
  nand nand_48 (nand_48_out, MOV_RAMfA, t3);
  nand nand_49 (nand_49_out, MOV_AfIO, t0);
  nand nand_50 (nand_50_out, MOV_AfIO, t1);
  nand nand_51 (nand_51_out, MOV_AfIO, t2);
  nand nand_52 (nand_52_out, MOV_AfIO, t3);
  nand nand_53 (nand_53_out, MOV_BfIO, t0);
  nand nand_54 (nand_54_out, MOV_BfIO, t1);
  nand nand_55 (nand_55_out, MOV_BfIO, t2);
  nand nand_56 (nand_56_out, MOV_BfIO, t3);
  nand nand_57 (nand_57_out, MOV_RAMfIO, t0);
  nand nand_58 (nand_58_out, MOV_RAMfIO, t1);
  nand nand_59 (nand_59_out, MOV_RAMfIO, t2);
  nand nand_60 (nand_60_out, MOV_RAMfIO, t3);
  nand nand_61 (nand_61_out, MOV_RAMfIO, t4);
  nand nand_62 (nand_62_out, MOV_IOfA, t0);
  nand nand_63 (nand_63_out, MOV_IOfA, t1);
  nand nand_64 (nand_64_out, MOV_IOfA, t2);
  nand nand_65 (nand_65_out, MOV_IOfA, t3);
  nand nand_66 (nand_66_out, MOV_IOfRAM, t0);
  nand nand_67 (nand_67_out, MOV_IOfRAM, t1);
  nand nand_68 (nand_68_out, MOV_IOfRAM, t2);
  nand nand_69 (nand_69_out, MOV_IOfRAM, t3);
  nand nand_70 (nand_70_out, MOV_IOfRAM, t4);
  nand nand_71 (nand_71_out, MOV_IOfROM, t0);
  nand nand_72 (nand_72_out, MOV_IOfROM, t1);
  nand nand_73 (nand_73_out, MOV_IOfROM, t2);
  nand nand_74 (nand_74_out, MOV_IOfROM, t3);
  nand nand_75 (nand_75_out, MOV_IOfROM, t4);
  nand nand_76 (nand_76_out, nand_21_out, nand_21_out);
  assign TimingReset_Buf = nand_76_out ? nand_76_out : 1'bz;  // Controlled_Buffer controlled_buffer_17
  assign ROM_Increment_Buf = nand_76_out ? nand_76_out : 1'bz;  // Controlled_Buffer controlled_buffer_18
  nand nand_77 (nand_77_out, nand_22_out, nand_22_out);
  assign ROM_Increment_Buf = nand_77_out ? nand_77_out : 1'bz;  // Controlled_Buffer controlled_buffer_19
  nand nand_78 (nand_78_out, nand_23_out, nand_23_out);
  assign Reg1_W_Buf = nand_78_out ? nand_78_out : 1'bz;  // Controlled_Buffer controlled_buffer_20
  assign BUS_Load_Reg1_Buf = nand_79_out ? nand_79_out : 1'bz;  // Controlled_Buffer controlled_buffer_21
  nand nand_79 (nand_79_out, nand_24_out, nand_24_out);
  assign RegA_Write = nand_79_out ? nand_79_out : 1'bz;  // Controlled_Buffer controlled_buffer_22
  nand nand_80 (nand_80_out, nand_25_out, nand_25_out);
  assign TimingReset_Buf = nand_80_out ? nand_80_out : 1'bz;  // Controlled_Buffer controlled_buffer_23
  assign ROM_Increment_Buf = nand_80_out ? nand_80_out : 1'bz;  // Controlled_Buffer controlled_buffer_24
  nand nand_81 (nand_81_out, nand_26_out, nand_26_out);
  assign ROM_Increment_Buf = nand_81_out ? nand_81_out : 1'bz;  // Controlled_Buffer controlled_buffer_25
  nand nand_82 (nand_82_out, nand_27_out, nand_27_out);
  assign Reg1_W_Buf = nand_82_out ? nand_82_out : 1'bz;  // Controlled_Buffer controlled_buffer_26
  nand nand_83 (nand_83_out, nand_28_out, nand_28_out);
  assign RAM_Load = nand_83_out ? nand_83_out : 1'bz;  // Controlled_Buffer controlled_buffer_27
  assign RegA_Write = nand_83_out ? nand_83_out : 1'bz;  // Controlled_Buffer controlled_buffer_28
  nand nand_84 (nand_84_out, nand_29_out, nand_29_out);
  assign TimingReset_Buf = nand_84_out ? nand_84_out : 1'bz;  // Controlled_Buffer controlled_buffer_29
  assign ROM_Increment_Buf = nand_84_out ? nand_84_out : 1'bz;  // Controlled_Buffer controlled_buffer_30
  assign RegA_Load = nand_85_out ? nand_85_out : 1'bz;  // Controlled_Buffer controlled_buffer_31
  nand nand_85 (nand_85_out, nand_30_out, nand_30_out);
  assign RegB_Write = nand_85_out ? nand_85_out : 1'bz;  // Controlled_Buffer controlled_buffer_32
  assign ROM_Increment_Buf = nand_86_out ? nand_86_out : 1'bz;  // Controlled_Buffer controlled_buffer_33
  nand nand_86 (nand_86_out, nand_31_out, nand_31_out);
  assign TimingReset_Buf = nand_86_out ? nand_86_out : 1'bz;  // Controlled_Buffer controlled_buffer_34
  nand nand_87 (nand_87_out, nand_32_out, nand_32_out);
  assign ROM_Increment_Buf = nand_87_out ? nand_87_out : 1'bz;  // Controlled_Buffer controlled_buffer_35
  nand nand_88 (nand_88_out, nand_33_out, nand_33_out);
  assign Reg1_W_Buf = nand_88_out ? nand_88_out : 1'bz;  // Controlled_Buffer controlled_buffer_36
  assign BUS_Load_Reg1_Buf = nand_89_out ? nand_89_out : 1'bz;  // Controlled_Buffer controlled_buffer_37
  nand nand_89 (nand_89_out, nand_34_out, nand_34_out);
  assign RegB_Write = nand_89_out ? nand_89_out : 1'bz;  // Controlled_Buffer controlled_buffer_38
  nand nand_90 (nand_90_out, nand_35_out, nand_35_out);
  assign TimingReset_Buf = nand_90_out ? nand_90_out : 1'bz;  // Controlled_Buffer controlled_buffer_39
  assign ROM_Increment_Buf = nand_90_out ? nand_90_out : 1'bz;  // Controlled_Buffer controlled_buffer_40
  nand nand_91 (nand_91_out, nand_36_out, nand_36_out);
  assign ROM_Increment_Buf = nand_91_out ? nand_91_out : 1'bz;  // Controlled_Buffer controlled_buffer_41
  nand nand_92 (nand_92_out, nand_37_out, nand_37_out);
  assign Reg1_W_Buf = nand_92_out ? nand_92_out : 1'bz;  // Controlled_Buffer controlled_buffer_42
  nand nand_93 (nand_93_out, nand_38_out, nand_38_out);
  assign RAM_Load = nand_93_out ? nand_93_out : 1'bz;  // Controlled_Buffer controlled_buffer_43
  assign RegB_Write = nand_93_out ? nand_93_out : 1'bz;  // Controlled_Buffer controlled_buffer_44
  nand nand_94 (nand_94_out, nand_39_out, nand_39_out);
  assign TimingReset_Buf = nand_94_out ? nand_94_out : 1'bz;  // Controlled_Buffer controlled_buffer_45
  assign ROM_Increment_Buf = nand_94_out ? nand_94_out : 1'bz;  // Controlled_Buffer controlled_buffer_46
  nand nand_95 (nand_95_out, nand_40_out, nand_40_out);
  assign ROM_Increment_Buf = nand_95_out ? nand_95_out : 1'bz;  // Controlled_Buffer controlled_buffer_47
  assign Reg1_W_Buf = nand_96_out ? nand_96_out : 1'bz;  // Controlled_Buffer controlled_buffer_48
  nand nand_96 (nand_96_out, nand_41_out, nand_41_out);
  assign ROM_Increment_Buf = nand_96_out ? nand_96_out : 1'bz;  // Controlled_Buffer controlled_buffer_49
  nand nand_97 (nand_97_out, nand_42_out, nand_42_out);
  assign Reg2_W_Buf = nand_97_out ? nand_97_out : 1'bz;  // Controlled_Buffer controlled_buffer_50
  nand nand_98 (nand_98_out, nand_43_out, nand_43_out);
  assign BUS_Load_Reg2_Buf = nand_98_out ? nand_98_out : 1'bz;  // Controlled_Buffer controlled_buffer_51
  assign RAM_Write = nand_98_out ? nand_98_out : 1'bz;  // Controlled_Buffer controlled_buffer_52
  nand nand_99 (nand_99_out, nand_44_out, nand_44_out);
  assign TimingReset_Buf = nand_99_out ? nand_99_out : 1'bz;  // Controlled_Buffer controlled_buffer_53
  assign ROM_Increment_Buf = nand_99_out ? nand_99_out : 1'bz;  // Controlled_Buffer controlled_buffer_54
  nand nand_100 (nand_100_out, nand_45_out, nand_45_out);
  assign ROM_Increment_Buf = nand_100_out ? nand_100_out : 1'bz;  // Controlled_Buffer controlled_buffer_55
  nand nand_101 (nand_101_out, nand_46_out, nand_46_out);
  assign Reg1_W_Buf = nand_101_out ? nand_101_out : 1'bz;  // Controlled_Buffer controlled_buffer_56
  nand nand_102 (nand_102_out, nand_47_out, nand_47_out);
  assign RegA_Load = nand_102_out ? nand_102_out : 1'bz;  // Controlled_Buffer controlled_buffer_57
  assign RAM_Write = nand_102_out ? nand_102_out : 1'bz;  // Controlled_Buffer controlled_buffer_58
  nand nand_103 (nand_103_out, nand_48_out, nand_48_out);
  assign TimingReset_Buf = nand_103_out ? nand_103_out : 1'bz;  // Controlled_Buffer controlled_buffer_59
  assign ROM_Increment_Buf = nand_103_out ? nand_103_out : 1'bz;  // Controlled_Buffer controlled_buffer_60
  nand nand_104 (nand_104_out, nand_49_out, nand_49_out);
  assign ROM_Increment_Buf = nand_104_out ? nand_104_out : 1'bz;  // Controlled_Buffer controlled_buffer_61
  nand nand_105 (nand_105_out, nand_50_out, nand_50_out);
  assign Reg2_W_Buf = nand_105_out ? nand_105_out : 1'bz;  // Controlled_Buffer controlled_buffer_62
  nand nand_106 (nand_106_out, nand_51_out, nand_51_out);
  assign IO_Load = nand_106_out ? nand_106_out : 1'bz;  // Controlled_Buffer controlled_buffer_63
  assign RegA_Write = nand_106_out ? nand_106_out : 1'bz;  // Controlled_Buffer controlled_buffer_64
  nand nand_107 (nand_107_out, nand_52_out, nand_52_out);
  assign TimingReset_Buf = nand_107_out ? nand_107_out : 1'bz;  // Controlled_Buffer controlled_buffer_65
  assign ROM_Increment_Buf = nand_107_out ? nand_107_out : 1'bz;  // Controlled_Buffer controlled_buffer_66
  nand nand_108 (nand_108_out, nand_53_out, nand_53_out);
  assign ROM_Increment_Buf = nand_108_out ? nand_108_out : 1'bz;  // Controlled_Buffer controlled_buffer_67
  nand nand_109 (nand_109_out, nand_54_out, nand_54_out);
  assign Reg2_W_Buf = nand_109_out ? nand_109_out : 1'bz;  // Controlled_Buffer controlled_buffer_68
  nand nand_110 (nand_110_out, nand_55_out, nand_55_out);
  assign IO_Load = nand_110_out ? nand_110_out : 1'bz;  // Controlled_Buffer controlled_buffer_69
  assign RegB_Write = nand_110_out ? nand_110_out : 1'bz;  // Controlled_Buffer controlled_buffer_70
  nand nand_111 (nand_111_out, nand_56_out, nand_56_out);
  assign TimingReset_Buf = nand_111_out ? nand_111_out : 1'bz;  // Controlled_Buffer controlled_buffer_71
  assign ROM_Increment_Buf = nand_111_out ? nand_111_out : 1'bz;  // Controlled_Buffer controlled_buffer_72
  nand nand_112 (nand_112_out, nand_57_out, nand_57_out);
  assign ROM_Increment_Buf = nand_112_out ? nand_112_out : 1'bz;  // Controlled_Buffer controlled_buffer_73
  nand nand_113 (nand_113_out, nand_58_out, nand_58_out);
  assign Reg1_W_Buf = nand_113_out ? nand_113_out : 1'bz;  // Controlled_Buffer controlled_buffer_74
  assign ROM_Increment_Buf = nand_113_out ? nand_113_out : 1'bz;  // Controlled_Buffer controlled_buffer_75
  nand nand_114 (nand_114_out, nand_59_out, nand_59_out);
  assign Reg2_W_Buf = nand_114_out ? nand_114_out : 1'bz;  // Controlled_Buffer controlled_buffer_76
  nand nand_115 (nand_115_out, nand_60_out, nand_60_out);
  assign RAM_Write = nand_115_out ? nand_115_out : 1'bz;  // Controlled_Buffer controlled_buffer_77
  assign IO_Load = nand_115_out ? nand_115_out : 1'bz;  // Controlled_Buffer controlled_buffer_78
  nand nand_116 (nand_116_out, nand_61_out, nand_61_out);
  assign TimingReset_Buf = nand_116_out ? nand_116_out : 1'bz;  // Controlled_Buffer controlled_buffer_79
  assign ROM_Increment_Buf = nand_116_out ? nand_116_out : 1'bz;  // Controlled_Buffer controlled_buffer_80
  nand nand_117 (nand_117_out, nand_62_out, nand_62_out);
  assign ROM_Increment_Buf = nand_117_out ? nand_117_out : 1'bz;  // Controlled_Buffer controlled_buffer_81
  nand nand_118 (nand_118_out, nand_63_out, nand_63_out);
  assign Reg2_W_Buf = nand_118_out ? nand_118_out : 1'bz;  // Controlled_Buffer controlled_buffer_82
  nand nand_119 (nand_119_out, nand_64_out, nand_64_out);
  assign RegA_Load = nand_119_out ? nand_119_out : 1'bz;  // Controlled_Buffer controlled_buffer_83
  assign IO_Write = nand_119_out ? nand_119_out : 1'bz;  // Controlled_Buffer controlled_buffer_84
  nand nand_120 (nand_120_out, nand_65_out, nand_65_out);
  assign TimingReset_Buf = nand_120_out ? nand_120_out : 1'bz;  // Controlled_Buffer controlled_buffer_85
  assign ROM_Increment_Buf = nand_120_out ? nand_120_out : 1'bz;  // Controlled_Buffer controlled_buffer_86
  nand nand_121 (nand_121_out, nand_66_out, nand_66_out);
  assign ROM_Increment_Buf = nand_121_out ? nand_121_out : 1'bz;  // Controlled_Buffer controlled_buffer_87
  nand nand_122 (nand_122_out, nand_67_out, nand_67_out);
  assign Reg2_W_Buf = nand_122_out ? nand_122_out : 1'bz;  // Controlled_Buffer controlled_buffer_88
  assign ROM_Increment_Buf = nand_122_out ? nand_122_out : 1'bz;  // Controlled_Buffer controlled_buffer_89
  nand nand_123 (nand_123_out, nand_68_out, nand_68_out);
  assign Reg1_W_Buf = nand_123_out ? nand_123_out : 1'bz;  // Controlled_Buffer controlled_buffer_90
  nand nand_124 (nand_124_out, nand_69_out, nand_69_out);
  assign RAM_Load = nand_124_out ? nand_124_out : 1'bz;  // Controlled_Buffer controlled_buffer_91
  assign IO_Write = nand_124_out ? nand_124_out : 1'bz;  // Controlled_Buffer controlled_buffer_92
  nand nand_125 (nand_125_out, nand_70_out, nand_70_out);
  assign TimingReset_Buf = nand_125_out ? nand_125_out : 1'bz;  // Controlled_Buffer controlled_buffer_93
  assign ROM_Increment_Buf = nand_125_out ? nand_125_out : 1'bz;  // Controlled_Buffer controlled_buffer_94
  nand nand_126 (nand_126_out, nand_71_out, nand_71_out);
  assign ROM_Increment_Buf = nand_126_out ? nand_126_out : 1'bz;  // Controlled_Buffer controlled_buffer_95
  nand nand_127 (nand_127_out, nand_72_out, nand_72_out);
  assign Reg2_W_Buf = nand_127_out ? nand_127_out : 1'bz;  // Controlled_Buffer controlled_buffer_96
  assign ROM_Increment_Buf = nand_127_out ? nand_127_out : 1'bz;  // Controlled_Buffer controlled_buffer_97
  nand nand_128 (nand_128_out, nand_73_out, nand_73_out);
  assign Reg1_W_Buf = nand_128_out ? nand_128_out : 1'bz;  // Controlled_Buffer controlled_buffer_98
  nand nand_129 (nand_129_out, nand_74_out, nand_74_out);
  assign BUS_Load_Reg1_Buf = nand_129_out ? nand_129_out : 1'bz;  // Controlled_Buffer controlled_buffer_99
  assign IO_Write = nand_129_out ? nand_129_out : 1'bz;  // Controlled_Buffer controlled_buffer_100
  nand nand_130 (nand_130_out, nand_75_out, nand_75_out);
  assign TimingReset_Buf = nand_130_out ? nand_130_out : 1'bz;  // Controlled_Buffer controlled_buffer_101
  assign ROM_Increment_Buf = nand_130_out ? nand_130_out : 1'bz;  // Controlled_Buffer controlled_buffer_102
  ID_MUX_x5 id_mux_x5_2 (
    .Gate(id_mux_x3_1_alu), .INPUT_x5(id_mux_x3_1_dw_x5),
    .OUTPUT_x32({id_mux_x5_2_output_x32, ALU_DWSHIFT, ALU_UPSHIFT, ALU_EXOR, ALU_OR, ALU_AND, ALU_SUB, ALU_ADD}));
  ID_MUX_x5 id_mux_x5_3 (
    .Gate(id_mux_x3_1_jump), .INPUT_x5(id_mux_x3_1_dw_x5),
    .OUTPUT_x32({id_mux_x5_3_output_x32, JNP_JS, JNP_JO, JNP_JLE, JNP_JL, JNP_JGE, JNP_JG, JNP_JBE, JNP_JA, JNP_JE, JNP_JC, JNP_JNP}));
  nand nand_131 (nand_131_out, ALU_ADD, t1);
  nand nand_132 (nand_132_out, nand_131_out, nand_131_out);
  nand nand_133 (nand_133_out, ALU_ADD, t2);
  nand nand_134 (nand_134_out, nand_133_out, nand_133_out);
  nand nand_135 (nand_135_out, ALU_SUB, t1);
  nand nand_136 (nand_136_out, nand_135_out, nand_135_out);
  nand nand_137 (nand_137_out, ALU_SUB, t2);
  nand nand_138 (nand_138_out, nand_137_out, nand_137_out);
  nand nand_139 (nand_139_out, ALU_AND, t1);
  nand nand_140 (nand_140_out, nand_139_out, nand_139_out);
  nand nand_141 (nand_141_out, ALU_AND, t2);
  nand nand_142 (nand_142_out, nand_141_out, nand_141_out);
  nand nand_143 (nand_143_out, ALU_OR, t1);
  nand nand_144 (nand_144_out, nand_143_out, nand_143_out);
  nand nand_145 (nand_145_out, ALU_OR, t2);
  nand nand_146 (nand_146_out, nand_145_out, nand_145_out);
  nand nand_147 (nand_147_out, ALU_EXOR, t1);
  nand nand_148 (nand_148_out, nand_147_out, nand_147_out);
  nand nand_149 (nand_149_out, ALU_EXOR, t2);
  nand nand_150 (nand_150_out, nand_149_out, nand_149_out);
  nand nand_151 (nand_151_out, ALU_UPSHIFT, t1);
  nand nand_152 (nand_152_out, nand_151_out, nand_151_out);
  nand nand_153 (nand_153_out, ALU_UPSHIFT, t2);
  nand nand_154 (nand_154_out, nand_153_out, nand_153_out);
  nand nand_155 (nand_155_out, ALU_DWSHIFT, t1);
  nand nand_156 (nand_156_out, nand_155_out, nand_155_out);
  nand nand_157 (nand_157_out, ALU_DWSHIFT, t2);
  nand nand_158 (nand_158_out, nand_157_out, nand_157_out);
  assign ALU_Mode[0] = nand_132_out ? nand_132_out : 1'bz;  // Controlled_Buffer controlled_buffer_103
  assign RegA_Write = nand_132_out ? nand_132_out : 1'bz;  // Controlled_Buffer controlled_buffer_104
  assign TimingReset_Buf = nand_134_out ? nand_134_out : 1'bz;  // Controlled_Buffer controlled_buffer_105
  assign ROM_Increment_Buf = nand_134_out ? nand_134_out : 1'bz;  // Controlled_Buffer controlled_buffer_106
  assign ALU_Mode[1] = nand_136_out ? nand_136_out : 1'bz;  // Controlled_Buffer controlled_buffer_107
  assign RegA_Write = nand_136_out ? nand_136_out : 1'bz;  // Controlled_Buffer controlled_buffer_108
  assign TimingReset_Buf = nand_138_out ? nand_138_out : 1'bz;  // Controlled_Buffer controlled_buffer_109
  assign ROM_Increment_Buf = nand_138_out ? nand_138_out : 1'bz;  // Controlled_Buffer controlled_buffer_110
  assign ALU_Mode[0] = nand_140_out ? nand_140_out : 1'bz;  // Controlled_Buffer controlled_buffer_111
  assign ALU_Mode[1] = nand_140_out ? nand_140_out : 1'bz;  // Controlled_Buffer controlled_buffer_112
  assign RegA_Write = nand_140_out ? nand_140_out : 1'bz;  // Controlled_Buffer controlled_buffer_113
  assign TimingReset_Buf = nand_142_out ? nand_142_out : 1'bz;  // Controlled_Buffer controlled_buffer_114
  assign ROM_Increment_Buf = nand_142_out ? nand_142_out : 1'bz;  // Controlled_Buffer controlled_buffer_115
  assign ALU_Mode[2] = nand_144_out ? nand_144_out : 1'bz;  // Controlled_Buffer controlled_buffer_116
  assign RegA_Write = nand_144_out ? nand_144_out : 1'bz;  // Controlled_Buffer controlled_buffer_117
  assign TimingReset_Buf = nand_146_out ? nand_146_out : 1'bz;  // Controlled_Buffer controlled_buffer_118
  assign ROM_Increment_Buf = nand_146_out ? nand_146_out : 1'bz;  // Controlled_Buffer controlled_buffer_119
  assign ALU_Mode[0] = nand_148_out ? nand_148_out : 1'bz;  // Controlled_Buffer controlled_buffer_120
  assign ALU_Mode[2] = nand_148_out ? nand_148_out : 1'bz;  // Controlled_Buffer controlled_buffer_121
  assign RegA_Write = nand_148_out ? nand_148_out : 1'bz;  // Controlled_Buffer controlled_buffer_122
  assign TimingReset_Buf = nand_150_out ? nand_150_out : 1'bz;  // Controlled_Buffer controlled_buffer_123
  assign ROM_Increment_Buf = nand_150_out ? nand_150_out : 1'bz;  // Controlled_Buffer controlled_buffer_124
  assign ALU_Mode[1] = nand_152_out ? nand_152_out : 1'bz;  // Controlled_Buffer controlled_buffer_125
  assign ALU_Mode[2] = nand_152_out ? nand_152_out : 1'bz;  // Controlled_Buffer controlled_buffer_126
  assign RegA_Write = nand_152_out ? nand_152_out : 1'bz;  // Controlled_Buffer controlled_buffer_127
  assign TimingReset_Buf = nand_154_out ? nand_154_out : 1'bz;  // Controlled_Buffer controlled_buffer_128
  assign ROM_Increment_Buf = nand_154_out ? nand_154_out : 1'bz;  // Controlled_Buffer controlled_buffer_129
  assign ALU_Mode[0] = nand_156_out ? nand_156_out : 1'bz;  // Controlled_Buffer controlled_buffer_130
  assign ALU_Mode[1] = nand_156_out ? nand_156_out : 1'bz;  // Controlled_Buffer controlled_buffer_131
  assign ALU_Mode[2] = nand_156_out ? nand_156_out : 1'bz;  // Controlled_Buffer controlled_buffer_132
  assign RegA_Write = nand_156_out ? nand_156_out : 1'bz;  // Controlled_Buffer controlled_buffer_133
  assign TimingReset_Buf = nand_158_out ? nand_158_out : 1'bz;  // Controlled_Buffer controlled_buffer_134
  assign ROM_Increment_Buf = nand_158_out ? nand_158_out : 1'bz;  // Controlled_Buffer controlled_buffer_135
  nand nand_159 (nand_159_out, undriven, t0);
  nand nand_160 (nand_160_out, undriven, t1);
  nand nand_161 (nand_161_out, undriven, t2);
  nand nand_162 (nand_162_out, undriven, t3);
  nand nand_163 (nand_163_out, undriven, t4);
  // NAND_Gate nand_164 has open pins: in0=nand_159_out, in1=nand_159_out, out=open
  // NAND_Gate nand_165 has open pins: in0=nand_160_out, in1=nand_160_out, out=open
  // NAND_Gate nand_166 has open pins: in0=nand_161_out, in1=nand_161_out, out=open
  // NAND_Gate nand_167 has open pins: in0=nand_162_out, in1=nand_162_out, out=open
  // NAND_Gate nand_168 has open pins: in0=nand_163_out, in1=nand_163_out, out=open
  nand nand_169 (nand_169_out, JNP_JNP, t0);
  nand nand_170 (nand_170_out, JNP_JNP, t1);
  nand nand_171 (nand_171_out, JNP_JNP, t2);
  nand nand_172 (nand_172_out, JNP_JNP, t3);
  nand nand_173 (nand_173_out, JNP_JNP, t4);
  nand nand_174 (nand_174_out, JNP_JC, t0);
  nand nand_175 (nand_175_out, JNP_JC, t1);
  nand nand_176 (nand_176_out, JNP_JC, t2);
  nand nand_177 (nand_177_out, JNP_JC, t3);
  nand nand_178 (nand_178_out, JNP_JC, t4);
  nand nand_179 (nand_179_out, JNP_JE, t0);
  nand nand_180 (nand_180_out, JNP_JE, t1);
  nand nand_181 (nand_181_out, JNP_JE, t2);
  nand nand_182 (nand_182_out, JNP_JE, t3);
  nand nand_183 (nand_183_out, JNP_JA, t0);
  nand nand_184 (nand_184_out, JNP_JA, t1);
  nand nand_185 (nand_185_out, JNP_JA, t2);
  nand nand_186 (nand_186_out, JNP_JA, t3);
  nand nand_187 (nand_187_out, JNP_JBE, t0);
  nand nand_188 (nand_188_out, JNP_JBE, t1);
  nand nand_189 (nand_189_out, JNP_JBE, t2);
  nand nand_190 (nand_190_out, JNP_JBE, t3);
  nand nand_191 (nand_191_out, JNP_JG, t0);
  nand nand_192 (nand_192_out, JNP_JG, t1);
  nand nand_193 (nand_193_out, JNP_JG, t2);
  nand nand_194 (nand_194_out, JNP_JG, t3);
  nand nand_195 (nand_195_out, JNP_JGE, t0);
  nand nand_196 (nand_196_out, JNP_JGE, t1);
  nand nand_197 (nand_197_out, JNP_JGE, t2);
  nand nand_198 (nand_198_out, JNP_JGE, t3);
  nand nand_199 (nand_199_out, JNP_JL, t0);
  nand nand_200 (nand_200_out, JNP_JL, t1);
  nand nand_201 (nand_201_out, JNP_JL, t2);
  nand nand_202 (nand_202_out, JNP_JL, t3);
  nand nand_203 (nand_203_out, JNP_JLE, t0);
  nand nand_204 (nand_204_out, JNP_JLE, t1);
  nand nand_205 (nand_205_out, JNP_JLE, t2);
  nand nand_206 (nand_206_out, JNP_JLE, t3);
  nand nand_207 (nand_207_out, JNP_JO, t0);
  nand nand_208 (nand_208_out, JNP_JO, t1);
  nand nand_209 (nand_209_out, JNP_JO, t2);
  nand nand_210 (nand_210_out, JNP_JS, t0);
  nand nand_211 (nand_211_out, JNP_JS, t1);
  nand nand_212 (nand_212_out, JNP_JS, t2);
  nand nand_213 (nand_213_out, JNP_JS, t3);
  nand nand_214 (nand_214_out, nand_169_out, nand_169_out);
  nand nand_215 (nand_215_out, nand_170_out, nand_170_out);
  nand nand_216 (nand_216_out, nand_171_out, nand_171_out);
  nand nand_217 (nand_217_out, nand_172_out, nand_172_out);
  nand nand_218 (nand_218_out, nand_173_out, nand_173_out);
  nand nand_219 (nand_219_out, nand_174_out, nand_174_out);
  nand nand_220 (nand_220_out, nand_175_out, nand_175_out);
  nand nand_221 (nand_221_out, nand_176_out, nand_176_out);
  nand nand_222 (nand_222_out, nand_177_out, nand_177_out);
  nand nand_223 (nand_223_out, nand_178_out, nand_178_out);
  nand nand_224 (nand_224_out, nand_179_out, nand_179_out);
  nand nand_225 (nand_225_out, nand_180_out, nand_180_out);
  nand nand_226 (nand_226_out, nand_181_out, nand_181_out);
  nand nand_227 (nand_227_out, nand_182_out, nand_182_out);
  nand nand_228 (nand_228_out, nand_183_out, nand_183_out);
  nand nand_229 (nand_229_out, nand_184_out, nand_184_out);
  nand nand_230 (nand_230_out, nand_185_out, nand_185_out);
  nand nand_231 (nand_231_out, nand_186_out, nand_186_out);
  nand nand_232 (nand_232_out, nand_187_out, nand_187_out);
  nand nand_233 (nand_233_out, nand_188_out, nand_188_out);
  nand nand_234 (nand_234_out, nand_189_out, nand_189_out);
  nand nand_235 (nand_235_out, nand_190_out, nand_190_out);
  nand nand_236 (nand_236_out, nand_191_out, nand_191_out);
  nand nand_237 (nand_237_out, nand_192_out, nand_192_out);
  nand nand_238 (nand_238_out, nand_193_out, nand_193_out);
  nand nand_239 (nand_239_out, nand_194_out, nand_194_out);
  nand nand_240 (nand_240_out, nand_195_out, nand_195_out);
  nand nand_241 (nand_241_out, nand_196_out, nand_196_out);
  nand nand_242 (nand_242_out, nand_197_out, nand_197_out);
  nand nand_243 (nand_243_out, nand_198_out, nand_198_out);
  nand nand_244 (nand_244_out, nand_199_out, nand_199_out);
  nand nand_245 (nand_245_out, nand_200_out, nand_200_out);
  nand nand_246 (nand_246_out, nand_201_out, nand_201_out);
  nand nand_247 (nand_247_out, nand_202_out, nand_202_out);
  nand nand_248 (nand_248_out, nand_203_out, nand_203_out);
  nand nand_249 (nand_249_out, nand_204_out, nand_204_out);
  nand nand_250 (nand_250_out, nand_205_out, nand_205_out);
  nand nand_251 (nand_251_out, nand_206_out, nand_206_out);
  nand nand_252 (nand_252_out, nand_207_out, nand_207_out);
  nand nand_253 (nand_253_out, nand_208_out, nand_208_out);
  nand nand_254 (nand_254_out, nand_209_out, nand_209_out);
  nand nand_255 (nand_255_out, JNP_JO, t3);
  nand nand_256 (nand_256_out, nand_255_out, nand_255_out);
  nand nand_257 (nand_257_out, nand_210_out, nand_210_out);
  nand nand_258 (nand_258_out, nand_211_out, nand_211_out);
  nand nand_259 (nand_259_out, nand_212_out, nand_212_out);
  nand nand_260 (nand_260_out, nand_213_out, nand_213_out);
  assign ROM_Increment_Buf = nand_214_out ? nand_214_out : 1'bz;  // Controlled_Buffer controlled_buffer_136
  assign Reg1_W_Buf = nand_215_out ? nand_215_out : 1'bz;  // Controlled_Buffer controlled_buffer_137
  assign ROM_Increment_Buf = nand_215_out ? nand_215_out : 1'bz;  // Controlled_Buffer controlled_buffer_138
  assign Reg2_W_Buf = nand_216_out ? nand_216_out : 1'bz;  // Controlled_Buffer controlled_buffer_139
  assign ROM_Addr_Select_Buf = nand_217_out ? nand_217_out : 1'bz;  // Controlled_Buffer controlled_buffer_140
  assign ROM_Increment_Buf = nand_217_out ? nand_217_out : 1'bz;  // Controlled_Buffer controlled_buffer_141
  assign TimingReset_Buf = nand_218_out ? nand_218_out : 1'bz;  // Controlled_Buffer controlled_buffer_142
  assign ROM_Increment_Buf = nand_219_out ? nand_219_out : 1'bz;  // Controlled_Buffer controlled_buffer_143
  assign Reg1_W_Buf = nand_220_out ? nand_220_out : 1'bz;  // Controlled_Buffer controlled_buffer_144
  assign ROM_Increment_Buf = nand_220_out ? nand_220_out : 1'bz;  // Controlled_Buffer controlled_buffer_145
  assign Reg2_W_Buf = nand_221_out ? nand_221_out : 1'bz;  // Controlled_Buffer controlled_buffer_146
  assign ROM_Increment_Buf = nand_222_out ? nand_222_out : 1'bz;  // Controlled_Buffer controlled_buffer_147
  assign TimingReset_Buf = nand_223_out ? nand_223_out : 1'bz;  // Controlled_Buffer controlled_buffer_148
  assign ROM_Increment_Buf = nand_224_out ? nand_224_out : 1'bz;  // Controlled_Buffer controlled_buffer_149
  assign Reg1_W_Buf = nand_225_out ? nand_225_out : 1'bz;  // Controlled_Buffer controlled_buffer_150
  assign ROM_Increment_Buf = nand_225_out ? nand_225_out : 1'bz;  // Controlled_Buffer controlled_buffer_151
  assign Reg2_W_Buf = nand_226_out ? nand_226_out : 1'bz;  // Controlled_Buffer controlled_buffer_152
  assign TimingReset_Buf = nand_227_out ? nand_227_out : 1'bz;  // Controlled_Buffer controlled_buffer_153
  assign ROM_Increment_Buf = nand_227_out ? nand_227_out : 1'bz;  // Controlled_Buffer controlled_buffer_154
  assign ROM_Increment_Buf = nand_228_out ? nand_228_out : 1'bz;  // Controlled_Buffer controlled_buffer_155
  assign Reg1_W_Buf = nand_229_out ? nand_229_out : 1'bz;  // Controlled_Buffer controlled_buffer_156
  assign ROM_Increment_Buf = nand_229_out ? nand_229_out : 1'bz;  // Controlled_Buffer controlled_buffer_157
  assign Reg2_W_Buf = nand_230_out ? nand_230_out : 1'bz;  // Controlled_Buffer controlled_buffer_158
  nand nand_261 (nand_261_out, Flag[0], Flag[0]);
  nand nand_262 (nand_262_out, Flag[2], Flag[2]);
  assign TimingReset_Buf = nand_231_out ? nand_231_out : 1'bz;  // Controlled_Buffer controlled_buffer_159
  assign ROM_Increment_Buf = nand_231_out ? nand_231_out : 1'bz;  // Controlled_Buffer controlled_buffer_160
  assign ROM_Increment_Buf = nand_232_out ? nand_232_out : 1'bz;  // Controlled_Buffer controlled_buffer_161
  assign Reg1_W_Buf = nand_233_out ? nand_233_out : 1'bz;  // Controlled_Buffer controlled_buffer_162
  assign ROM_Increment_Buf = nand_233_out ? nand_233_out : 1'bz;  // Controlled_Buffer controlled_buffer_163
  assign Reg2_W_Buf = nand_234_out ? nand_234_out : 1'bz;  // Controlled_Buffer controlled_buffer_164
  assign TimingReset_Buf = nand_235_out ? nand_235_out : 1'bz;  // Controlled_Buffer controlled_buffer_165
  assign ROM_Increment_Buf = nand_235_out ? nand_235_out : 1'bz;  // Controlled_Buffer controlled_buffer_166
  assign ROM_Increment_Buf = nand_236_out ? nand_236_out : 1'bz;  // Controlled_Buffer controlled_buffer_167
  assign Reg1_W_Buf = nand_237_out ? nand_237_out : 1'bz;  // Controlled_Buffer controlled_buffer_168
  assign ROM_Increment_Buf = nand_237_out ? nand_237_out : 1'bz;  // Controlled_Buffer controlled_buffer_169
  Controlled_Buffer controlled_buffer_170 (.in(nand_238_out), .out(Reg2_W_Buf));  // open: en
  nand nand_263 (nand_263_out, Flag[1], Flag[3]);
  assign TimingReset_Buf = nand_239_out ? nand_239_out : 1'bz;  // Controlled_Buffer controlled_buffer_171
  assign ROM_Increment_Buf = nand_239_out ? nand_239_out : 1'bz;  // Controlled_Buffer controlled_buffer_172
  assign ROM_Increment_Buf = nand_240_out ? nand_240_out : 1'bz;  // Controlled_Buffer controlled_buffer_173
  assign Reg1_W_Buf = nand_241_out ? nand_241_out : 1'bz;  // Controlled_Buffer controlled_buffer_174
  assign ROM_Increment_Buf = nand_241_out ? nand_241_out : 1'bz;  // Controlled_Buffer controlled_buffer_175
  assign Reg2_W_Buf = nand_242_out ? nand_242_out : 1'bz;  // Controlled_Buffer controlled_buffer_176
  nand nand_264 (nand_264_out, Flag[1], Flag[3]);
  assign TimingReset_Buf = nand_243_out ? nand_243_out : 1'bz;  // Controlled_Buffer controlled_buffer_177
  assign ROM_Increment_Buf = nand_243_out ? nand_243_out : 1'bz;  // Controlled_Buffer controlled_buffer_178
  assign ROM_Increment_Buf = nand_244_out ? nand_244_out : 1'bz;  // Controlled_Buffer controlled_buffer_179
  assign Reg1_W_Buf = nand_245_out ? nand_245_out : 1'bz;  // Controlled_Buffer controlled_buffer_180
  assign ROM_Increment_Buf = nand_245_out ? nand_245_out : 1'bz;  // Controlled_Buffer controlled_buffer_181
  assign Reg2_W_Buf = nand_246_out ? nand_246_out : 1'bz;  // Controlled_Buffer controlled_buffer_182
  assign TimingReset_Buf = nand_247_out ? nand_247_out : 1'bz;  // Controlled_Buffer controlled_buffer_183
  assign ROM_Increment_Buf = nand_247_out ? nand_247_out : 1'bz;  // Controlled_Buffer controlled_buffer_184
  assign ROM_Increment_Buf = nand_248_out ? nand_248_out : 1'bz;  // Controlled_Buffer controlled_buffer_185
  assign Reg1_W_Buf = nand_249_out ? nand_249_out : 1'bz;  // Controlled_Buffer controlled_buffer_186
  assign ROM_Increment_Buf = nand_249_out ? nand_249_out : 1'bz;  // Controlled_Buffer controlled_buffer_187
  assign Reg2_W_Buf = nand_250_out ? nand_250_out : 1'bz;  // Controlled_Buffer controlled_buffer_188
  nand nand_265 (nand_265_out, Flag[1], Flag[3]);
  assign TimingReset_Buf = nand_251_out ? nand_251_out : 1'bz;  // Controlled_Buffer controlled_buffer_189
  assign ROM_Increment_Buf = nand_251_out ? nand_251_out : 1'bz;  // Controlled_Buffer controlled_buffer_190
  assign ROM_Increment_Buf = nand_252_out ? nand_252_out : 1'bz;  // Controlled_Buffer controlled_buffer_191
  assign Reg1_W_Buf = nand_253_out ? nand_253_out : 1'bz;  // Controlled_Buffer controlled_buffer_192
  assign ROM_Increment_Buf = nand_253_out ? nand_253_out : 1'bz;  // Controlled_Buffer controlled_buffer_193
  assign Reg2_W_Buf = nand_254_out ? nand_254_out : 1'bz;  // Controlled_Buffer controlled_buffer_194
  assign TimingReset_Buf = nand_256_out ? nand_256_out : 1'bz;  // Controlled_Buffer controlled_buffer_195
  assign ROM_Increment_Buf = nand_256_out ? nand_256_out : 1'bz;  // Controlled_Buffer controlled_buffer_196
  assign ROM_Increment_Buf = nand_257_out ? nand_257_out : 1'bz;  // Controlled_Buffer controlled_buffer_197
  assign Reg1_W_Buf = nand_258_out ? nand_258_out : 1'bz;  // Controlled_Buffer controlled_buffer_198
  assign ROM_Increment_Buf = nand_258_out ? nand_258_out : 1'bz;  // Controlled_Buffer controlled_buffer_199
  assign Reg2_W_Buf = nand_259_out ? nand_259_out : 1'bz;  // Controlled_Buffer controlled_buffer_200
  assign TimingReset_Buf = nand_260_out ? nand_260_out : 1'bz;  // Controlled_Buffer controlled_buffer_201
  assign ROM_Increment_Buf = nand_260_out ? nand_260_out : 1'bz;  // Controlled_Buffer controlled_buffer_202
  nand nand_266 (nand_266_out, Flag[2], nand_222_out);
  nand nand_267 (nand_267_out, nand_266_out, nand_266_out);
  nand nand_268 (nand_268_out, Flag[0], nand_227_out);
  nand nand_269 (nand_269_out, nand_268_out, nand_268_out);
  nand nand_270 (nand_270_out, nand_261_out, nand_262_out);
  nand nand_271 (nand_271_out, Flag[2], Flag[2]);
  nand nand_272 (nand_272_out, nand_271_out, nand_273_out);
  nand nand_273 (nand_273_out, Flag[0], Flag[0]);
  nand nand_274 (nand_274_out, Flag[1], nand_263_out);
  nand nand_275 (nand_275_out, nand_263_out, Flag[3]);
  nand nand_276 (nand_276_out, Flag[1], nand_264_out);
  nand nand_277 (nand_277_out, nand_276_out, nand_278_out);
  nand nand_278 (nand_278_out, nand_264_out, Flag[3]);
  nand nand_279 (nand_279_out, Flag[1], nand_280_out);
  nand nand_280 (nand_280_out, Flag[1], Flag[3]);
  nand nand_281 (nand_281_out, nand_280_out, Flag[3]);
  nand nand_282 (nand_282_out, Flag[1], nand_265_out);
  nand nand_283 (nand_283_out, nand_265_out, Flag[3]);
  nand nand_284 (nand_284_out, Flag[3], nand_256_out);
  nand nand_285 (nand_285_out, nand_284_out, nand_284_out);
  nand nand_286 (nand_286_out, Flag[1], nand_260_out);
  nand nand_287 (nand_287_out, nand_286_out, nand_286_out);
  assign ROM_Addr_Select_Buf = nand_267_out ? nand_267_out : 1'bz;  // Controlled_Buffer controlled_buffer_203
  assign ROM_Addr_Select_Buf = nand_269_out ? nand_269_out : 1'bz;  // Controlled_Buffer controlled_buffer_204
  nand nand_288 (nand_288_out, nand_270_out, nand_270_out);
  nand nand_289 (nand_289_out, nand_288_out, nand_231_out);
  nand nand_290 (nand_290_out, nand_272_out, nand_235_out);
  nand nand_291 (nand_291_out, nand_274_out, nand_275_out);
  nand nand_292 (nand_292_out, nand_291_out, nand_291_out);
  nand nand_293 (nand_293_out, Flag[0], Flag[0]);
  nand nand_294 (nand_294_out, nand_277_out, nand_277_out);
  nand nand_295 (nand_295_out, nand_279_out, nand_281_out);
  nand nand_296 (nand_296_out, nand_282_out, nand_283_out);
  nand nand_297 (nand_297_out, nand_296_out, Flag[0]);
  assign ROM_Addr_Select_Buf = nand_285_out ? nand_285_out : 1'bz;  // Controlled_Buffer controlled_buffer_205
  assign ROM_Addr_Select_Buf = nand_287_out ? nand_287_out : 1'bz;  // Controlled_Buffer controlled_buffer_206
  nand nand_298 (nand_298_out, nand_289_out, nand_289_out);
  assign ROM_Addr_Select_Buf = nand_298_out ? nand_298_out : 1'bz;  // Controlled_Buffer controlled_buffer_207
  nand nand_299 (nand_299_out, nand_290_out, nand_290_out);
  assign ROM_Addr_Select_Buf = nand_299_out ? nand_299_out : 1'bz;  // Controlled_Buffer controlled_buffer_208
  nand nand_300 (nand_300_out, nand_292_out, nand_293_out);
  nand nand_301 (nand_301_out, nand_300_out, nand_300_out);
  nand nand_302 (nand_302_out, nand_294_out, nand_243_out);
  nand nand_303 (nand_303_out, nand_302_out, nand_302_out);
  nand nand_304 (nand_304_out, nand_295_out, nand_247_out);
  nand nand_305 (nand_305_out, nand_304_out, nand_304_out);
  nand nand_306 (nand_306_out, nand_297_out, nand_297_out);
  nand nand_307 (nand_307_out, nand_306_out, nand_251_out);
  nand nand_308 (nand_308_out, nand_301_out, nand_239_out);
  assign ROM_Addr_Select_Buf = nand_303_out ? nand_303_out : 1'bz;  // Controlled_Buffer controlled_buffer_209
  assign ROM_Addr_Select_Buf = nand_305_out ? nand_305_out : 1'bz;  // Controlled_Buffer controlled_buffer_210
  nand nand_309 (nand_309_out, nand_307_out, nand_307_out);
  nand nand_310 (nand_310_out, nand_308_out, nand_308_out);
  assign ROM_Addr_Select_Buf = nand_310_out ? nand_310_out : 1'bz;  // Controlled_Buffer controlled_buffer_211
  assign ROM_Addr_Select_Buf = nand_309_out ? nand_309_out : 1'bz;  // Controlled_Buffer controlled_buffer_212

  assign CLK = CLK_Input;
  assign M_IDR2 = IO_Addr;
  assign RAM_Addr = M_IDR1;
  assign ROM_Addr = {M_IDR1, IO_Addr};

  // Other names for the same wires on the sheet: ALU_Mode_Buf[2:0] = ALU_Mode; Flag_Zero = Flag[0];
  //   Flag_Sign = Flag[1]; Flag_OverCarry = Flag[2]; Flag_OverFlow = Flag[3]; IO_Load_Buf = IO_Load;
  //   IO_Write_Buf = IO_Write; IR[7:0] = M_IR; RAM_Load_Buf = RAM_Load; RAM_Write_Buf = RAM_Write;
  //   Reg_A_Load_Buf = RegA_Load; Reg_A_Write_Buf = RegA_Write; Reg_B_Write_Buf = RegB_Write;
  //   DATA_REG2[7:0] = IO_Addr; DATA_REG1[7:0] = M_IDR1; ROM_Addr_Select_OUTPUT = ROM_Addr_Select;
  //   ROM_Increment_OUTPUT = ROM_Increment
endmodule

module ID_MUX_x3 (
  input  [7:0] InstructionData,
  output [4:0] DW_x5,
  output MOV,
  output ALU,
  output JUMP
);

  wire nand_4_out, nand_5_out, nand_6_out, nand_8_out, nand_9_out, nand_10_out, nand_12_out, nand_13_out,
       nand_14_out;
  wire [5:1] nand_1_out;

  nand nand_1 (nand_1_out[1], InstructionData[5], InstructionData[5]);
  nand nand_2 (nand_1_out[3], InstructionData[6], InstructionData[6]);
  nand nand_3 (nand_1_out[5], InstructionData[7], InstructionData[7]);
  nand nand_4 (nand_4_out, nand_1_out[5], nand_1_out[3]);
  nand nand_5 (nand_5_out, nand_4_out, nand_4_out);
  nand nand_6 (nand_6_out, nand_5_out, nand_1_out[1]);
  nand nand_7 (MOV, nand_6_out, nand_6_out);
  nand nand_8 (nand_8_out, nand_1_out[5], nand_1_out[3]);
  nand nand_9 (nand_9_out, nand_8_out, nand_8_out);
  nand nand_10 (nand_10_out, nand_9_out, InstructionData[5]);
  nand nand_11 (ALU, nand_10_out, nand_10_out);
  nand nand_12 (nand_12_out, nand_1_out[5], InstructionData[6]);
  nand nand_13 (nand_13_out, nand_12_out, nand_12_out);
  nand nand_14 (nand_14_out, nand_13_out, nand_1_out[1]);
  nand nand_15 (JUMP, nand_14_out, nand_14_out);

  assign DW_x5 = InstructionData[4:0];
endmodule
module ID_MUX_x5 (
  input  Gate,
  input  [4:0] INPUT_x5,
  output [31:0] OUTPUT_x32
);

  wire nand_6_out, nand_7_out, nand_8_out, nand_9_out, nand_10_out, nand_11_out, nand_12_out, nand_13_out,
       nand_14_out, nand_15_out, nand_16_out, nand_17_out, nand_18_out, nand_19_out, nand_20_out,
       nand_21_out, nand_22_out, nand_23_out, nand_24_out, nand_25_out, nand_26_out, nand_28_out,
       nand_29_out, nand_30_out, nand_31_out, nand_32_out, nand_34_out, nand_35_out, nand_36_out,
       nand_37_out, nand_38_out, nand_40_out, nand_41_out, nand_42_out, nand_43_out, nand_44_out,
       nand_46_out, nand_47_out, nand_48_out, nand_49_out, nand_50_out, nand_52_out, nand_53_out,
       nand_54_out, nand_55_out, nand_56_out, nand_58_out, nand_59_out, nand_60_out, nand_61_out,
       nand_62_out, nand_64_out, nand_65_out, nand_66_out, nand_67_out, nand_68_out, nand_70_out,
       nand_71_out, nand_72_out, nand_73_out, nand_74_out, nand_75_out, nand_76_out, nand_78_out,
       nand_79_out, nand_80_out, nand_81_out, nand_82_out, nand_83_out, nand_84_out, nand_86_out,
       nand_87_out, nand_88_out, nand_89_out, nand_90_out, nand_91_out, nand_92_out, nand_94_out,
       nand_95_out, nand_96_out, nand_97_out, nand_98_out, nand_99_out, nand_100_out, nand_102_out,
       nand_103_out, nand_104_out, nand_105_out, nand_106_out, nand_107_out, nand_108_out, nand_109_out,
       nand_110_out, nand_111_out, nand_112_out, nand_113_out, nand_114_out, nand_115_out, nand_116_out,
       nand_117_out, nand_118_out, nand_119_out, nand_120_out, nand_121_out, nand_122_out, nand_123_out,
       nand_124_out, nand_125_out, nand_126_out, nand_127_out, nand_128_out, nand_129_out, nand_130_out,
       nand_132_out, nand_133_out, nand_134_out, nand_135_out, nand_136_out, nand_138_out, nand_139_out,
       nand_140_out, nand_141_out, nand_142_out, nand_144_out, nand_145_out, nand_146_out, nand_147_out,
       nand_148_out, nand_150_out, nand_151_out, nand_152_out, nand_153_out, nand_154_out, nand_156_out,
       nand_157_out, nand_158_out, nand_159_out, nand_160_out, nand_162_out, nand_163_out, nand_164_out,
       nand_165_out, nand_166_out, nand_168_out, nand_169_out, nand_170_out, nand_171_out, nand_172_out,
       nand_174_out, nand_175_out, nand_176_out, nand_177_out, nand_178_out, nand_180_out, nand_181_out,
       nand_182_out, nand_183_out, nand_184_out, nand_186_out, nand_187_out, nand_188_out, nand_189_out,
       nand_190_out, nand_192_out, nand_193_out, nand_194_out, nand_195_out, nand_196_out, nand_198_out,
       nand_199_out, nand_200_out, nand_201_out, nand_202_out, nand_203_out, nand_204_out, nand_206_out,
       nand_207_out, nand_208_out, nand_209_out, nand_210_out, nand_211_out, nand_212_out, nand_214_out,
       nand_215_out, nand_216_out, nand_217_out, nand_218_out, nand_219_out, nand_220_out, nand_222_out,
       nand_223_out, nand_224_out, nand_225_out, nand_226_out, nand_227_out, nand_228_out, nand_230_out,
       nand_231_out, nand_232_out, nand_233_out, nand_234_out, nand_235_out, nand_236_out, nand_237_out,
       nand_238_out, nand_239_out, nand_240_out, nand_241_out, nand_242_out, nand_243_out, nand_244_out,
       nand_245_out, nand_246_out, nand_247_out, nand_248_out, nand_249_out, nand_250_out, nand_251_out,
       nand_252_out, nand_253_out, nand_254_out, nand_256_out, nand_258_out, nand_260_out, nand_263_out,
       nand_266_out, nand_267_out, nand_270_out, nand_271_out, nand_274_out, nand_275_out, nand_278_out,
       nand_279_out, nand_282_out, nand_283_out, nand_286_out, nand_287_out, nand_290_out, nand_291_out,
       nand_294_out, nand_295_out, nand_298_out, nand_299_out, nand_302_out, nand_303_out, nand_306_out,
       nand_307_out, nand_310_out, nand_311_out, nand_314_out, nand_315_out, nand_318_out, nand_319_out,
       nand_322_out, nand_323_out, nand_325_out;
  wire [7:0] nand_27_out, nand_33_out, nand_39_out, nand_45_out;
  wire [9:1] nand_1_out;

  nand nand_1 (nand_1_out[1], INPUT_x5[0], INPUT_x5[0]);
  nand nand_2 (nand_1_out[3], INPUT_x5[1], INPUT_x5[1]);
  nand nand_3 (nand_1_out[5], INPUT_x5[2], INPUT_x5[2]);
  nand nand_4 (nand_1_out[7], INPUT_x5[3], INPUT_x5[3]);
  nand nand_5 (nand_1_out[9], INPUT_x5[4], INPUT_x5[4]);
  nand nand_6 (nand_6_out, nand_1_out[1], nand_1_out[3]);
  nand nand_7 (nand_7_out, nand_6_out, nand_6_out);
  nand nand_8 (nand_8_out, nand_7_out, nand_24_out);
  nand nand_9 (nand_9_out, nand_8_out, nand_8_out);
  nand nand_10 (nand_10_out, nand_1_out[1], nand_1_out[3]);
  nand nand_11 (nand_11_out, nand_10_out, nand_10_out);
  nand nand_12 (nand_12_out, nand_11_out, nand_30_out);
  nand nand_13 (nand_13_out, nand_12_out, nand_12_out);
  nand nand_14 (nand_14_out, nand_1_out[1], nand_1_out[3]);
  nand nand_15 (nand_15_out, nand_14_out, nand_14_out);
  nand nand_16 (nand_16_out, nand_15_out, nand_36_out);
  nand nand_17 (nand_17_out, nand_16_out, nand_16_out);
  nand nand_18 (nand_18_out, nand_1_out[1], nand_1_out[3]);
  nand nand_19 (nand_19_out, nand_18_out, nand_18_out);
  nand nand_20 (nand_20_out, nand_19_out, nand_42_out);
  nand nand_21 (nand_21_out, nand_20_out, nand_20_out);
  nand nand_22 (nand_22_out, nand_1_out[5], nand_1_out[7]);
  nand nand_23 (nand_23_out, INPUT_x5[0], nand_1_out[3]);
  nand nand_24 (nand_24_out, nand_22_out, nand_22_out);
  nand nand_25 (nand_25_out, nand_23_out, nand_23_out);
  nand nand_26 (nand_26_out, nand_9_out, nand_1_out[9]);
  nand nand_27 (nand_27_out[0], nand_26_out, nand_26_out);
  nand nand_28 (nand_28_out, nand_1_out[5], INPUT_x5[3]);
  nand nand_29 (nand_29_out, INPUT_x5[0], nand_1_out[3]);
  nand nand_30 (nand_30_out, nand_28_out, nand_28_out);
  nand nand_31 (nand_31_out, nand_29_out, nand_29_out);
  nand nand_32 (nand_32_out, nand_13_out, nand_1_out[9]);
  nand nand_33 (nand_33_out[0], nand_32_out, nand_32_out);
  nand nand_34 (nand_34_out, nand_1_out[5], nand_1_out[7]);
  nand nand_35 (nand_35_out, INPUT_x5[0], nand_1_out[3]);
  nand nand_36 (nand_36_out, nand_34_out, nand_34_out);
  nand nand_37 (nand_37_out, nand_35_out, nand_35_out);
  nand nand_38 (nand_38_out, nand_17_out, INPUT_x5[4]);
  nand nand_39 (nand_39_out[0], nand_38_out, nand_38_out);
  nand nand_40 (nand_40_out, nand_1_out[5], INPUT_x5[3]);
  nand nand_41 (nand_41_out, INPUT_x5[0], nand_1_out[3]);
  nand nand_42 (nand_42_out, nand_40_out, nand_40_out);
  nand nand_43 (nand_43_out, nand_41_out, nand_41_out);
  nand nand_44 (nand_44_out, nand_21_out, INPUT_x5[4]);
  nand nand_45 (nand_45_out[0], nand_44_out, nand_44_out);
  nand nand_46 (nand_46_out, nand_1_out[5], nand_1_out[7]);
  nand nand_47 (nand_47_out, nand_46_out, nand_46_out);
  nand nand_48 (nand_48_out, nand_25_out, nand_47_out);
  nand nand_49 (nand_49_out, nand_48_out, nand_48_out);
  nand nand_50 (nand_50_out, nand_49_out, nand_1_out[9]);
  nand nand_51 (nand_27_out[1], nand_50_out, nand_50_out);
  nand nand_52 (nand_52_out, nand_1_out[5], INPUT_x5[3]);
  nand nand_53 (nand_53_out, nand_52_out, nand_52_out);
  nand nand_54 (nand_54_out, nand_31_out, nand_53_out);
  nand nand_55 (nand_55_out, nand_54_out, nand_54_out);
  nand nand_56 (nand_56_out, nand_55_out, nand_1_out[9]);
  nand nand_57 (nand_33_out[1], nand_56_out, nand_56_out);
  nand nand_58 (nand_58_out, nand_1_out[5], nand_1_out[7]);
  nand nand_59 (nand_59_out, nand_58_out, nand_58_out);
  nand nand_60 (nand_60_out, nand_37_out, nand_59_out);
  nand nand_61 (nand_61_out, nand_60_out, nand_60_out);
  nand nand_62 (nand_62_out, nand_61_out, INPUT_x5[4]);
  nand nand_63 (nand_39_out[1], nand_62_out, nand_62_out);
  nand nand_64 (nand_64_out, nand_1_out[5], INPUT_x5[3]);
  nand nand_65 (nand_65_out, nand_64_out, nand_64_out);
  nand nand_66 (nand_66_out, nand_43_out, nand_65_out);
  nand nand_67 (nand_67_out, nand_66_out, nand_66_out);
  nand nand_68 (nand_68_out, nand_67_out, INPUT_x5[4]);
  nand nand_69 (nand_45_out[1], nand_68_out, nand_68_out);
  nand nand_70 (nand_70_out, nand_1_out[1], INPUT_x5[1]);
  nand nand_71 (nand_71_out, nand_1_out[5], nand_1_out[7]);
  nand nand_72 (nand_72_out, nand_70_out, nand_70_out);
  nand nand_73 (nand_73_out, nand_71_out, nand_71_out);
  nand nand_74 (nand_74_out, nand_72_out, nand_73_out);
  nand nand_75 (nand_75_out, nand_74_out, nand_74_out);
  nand nand_76 (nand_76_out, nand_75_out, nand_1_out[9]);
  nand nand_77 (nand_27_out[2], nand_76_out, nand_76_out);
  nand nand_78 (nand_78_out, nand_1_out[1], INPUT_x5[1]);
  nand nand_79 (nand_79_out, nand_1_out[5], INPUT_x5[3]);
  nand nand_80 (nand_80_out, nand_78_out, nand_78_out);
  nand nand_81 (nand_81_out, nand_79_out, nand_79_out);
  nand nand_82 (nand_82_out, nand_80_out, nand_81_out);
  nand nand_83 (nand_83_out, nand_82_out, nand_82_out);
  nand nand_84 (nand_84_out, nand_83_out, nand_1_out[9]);
  nand nand_85 (nand_33_out[2], nand_84_out, nand_84_out);
  nand nand_86 (nand_86_out, nand_1_out[1], INPUT_x5[1]);
  nand nand_87 (nand_87_out, nand_1_out[5], nand_1_out[7]);
  nand nand_88 (nand_88_out, nand_86_out, nand_86_out);
  nand nand_89 (nand_89_out, nand_87_out, nand_87_out);
  nand nand_90 (nand_90_out, nand_88_out, nand_89_out);
  nand nand_91 (nand_91_out, nand_90_out, nand_90_out);
  nand nand_92 (nand_92_out, nand_91_out, INPUT_x5[4]);
  nand nand_93 (nand_39_out[2], nand_92_out, nand_92_out);
  nand nand_94 (nand_94_out, nand_1_out[1], INPUT_x5[1]);
  nand nand_95 (nand_95_out, nand_1_out[5], INPUT_x5[3]);
  nand nand_96 (nand_96_out, nand_94_out, nand_94_out);
  nand nand_97 (nand_97_out, nand_95_out, nand_95_out);
  nand nand_98 (nand_98_out, nand_96_out, nand_97_out);
  nand nand_99 (nand_99_out, nand_98_out, nand_98_out);
  nand nand_100 (nand_100_out, nand_99_out, INPUT_x5[4]);
  nand nand_101 (nand_45_out[2], nand_100_out, nand_100_out);
  nand nand_102 (nand_102_out, INPUT_x5[0], INPUT_x5[1]);
  nand nand_103 (nand_103_out, nand_1_out[5], nand_1_out[7]);
  nand nand_104 (nand_104_out, nand_102_out, nand_102_out);
  nand nand_105 (nand_105_out, nand_103_out, nand_103_out);
  nand nand_106 (nand_106_out, nand_104_out, nand_105_out);
  nand nand_107 (nand_107_out, nand_106_out, nand_106_out);
  nand nand_108 (nand_108_out, INPUT_x5[0], INPUT_x5[1]);
  nand nand_109 (nand_109_out, nand_1_out[5], INPUT_x5[3]);
  nand nand_110 (nand_110_out, nand_108_out, nand_108_out);
  nand nand_111 (nand_111_out, nand_109_out, nand_109_out);
  nand nand_112 (nand_112_out, nand_110_out, nand_111_out);
  nand nand_113 (nand_113_out, nand_112_out, nand_112_out);
  nand nand_114 (nand_114_out, INPUT_x5[0], INPUT_x5[1]);
  nand nand_115 (nand_115_out, nand_1_out[5], nand_1_out[7]);
  nand nand_116 (nand_116_out, nand_114_out, nand_114_out);
  nand nand_117 (nand_117_out, nand_115_out, nand_115_out);
  nand nand_118 (nand_118_out, nand_116_out, nand_117_out);
  nand nand_119 (nand_119_out, nand_118_out, nand_118_out);
  nand nand_120 (nand_120_out, INPUT_x5[0], INPUT_x5[1]);
  nand nand_121 (nand_121_out, nand_1_out[5], INPUT_x5[3]);
  nand nand_122 (nand_122_out, nand_120_out, nand_120_out);
  nand nand_123 (nand_123_out, nand_121_out, nand_121_out);
  nand nand_124 (nand_124_out, nand_122_out, nand_123_out);
  nand nand_125 (nand_125_out, nand_124_out, nand_124_out);
  nand nand_126 (nand_126_out, nand_1_out[1], nand_1_out[3]);
  nand nand_127 (nand_127_out, nand_126_out, nand_126_out);
  nand nand_128 (nand_128_out, nand_127_out, nand_152_out);
  nand nand_129 (nand_129_out, nand_128_out, nand_128_out);
  nand nand_130 (nand_130_out, nand_107_out, nand_1_out[9]);
  nand nand_131 (nand_27_out[3], nand_130_out, nand_130_out);
  nand nand_132 (nand_132_out, nand_1_out[1], nand_1_out[3]);
  nand nand_133 (nand_133_out, nand_132_out, nand_132_out);
  nand nand_134 (nand_134_out, nand_133_out, nand_158_out);
  nand nand_135 (nand_135_out, nand_134_out, nand_134_out);
  nand nand_136 (nand_136_out, nand_113_out, nand_1_out[9]);
  nand nand_137 (nand_33_out[3], nand_136_out, nand_136_out);
  nand nand_138 (nand_138_out, nand_1_out[1], nand_1_out[3]);
  nand nand_139 (nand_139_out, nand_138_out, nand_138_out);
  nand nand_140 (nand_140_out, nand_139_out, nand_164_out);
  nand nand_141 (nand_141_out, nand_140_out, nand_140_out);
  nand nand_142 (nand_142_out, nand_119_out, INPUT_x5[4]);
  nand nand_143 (nand_39_out[3], nand_142_out, nand_142_out);
  nand nand_144 (nand_144_out, nand_1_out[1], nand_1_out[3]);
  nand nand_145 (nand_145_out, nand_144_out, nand_144_out);
  nand nand_146 (nand_146_out, nand_145_out, nand_170_out);
  nand nand_147 (nand_147_out, nand_146_out, nand_146_out);
  nand nand_148 (nand_148_out, nand_125_out, INPUT_x5[4]);
  nand nand_149 (nand_45_out[3], nand_148_out, nand_148_out);
  nand nand_150 (nand_150_out, INPUT_x5[2], nand_1_out[7]);
  nand nand_151 (nand_151_out, INPUT_x5[0], nand_1_out[3]);
  nand nand_152 (nand_152_out, nand_150_out, nand_150_out);
  nand nand_153 (nand_153_out, nand_151_out, nand_151_out);
  nand nand_154 (nand_154_out, nand_129_out, nand_1_out[9]);
  nand nand_155 (nand_27_out[4], nand_154_out, nand_154_out);
  nand nand_156 (nand_156_out, INPUT_x5[2], INPUT_x5[3]);
  nand nand_157 (nand_157_out, INPUT_x5[0], nand_1_out[3]);
  nand nand_158 (nand_158_out, nand_156_out, nand_156_out);
  nand nand_159 (nand_159_out, nand_157_out, nand_157_out);
  nand nand_160 (nand_160_out, nand_135_out, nand_1_out[9]);
  nand nand_161 (nand_33_out[4], nand_160_out, nand_160_out);
  nand nand_162 (nand_162_out, INPUT_x5[2], nand_1_out[7]);
  nand nand_163 (nand_163_out, INPUT_x5[0], nand_1_out[3]);
  nand nand_164 (nand_164_out, nand_162_out, nand_162_out);
  nand nand_165 (nand_165_out, nand_163_out, nand_163_out);
  nand nand_166 (nand_166_out, nand_141_out, INPUT_x5[4]);
  nand nand_167 (nand_39_out[4], nand_166_out, nand_166_out);
  nand nand_168 (nand_168_out, INPUT_x5[2], INPUT_x5[3]);
  nand nand_169 (nand_169_out, INPUT_x5[0], nand_1_out[3]);
  nand nand_170 (nand_170_out, nand_168_out, nand_168_out);
  nand nand_171 (nand_171_out, nand_169_out, nand_169_out);
  nand nand_172 (nand_172_out, nand_147_out, INPUT_x5[4]);
  nand nand_173 (nand_45_out[4], nand_172_out, nand_172_out);
  nand nand_174 (nand_174_out, INPUT_x5[2], nand_1_out[7]);
  nand nand_175 (nand_175_out, nand_174_out, nand_174_out);
  nand nand_176 (nand_176_out, nand_153_out, nand_175_out);
  nand nand_177 (nand_177_out, nand_176_out, nand_176_out);
  nand nand_178 (nand_178_out, nand_177_out, nand_1_out[9]);
  nand nand_179 (nand_27_out[5], nand_178_out, nand_178_out);
  nand nand_180 (nand_180_out, INPUT_x5[2], INPUT_x5[3]);
  nand nand_181 (nand_181_out, nand_180_out, nand_180_out);
  nand nand_182 (nand_182_out, nand_159_out, nand_181_out);
  nand nand_183 (nand_183_out, nand_182_out, nand_182_out);
  nand nand_184 (nand_184_out, nand_183_out, nand_1_out[9]);
  nand nand_185 (nand_33_out[5], nand_184_out, nand_184_out);
  nand nand_186 (nand_186_out, INPUT_x5[2], nand_1_out[7]);
  nand nand_187 (nand_187_out, nand_186_out, nand_186_out);
  nand nand_188 (nand_188_out, nand_165_out, nand_187_out);
  nand nand_189 (nand_189_out, nand_188_out, nand_188_out);
  nand nand_190 (nand_190_out, nand_189_out, INPUT_x5[4]);
  nand nand_191 (nand_39_out[5], nand_190_out, nand_190_out);
  nand nand_192 (nand_192_out, INPUT_x5[2], INPUT_x5[3]);
  nand nand_193 (nand_193_out, nand_192_out, nand_192_out);
  nand nand_194 (nand_194_out, nand_171_out, nand_193_out);
  nand nand_195 (nand_195_out, nand_194_out, nand_194_out);
  nand nand_196 (nand_196_out, nand_195_out, INPUT_x5[4]);
  nand nand_197 (nand_45_out[5], nand_196_out, nand_196_out);
  nand nand_198 (nand_198_out, nand_1_out[1], INPUT_x5[1]);
  nand nand_199 (nand_199_out, INPUT_x5[2], nand_1_out[7]);
  nand nand_200 (nand_200_out, nand_198_out, nand_198_out);
  nand nand_201 (nand_201_out, nand_199_out, nand_199_out);
  nand nand_202 (nand_202_out, nand_200_out, nand_201_out);
  nand nand_203 (nand_203_out, nand_202_out, nand_202_out);
  nand nand_204 (nand_204_out, nand_203_out, nand_1_out[9]);
  nand nand_205 (nand_27_out[6], nand_204_out, nand_204_out);
  nand nand_206 (nand_206_out, nand_1_out[1], INPUT_x5[1]);
  nand nand_207 (nand_207_out, INPUT_x5[2], INPUT_x5[3]);
  nand nand_208 (nand_208_out, nand_206_out, nand_206_out);
  nand nand_209 (nand_209_out, nand_207_out, nand_207_out);
  nand nand_210 (nand_210_out, nand_208_out, nand_209_out);
  nand nand_211 (nand_211_out, nand_210_out, nand_210_out);
  nand nand_212 (nand_212_out, nand_211_out, nand_1_out[9]);
  nand nand_213 (nand_33_out[6], nand_212_out, nand_212_out);
  nand nand_214 (nand_214_out, nand_1_out[1], INPUT_x5[1]);
  nand nand_215 (nand_215_out, INPUT_x5[2], nand_1_out[7]);
  nand nand_216 (nand_216_out, nand_214_out, nand_214_out);
  nand nand_217 (nand_217_out, nand_215_out, nand_215_out);
  nand nand_218 (nand_218_out, nand_216_out, nand_217_out);
  nand nand_219 (nand_219_out, nand_218_out, nand_218_out);
  nand nand_220 (nand_220_out, nand_219_out, INPUT_x5[4]);
  nand nand_221 (nand_39_out[6], nand_220_out, nand_220_out);
  nand nand_222 (nand_222_out, nand_1_out[1], INPUT_x5[1]);
  nand nand_223 (nand_223_out, INPUT_x5[2], INPUT_x5[3]);
  nand nand_224 (nand_224_out, nand_222_out, nand_222_out);
  nand nand_225 (nand_225_out, nand_223_out, nand_223_out);
  nand nand_226 (nand_226_out, nand_224_out, nand_225_out);
  nand nand_227 (nand_227_out, nand_226_out, nand_226_out);
  nand nand_228 (nand_228_out, nand_227_out, INPUT_x5[4]);
  nand nand_229 (nand_45_out[6], nand_228_out, nand_228_out);
  nand nand_230 (nand_230_out, INPUT_x5[0], INPUT_x5[1]);
  nand nand_231 (nand_231_out, INPUT_x5[2], nand_1_out[7]);
  nand nand_232 (nand_232_out, nand_230_out, nand_230_out);
  nand nand_233 (nand_233_out, nand_231_out, nand_231_out);
  nand nand_234 (nand_234_out, nand_232_out, nand_233_out);
  nand nand_235 (nand_235_out, nand_234_out, nand_234_out);
  nand nand_236 (nand_236_out, INPUT_x5[0], INPUT_x5[1]);
  nand nand_237 (nand_237_out, INPUT_x5[2], INPUT_x5[3]);
  nand nand_238 (nand_238_out, nand_236_out, nand_236_out);
  nand nand_239 (nand_239_out, nand_237_out, nand_237_out);
  nand nand_240 (nand_240_out, nand_238_out, nand_239_out);
  nand nand_241 (nand_241_out, nand_240_out, nand_240_out);
  nand nand_242 (nand_242_out, INPUT_x5[0], INPUT_x5[1]);
  nand nand_243 (nand_243_out, INPUT_x5[2], nand_1_out[7]);
  nand nand_244 (nand_244_out, nand_242_out, nand_242_out);
  nand nand_245 (nand_245_out, nand_243_out, nand_243_out);
  nand nand_246 (nand_246_out, nand_244_out, nand_245_out);
  nand nand_247 (nand_247_out, nand_246_out, nand_246_out);
  nand nand_248 (nand_248_out, INPUT_x5[0], INPUT_x5[1]);
  nand nand_249 (nand_249_out, INPUT_x5[2], INPUT_x5[3]);
  nand nand_250 (nand_250_out, nand_248_out, nand_248_out);
  nand nand_251 (nand_251_out, nand_249_out, nand_249_out);
  nand nand_252 (nand_252_out, nand_250_out, nand_251_out);
  nand nand_253 (nand_253_out, nand_252_out, nand_252_out);
  nand nand_254 (nand_254_out, nand_235_out, nand_1_out[9]);
  nand nand_255 (nand_27_out[7], nand_254_out, nand_254_out);
  nand nand_256 (nand_256_out, nand_241_out, nand_1_out[9]);
  nand nand_257 (nand_33_out[7], nand_256_out, nand_256_out);
  nand nand_258 (nand_258_out, nand_247_out, INPUT_x5[4]);
  nand nand_259 (nand_39_out[7], nand_258_out, nand_258_out);
  nand nand_260 (nand_260_out, nand_253_out, INPUT_x5[4]);
  nand nand_261 (nand_45_out[7], nand_260_out, nand_260_out);
  nand nand_262 (OUTPUT_x32[0], nand_263_out, nand_263_out);
  nand nand_263 (nand_263_out, nand_27_out[0], Gate);
  nand nand_264 (OUTPUT_x32[1], nand_266_out, nand_266_out);
  nand nand_265 (OUTPUT_x32[2], nand_267_out, nand_267_out);
  nand nand_266 (nand_266_out, nand_27_out[1], Gate);
  nand nand_267 (nand_267_out, nand_27_out[2], Gate);
  nand nand_268 (OUTPUT_x32[3], nand_270_out, nand_270_out);
  nand nand_269 (OUTPUT_x32[4], nand_271_out, nand_271_out);
  nand nand_270 (nand_270_out, nand_27_out[3], Gate);
  nand nand_271 (nand_271_out, nand_27_out[4], Gate);
  nand nand_272 (OUTPUT_x32[5], nand_274_out, nand_274_out);
  nand nand_273 (OUTPUT_x32[6], nand_275_out, nand_275_out);
  nand nand_274 (nand_274_out, nand_27_out[5], Gate);
  nand nand_275 (nand_275_out, nand_27_out[6], Gate);
  nand nand_276 (OUTPUT_x32[7], nand_278_out, nand_278_out);
  nand nand_277 (OUTPUT_x32[8], nand_279_out, nand_279_out);
  nand nand_278 (nand_278_out, nand_27_out[7], Gate);
  nand nand_279 (nand_279_out, nand_33_out[0], Gate);
  nand nand_280 (OUTPUT_x32[9], nand_282_out, nand_282_out);
  nand nand_281 (OUTPUT_x32[10], nand_283_out, nand_283_out);
  nand nand_282 (nand_282_out, nand_33_out[1], Gate);
  nand nand_283 (nand_283_out, nand_33_out[2], Gate);
  nand nand_284 (OUTPUT_x32[11], nand_286_out, nand_286_out);
  nand nand_285 (OUTPUT_x32[12], nand_287_out, nand_287_out);
  nand nand_286 (nand_286_out, nand_33_out[3], Gate);
  nand nand_287 (nand_287_out, nand_33_out[4], Gate);
  nand nand_288 (OUTPUT_x32[13], nand_290_out, nand_290_out);
  nand nand_289 (OUTPUT_x32[14], nand_291_out, nand_291_out);
  nand nand_290 (nand_290_out, nand_33_out[5], Gate);
  nand nand_291 (nand_291_out, nand_33_out[6], Gate);
  nand nand_292 (OUTPUT_x32[15], nand_294_out, nand_294_out);
  nand nand_293 (OUTPUT_x32[16], nand_295_out, nand_295_out);
  nand nand_294 (nand_294_out, nand_33_out[7], Gate);
  nand nand_295 (nand_295_out, nand_39_out[0], Gate);
  nand nand_296 (OUTPUT_x32[17], nand_298_out, nand_298_out);
  nand nand_297 (OUTPUT_x32[18], nand_299_out, nand_299_out);
  nand nand_298 (nand_298_out, nand_39_out[1], Gate);
  nand nand_299 (nand_299_out, nand_39_out[2], Gate);
  nand nand_300 (OUTPUT_x32[19], nand_302_out, nand_302_out);
  nand nand_301 (OUTPUT_x32[20], nand_303_out, nand_303_out);
  nand nand_302 (nand_302_out, nand_39_out[3], Gate);
  nand nand_303 (nand_303_out, nand_39_out[4], Gate);
  nand nand_304 (OUTPUT_x32[21], nand_306_out, nand_306_out);
  nand nand_305 (OUTPUT_x32[22], nand_307_out, nand_307_out);
  nand nand_306 (nand_306_out, nand_39_out[5], Gate);
  nand nand_307 (nand_307_out, nand_39_out[6], Gate);
  nand nand_308 (OUTPUT_x32[23], nand_310_out, nand_310_out);
  nand nand_309 (OUTPUT_x32[24], nand_311_out, nand_311_out);
  nand nand_310 (nand_310_out, nand_39_out[7], Gate);
  nand nand_311 (nand_311_out, nand_45_out[0], Gate);
  nand nand_312 (OUTPUT_x32[25], nand_314_out, nand_314_out);
  nand nand_313 (OUTPUT_x32[26], nand_315_out, nand_315_out);
  nand nand_314 (nand_314_out, nand_45_out[1], Gate);
  nand nand_315 (nand_315_out, nand_45_out[2], Gate);
  nand nand_316 (OUTPUT_x32[27], nand_318_out, nand_318_out);
  nand nand_317 (OUTPUT_x32[28], nand_319_out, nand_319_out);
  nand nand_318 (nand_318_out, nand_45_out[3], Gate);
  nand nand_319 (nand_319_out, nand_45_out[4], Gate);
  nand nand_320 (OUTPUT_x32[29], nand_322_out, nand_322_out);
  nand nand_321 (OUTPUT_x32[30], nand_323_out, nand_323_out);
  nand nand_322 (nand_322_out, nand_45_out[5], Gate);
  nand nand_323 (nand_323_out, nand_45_out[6], Gate);
  nand nand_324 (OUTPUT_x32[31], nand_325_out, nand_325_out);
  nand nand_325 (nand_325_out, nand_45_out[7], Gate);
endmodule

module ID_BUS_Reg_x8 (
  input  [7:0] lINPUT_x8,
  input  RST,
  input  CLK,
  output [7:0] OUTPUT_x8
);

  NAND_DFF nand_dff_1 (.Din(lINPUT_x8[0]), .Clk(CLK), .Rst(RST), .data(OUTPUT_x8[0]));
  NAND_DFF nand_dff_2 (.Din(lINPUT_x8[1]), .Clk(CLK), .Rst(RST), .data(OUTPUT_x8[1]));
  NAND_DFF nand_dff_3 (.Din(lINPUT_x8[2]), .Clk(CLK), .Rst(RST), .data(OUTPUT_x8[2]));
  NAND_DFF nand_dff_4 (.Din(lINPUT_x8[3]), .Clk(CLK), .Rst(RST), .data(OUTPUT_x8[3]));
  NAND_DFF nand_dff_5 (.Din(lINPUT_x8[4]), .Clk(CLK), .Rst(RST), .data(OUTPUT_x8[4]));
  NAND_DFF nand_dff_6 (.Din(lINPUT_x8[5]), .Clk(CLK), .Rst(RST), .data(OUTPUT_x8[5]));
  NAND_DFF nand_dff_7 (.Din(lINPUT_x8[6]), .Clk(CLK), .Rst(RST), .data(OUTPUT_x8[6]));
  NAND_DFF nand_dff_8 (.Din(lINPUT_x8[7]), .Clk(CLK), .Rst(RST), .data(OUTPUT_x8[7]));
endmodule

module ID_TimingController (
  input  ReSet,
  input  CLR,
  input  CLK,
  output t0,
  output t1,
  output t2,
  output t3,
  output t4,
  output t5
);

  wire nand_1_out, nand_2_out, nand_5_out, nand_6_out, nand_7_out, nand_8_out, nand_9_out, nand_10_out,
       nand_11_out, nand_12_out, nand_13_out, nand_14_out, nand_15_out, nand_16_out, nand_17_out,
       nand_18_out, nand_19_out;
  wire [1:0] nand_4_out;

  nand nand_1 (nand_1_out, t5, t5);
  nand nand_2 (nand_2_out, ReSet, ReSet);
  nand nand_3 (nand_4_out[1], nand_4_out[0], nand_4_out[0]);
  nand nand_4 (nand_4_out[0], nand_1_out, nand_2_out);
  NAND_DFF nand_dff_1 (.Din(nand_4_out[0]), .Clk(CLK), .Rst(CLR), .data(t0));
  nand nand_5 (nand_5_out, nand_4_out[0], 1'b0);
  nand nand_6 (nand_6_out, nand_5_out, nand_7_out);
  nand nand_7 (nand_7_out, nand_4_out[1], t0);
  NAND_DFF nand_dff_2 (.Din(nand_6_out), .Clk(CLK), .Rst(CLR), .data(t1));
  nand nand_8 (nand_8_out, nand_4_out[0], 1'b0);
  nand nand_9 (nand_9_out, nand_4_out[1], t1);
  nand nand_10 (nand_10_out, nand_8_out, nand_9_out);
  NAND_DFF nand_dff_3 (.Din(nand_10_out), .Clk(CLK), .Rst(CLR), .data(t2));
  nand nand_11 (nand_11_out, nand_4_out[0], 1'b0);
  nand nand_12 (nand_12_out, nand_4_out[1], t2);
  nand nand_13 (nand_13_out, nand_11_out, nand_12_out);
  NAND_DFF nand_dff_4 (.Din(nand_13_out), .Clk(CLK), .Rst(CLR), .data(t3));
  nand nand_14 (nand_14_out, nand_4_out[0], 1'b0);
  nand nand_15 (nand_15_out, nand_14_out, nand_16_out);
  nand nand_16 (nand_16_out, nand_4_out[1], t3);
  NAND_DFF nand_dff_5 (.Din(nand_15_out), .Clk(CLK), .Rst(CLR), .data(t4));
  nand nand_17 (nand_17_out, nand_4_out[0], 1'b0);
  nand nand_18 (nand_18_out, nand_4_out[1], t4);
  nand nand_19 (nand_19_out, nand_17_out, nand_18_out);
  NAND_DFF nand_dff_6 (.Din(nand_19_out), .Clk(CLK), .Rst(CLR), .data(t5));
endmodule

module RAM_Module (
  input  [7:0] Addr,
  input  [7:0] DATA_INPUT,
  input  RegCLK,
  input  Write,
  input  Load,
  output [7:0] OUTPUT_BUS
);

  wire nand_1_out, nand_2_out, nand_3_out, nand_4_out, nand_5_out, nand_6_out, nand_7_out, nand_8_out,
       nand_9_out, nand_10_out, nand_11_out, nand_12_out, nand_13_out, nand_14_out, nand_15_out, nand_16_out,
       nand_17_out, nand_18_out, nand_19_out, nand_20_out, nand_21_out;
  wire [7:0] ram_1_dout;

  nand nand_1 (nand_1_out, RegCLK, Write);
  nand nand_2 (nand_2_out, nand_1_out, nand_1_out);
  nand nand_3 (nand_3_out, Load, Load);
  nand nand_4 (nand_4_out, nand_3_out, nand_5_out);
  nand nand_5 (nand_5_out, nand_2_out, nand_2_out);
  RAM ram_1 (.addr(Addr), .we(nand_2_out), .oe(Load), .clk(nand_4_out), .din(DATA_INPUT), .dout(ram_1_dout));
  assign OUTPUT_BUS[7] = nand_6_out ? nand_6_out : 1'bz;  // Controlled_Buffer controlled_buffer_1
  nand nand_6 (nand_6_out, nand_7_out, nand_7_out);
  nand nand_7 (nand_7_out, Load, ram_1_dout[7]);
  assign OUTPUT_BUS[6] = nand_8_out ? nand_8_out : 1'bz;  // Controlled_Buffer controlled_buffer_2
  assign OUTPUT_BUS[5] = nand_9_out ? nand_9_out : 1'bz;  // Controlled_Buffer controlled_buffer_3
  nand nand_8 (nand_8_out, nand_10_out, nand_10_out);
  nand nand_9 (nand_9_out, nand_11_out, nand_11_out);
  nand nand_10 (nand_10_out, Load, ram_1_dout[6]);
  nand nand_11 (nand_11_out, Load, ram_1_dout[5]);
  Pull_Resistor pull_resistor_1 (.node(ram_1_dout));
  assign OUTPUT_BUS[3] = nand_12_out ? nand_12_out : 1'bz;  // Controlled_Buffer controlled_buffer_4
  assign OUTPUT_BUS[4] = nand_13_out ? nand_13_out : 1'bz;  // Controlled_Buffer controlled_buffer_5
  nand nand_12 (nand_12_out, nand_14_out, nand_14_out);
  nand nand_13 (nand_13_out, nand_15_out, nand_15_out);
  nand nand_14 (nand_14_out, Load, ram_1_dout[3]);
  nand nand_15 (nand_15_out, Load, ram_1_dout[4]);
  assign OUTPUT_BUS[2] = nand_16_out ? nand_16_out : 1'bz;  // Controlled_Buffer controlled_buffer_6
  assign OUTPUT_BUS[1] = nand_17_out ? nand_17_out : 1'bz;  // Controlled_Buffer controlled_buffer_7
  nand nand_16 (nand_16_out, nand_18_out, nand_18_out);
  nand nand_17 (nand_17_out, nand_19_out, nand_19_out);
  nand nand_18 (nand_18_out, Load, ram_1_dout[2]);
  nand nand_19 (nand_19_out, Load, ram_1_dout[1]);
  assign OUTPUT_BUS[0] = nand_20_out ? nand_20_out : 1'bz;  // Controlled_Buffer controlled_buffer_8
  nand nand_20 (nand_20_out, nand_21_out, nand_21_out);
  nand nand_21 (nand_21_out, Load, ram_1_dout[0]);
endmodule

module BCD_FA_x4 (
  input  I0,
  input  I1,
  input  I2,
  input  I3,
  input  ADD_F,
  input  A0,
  input  A1,
  input  A2,
  input  A3,
  output O0,
  output O1,
  output O2,
  output O3
);

  wire nand_1_out, nand_2_out, nand_3_out, nand_4_out, nand_5_out, nand_6_out, nand_7_out, nand_8_out,
       nand_fa_1_carry, nand_fa_2_carry, nand_fa_3_carry;

  nand nand_1 (nand_1_out, ADD_F, A0);
  nand nand_2 (nand_2_out, nand_1_out, nand_1_out);
  nand nand_3 (nand_3_out, ADD_F, A1);
  nand nand_4 (nand_4_out, nand_3_out, nand_3_out);
  nand nand_5 (nand_5_out, ADD_F, A2);
  nand nand_6 (nand_6_out, nand_5_out, nand_5_out);
  nand nand_7 (nand_7_out, ADD_F, A3);
  nand nand_8 (nand_8_out, nand_7_out, nand_7_out);
  NAND_FA nand_fa_1 (.Carry_in(1'b0), .A(I0), .B(nand_2_out), .O(O0), .Carry(nand_fa_1_carry));
  NAND_FA nand_fa_2 (.Carry_in(nand_fa_1_carry), .A(I1), .B(nand_4_out), .O(O1), .Carry(nand_fa_2_carry));
  NAND_FA nand_fa_3 (.Carry_in(nand_fa_2_carry), .A(I2), .B(nand_6_out), .O(O2), .Carry(nand_fa_3_carry));
  NAND_FA nand_fa_4 (.Carry_in(nand_fa_3_carry), .A(I3), .B(nand_8_out), .O(O3));  // open: Carry
endmodule

module BCD_if5_p3 (
  input  I0,
  input  I1,
  input  I2,
  input  I3,
  output O0,
  output O1,
  output O2,
  output O3
);

  wire nand_1_out, nand_2_out, nand_3_out, nand_4_out, nand_5_out, nand_6_out;

  nand nand_1 (nand_1_out, I1, I1);
  nand nand_2 (nand_2_out, nand_1_out, nand_3_out);
  nand nand_3 (nand_3_out, I0, I0);
  nand nand_4 (nand_4_out, I3, I3);
  nand nand_5 (nand_5_out, nand_4_out, nand_6_out);
  nand nand_6 (nand_6_out, I2, nand_2_out);
  BCD_FA_x4 bcd_fa_x4_1 (
    .I0(I0), .I1(I1), .I2(I2), .I3(I3), .ADD_F(nand_5_out), .A0(1'b1), .A1(1'b1), .A2(1'b0), .A3(1'b0),
    .O0(O0), .O1(O1), .O2(O2), .O3(O3));
endmodule

module BCD_x8 (
  input  [7:0] HEX_INPUT,
  output [3:0] BCD_1,
  output [3:0] BCD_10,
  output [3:0] BCD_100
);

  wire bcd_if5_p3_1_o0, bcd_if5_p3_1_o1, bcd_if5_p3_1_o2, bcd_if5_p3_1_o3, bcd_if5_p3_2_o0, bcd_if5_p3_2_o1,
       bcd_if5_p3_2_o2, bcd_if5_p3_2_o3, bcd_if5_p3_3_o0, bcd_if5_p3_3_o1, bcd_if5_p3_3_o2, bcd_if5_p3_3_o3,
       bcd_if5_p3_4_o0, bcd_if5_p3_4_o1, bcd_if5_p3_4_o2, bcd_if5_p3_4_o3, bcd_if5_p3_5_o0, bcd_if5_p3_5_o1,
       bcd_if5_p3_5_o2;

  BCD_if5_p3 bcd_if5_p3_1 (
    .I0(HEX_INPUT[5]), .I1(HEX_INPUT[6]), .I2(HEX_INPUT[7]), .I3(1'b0), .O0(bcd_if5_p3_1_o0),
    .O1(bcd_if5_p3_1_o1), .O2(bcd_if5_p3_1_o2), .O3(bcd_if5_p3_1_o3));
  BCD_if5_p3 bcd_if5_p3_2 (
    .I0(HEX_INPUT[4]), .I1(bcd_if5_p3_1_o0), .I2(bcd_if5_p3_1_o1), .I3(bcd_if5_p3_1_o2),
    .O0(bcd_if5_p3_2_o0), .O1(bcd_if5_p3_2_o1), .O2(bcd_if5_p3_2_o2), .O3(bcd_if5_p3_2_o3));
  BCD_if5_p3 bcd_if5_p3_3 (
    .I0(HEX_INPUT[3]), .I1(bcd_if5_p3_2_o0), .I2(bcd_if5_p3_2_o1), .I3(bcd_if5_p3_2_o2),
    .O0(bcd_if5_p3_3_o0), .O1(bcd_if5_p3_3_o1), .O2(bcd_if5_p3_3_o2), .O3(bcd_if5_p3_3_o3));
  BCD_if5_p3 bcd_if5_p3_4 (
    .I0(HEX_INPUT[2]), .I1(bcd_if5_p3_3_o0), .I2(bcd_if5_p3_3_o1), .I3(bcd_if5_p3_3_o2),
    .O0(bcd_if5_p3_4_o0), .O1(bcd_if5_p3_4_o1), .O2(bcd_if5_p3_4_o2), .O3(bcd_if5_p3_4_o3));
  BCD_if5_p3 bcd_if5_p3_5 (
    .I0(bcd_if5_p3_3_o3), .I1(bcd_if5_p3_2_o3), .I2(bcd_if5_p3_1_o3), .I3(1'b0), .O0(bcd_if5_p3_5_o0),
    .O1(bcd_if5_p3_5_o1), .O2(bcd_if5_p3_5_o2), .O3(BCD_100[1]));
  BCD_if5_p3 bcd_if5_p3_6 (
    .I0(HEX_INPUT[1]), .I1(bcd_if5_p3_4_o0), .I2(bcd_if5_p3_4_o1), .I3(bcd_if5_p3_4_o2), .O0(BCD_1[1]),
    .O1(BCD_1[2]), .O2(BCD_1[3]), .O3(BCD_10[0]));
  BCD_if5_p3 bcd_if5_p3_7 (
    .I0(bcd_if5_p3_4_o3), .I1(bcd_if5_p3_5_o0), .I2(bcd_if5_p3_5_o1), .I3(bcd_if5_p3_5_o2), .O0(BCD_10[1]),
    .O1(BCD_10[2]), .O2(BCD_10[3]), .O3(BCD_100[0]));

  assign BCD_1[0] = HEX_INPUT[0];
  assign BCD_100[3:2] = 2'b00;
endmodule

module PORT_Output_x8 (
  input  [7:0] DATA,
  input  [7:0] Address_x8,
  input  Write,
  input  RegCLK,
  input  RST,
  output [7:0] OP0,
  output [7:0] OP1,
  output [7:0] OP2,
  output [7:0] OP3,
  output [7:0] OP4,
  output [7:0] OP5,
  output [7:0] OP6,
  output [7:0] OP7
);

  wire nand_1_out, nand_2_out, nand_3_out, nand_4_out, nand_5_out, nand_6_out, nand_7_out, nand_8_out,
       nand_9_out, nand_10_out, nand_11_out, nand_12_out, nand_13_out, nand_14_out, nand_16_out, nand_17_out,
       nand_18_out, nand_19_out, nand_20_out, nand_21_out, nand_24_out, nand_25_out, nand_26_out,
       nand_27_out, nand_28_out, nand_29_out, nand_30_out, nand_31_out, nand_32_out, nand_33_out,
       nand_36_out, nand_37_out, nand_38_out, nand_39_out, nand_40_out, nand_41_out, nand_42_out,
       nand_44_out, nand_45_out, nand_46_out, nand_47_out, nand_48_out, nand_49_out, nand_50_out,
       nand_51_out, s0, s1, s2, s3, s4, s5, s6, s7;

  nand nand_1 (nand_1_out, Address_x8[0], Address_x8[0]);
  nand nand_2 (nand_2_out, Address_x8[1], Address_x8[1]);
  nand nand_3 (nand_3_out, Address_x8[2], Address_x8[2]);
  nand nand_4 (nand_4_out, Write, RegCLK);
  nand nand_5 (nand_5_out, nand_3_out, nand_2_out);
  nand nand_6 (nand_6_out, nand_3_out, nand_2_out);
  nand nand_7 (nand_7_out, nand_5_out, nand_5_out);
  nand nand_8 (nand_8_out, nand_6_out, nand_6_out);
  nand nand_9 (nand_9_out, nand_7_out, nand_1_out);
  nand nand_10 (nand_10_out, nand_8_out, Address_x8[0]);
  nand nand_11 (nand_11_out, nand_9_out, nand_9_out);
  nand nand_12 (nand_12_out, nand_10_out, nand_10_out);
  nand nand_13 (nand_13_out, nand_4_out, nand_4_out);
  nand nand_14 (nand_14_out, nand_11_out, nand_13_out);
  nand nand_15 (s0, nand_14_out, nand_14_out);
  nand nand_16 (nand_16_out, nand_3_out, Address_x8[1]);
  nand nand_17 (nand_17_out, nand_16_out, nand_16_out);
  nand nand_18 (nand_18_out, nand_17_out, nand_1_out);
  nand nand_19 (nand_19_out, nand_18_out, nand_18_out);
  nand nand_20 (nand_20_out, nand_12_out, nand_13_out);
  nand nand_21 (nand_21_out, nand_19_out, nand_13_out);
  nand nand_22 (s1, nand_20_out, nand_20_out);
  nand nand_23 (s2, nand_21_out, nand_21_out);
  nand nand_24 (nand_24_out, nand_3_out, Address_x8[1]);
  nand nand_25 (nand_25_out, Address_x8[2], nand_2_out);
  nand nand_26 (nand_26_out, nand_24_out, nand_24_out);
  nand nand_27 (nand_27_out, nand_25_out, nand_25_out);
  nand nand_28 (nand_28_out, nand_26_out, Address_x8[0]);
  nand nand_29 (nand_29_out, nand_27_out, nand_1_out);
  nand nand_30 (nand_30_out, nand_28_out, nand_28_out);
  nand nand_31 (nand_31_out, nand_29_out, nand_29_out);
  nand nand_32 (nand_32_out, nand_30_out, nand_13_out);
  nand nand_33 (nand_33_out, nand_31_out, nand_13_out);
  nand nand_34 (s3, nand_32_out, nand_32_out);
  nand nand_35 (s4, nand_33_out, nand_33_out);
  nand nand_36 (nand_36_out, Address_x8[2], nand_2_out);
  nand nand_37 (nand_37_out, Address_x8[2], Address_x8[1]);
  nand nand_38 (nand_38_out, nand_36_out, nand_36_out);
  nand nand_39 (nand_39_out, nand_37_out, nand_37_out);
  nand nand_40 (nand_40_out, nand_38_out, Address_x8[0]);
  nand nand_41 (nand_41_out, nand_40_out, nand_40_out);
  nand nand_42 (nand_42_out, nand_41_out, nand_13_out);
  nand nand_43 (s5, nand_42_out, nand_42_out);
  nand nand_44 (nand_44_out, Address_x8[2], Address_x8[1]);
  nand nand_45 (nand_45_out, nand_44_out, nand_44_out);
  nand nand_46 (nand_46_out, nand_39_out, nand_1_out);
  nand nand_47 (nand_47_out, nand_45_out, Address_x8[0]);
  nand nand_48 (nand_48_out, nand_46_out, nand_46_out);
  nand nand_49 (nand_49_out, nand_47_out, nand_47_out);
  nand nand_50 (nand_50_out, nand_48_out, nand_13_out);
  nand nand_51 (nand_51_out, nand_49_out, nand_13_out);
  nand nand_52 (s6, nand_50_out, nand_50_out);
  nand nand_53 (s7, nand_51_out, nand_51_out);
  NAND_Reg_x8 nand_reg_x8_1 (
    .D0(DATA[0]), .D1(DATA[1]), .D2(DATA[2]), .D3(DATA[3]), .D4(DATA[4]), .D5(DATA[5]), .D6(DATA[6]),
    .D7(DATA[7]), .RST(RST), .CLK(s0), .O0(OP0[0]), .O1(OP0[1]), .O2(OP0[2]), .O3(OP0[3]), .O4(OP0[4]),
    .O5(OP0[5]), .O6(OP0[6]), .O7(OP0[7]));
  NAND_Reg_x8 nand_reg_x8_2 (
    .D0(DATA[0]), .D1(DATA[1]), .D2(DATA[2]), .D3(DATA[3]), .D4(DATA[4]), .D5(DATA[5]), .D6(DATA[6]),
    .D7(DATA[7]), .RST(RST), .CLK(s1), .O0(OP1[0]), .O1(OP1[1]), .O2(OP1[2]), .O3(OP1[3]), .O4(OP1[4]),
    .O5(OP1[5]), .O6(OP1[6]), .O7(OP1[7]));
  NAND_Reg_x8 nand_reg_x8_3 (
    .D0(DATA[0]), .D1(DATA[1]), .D2(DATA[2]), .D3(DATA[3]), .D4(DATA[4]), .D5(DATA[5]), .D6(DATA[6]),
    .D7(DATA[7]), .RST(RST), .CLK(s2), .O0(OP2[0]), .O1(OP2[1]), .O2(OP2[2]), .O3(OP2[3]), .O4(OP2[4]),
    .O5(OP2[5]), .O6(OP2[6]), .O7(OP2[7]));
  NAND_Reg_x8 nand_reg_x8_4 (
    .D0(DATA[0]), .D1(DATA[1]), .D2(DATA[2]), .D3(DATA[3]), .D4(DATA[4]), .D5(DATA[5]), .D6(DATA[6]),
    .D7(DATA[7]), .RST(RST), .CLK(s3), .O0(OP3[0]), .O1(OP3[1]), .O2(OP3[2]), .O3(OP3[3]), .O4(OP3[4]),
    .O5(OP3[5]), .O6(OP3[6]), .O7(OP3[7]));
  NAND_Reg_x8 nand_reg_x8_5 (
    .D0(DATA[0]), .D1(DATA[1]), .D2(DATA[2]), .D3(DATA[3]), .D4(DATA[4]), .D5(DATA[5]), .D6(DATA[6]),
    .D7(DATA[7]), .RST(RST), .CLK(s4), .O0(OP4[0]), .O1(OP4[1]), .O2(OP4[2]), .O3(OP4[3]), .O4(OP4[4]),
    .O5(OP4[5]), .O6(OP4[6]), .O7(OP4[7]));
  NAND_Reg_x8 nand_reg_x8_6 (
    .D0(DATA[0]), .D1(DATA[1]), .D2(DATA[2]), .D3(DATA[3]), .D4(DATA[4]), .D5(DATA[5]), .D6(DATA[6]),
    .D7(DATA[7]), .RST(RST), .CLK(s5), .O0(OP5[0]), .O1(OP5[1]), .O2(OP5[2]), .O3(OP5[3]), .O4(OP5[4]),
    .O5(OP5[5]), .O6(OP5[6]), .O7(OP5[7]));
  NAND_Reg_x8 nand_reg_x8_7 (
    .D0(DATA[0]), .D1(DATA[1]), .D2(DATA[2]), .D3(DATA[3]), .D4(DATA[4]), .D5(DATA[5]), .D6(DATA[6]),
    .D7(DATA[7]), .RST(RST), .CLK(s6), .O0(OP6[0]), .O1(OP6[1]), .O2(OP6[2]), .O3(OP6[3]), .O4(OP6[4]),
    .O5(OP6[5]), .O6(OP6[6]), .O7(OP6[7]));
  NAND_Reg_x8 nand_reg_x8_8 (
    .D0(DATA[0]), .D1(DATA[1]), .D2(DATA[2]), .D3(DATA[3]), .D4(DATA[4]), .D5(DATA[5]), .D6(DATA[6]),
    .D7(DATA[7]), .RST(RST), .CLK(s7), .O0(OP7[0]), .O1(OP7[1]), .O2(OP7[2]), .O3(OP7[3]), .O4(OP7[4]),
    .O5(OP7[5]), .O6(OP7[6]), .O7(OP7[7]));
endmodule

module PORT_Input_x8 (
  input  [7:0] Address_x8,
  input  Load,
  input  [7:0] IP0,
  input  [7:0] IP1,
  input  [7:0] IP2,
  input  [7:0] IP3,
  input  [7:0] IP4,
  input  [7:0] IP5,
  input  [7:0] IP6,
  input  [7:0] IP7,
  output [7:0] DATA_BUS
);

  wire nand_1_out, nand_2_out, nand_3_out, nand_4_out, nand_5_out, nand_6_out, nand_7_out, nand_8_out,
       nand_9_out, nand_10_out, nand_11_out, nand_12_out, nand_14_out, nand_15_out, nand_16_out, nand_17_out,
       nand_18_out, nand_19_out, nand_22_out, nand_23_out, nand_24_out, nand_25_out, nand_26_out,
       nand_27_out, nand_28_out, nand_29_out, nand_30_out, nand_31_out, nand_34_out, nand_35_out,
       nand_36_out, nand_37_out, nand_38_out, nand_39_out, nand_40_out, nand_42_out, nand_43_out,
       nand_44_out, nand_45_out, nand_46_out, nand_47_out, nand_48_out, nand_49_out, s0, s1, s2, s3, s4, s5,
       s6, s7;

  nand nand_1 (nand_1_out, Address_x8[0], Address_x8[0]);
  nand nand_2 (nand_2_out, Address_x8[1], Address_x8[1]);
  nand nand_3 (nand_3_out, Address_x8[2], Address_x8[2]);
  nand nand_4 (nand_4_out, nand_3_out, nand_2_out);
  nand nand_5 (nand_5_out, nand_3_out, nand_2_out);
  nand nand_6 (nand_6_out, nand_4_out, nand_4_out);
  nand nand_7 (nand_7_out, nand_5_out, nand_5_out);
  nand nand_8 (nand_8_out, nand_6_out, nand_1_out);
  nand nand_9 (nand_9_out, nand_7_out, Address_x8[0]);
  nand nand_10 (nand_10_out, nand_8_out, nand_8_out);
  nand nand_11 (nand_11_out, nand_9_out, nand_9_out);
  nand nand_12 (nand_12_out, nand_10_out, Load);
  nand nand_13 (s0, nand_12_out, nand_12_out);
  nand nand_14 (nand_14_out, nand_3_out, Address_x8[1]);
  nand nand_15 (nand_15_out, nand_14_out, nand_14_out);
  nand nand_16 (nand_16_out, nand_15_out, nand_1_out);
  nand nand_17 (nand_17_out, nand_16_out, nand_16_out);
  nand nand_18 (nand_18_out, nand_11_out, Load);
  nand nand_19 (nand_19_out, nand_17_out, Load);
  nand nand_20 (s1, nand_18_out, nand_18_out);
  nand nand_21 (s2, nand_19_out, nand_19_out);
  nand nand_22 (nand_22_out, nand_3_out, Address_x8[1]);
  nand nand_23 (nand_23_out, Address_x8[2], nand_2_out);
  nand nand_24 (nand_24_out, nand_22_out, nand_22_out);
  nand nand_25 (nand_25_out, nand_23_out, nand_23_out);
  nand nand_26 (nand_26_out, nand_24_out, Address_x8[0]);
  nand nand_27 (nand_27_out, nand_25_out, nand_1_out);
  nand nand_28 (nand_28_out, nand_26_out, nand_26_out);
  nand nand_29 (nand_29_out, nand_27_out, nand_27_out);
  nand nand_30 (nand_30_out, nand_28_out, Load);
  nand nand_31 (nand_31_out, nand_29_out, Load);
  nand nand_32 (s3, nand_30_out, nand_30_out);
  nand nand_33 (s4, nand_31_out, nand_31_out);
  nand nand_34 (nand_34_out, Address_x8[2], nand_2_out);
  nand nand_35 (nand_35_out, Address_x8[2], Address_x8[1]);
  nand nand_36 (nand_36_out, nand_34_out, nand_34_out);
  nand nand_37 (nand_37_out, nand_35_out, nand_35_out);
  nand nand_38 (nand_38_out, nand_36_out, Address_x8[0]);
  nand nand_39 (nand_39_out, nand_38_out, nand_38_out);
  nand nand_40 (nand_40_out, nand_39_out, Load);
  nand nand_41 (s5, nand_40_out, nand_40_out);
  nand nand_42 (nand_42_out, Address_x8[2], Address_x8[1]);
  nand nand_43 (nand_43_out, nand_42_out, nand_42_out);
  nand nand_44 (nand_44_out, nand_37_out, nand_1_out);
  nand nand_45 (nand_45_out, nand_43_out, Address_x8[0]);
  nand nand_46 (nand_46_out, nand_44_out, nand_44_out);
  nand nand_47 (nand_47_out, nand_45_out, nand_45_out);
  nand nand_48 (nand_48_out, nand_46_out, Load);
  nand nand_49 (nand_49_out, nand_47_out, Load);
  nand nand_50 (s6, nand_48_out, nand_48_out);
  nand nand_51 (s7, nand_49_out, nand_49_out);
  BUS_Gate bus_gate_1 (.Gate(s0), .Data_x8(IP0), .DataO_x8(DATA_BUS));
  BUS_Gate bus_gate_2 (.Gate(s1), .Data_x8(IP1), .DataO_x8(DATA_BUS));
  BUS_Gate bus_gate_3 (.Gate(s2), .Data_x8(IP2), .DataO_x8(DATA_BUS));
  BUS_Gate bus_gate_4 (.Gate(s3), .Data_x8(IP3), .DataO_x8(DATA_BUS));
  BUS_Gate bus_gate_5 (.Gate(s4), .Data_x8(IP4), .DataO_x8(DATA_BUS));
  BUS_Gate bus_gate_6 (.Gate(s5), .Data_x8(IP5), .DataO_x8(DATA_BUS));
  BUS_Gate bus_gate_7 (.Gate(s6), .Data_x8(IP6), .DataO_x8(DATA_BUS));
  BUS_Gate bus_gate_8 (.Gate(s7), .Data_x8(IP7), .DataO_x8(DATA_BUS));
endmodule

module BUS_Gate (
  input  Gate,
  input  [7:0] Data_x8,
  output [7:0] DataO_x8
);

  wire nand_1_out, nand_2_out, nand_3_out, nand_4_out, nand_5_out, nand_6_out, nand_7_out, nand_8_out,
       nand_9_out, nand_10_out, nand_11_out, nand_12_out, nand_13_out, nand_14_out, nand_15_out, nand_16_out;

  nand nand_1 (nand_1_out, Gate, Data_x8[0]);
  nand nand_2 (nand_2_out, Gate, Data_x8[1]);
  nand nand_3 (nand_3_out, Gate, Data_x8[2]);
  nand nand_4 (nand_4_out, Gate, Data_x8[3]);
  nand nand_5 (nand_5_out, Gate, Data_x8[4]);
  nand nand_6 (nand_6_out, Gate, Data_x8[5]);
  nand nand_7 (nand_7_out, Gate, Data_x8[6]);
  nand nand_8 (nand_8_out, Gate, Data_x8[7]);
  nand nand_9 (nand_9_out, nand_1_out, nand_1_out);
  assign DataO_x8[0] = nand_9_out ? nand_9_out : 1'bz;  // Controlled_Buffer controlled_buffer_1
  nand nand_10 (nand_10_out, nand_2_out, nand_2_out);
  assign DataO_x8[1] = nand_10_out ? nand_10_out : 1'bz;  // Controlled_Buffer controlled_buffer_2
  nand nand_11 (nand_11_out, nand_3_out, nand_3_out);
  assign DataO_x8[2] = nand_11_out ? nand_11_out : 1'bz;  // Controlled_Buffer controlled_buffer_3
  nand nand_12 (nand_12_out, nand_4_out, nand_4_out);
  assign DataO_x8[3] = nand_12_out ? nand_12_out : 1'bz;  // Controlled_Buffer controlled_buffer_4
  nand nand_13 (nand_13_out, nand_5_out, nand_5_out);
  assign DataO_x8[4] = nand_13_out ? nand_13_out : 1'bz;  // Controlled_Buffer controlled_buffer_5
  nand nand_14 (nand_14_out, nand_6_out, nand_6_out);
  assign DataO_x8[5] = nand_14_out ? nand_14_out : 1'bz;  // Controlled_Buffer controlled_buffer_6
  nand nand_15 (nand_15_out, nand_7_out, nand_7_out);
  assign DataO_x8[6] = nand_15_out ? nand_15_out : 1'bz;  // Controlled_Buffer controlled_buffer_7
  nand nand_16 (nand_16_out, nand_8_out, nand_8_out);
  assign DataO_x8[7] = nand_16_out ? nand_16_out : 1'bz;  // Controlled_Buffer controlled_buffer_8
endmodule

module USE_CPU_FibonacciSequence (
  input  in_1,
  input  [7:0] in_2,
  input  [7:0] in_3,
  input  [7:0] in_4,
  input  [7:0] in_5,
  input  [7:0] in_6,
  input  [7:0] in_7,
  input  [7:0] in_8,
  input  [7:0] in_9
);

  wire button_1_out, clock_1_out;
  wire [3:0] bcd_x8_1_bcd_1, bcd_x8_1_bcd_10, bcd_x8_1_bcd_100;
  wire [7:0] m_all_cpu_m_1_port_output_0, rom_1_data;
  wire [15:0] m_all_cpu_m_1_rom_address;

  ROM #(.addrWidth(16)) rom_1 (.addr(m_all_cpu_m_1_rom_address), .data(rom_1_data));
  Button button_1 (.out(button_1_out));
  Clock clock_1 (.out(clock_1_out));
  M_ALL_CPU_M m_all_cpu_m_1 (
    .ROM_Data(rom_1_data), .RST(button_1_out), .CLK(clock_1_out), .IDReset(in_1), .Port_Input_0(in_2),
    .Port_Input_1(in_3), .Port_Input_2(in_4), .Port_Input_3(in_5), .Port_Input_4(in_6), .Port_Input_5(in_7),
    .Port_Input_6(in_8), .Port_Input_7(in_9), .Port_Output_0(m_all_cpu_m_1_port_output_0),
    .ROM_Address(m_all_cpu_m_1_rom_address));  // open: Port_Output_1, Port_Output_2, Port_Output_3, Port_Output_4, Port_Output_5, Port_Output_6, Port_Output_7
  Hex_Digit_Display hex_digit_display_1 (.value(bcd_x8_1_bcd_100));  // open: dp
  Hex_Digit_Display hex_digit_display_2 (.value(bcd_x8_1_bcd_10));  // open: dp
  BCD_x8 bcd_x8_1 (
    .HEX_INPUT(m_all_cpu_m_1_port_output_0), .BCD_1(bcd_x8_1_bcd_1), .BCD_10(bcd_x8_1_bcd_10),
    .BCD_100(bcd_x8_1_bcd_100));
  Hex_Digit_Display hex_digit_display_3 (.value(bcd_x8_1_bcd_1));  // open: dp

  // Notes on the sheet:
  //   ２，IDResetを1にします
  //   ４，IDResetを0にします
  //   contents of rom_1 (hex, n*v repeats v):
  //   0 6 0 0 6 1 0 1 0 4 1 20 41 0 1b c 0 1 b 0 5 0 7 0 40 0 b 6 0 6f 6 1 de c 0 0 c 0 1 40 0 21
  //   CPUのリセット方法
  //   ３，CLKを1パルスだけ入力します
  //   5, クロックを有効にします
  //   １，CLKとIDResetが0の状態でRSTを押します
  //   フィボナッチ数列の演算ができます
  //   8bitなのですぐにオーバーフローします
  //   オーバーフローすると，出力が111と222を繰り返すようになります
endmodule
module MatrixLED_Controller_32x32 (
  input  [7:0] INPUT_Y,
  input  [7:0] INPUT_X,
  output [31:0] out_3,
  output [31:0] out_4,
  output [31:0] out_5,
  output [31:0] out_6,
  output [31:0] out_7,
  output [31:0] out_8,
  output [31:0] out_9,
  output [31:0] out_10,
  output [31:0] out_11,
  output [31:0] out_12,
  output [31:0] out_13,
  output [31:0] out_14,
  output [31:0] out_15,
  output [31:0] out_16,
  output [31:0] out_17,
  output [31:0] out_18,
  output [31:0] out_19,
  output [31:0] out_20,
  output [31:0] out_21,
  output [31:0] out_22,
  output [31:0] out_23,
  output [31:0] out_24,
  output [31:0] out_25,
  output [31:0] out_26,
  output [31:0] out_27,
  output [31:0] out_28,
  output [31:0] out_29,
  output [31:0] out_30,
  output [31:0] out_31,
  output [31:0] out_32,
  output [31:0] out_33,
  output [31:0] out_34
);

  wire nand_2_out, nand_4_out, nand_6_out, nand_8_out, nand_10_out, nand_12_out, nand_14_out, nand_16_out,
       nand_18_out, nand_20_out, nand_22_out, nand_24_out, nand_26_out, nand_28_out, nand_30_out,
       nand_32_out, nand_34_out, nand_36_out, nand_38_out, nand_40_out, nand_42_out, nand_44_out,
       nand_46_out, nand_48_out, nand_50_out, nand_52_out, nand_54_out, nand_56_out, nand_58_out,
       nand_60_out, nand_62_out, nand_64_out, nand_66_out, nand_68_out, nand_70_out, nand_72_out,
       nand_74_out, nand_76_out, nand_78_out, nand_80_out, nand_82_out, nand_84_out, nand_86_out,
       nand_88_out, nand_90_out, nand_92_out, nand_94_out, nand_96_out, nand_98_out, nand_100_out,
       nand_102_out, nand_104_out, nand_106_out, nand_108_out, nand_110_out, nand_112_out, nand_114_out,
       nand_116_out, nand_118_out, nand_120_out, nand_122_out, nand_124_out, nand_126_out, nand_128_out,
       nand_130_out, nand_132_out, nand_134_out, nand_136_out, nand_138_out, nand_140_out, nand_142_out,
       nand_144_out, nand_146_out, nand_148_out, nand_150_out, nand_152_out, nand_154_out, nand_156_out,
       nand_158_out, nand_160_out, nand_162_out, nand_164_out, nand_166_out, nand_168_out, nand_170_out,
       nand_172_out, nand_174_out, nand_176_out, nand_178_out, nand_180_out, nand_182_out, nand_184_out,
       nand_186_out, nand_188_out, nand_190_out, nand_192_out, nand_194_out, nand_196_out, nand_198_out,
       nand_200_out, nand_202_out, nand_204_out, nand_206_out, nand_208_out, nand_210_out, nand_212_out,
       nand_214_out, nand_216_out, nand_218_out, nand_220_out, nand_222_out, nand_224_out, nand_226_out,
       nand_228_out, nand_230_out, nand_232_out, nand_234_out, nand_236_out, nand_238_out, nand_240_out,
       nand_242_out, nand_244_out, nand_246_out, nand_248_out, nand_250_out, nand_252_out, nand_254_out,
       nand_256_out, nand_258_out, nand_260_out, nand_262_out, nand_264_out, nand_266_out, nand_268_out,
       nand_270_out, nand_272_out, nand_274_out, nand_276_out, nand_278_out, nand_280_out, nand_282_out,
       nand_284_out, nand_286_out, nand_288_out, nand_290_out, nand_292_out, nand_294_out, nand_296_out,
       nand_298_out, nand_300_out, nand_302_out, nand_304_out, nand_306_out, nand_308_out, nand_310_out,
       nand_312_out, nand_314_out, nand_316_out, nand_318_out, nand_320_out, nand_322_out, nand_324_out,
       nand_326_out, nand_328_out, nand_330_out, nand_332_out, nand_334_out, nand_336_out, nand_338_out,
       nand_340_out, nand_342_out, nand_344_out, nand_346_out, nand_348_out, nand_350_out, nand_352_out,
       nand_354_out, nand_356_out, nand_358_out, nand_360_out, nand_362_out, nand_364_out, nand_366_out,
       nand_368_out, nand_370_out, nand_372_out, nand_374_out, nand_376_out, nand_378_out, nand_380_out,
       nand_382_out, nand_384_out, nand_386_out, nand_388_out, nand_390_out, nand_392_out, nand_394_out,
       nand_396_out, nand_398_out, nand_400_out, nand_402_out, nand_404_out, nand_406_out, nand_408_out,
       nand_410_out, nand_412_out, nand_414_out, nand_416_out, nand_418_out, nand_420_out, nand_422_out,
       nand_424_out, nand_426_out, nand_428_out, nand_430_out, nand_432_out, nand_434_out, nand_436_out,
       nand_438_out, nand_440_out, nand_442_out, nand_444_out, nand_446_out, nand_448_out, nand_450_out,
       nand_452_out, nand_454_out, nand_456_out, nand_458_out, nand_460_out, nand_462_out, nand_464_out,
       nand_466_out, nand_468_out, nand_470_out, nand_472_out, nand_474_out, nand_476_out, nand_478_out,
       nand_480_out, nand_482_out, nand_484_out, nand_486_out, nand_488_out, nand_490_out, nand_492_out,
       nand_494_out, nand_496_out, nand_498_out, nand_500_out, nand_502_out, nand_504_out, nand_506_out,
       nand_508_out, nand_510_out, nand_512_out, nand_514_out, nand_516_out, nand_518_out, nand_520_out,
       nand_522_out, nand_524_out, nand_526_out, nand_528_out, nand_530_out, nand_532_out, nand_534_out,
       nand_536_out, nand_538_out, nand_540_out, nand_542_out, nand_544_out, nand_546_out, nand_548_out,
       nand_550_out, nand_552_out, nand_554_out, nand_556_out, nand_558_out, nand_560_out, nand_562_out,
       nand_564_out, nand_566_out, nand_568_out, nand_570_out, nand_572_out, nand_574_out, nand_576_out,
       nand_578_out, nand_580_out, nand_582_out, nand_584_out, nand_586_out, nand_588_out, nand_590_out,
       nand_592_out, nand_594_out, nand_596_out, nand_598_out, nand_600_out, nand_602_out, nand_604_out,
       nand_606_out, nand_608_out, nand_610_out, nand_612_out, nand_614_out, nand_616_out, nand_618_out,
       nand_620_out, nand_622_out, nand_624_out, nand_626_out, nand_628_out, nand_630_out, nand_632_out,
       nand_634_out, nand_636_out, nand_638_out, nand_640_out, nand_642_out, nand_644_out, nand_646_out,
       nand_648_out, nand_650_out, nand_652_out, nand_654_out, nand_656_out, nand_658_out, nand_660_out,
       nand_662_out, nand_664_out, nand_666_out, nand_668_out, nand_670_out, nand_672_out, nand_674_out,
       nand_676_out, nand_678_out, nand_680_out, nand_682_out, nand_684_out, nand_686_out, nand_688_out,
       nand_690_out, nand_692_out, nand_694_out, nand_696_out, nand_698_out, nand_700_out, nand_702_out,
       nand_704_out, nand_706_out, nand_708_out, nand_710_out, nand_712_out, nand_714_out, nand_716_out,
       nand_718_out, nand_720_out, nand_722_out, nand_724_out, nand_726_out, nand_728_out, nand_730_out,
       nand_732_out, nand_734_out, nand_736_out, nand_738_out, nand_740_out, nand_742_out, nand_744_out,
       nand_746_out, nand_748_out, nand_750_out, nand_752_out, nand_754_out, nand_756_out, nand_758_out,
       nand_760_out, nand_762_out, nand_764_out, nand_766_out, nand_768_out, nand_770_out, nand_772_out,
       nand_774_out, nand_776_out, nand_778_out, nand_780_out, nand_782_out, nand_784_out, nand_786_out,
       nand_788_out, nand_790_out, nand_792_out, nand_794_out, nand_796_out, nand_798_out, nand_800_out,
       nand_802_out, nand_804_out, nand_806_out, nand_808_out, nand_810_out, nand_812_out, nand_814_out,
       nand_816_out, nand_818_out, nand_820_out, nand_822_out, nand_824_out, nand_826_out, nand_828_out,
       nand_830_out, nand_832_out, nand_834_out, nand_836_out, nand_838_out, nand_840_out, nand_842_out,
       nand_844_out, nand_846_out, nand_848_out, nand_850_out, nand_852_out, nand_854_out, nand_856_out,
       nand_858_out, nand_860_out, nand_862_out, nand_864_out, nand_866_out, nand_868_out, nand_870_out,
       nand_872_out, nand_874_out, nand_876_out, nand_878_out, nand_880_out, nand_882_out, nand_884_out,
       nand_886_out, nand_888_out, nand_890_out, nand_892_out, nand_894_out, nand_896_out, nand_898_out,
       nand_900_out, nand_902_out, nand_904_out, nand_906_out, nand_908_out, nand_910_out, nand_912_out,
       nand_914_out, nand_916_out, nand_918_out, nand_920_out, nand_922_out, nand_924_out, nand_926_out,
       nand_928_out, nand_930_out, nand_932_out, nand_934_out, nand_936_out, nand_938_out, nand_940_out,
       nand_942_out, nand_944_out, nand_946_out, nand_948_out, nand_950_out, nand_952_out, nand_954_out,
       nand_956_out, nand_958_out, nand_960_out, nand_962_out, nand_964_out, nand_966_out, nand_968_out,
       nand_970_out, nand_972_out, nand_974_out, nand_976_out, nand_978_out, nand_980_out, nand_982_out,
       nand_984_out, nand_986_out, nand_988_out, nand_990_out, nand_992_out, nand_994_out, nand_996_out,
       nand_998_out, nand_1000_out, nand_1002_out, nand_1004_out, nand_1006_out, nand_1008_out,
       nand_1010_out, nand_1012_out, nand_1014_out, nand_1016_out, nand_1018_out, nand_1020_out,
       nand_1022_out, nand_1024_out, nand_1026_out, nand_1028_out, nand_1030_out, nand_1032_out,
       nand_1034_out, nand_1036_out, nand_1038_out, nand_1040_out, nand_1042_out, nand_1044_out,
       nand_1046_out, nand_1048_out, nand_1050_out, nand_1052_out, nand_1054_out, nand_1056_out,
       nand_1058_out, nand_1060_out, nand_1062_out, nand_1064_out, nand_1066_out, nand_1068_out,
       nand_1070_out, nand_1072_out, nand_1074_out, nand_1076_out, nand_1078_out, nand_1080_out,
       nand_1082_out, nand_1084_out, nand_1086_out, nand_1088_out, nand_1090_out, nand_1092_out,
       nand_1094_out, nand_1096_out, nand_1098_out, nand_1100_out, nand_1102_out, nand_1104_out,
       nand_1106_out, nand_1108_out, nand_1110_out, nand_1112_out, nand_1114_out, nand_1116_out,
       nand_1118_out, nand_1120_out, nand_1122_out, nand_1124_out, nand_1126_out, nand_1128_out,
       nand_1130_out, nand_1132_out, nand_1134_out, nand_1136_out, nand_1138_out, nand_1140_out,
       nand_1142_out, nand_1144_out, nand_1146_out, nand_1148_out, nand_1150_out, nand_1152_out,
       nand_1154_out, nand_1156_out, nand_1158_out, nand_1160_out, nand_1162_out, nand_1164_out,
       nand_1166_out, nand_1168_out, nand_1170_out, nand_1172_out, nand_1174_out, nand_1176_out,
       nand_1178_out, nand_1180_out, nand_1182_out, nand_1184_out, nand_1186_out, nand_1188_out,
       nand_1190_out, nand_1192_out, nand_1194_out, nand_1196_out, nand_1198_out, nand_1200_out,
       nand_1202_out, nand_1204_out, nand_1206_out, nand_1208_out, nand_1210_out, nand_1212_out,
       nand_1214_out, nand_1216_out, nand_1218_out, nand_1220_out, nand_1222_out, nand_1224_out,
       nand_1226_out, nand_1228_out, nand_1230_out, nand_1232_out, nand_1234_out, nand_1236_out,
       nand_1238_out, nand_1240_out, nand_1242_out, nand_1244_out, nand_1246_out, nand_1248_out,
       nand_1250_out, nand_1252_out, nand_1254_out, nand_1256_out, nand_1258_out, nand_1260_out,
       nand_1262_out, nand_1264_out, nand_1266_out, nand_1268_out, nand_1270_out, nand_1272_out,
       nand_1274_out, nand_1276_out, nand_1278_out, nand_1280_out, nand_1282_out, nand_1284_out,
       nand_1286_out, nand_1288_out, nand_1290_out, nand_1292_out, nand_1294_out, nand_1296_out,
       nand_1298_out, nand_1300_out, nand_1302_out, nand_1304_out, nand_1306_out, nand_1308_out,
       nand_1310_out, nand_1312_out, nand_1314_out, nand_1316_out, nand_1318_out, nand_1320_out,
       nand_1322_out, nand_1324_out, nand_1326_out, nand_1328_out, nand_1330_out, nand_1332_out,
       nand_1334_out, nand_1336_out, nand_1338_out, nand_1340_out, nand_1342_out, nand_1344_out,
       nand_1346_out, nand_1348_out, nand_1350_out, nand_1352_out, nand_1354_out, nand_1356_out,
       nand_1358_out, nand_1360_out, nand_1362_out, nand_1364_out, nand_1366_out, nand_1368_out,
       nand_1370_out, nand_1372_out, nand_1374_out, nand_1376_out, nand_1378_out, nand_1380_out,
       nand_1382_out, nand_1384_out, nand_1386_out, nand_1388_out, nand_1390_out, nand_1392_out,
       nand_1394_out, nand_1396_out, nand_1398_out, nand_1400_out, nand_1402_out, nand_1404_out,
       nand_1406_out, nand_1408_out, nand_1410_out, nand_1412_out, nand_1414_out, nand_1416_out,
       nand_1418_out, nand_1420_out, nand_1422_out, nand_1424_out, nand_1426_out, nand_1428_out,
       nand_1430_out, nand_1432_out, nand_1434_out, nand_1436_out, nand_1438_out, nand_1440_out,
       nand_1442_out, nand_1444_out, nand_1446_out, nand_1448_out, nand_1450_out, nand_1452_out,
       nand_1454_out, nand_1456_out, nand_1458_out, nand_1460_out, nand_1462_out, nand_1464_out,
       nand_1466_out, nand_1468_out, nand_1470_out, nand_1472_out, nand_1474_out, nand_1476_out,
       nand_1478_out, nand_1480_out, nand_1482_out, nand_1484_out, nand_1486_out, nand_1488_out,
       nand_1490_out, nand_1492_out, nand_1494_out, nand_1496_out, nand_1498_out, nand_1500_out,
       nand_1502_out, nand_1504_out, nand_1506_out, nand_1508_out, nand_1510_out, nand_1512_out,
       nand_1514_out, nand_1516_out, nand_1518_out, nand_1520_out, nand_1522_out, nand_1524_out,
       nand_1526_out, nand_1528_out, nand_1530_out, nand_1532_out, nand_1534_out, nand_1536_out,
       nand_1538_out, nand_1540_out, nand_1542_out, nand_1544_out, nand_1546_out, nand_1548_out,
       nand_1550_out, nand_1552_out, nand_1554_out, nand_1556_out, nand_1558_out, nand_1560_out,
       nand_1562_out, nand_1564_out, nand_1566_out, nand_1568_out, nand_1570_out, nand_1572_out,
       nand_1574_out, nand_1576_out, nand_1578_out, nand_1580_out, nand_1582_out, nand_1584_out,
       nand_1586_out, nand_1588_out, nand_1590_out, nand_1592_out, nand_1594_out, nand_1596_out,
       nand_1598_out, nand_1600_out, nand_1602_out, nand_1604_out, nand_1606_out, nand_1608_out,
       nand_1610_out, nand_1612_out, nand_1614_out, nand_1616_out, nand_1618_out, nand_1620_out,
       nand_1622_out, nand_1624_out, nand_1626_out, nand_1628_out, nand_1630_out, nand_1632_out,
       nand_1634_out, nand_1636_out, nand_1638_out, nand_1640_out, nand_1642_out, nand_1644_out,
       nand_1646_out, nand_1648_out, nand_1650_out, nand_1652_out, nand_1654_out, nand_1656_out,
       nand_1658_out, nand_1660_out, nand_1662_out, nand_1664_out, nand_1666_out, nand_1668_out,
       nand_1670_out, nand_1672_out, nand_1674_out, nand_1676_out, nand_1678_out, nand_1680_out,
       nand_1682_out, nand_1684_out, nand_1686_out, nand_1688_out, nand_1690_out, nand_1692_out,
       nand_1694_out, nand_1696_out, nand_1698_out, nand_1700_out, nand_1702_out, nand_1704_out,
       nand_1706_out, nand_1708_out, nand_1710_out, nand_1712_out, nand_1714_out, nand_1716_out,
       nand_1718_out, nand_1720_out, nand_1722_out, nand_1724_out, nand_1726_out, nand_1728_out,
       nand_1730_out, nand_1732_out, nand_1734_out, nand_1736_out, nand_1738_out, nand_1740_out,
       nand_1742_out, nand_1744_out, nand_1746_out, nand_1748_out, nand_1750_out, nand_1752_out,
       nand_1754_out, nand_1756_out, nand_1758_out, nand_1760_out, nand_1762_out, nand_1764_out,
       nand_1766_out, nand_1768_out, nand_1770_out, nand_1772_out, nand_1774_out, nand_1776_out,
       nand_1778_out, nand_1780_out, nand_1782_out, nand_1784_out, nand_1786_out, nand_1788_out,
       nand_1790_out, nand_1792_out, nand_1794_out, nand_1796_out, nand_1798_out, nand_1800_out,
       nand_1802_out, nand_1804_out, nand_1806_out, nand_1808_out, nand_1810_out, nand_1812_out,
       nand_1814_out, nand_1816_out, nand_1818_out, nand_1820_out, nand_1822_out, nand_1824_out,
       nand_1826_out, nand_1828_out, nand_1830_out, nand_1832_out, nand_1834_out, nand_1836_out,
       nand_1838_out, nand_1840_out, nand_1842_out, nand_1844_out, nand_1846_out, nand_1848_out,
       nand_1850_out, nand_1852_out, nand_1854_out, nand_1856_out, nand_1858_out, nand_1860_out,
       nand_1862_out, nand_1864_out, nand_1866_out, nand_1868_out, nand_1870_out, nand_1872_out,
       nand_1874_out, nand_1876_out, nand_1878_out, nand_1880_out, nand_1882_out, nand_1884_out,
       nand_1886_out, nand_1888_out, nand_1890_out, nand_1892_out, nand_1894_out, nand_1896_out,
       nand_1898_out, nand_1900_out, nand_1902_out, nand_1904_out, nand_1906_out, nand_1908_out,
       nand_1910_out, nand_1912_out, nand_1914_out, nand_1916_out, nand_1918_out, nand_1920_out,
       nand_1922_out, nand_1924_out, nand_1926_out, nand_1928_out, nand_1930_out, nand_1932_out,
       nand_1934_out, nand_1936_out, nand_1938_out, nand_1940_out, nand_1942_out, nand_1944_out,
       nand_1946_out, nand_1948_out, nand_1950_out, nand_1952_out, nand_1954_out, nand_1956_out,
       nand_1958_out, nand_1960_out, nand_1962_out, nand_1964_out, nand_1966_out, nand_1968_out,
       nand_1970_out, nand_1972_out, nand_1974_out, nand_1976_out, nand_1978_out, nand_1980_out,
       nand_1982_out, nand_1984_out, nand_1986_out, nand_1988_out, nand_1990_out, nand_1992_out,
       nand_1994_out, nand_1996_out, nand_1998_out, nand_2000_out, nand_2002_out, nand_2004_out,
       nand_2006_out, nand_2008_out, nand_2010_out, nand_2012_out, nand_2014_out, nand_2016_out,
       nand_2018_out, nand_2020_out, nand_2022_out, nand_2024_out, nand_2026_out, nand_2028_out,
       nand_2030_out, nand_2032_out, nand_2034_out, nand_2036_out, nand_2038_out, nand_2040_out,
       nand_2042_out, nand_2044_out, nand_2046_out, nand_2048_out;
  wire [31:0] id_mux_x5_1_output_x32, id_mux_x5_2_output_x32;

  ID_MUX_x5 id_mux_x5_1 (.Gate(1'b1), .INPUT_x5(INPUT_Y[4:0]), .OUTPUT_x32(id_mux_x5_1_output_x32));
  ID_MUX_x5 id_mux_x5_2 (.Gate(1'b1), .INPUT_x5(INPUT_X[4:0]), .OUTPUT_x32(id_mux_x5_2_output_x32));
  nand nand_1 (out_3[0], nand_2_out, nand_2_out);
  nand nand_2 (nand_2_out, id_mux_x5_1_output_x32[0], id_mux_x5_2_output_x32[0]);
  nand nand_3 (out_3[1], nand_4_out, nand_4_out);
  nand nand_4 (nand_4_out, id_mux_x5_1_output_x32[1], id_mux_x5_2_output_x32[0]);
  nand nand_5 (out_3[2], nand_6_out, nand_6_out);
  nand nand_6 (nand_6_out, id_mux_x5_1_output_x32[2], id_mux_x5_2_output_x32[0]);
  nand nand_7 (out_3[3], nand_8_out, nand_8_out);
  nand nand_8 (nand_8_out, id_mux_x5_1_output_x32[3], id_mux_x5_2_output_x32[0]);
  nand nand_9 (out_3[4], nand_10_out, nand_10_out);
  nand nand_10 (nand_10_out, id_mux_x5_1_output_x32[4], id_mux_x5_2_output_x32[0]);
  nand nand_11 (out_3[5], nand_12_out, nand_12_out);
  nand nand_12 (nand_12_out, id_mux_x5_1_output_x32[5], id_mux_x5_2_output_x32[0]);
  nand nand_13 (out_3[6], nand_14_out, nand_14_out);
  nand nand_14 (nand_14_out, id_mux_x5_1_output_x32[6], id_mux_x5_2_output_x32[0]);
  nand nand_15 (out_3[7], nand_16_out, nand_16_out);
  nand nand_16 (nand_16_out, id_mux_x5_1_output_x32[7], id_mux_x5_2_output_x32[0]);
  nand nand_17 (out_3[8], nand_18_out, nand_18_out);
  nand nand_18 (nand_18_out, id_mux_x5_1_output_x32[8], id_mux_x5_2_output_x32[0]);
  nand nand_19 (out_3[9], nand_20_out, nand_20_out);
  nand nand_20 (nand_20_out, id_mux_x5_1_output_x32[9], id_mux_x5_2_output_x32[0]);
  nand nand_21 (out_3[10], nand_22_out, nand_22_out);
  nand nand_22 (nand_22_out, id_mux_x5_1_output_x32[10], id_mux_x5_2_output_x32[0]);
  nand nand_23 (out_3[11], nand_24_out, nand_24_out);
  nand nand_24 (nand_24_out, id_mux_x5_1_output_x32[11], id_mux_x5_2_output_x32[0]);
  nand nand_25 (out_3[12], nand_26_out, nand_26_out);
  nand nand_26 (nand_26_out, id_mux_x5_1_output_x32[12], id_mux_x5_2_output_x32[0]);
  nand nand_27 (out_3[13], nand_28_out, nand_28_out);
  nand nand_28 (nand_28_out, id_mux_x5_1_output_x32[13], id_mux_x5_2_output_x32[0]);
  nand nand_29 (out_3[14], nand_30_out, nand_30_out);
  nand nand_30 (nand_30_out, id_mux_x5_1_output_x32[14], id_mux_x5_2_output_x32[0]);
  nand nand_31 (out_3[15], nand_32_out, nand_32_out);
  nand nand_32 (nand_32_out, id_mux_x5_1_output_x32[15], id_mux_x5_2_output_x32[0]);
  nand nand_33 (out_3[16], nand_34_out, nand_34_out);
  nand nand_34 (nand_34_out, id_mux_x5_1_output_x32[16], id_mux_x5_2_output_x32[0]);
  nand nand_35 (out_3[17], nand_36_out, nand_36_out);
  nand nand_36 (nand_36_out, id_mux_x5_1_output_x32[17], id_mux_x5_2_output_x32[0]);
  nand nand_37 (out_3[18], nand_38_out, nand_38_out);
  nand nand_38 (nand_38_out, id_mux_x5_1_output_x32[18], id_mux_x5_2_output_x32[0]);
  nand nand_39 (out_3[19], nand_40_out, nand_40_out);
  nand nand_40 (nand_40_out, id_mux_x5_1_output_x32[19], id_mux_x5_2_output_x32[0]);
  nand nand_41 (out_3[20], nand_42_out, nand_42_out);
  nand nand_42 (nand_42_out, id_mux_x5_1_output_x32[20], id_mux_x5_2_output_x32[0]);
  nand nand_43 (out_3[21], nand_44_out, nand_44_out);
  nand nand_44 (nand_44_out, id_mux_x5_1_output_x32[21], id_mux_x5_2_output_x32[0]);
  nand nand_45 (out_3[22], nand_46_out, nand_46_out);
  nand nand_46 (nand_46_out, id_mux_x5_1_output_x32[22], id_mux_x5_2_output_x32[0]);
  nand nand_47 (out_3[23], nand_48_out, nand_48_out);
  nand nand_48 (nand_48_out, id_mux_x5_1_output_x32[23], id_mux_x5_2_output_x32[0]);
  nand nand_49 (out_3[24], nand_50_out, nand_50_out);
  nand nand_50 (nand_50_out, id_mux_x5_1_output_x32[24], id_mux_x5_2_output_x32[0]);
  nand nand_51 (out_3[25], nand_52_out, nand_52_out);
  nand nand_52 (nand_52_out, id_mux_x5_1_output_x32[25], id_mux_x5_2_output_x32[0]);
  nand nand_53 (out_3[26], nand_54_out, nand_54_out);
  nand nand_54 (nand_54_out, id_mux_x5_1_output_x32[26], id_mux_x5_2_output_x32[0]);
  nand nand_55 (out_3[27], nand_56_out, nand_56_out);
  nand nand_56 (nand_56_out, id_mux_x5_1_output_x32[27], id_mux_x5_2_output_x32[0]);
  nand nand_57 (out_3[28], nand_58_out, nand_58_out);
  nand nand_58 (nand_58_out, id_mux_x5_1_output_x32[28], id_mux_x5_2_output_x32[0]);
  nand nand_59 (out_3[29], nand_60_out, nand_60_out);
  nand nand_60 (nand_60_out, id_mux_x5_1_output_x32[29], id_mux_x5_2_output_x32[0]);
  nand nand_61 (out_3[30], nand_62_out, nand_62_out);
  nand nand_62 (nand_62_out, id_mux_x5_1_output_x32[30], id_mux_x5_2_output_x32[0]);
  nand nand_63 (out_3[31], nand_64_out, nand_64_out);
  nand nand_64 (nand_64_out, id_mux_x5_1_output_x32[31], id_mux_x5_2_output_x32[0]);
  nand nand_65 (out_4[0], nand_66_out, nand_66_out);
  nand nand_66 (nand_66_out, id_mux_x5_1_output_x32[0], id_mux_x5_2_output_x32[1]);
  nand nand_67 (out_4[1], nand_68_out, nand_68_out);
  nand nand_68 (nand_68_out, id_mux_x5_1_output_x32[1], id_mux_x5_2_output_x32[1]);
  nand nand_69 (out_4[2], nand_70_out, nand_70_out);
  nand nand_70 (nand_70_out, id_mux_x5_1_output_x32[2], id_mux_x5_2_output_x32[1]);
  nand nand_71 (out_4[3], nand_72_out, nand_72_out);
  nand nand_72 (nand_72_out, id_mux_x5_1_output_x32[3], id_mux_x5_2_output_x32[1]);
  nand nand_73 (out_4[4], nand_74_out, nand_74_out);
  nand nand_74 (nand_74_out, id_mux_x5_1_output_x32[4], id_mux_x5_2_output_x32[1]);
  nand nand_75 (out_4[5], nand_76_out, nand_76_out);
  nand nand_76 (nand_76_out, id_mux_x5_1_output_x32[5], id_mux_x5_2_output_x32[1]);
  nand nand_77 (out_4[6], nand_78_out, nand_78_out);
  nand nand_78 (nand_78_out, id_mux_x5_1_output_x32[6], id_mux_x5_2_output_x32[1]);
  nand nand_79 (out_4[7], nand_80_out, nand_80_out);
  nand nand_80 (nand_80_out, id_mux_x5_1_output_x32[7], id_mux_x5_2_output_x32[1]);
  nand nand_81 (out_4[8], nand_82_out, nand_82_out);
  nand nand_82 (nand_82_out, id_mux_x5_1_output_x32[8], id_mux_x5_2_output_x32[1]);
  nand nand_83 (out_4[9], nand_84_out, nand_84_out);
  nand nand_84 (nand_84_out, id_mux_x5_1_output_x32[9], id_mux_x5_2_output_x32[1]);
  nand nand_85 (out_4[10], nand_86_out, nand_86_out);
  nand nand_86 (nand_86_out, id_mux_x5_1_output_x32[10], id_mux_x5_2_output_x32[1]);
  nand nand_87 (out_4[11], nand_88_out, nand_88_out);
  nand nand_88 (nand_88_out, id_mux_x5_1_output_x32[11], id_mux_x5_2_output_x32[1]);
  nand nand_89 (out_4[12], nand_90_out, nand_90_out);
  nand nand_90 (nand_90_out, id_mux_x5_1_output_x32[12], id_mux_x5_2_output_x32[1]);
  nand nand_91 (out_4[13], nand_92_out, nand_92_out);
  nand nand_92 (nand_92_out, id_mux_x5_1_output_x32[13], id_mux_x5_2_output_x32[1]);
  nand nand_93 (out_4[14], nand_94_out, nand_94_out);
  nand nand_94 (nand_94_out, id_mux_x5_1_output_x32[14], id_mux_x5_2_output_x32[1]);
  nand nand_95 (out_4[15], nand_96_out, nand_96_out);
  nand nand_96 (nand_96_out, id_mux_x5_1_output_x32[15], id_mux_x5_2_output_x32[1]);
  nand nand_97 (out_4[16], nand_98_out, nand_98_out);
  nand nand_98 (nand_98_out, id_mux_x5_1_output_x32[16], id_mux_x5_2_output_x32[1]);
  nand nand_99 (out_4[17], nand_100_out, nand_100_out);
  nand nand_100 (nand_100_out, id_mux_x5_1_output_x32[17], id_mux_x5_2_output_x32[1]);
  nand nand_101 (out_4[18], nand_102_out, nand_102_out);
  nand nand_102 (nand_102_out, id_mux_x5_1_output_x32[18], id_mux_x5_2_output_x32[1]);
  nand nand_103 (out_4[19], nand_104_out, nand_104_out);
  nand nand_104 (nand_104_out, id_mux_x5_1_output_x32[19], id_mux_x5_2_output_x32[1]);
  nand nand_105 (out_4[20], nand_106_out, nand_106_out);
  nand nand_106 (nand_106_out, id_mux_x5_1_output_x32[20], id_mux_x5_2_output_x32[1]);
  nand nand_107 (out_4[21], nand_108_out, nand_108_out);
  nand nand_108 (nand_108_out, id_mux_x5_1_output_x32[21], id_mux_x5_2_output_x32[1]);
  nand nand_109 (out_4[22], nand_110_out, nand_110_out);
  nand nand_110 (nand_110_out, id_mux_x5_1_output_x32[22], id_mux_x5_2_output_x32[1]);
  nand nand_111 (out_4[23], nand_112_out, nand_112_out);
  nand nand_112 (nand_112_out, id_mux_x5_1_output_x32[23], id_mux_x5_2_output_x32[1]);
  nand nand_113 (out_4[24], nand_114_out, nand_114_out);
  nand nand_114 (nand_114_out, id_mux_x5_1_output_x32[24], id_mux_x5_2_output_x32[1]);
  nand nand_115 (out_4[25], nand_116_out, nand_116_out);
  nand nand_116 (nand_116_out, id_mux_x5_1_output_x32[25], id_mux_x5_2_output_x32[1]);
  nand nand_117 (out_4[26], nand_118_out, nand_118_out);
  nand nand_118 (nand_118_out, id_mux_x5_1_output_x32[26], id_mux_x5_2_output_x32[1]);
  nand nand_119 (out_4[27], nand_120_out, nand_120_out);
  nand nand_120 (nand_120_out, id_mux_x5_1_output_x32[27], id_mux_x5_2_output_x32[1]);
  nand nand_121 (out_4[28], nand_122_out, nand_122_out);
  nand nand_122 (nand_122_out, id_mux_x5_1_output_x32[28], id_mux_x5_2_output_x32[1]);
  nand nand_123 (out_4[29], nand_124_out, nand_124_out);
  nand nand_124 (nand_124_out, id_mux_x5_1_output_x32[29], id_mux_x5_2_output_x32[1]);
  nand nand_125 (out_4[30], nand_126_out, nand_126_out);
  nand nand_126 (nand_126_out, id_mux_x5_1_output_x32[30], id_mux_x5_2_output_x32[1]);
  nand nand_127 (out_4[31], nand_128_out, nand_128_out);
  nand nand_128 (nand_128_out, id_mux_x5_1_output_x32[31], id_mux_x5_2_output_x32[1]);
  nand nand_129 (out_5[0], nand_130_out, nand_130_out);
  nand nand_130 (nand_130_out, id_mux_x5_1_output_x32[0], id_mux_x5_2_output_x32[2]);
  nand nand_131 (out_5[1], nand_132_out, nand_132_out);
  nand nand_132 (nand_132_out, id_mux_x5_1_output_x32[1], id_mux_x5_2_output_x32[2]);
  nand nand_133 (out_5[2], nand_134_out, nand_134_out);
  nand nand_134 (nand_134_out, id_mux_x5_1_output_x32[2], id_mux_x5_2_output_x32[2]);
  nand nand_135 (out_5[3], nand_136_out, nand_136_out);
  nand nand_136 (nand_136_out, id_mux_x5_1_output_x32[3], id_mux_x5_2_output_x32[2]);
  nand nand_137 (out_5[4], nand_138_out, nand_138_out);
  nand nand_138 (nand_138_out, id_mux_x5_1_output_x32[4], id_mux_x5_2_output_x32[2]);
  nand nand_139 (out_5[5], nand_140_out, nand_140_out);
  nand nand_140 (nand_140_out, id_mux_x5_1_output_x32[5], id_mux_x5_2_output_x32[2]);
  nand nand_141 (out_5[6], nand_142_out, nand_142_out);
  nand nand_142 (nand_142_out, id_mux_x5_1_output_x32[6], id_mux_x5_2_output_x32[2]);
  nand nand_143 (out_5[7], nand_144_out, nand_144_out);
  nand nand_144 (nand_144_out, id_mux_x5_1_output_x32[7], id_mux_x5_2_output_x32[2]);
  nand nand_145 (out_5[8], nand_146_out, nand_146_out);
  nand nand_146 (nand_146_out, id_mux_x5_1_output_x32[8], id_mux_x5_2_output_x32[2]);
  nand nand_147 (out_5[9], nand_148_out, nand_148_out);
  nand nand_148 (nand_148_out, id_mux_x5_1_output_x32[9], id_mux_x5_2_output_x32[2]);
  nand nand_149 (out_5[10], nand_150_out, nand_150_out);
  nand nand_150 (nand_150_out, id_mux_x5_1_output_x32[10], id_mux_x5_2_output_x32[2]);
  nand nand_151 (out_5[11], nand_152_out, nand_152_out);
  nand nand_152 (nand_152_out, id_mux_x5_1_output_x32[11], id_mux_x5_2_output_x32[2]);
  nand nand_153 (out_5[12], nand_154_out, nand_154_out);
  nand nand_154 (nand_154_out, id_mux_x5_1_output_x32[12], id_mux_x5_2_output_x32[2]);
  nand nand_155 (out_5[13], nand_156_out, nand_156_out);
  nand nand_156 (nand_156_out, id_mux_x5_1_output_x32[13], id_mux_x5_2_output_x32[2]);
  nand nand_157 (out_5[14], nand_158_out, nand_158_out);
  nand nand_158 (nand_158_out, id_mux_x5_1_output_x32[14], id_mux_x5_2_output_x32[2]);
  nand nand_159 (out_5[15], nand_160_out, nand_160_out);
  nand nand_160 (nand_160_out, id_mux_x5_1_output_x32[15], id_mux_x5_2_output_x32[2]);
  nand nand_161 (out_5[16], nand_162_out, nand_162_out);
  nand nand_162 (nand_162_out, id_mux_x5_1_output_x32[16], id_mux_x5_2_output_x32[2]);
  nand nand_163 (out_5[17], nand_164_out, nand_164_out);
  nand nand_164 (nand_164_out, id_mux_x5_1_output_x32[17], id_mux_x5_2_output_x32[2]);
  nand nand_165 (out_5[18], nand_166_out, nand_166_out);
  nand nand_166 (nand_166_out, id_mux_x5_1_output_x32[18], id_mux_x5_2_output_x32[2]);
  nand nand_167 (out_5[19], nand_168_out, nand_168_out);
  nand nand_168 (nand_168_out, id_mux_x5_1_output_x32[19], id_mux_x5_2_output_x32[2]);
  nand nand_169 (out_5[20], nand_170_out, nand_170_out);
  nand nand_170 (nand_170_out, id_mux_x5_1_output_x32[20], id_mux_x5_2_output_x32[2]);
  nand nand_171 (out_5[21], nand_172_out, nand_172_out);
  nand nand_172 (nand_172_out, id_mux_x5_1_output_x32[21], id_mux_x5_2_output_x32[2]);
  nand nand_173 (out_5[22], nand_174_out, nand_174_out);
  nand nand_174 (nand_174_out, id_mux_x5_1_output_x32[22], id_mux_x5_2_output_x32[2]);
  nand nand_175 (out_5[23], nand_176_out, nand_176_out);
  nand nand_176 (nand_176_out, id_mux_x5_1_output_x32[23], id_mux_x5_2_output_x32[2]);
  nand nand_177 (out_5[24], nand_178_out, nand_178_out);
  nand nand_178 (nand_178_out, id_mux_x5_1_output_x32[24], id_mux_x5_2_output_x32[2]);
  nand nand_179 (out_5[25], nand_180_out, nand_180_out);
  nand nand_180 (nand_180_out, id_mux_x5_1_output_x32[25], id_mux_x5_2_output_x32[2]);
  nand nand_181 (out_5[26], nand_182_out, nand_182_out);
  nand nand_182 (nand_182_out, id_mux_x5_1_output_x32[26], id_mux_x5_2_output_x32[2]);
  nand nand_183 (out_5[27], nand_184_out, nand_184_out);
  nand nand_184 (nand_184_out, id_mux_x5_1_output_x32[27], id_mux_x5_2_output_x32[2]);
  nand nand_185 (out_5[28], nand_186_out, nand_186_out);
  nand nand_186 (nand_186_out, id_mux_x5_1_output_x32[28], id_mux_x5_2_output_x32[2]);
  nand nand_187 (out_5[29], nand_188_out, nand_188_out);
  nand nand_188 (nand_188_out, id_mux_x5_1_output_x32[29], id_mux_x5_2_output_x32[2]);
  nand nand_189 (out_5[30], nand_190_out, nand_190_out);
  nand nand_190 (nand_190_out, id_mux_x5_1_output_x32[30], id_mux_x5_2_output_x32[2]);
  nand nand_191 (out_5[31], nand_192_out, nand_192_out);
  nand nand_192 (nand_192_out, id_mux_x5_1_output_x32[31], id_mux_x5_2_output_x32[2]);
  nand nand_193 (out_6[0], nand_194_out, nand_194_out);
  nand nand_194 (nand_194_out, id_mux_x5_1_output_x32[0], id_mux_x5_2_output_x32[3]);
  nand nand_195 (out_6[1], nand_196_out, nand_196_out);
  nand nand_196 (nand_196_out, id_mux_x5_1_output_x32[1], id_mux_x5_2_output_x32[3]);
  nand nand_197 (out_6[2], nand_198_out, nand_198_out);
  nand nand_198 (nand_198_out, id_mux_x5_1_output_x32[2], id_mux_x5_2_output_x32[3]);
  nand nand_199 (out_6[3], nand_200_out, nand_200_out);
  nand nand_200 (nand_200_out, id_mux_x5_1_output_x32[3], id_mux_x5_2_output_x32[3]);
  nand nand_201 (out_6[4], nand_202_out, nand_202_out);
  nand nand_202 (nand_202_out, id_mux_x5_1_output_x32[4], id_mux_x5_2_output_x32[3]);
  nand nand_203 (out_6[5], nand_204_out, nand_204_out);
  nand nand_204 (nand_204_out, id_mux_x5_1_output_x32[5], id_mux_x5_2_output_x32[3]);
  nand nand_205 (out_6[6], nand_206_out, nand_206_out);
  nand nand_206 (nand_206_out, id_mux_x5_1_output_x32[6], id_mux_x5_2_output_x32[3]);
  nand nand_207 (out_6[7], nand_208_out, nand_208_out);
  nand nand_208 (nand_208_out, id_mux_x5_1_output_x32[7], id_mux_x5_2_output_x32[3]);
  nand nand_209 (out_6[8], nand_210_out, nand_210_out);
  nand nand_210 (nand_210_out, id_mux_x5_1_output_x32[8], id_mux_x5_2_output_x32[3]);
  nand nand_211 (out_6[9], nand_212_out, nand_212_out);
  nand nand_212 (nand_212_out, id_mux_x5_1_output_x32[9], id_mux_x5_2_output_x32[3]);
  nand nand_213 (out_6[10], nand_214_out, nand_214_out);
  nand nand_214 (nand_214_out, id_mux_x5_1_output_x32[10], id_mux_x5_2_output_x32[3]);
  nand nand_215 (out_6[11], nand_216_out, nand_216_out);
  nand nand_216 (nand_216_out, id_mux_x5_1_output_x32[11], id_mux_x5_2_output_x32[3]);
  nand nand_217 (out_6[12], nand_218_out, nand_218_out);
  nand nand_218 (nand_218_out, id_mux_x5_1_output_x32[12], id_mux_x5_2_output_x32[3]);
  nand nand_219 (out_6[13], nand_220_out, nand_220_out);
  nand nand_220 (nand_220_out, id_mux_x5_1_output_x32[13], id_mux_x5_2_output_x32[3]);
  nand nand_221 (out_6[14], nand_222_out, nand_222_out);
  nand nand_222 (nand_222_out, id_mux_x5_1_output_x32[14], id_mux_x5_2_output_x32[3]);
  nand nand_223 (out_6[15], nand_224_out, nand_224_out);
  nand nand_224 (nand_224_out, id_mux_x5_1_output_x32[15], id_mux_x5_2_output_x32[3]);
  nand nand_225 (out_6[16], nand_226_out, nand_226_out);
  nand nand_226 (nand_226_out, id_mux_x5_1_output_x32[16], id_mux_x5_2_output_x32[3]);
  nand nand_227 (out_6[17], nand_228_out, nand_228_out);
  nand nand_228 (nand_228_out, id_mux_x5_1_output_x32[17], id_mux_x5_2_output_x32[3]);
  nand nand_229 (out_6[18], nand_230_out, nand_230_out);
  nand nand_230 (nand_230_out, id_mux_x5_1_output_x32[18], id_mux_x5_2_output_x32[3]);
  nand nand_231 (out_6[19], nand_232_out, nand_232_out);
  nand nand_232 (nand_232_out, id_mux_x5_1_output_x32[19], id_mux_x5_2_output_x32[3]);
  nand nand_233 (out_6[20], nand_234_out, nand_234_out);
  nand nand_234 (nand_234_out, id_mux_x5_1_output_x32[20], id_mux_x5_2_output_x32[3]);
  nand nand_235 (out_6[21], nand_236_out, nand_236_out);
  nand nand_236 (nand_236_out, id_mux_x5_1_output_x32[21], id_mux_x5_2_output_x32[3]);
  nand nand_237 (out_6[22], nand_238_out, nand_238_out);
  nand nand_238 (nand_238_out, id_mux_x5_1_output_x32[22], id_mux_x5_2_output_x32[3]);
  nand nand_239 (out_6[23], nand_240_out, nand_240_out);
  nand nand_240 (nand_240_out, id_mux_x5_1_output_x32[23], id_mux_x5_2_output_x32[3]);
  nand nand_241 (out_6[24], nand_242_out, nand_242_out);
  nand nand_242 (nand_242_out, id_mux_x5_1_output_x32[24], id_mux_x5_2_output_x32[3]);
  nand nand_243 (out_6[25], nand_244_out, nand_244_out);
  nand nand_244 (nand_244_out, id_mux_x5_1_output_x32[25], id_mux_x5_2_output_x32[3]);
  nand nand_245 (out_6[26], nand_246_out, nand_246_out);
  nand nand_246 (nand_246_out, id_mux_x5_1_output_x32[26], id_mux_x5_2_output_x32[3]);
  nand nand_247 (out_6[27], nand_248_out, nand_248_out);
  nand nand_248 (nand_248_out, id_mux_x5_1_output_x32[27], id_mux_x5_2_output_x32[3]);
  nand nand_249 (out_6[28], nand_250_out, nand_250_out);
  nand nand_250 (nand_250_out, id_mux_x5_1_output_x32[28], id_mux_x5_2_output_x32[3]);
  nand nand_251 (out_6[29], nand_252_out, nand_252_out);
  nand nand_252 (nand_252_out, id_mux_x5_1_output_x32[29], id_mux_x5_2_output_x32[3]);
  nand nand_253 (out_6[30], nand_254_out, nand_254_out);
  nand nand_254 (nand_254_out, id_mux_x5_1_output_x32[30], id_mux_x5_2_output_x32[3]);
  nand nand_255 (out_6[31], nand_256_out, nand_256_out);
  nand nand_256 (nand_256_out, id_mux_x5_1_output_x32[31], id_mux_x5_2_output_x32[3]);
  nand nand_257 (out_7[0], nand_258_out, nand_258_out);
  nand nand_258 (nand_258_out, id_mux_x5_1_output_x32[0], id_mux_x5_2_output_x32[4]);
  nand nand_259 (out_7[1], nand_260_out, nand_260_out);
  nand nand_260 (nand_260_out, id_mux_x5_1_output_x32[1], id_mux_x5_2_output_x32[4]);
  nand nand_261 (out_7[2], nand_262_out, nand_262_out);
  nand nand_262 (nand_262_out, id_mux_x5_1_output_x32[2], id_mux_x5_2_output_x32[4]);
  nand nand_263 (out_7[3], nand_264_out, nand_264_out);
  nand nand_264 (nand_264_out, id_mux_x5_1_output_x32[3], id_mux_x5_2_output_x32[4]);
  nand nand_265 (out_7[4], nand_266_out, nand_266_out);
  nand nand_266 (nand_266_out, id_mux_x5_1_output_x32[4], id_mux_x5_2_output_x32[4]);
  nand nand_267 (out_7[5], nand_268_out, nand_268_out);
  nand nand_268 (nand_268_out, id_mux_x5_1_output_x32[5], id_mux_x5_2_output_x32[4]);
  nand nand_269 (out_7[6], nand_270_out, nand_270_out);
  nand nand_270 (nand_270_out, id_mux_x5_1_output_x32[6], id_mux_x5_2_output_x32[4]);
  nand nand_271 (out_7[7], nand_272_out, nand_272_out);
  nand nand_272 (nand_272_out, id_mux_x5_1_output_x32[7], id_mux_x5_2_output_x32[4]);
  nand nand_273 (out_7[8], nand_274_out, nand_274_out);
  nand nand_274 (nand_274_out, id_mux_x5_1_output_x32[8], id_mux_x5_2_output_x32[4]);
  nand nand_275 (out_7[9], nand_276_out, nand_276_out);
  nand nand_276 (nand_276_out, id_mux_x5_1_output_x32[9], id_mux_x5_2_output_x32[4]);
  nand nand_277 (out_7[10], nand_278_out, nand_278_out);
  nand nand_278 (nand_278_out, id_mux_x5_1_output_x32[10], id_mux_x5_2_output_x32[4]);
  nand nand_279 (out_7[11], nand_280_out, nand_280_out);
  nand nand_280 (nand_280_out, id_mux_x5_1_output_x32[11], id_mux_x5_2_output_x32[4]);
  nand nand_281 (out_7[12], nand_282_out, nand_282_out);
  nand nand_282 (nand_282_out, id_mux_x5_1_output_x32[12], id_mux_x5_2_output_x32[4]);
  nand nand_283 (out_7[13], nand_284_out, nand_284_out);
  nand nand_284 (nand_284_out, id_mux_x5_1_output_x32[13], id_mux_x5_2_output_x32[4]);
  nand nand_285 (out_7[14], nand_286_out, nand_286_out);
  nand nand_286 (nand_286_out, id_mux_x5_1_output_x32[14], id_mux_x5_2_output_x32[4]);
  nand nand_287 (out_7[15], nand_288_out, nand_288_out);
  nand nand_288 (nand_288_out, id_mux_x5_1_output_x32[15], id_mux_x5_2_output_x32[4]);
  nand nand_289 (out_7[16], nand_290_out, nand_290_out);
  nand nand_290 (nand_290_out, id_mux_x5_1_output_x32[16], id_mux_x5_2_output_x32[4]);
  nand nand_291 (out_7[17], nand_292_out, nand_292_out);
  nand nand_292 (nand_292_out, id_mux_x5_1_output_x32[17], id_mux_x5_2_output_x32[4]);
  nand nand_293 (out_7[18], nand_294_out, nand_294_out);
  nand nand_294 (nand_294_out, id_mux_x5_1_output_x32[18], id_mux_x5_2_output_x32[4]);
  nand nand_295 (out_7[19], nand_296_out, nand_296_out);
  nand nand_296 (nand_296_out, id_mux_x5_1_output_x32[19], id_mux_x5_2_output_x32[4]);
  nand nand_297 (out_7[20], nand_298_out, nand_298_out);
  nand nand_298 (nand_298_out, id_mux_x5_1_output_x32[20], id_mux_x5_2_output_x32[4]);
  nand nand_299 (out_7[21], nand_300_out, nand_300_out);
  nand nand_300 (nand_300_out, id_mux_x5_1_output_x32[21], id_mux_x5_2_output_x32[4]);
  nand nand_301 (out_7[22], nand_302_out, nand_302_out);
  nand nand_302 (nand_302_out, id_mux_x5_1_output_x32[22], id_mux_x5_2_output_x32[4]);
  nand nand_303 (out_7[23], nand_304_out, nand_304_out);
  nand nand_304 (nand_304_out, id_mux_x5_1_output_x32[23], id_mux_x5_2_output_x32[4]);
  nand nand_305 (out_7[24], nand_306_out, nand_306_out);
  nand nand_306 (nand_306_out, id_mux_x5_1_output_x32[24], id_mux_x5_2_output_x32[4]);
  nand nand_307 (out_7[25], nand_308_out, nand_308_out);
  nand nand_308 (nand_308_out, id_mux_x5_1_output_x32[25], id_mux_x5_2_output_x32[4]);
  nand nand_309 (out_7[26], nand_310_out, nand_310_out);
  nand nand_310 (nand_310_out, id_mux_x5_1_output_x32[26], id_mux_x5_2_output_x32[4]);
  nand nand_311 (out_7[27], nand_312_out, nand_312_out);
  nand nand_312 (nand_312_out, id_mux_x5_1_output_x32[27], id_mux_x5_2_output_x32[4]);
  nand nand_313 (out_7[28], nand_314_out, nand_314_out);
  nand nand_314 (nand_314_out, id_mux_x5_1_output_x32[28], id_mux_x5_2_output_x32[4]);
  nand nand_315 (out_7[29], nand_316_out, nand_316_out);
  nand nand_316 (nand_316_out, id_mux_x5_1_output_x32[29], id_mux_x5_2_output_x32[4]);
  nand nand_317 (out_7[30], nand_318_out, nand_318_out);
  nand nand_318 (nand_318_out, id_mux_x5_1_output_x32[30], id_mux_x5_2_output_x32[4]);
  nand nand_319 (out_7[31], nand_320_out, nand_320_out);
  nand nand_320 (nand_320_out, id_mux_x5_1_output_x32[31], id_mux_x5_2_output_x32[4]);
  nand nand_321 (out_8[0], nand_322_out, nand_322_out);
  nand nand_322 (nand_322_out, id_mux_x5_1_output_x32[0], id_mux_x5_2_output_x32[5]);
  nand nand_323 (out_8[1], nand_324_out, nand_324_out);
  nand nand_324 (nand_324_out, id_mux_x5_1_output_x32[1], id_mux_x5_2_output_x32[5]);
  nand nand_325 (out_8[2], nand_326_out, nand_326_out);
  nand nand_326 (nand_326_out, id_mux_x5_1_output_x32[2], id_mux_x5_2_output_x32[5]);
  nand nand_327 (out_8[3], nand_328_out, nand_328_out);
  nand nand_328 (nand_328_out, id_mux_x5_1_output_x32[3], id_mux_x5_2_output_x32[5]);
  nand nand_329 (out_8[4], nand_330_out, nand_330_out);
  nand nand_330 (nand_330_out, id_mux_x5_1_output_x32[4], id_mux_x5_2_output_x32[5]);
  nand nand_331 (out_8[5], nand_332_out, nand_332_out);
  nand nand_332 (nand_332_out, id_mux_x5_1_output_x32[5], id_mux_x5_2_output_x32[5]);
  nand nand_333 (out_8[6], nand_334_out, nand_334_out);
  nand nand_334 (nand_334_out, id_mux_x5_1_output_x32[6], id_mux_x5_2_output_x32[5]);
  nand nand_335 (out_8[7], nand_336_out, nand_336_out);
  nand nand_336 (nand_336_out, id_mux_x5_1_output_x32[7], id_mux_x5_2_output_x32[5]);
  nand nand_337 (out_8[8], nand_338_out, nand_338_out);
  nand nand_338 (nand_338_out, id_mux_x5_1_output_x32[8], id_mux_x5_2_output_x32[5]);
  nand nand_339 (out_8[9], nand_340_out, nand_340_out);
  nand nand_340 (nand_340_out, id_mux_x5_1_output_x32[9], id_mux_x5_2_output_x32[5]);
  nand nand_341 (out_8[10], nand_342_out, nand_342_out);
  nand nand_342 (nand_342_out, id_mux_x5_1_output_x32[10], id_mux_x5_2_output_x32[5]);
  nand nand_343 (out_8[11], nand_344_out, nand_344_out);
  nand nand_344 (nand_344_out, id_mux_x5_1_output_x32[11], id_mux_x5_2_output_x32[5]);
  nand nand_345 (out_8[12], nand_346_out, nand_346_out);
  nand nand_346 (nand_346_out, id_mux_x5_1_output_x32[12], id_mux_x5_2_output_x32[5]);
  nand nand_347 (out_8[13], nand_348_out, nand_348_out);
  nand nand_348 (nand_348_out, id_mux_x5_1_output_x32[13], id_mux_x5_2_output_x32[5]);
  nand nand_349 (out_8[14], nand_350_out, nand_350_out);
  nand nand_350 (nand_350_out, id_mux_x5_1_output_x32[14], id_mux_x5_2_output_x32[5]);
  nand nand_351 (out_8[15], nand_352_out, nand_352_out);
  nand nand_352 (nand_352_out, id_mux_x5_1_output_x32[15], id_mux_x5_2_output_x32[5]);
  nand nand_353 (out_8[16], nand_354_out, nand_354_out);
  nand nand_354 (nand_354_out, id_mux_x5_1_output_x32[16], id_mux_x5_2_output_x32[5]);
  nand nand_355 (out_8[17], nand_356_out, nand_356_out);
  nand nand_356 (nand_356_out, id_mux_x5_1_output_x32[17], id_mux_x5_2_output_x32[5]);
  nand nand_357 (out_8[18], nand_358_out, nand_358_out);
  nand nand_358 (nand_358_out, id_mux_x5_1_output_x32[18], id_mux_x5_2_output_x32[5]);
  nand nand_359 (out_8[19], nand_360_out, nand_360_out);
  nand nand_360 (nand_360_out, id_mux_x5_1_output_x32[19], id_mux_x5_2_output_x32[5]);
  nand nand_361 (out_8[20], nand_362_out, nand_362_out);
  nand nand_362 (nand_362_out, id_mux_x5_1_output_x32[20], id_mux_x5_2_output_x32[5]);
  nand nand_363 (out_8[21], nand_364_out, nand_364_out);
  nand nand_364 (nand_364_out, id_mux_x5_1_output_x32[21], id_mux_x5_2_output_x32[5]);
  nand nand_365 (out_8[22], nand_366_out, nand_366_out);
  nand nand_366 (nand_366_out, id_mux_x5_1_output_x32[22], id_mux_x5_2_output_x32[5]);
  nand nand_367 (out_8[23], nand_368_out, nand_368_out);
  nand nand_368 (nand_368_out, id_mux_x5_1_output_x32[23], id_mux_x5_2_output_x32[5]);
  nand nand_369 (out_8[24], nand_370_out, nand_370_out);
  nand nand_370 (nand_370_out, id_mux_x5_1_output_x32[24], id_mux_x5_2_output_x32[5]);
  nand nand_371 (out_8[25], nand_372_out, nand_372_out);
  nand nand_372 (nand_372_out, id_mux_x5_1_output_x32[25], id_mux_x5_2_output_x32[5]);
  nand nand_373 (out_8[26], nand_374_out, nand_374_out);
  nand nand_374 (nand_374_out, id_mux_x5_1_output_x32[26], id_mux_x5_2_output_x32[5]);
  nand nand_375 (out_8[27], nand_376_out, nand_376_out);
  nand nand_376 (nand_376_out, id_mux_x5_1_output_x32[27], id_mux_x5_2_output_x32[5]);
  nand nand_377 (out_8[28], nand_378_out, nand_378_out);
  nand nand_378 (nand_378_out, id_mux_x5_1_output_x32[28], id_mux_x5_2_output_x32[5]);
  nand nand_379 (out_8[29], nand_380_out, nand_380_out);
  nand nand_380 (nand_380_out, id_mux_x5_1_output_x32[29], id_mux_x5_2_output_x32[5]);
  nand nand_381 (out_8[30], nand_382_out, nand_382_out);
  nand nand_382 (nand_382_out, id_mux_x5_1_output_x32[30], id_mux_x5_2_output_x32[5]);
  nand nand_383 (out_8[31], nand_384_out, nand_384_out);
  nand nand_384 (nand_384_out, id_mux_x5_1_output_x32[31], id_mux_x5_2_output_x32[5]);
  nand nand_385 (out_9[0], nand_386_out, nand_386_out);
  nand nand_386 (nand_386_out, id_mux_x5_1_output_x32[0], id_mux_x5_2_output_x32[6]);
  nand nand_387 (out_9[1], nand_388_out, nand_388_out);
  nand nand_388 (nand_388_out, id_mux_x5_1_output_x32[1], id_mux_x5_2_output_x32[6]);
  nand nand_389 (out_9[2], nand_390_out, nand_390_out);
  nand nand_390 (nand_390_out, id_mux_x5_1_output_x32[2], id_mux_x5_2_output_x32[6]);
  nand nand_391 (out_9[3], nand_392_out, nand_392_out);
  nand nand_392 (nand_392_out, id_mux_x5_1_output_x32[3], id_mux_x5_2_output_x32[6]);
  nand nand_393 (out_9[4], nand_394_out, nand_394_out);
  nand nand_394 (nand_394_out, id_mux_x5_1_output_x32[4], id_mux_x5_2_output_x32[6]);
  nand nand_395 (out_9[5], nand_396_out, nand_396_out);
  nand nand_396 (nand_396_out, id_mux_x5_1_output_x32[5], id_mux_x5_2_output_x32[6]);
  nand nand_397 (out_9[6], nand_398_out, nand_398_out);
  nand nand_398 (nand_398_out, id_mux_x5_1_output_x32[6], id_mux_x5_2_output_x32[6]);
  nand nand_399 (out_9[7], nand_400_out, nand_400_out);
  nand nand_400 (nand_400_out, id_mux_x5_1_output_x32[7], id_mux_x5_2_output_x32[6]);
  nand nand_401 (out_9[8], nand_402_out, nand_402_out);
  nand nand_402 (nand_402_out, id_mux_x5_1_output_x32[8], id_mux_x5_2_output_x32[6]);
  nand nand_403 (out_9[9], nand_404_out, nand_404_out);
  nand nand_404 (nand_404_out, id_mux_x5_1_output_x32[9], id_mux_x5_2_output_x32[6]);
  nand nand_405 (out_9[10], nand_406_out, nand_406_out);
  nand nand_406 (nand_406_out, id_mux_x5_1_output_x32[10], id_mux_x5_2_output_x32[6]);
  nand nand_407 (out_9[11], nand_408_out, nand_408_out);
  nand nand_408 (nand_408_out, id_mux_x5_1_output_x32[11], id_mux_x5_2_output_x32[6]);
  nand nand_409 (out_9[12], nand_410_out, nand_410_out);
  nand nand_410 (nand_410_out, id_mux_x5_1_output_x32[12], id_mux_x5_2_output_x32[6]);
  nand nand_411 (out_9[13], nand_412_out, nand_412_out);
  nand nand_412 (nand_412_out, id_mux_x5_1_output_x32[13], id_mux_x5_2_output_x32[6]);
  nand nand_413 (out_9[14], nand_414_out, nand_414_out);
  nand nand_414 (nand_414_out, id_mux_x5_1_output_x32[14], id_mux_x5_2_output_x32[6]);
  nand nand_415 (out_9[15], nand_416_out, nand_416_out);
  nand nand_416 (nand_416_out, id_mux_x5_1_output_x32[15], id_mux_x5_2_output_x32[6]);
  nand nand_417 (out_9[16], nand_418_out, nand_418_out);
  nand nand_418 (nand_418_out, id_mux_x5_1_output_x32[16], id_mux_x5_2_output_x32[6]);
  nand nand_419 (out_9[17], nand_420_out, nand_420_out);
  nand nand_420 (nand_420_out, id_mux_x5_1_output_x32[17], id_mux_x5_2_output_x32[6]);
  nand nand_421 (out_9[18], nand_422_out, nand_422_out);
  nand nand_422 (nand_422_out, id_mux_x5_1_output_x32[18], id_mux_x5_2_output_x32[6]);
  nand nand_423 (out_9[19], nand_424_out, nand_424_out);
  nand nand_424 (nand_424_out, id_mux_x5_1_output_x32[19], id_mux_x5_2_output_x32[6]);
  nand nand_425 (out_9[20], nand_426_out, nand_426_out);
  nand nand_426 (nand_426_out, id_mux_x5_1_output_x32[20], id_mux_x5_2_output_x32[6]);
  nand nand_427 (out_9[21], nand_428_out, nand_428_out);
  nand nand_428 (nand_428_out, id_mux_x5_1_output_x32[21], id_mux_x5_2_output_x32[6]);
  nand nand_429 (out_9[22], nand_430_out, nand_430_out);
  nand nand_430 (nand_430_out, id_mux_x5_1_output_x32[22], id_mux_x5_2_output_x32[6]);
  nand nand_431 (out_9[23], nand_432_out, nand_432_out);
  nand nand_432 (nand_432_out, id_mux_x5_1_output_x32[23], id_mux_x5_2_output_x32[6]);
  nand nand_433 (out_9[24], nand_434_out, nand_434_out);
  nand nand_434 (nand_434_out, id_mux_x5_1_output_x32[24], id_mux_x5_2_output_x32[6]);
  nand nand_435 (out_9[25], nand_436_out, nand_436_out);
  nand nand_436 (nand_436_out, id_mux_x5_1_output_x32[25], id_mux_x5_2_output_x32[6]);
  nand nand_437 (out_9[26], nand_438_out, nand_438_out);
  nand nand_438 (nand_438_out, id_mux_x5_1_output_x32[26], id_mux_x5_2_output_x32[6]);
  nand nand_439 (out_9[27], nand_440_out, nand_440_out);
  nand nand_440 (nand_440_out, id_mux_x5_1_output_x32[27], id_mux_x5_2_output_x32[6]);
  nand nand_441 (out_9[28], nand_442_out, nand_442_out);
  nand nand_442 (nand_442_out, id_mux_x5_1_output_x32[28], id_mux_x5_2_output_x32[6]);
  nand nand_443 (out_9[29], nand_444_out, nand_444_out);
  nand nand_444 (nand_444_out, id_mux_x5_1_output_x32[29], id_mux_x5_2_output_x32[6]);
  nand nand_445 (out_9[30], nand_446_out, nand_446_out);
  nand nand_446 (nand_446_out, id_mux_x5_1_output_x32[30], id_mux_x5_2_output_x32[6]);
  nand nand_447 (out_9[31], nand_448_out, nand_448_out);
  nand nand_448 (nand_448_out, id_mux_x5_1_output_x32[31], id_mux_x5_2_output_x32[6]);
  nand nand_449 (out_10[0], nand_450_out, nand_450_out);
  nand nand_450 (nand_450_out, id_mux_x5_1_output_x32[0], id_mux_x5_2_output_x32[7]);
  nand nand_451 (out_10[1], nand_452_out, nand_452_out);
  nand nand_452 (nand_452_out, id_mux_x5_1_output_x32[1], id_mux_x5_2_output_x32[7]);
  nand nand_453 (out_10[2], nand_454_out, nand_454_out);
  nand nand_454 (nand_454_out, id_mux_x5_1_output_x32[2], id_mux_x5_2_output_x32[7]);
  nand nand_455 (out_10[3], nand_456_out, nand_456_out);
  nand nand_456 (nand_456_out, id_mux_x5_1_output_x32[3], id_mux_x5_2_output_x32[7]);
  nand nand_457 (out_10[4], nand_458_out, nand_458_out);
  nand nand_458 (nand_458_out, id_mux_x5_1_output_x32[4], id_mux_x5_2_output_x32[7]);
  nand nand_459 (out_10[5], nand_460_out, nand_460_out);
  nand nand_460 (nand_460_out, id_mux_x5_1_output_x32[5], id_mux_x5_2_output_x32[7]);
  nand nand_461 (out_10[6], nand_462_out, nand_462_out);
  nand nand_462 (nand_462_out, id_mux_x5_1_output_x32[6], id_mux_x5_2_output_x32[7]);
  nand nand_463 (out_10[7], nand_464_out, nand_464_out);
  nand nand_464 (nand_464_out, id_mux_x5_1_output_x32[7], id_mux_x5_2_output_x32[7]);
  nand nand_465 (out_10[8], nand_466_out, nand_466_out);
  nand nand_466 (nand_466_out, id_mux_x5_1_output_x32[8], id_mux_x5_2_output_x32[7]);
  nand nand_467 (out_10[9], nand_468_out, nand_468_out);
  nand nand_468 (nand_468_out, id_mux_x5_1_output_x32[9], id_mux_x5_2_output_x32[7]);
  nand nand_469 (out_10[10], nand_470_out, nand_470_out);
  nand nand_470 (nand_470_out, id_mux_x5_1_output_x32[10], id_mux_x5_2_output_x32[7]);
  nand nand_471 (out_10[11], nand_472_out, nand_472_out);
  nand nand_472 (nand_472_out, id_mux_x5_1_output_x32[11], id_mux_x5_2_output_x32[7]);
  nand nand_473 (out_10[12], nand_474_out, nand_474_out);
  nand nand_474 (nand_474_out, id_mux_x5_1_output_x32[12], id_mux_x5_2_output_x32[7]);
  nand nand_475 (out_10[13], nand_476_out, nand_476_out);
  nand nand_476 (nand_476_out, id_mux_x5_1_output_x32[13], id_mux_x5_2_output_x32[7]);
  nand nand_477 (out_10[14], nand_478_out, nand_478_out);
  nand nand_478 (nand_478_out, id_mux_x5_1_output_x32[14], id_mux_x5_2_output_x32[7]);
  nand nand_479 (out_10[15], nand_480_out, nand_480_out);
  nand nand_480 (nand_480_out, id_mux_x5_1_output_x32[15], id_mux_x5_2_output_x32[7]);
  nand nand_481 (out_10[16], nand_482_out, nand_482_out);
  nand nand_482 (nand_482_out, id_mux_x5_1_output_x32[16], id_mux_x5_2_output_x32[7]);
  nand nand_483 (out_10[17], nand_484_out, nand_484_out);
  nand nand_484 (nand_484_out, id_mux_x5_1_output_x32[17], id_mux_x5_2_output_x32[7]);
  nand nand_485 (out_10[18], nand_486_out, nand_486_out);
  nand nand_486 (nand_486_out, id_mux_x5_1_output_x32[18], id_mux_x5_2_output_x32[7]);
  nand nand_487 (out_10[19], nand_488_out, nand_488_out);
  nand nand_488 (nand_488_out, id_mux_x5_1_output_x32[19], id_mux_x5_2_output_x32[7]);
  nand nand_489 (out_10[20], nand_490_out, nand_490_out);
  nand nand_490 (nand_490_out, id_mux_x5_1_output_x32[20], id_mux_x5_2_output_x32[7]);
  nand nand_491 (out_10[21], nand_492_out, nand_492_out);
  nand nand_492 (nand_492_out, id_mux_x5_1_output_x32[21], id_mux_x5_2_output_x32[7]);
  nand nand_493 (out_10[22], nand_494_out, nand_494_out);
  nand nand_494 (nand_494_out, id_mux_x5_1_output_x32[22], id_mux_x5_2_output_x32[7]);
  nand nand_495 (out_10[23], nand_496_out, nand_496_out);
  nand nand_496 (nand_496_out, id_mux_x5_1_output_x32[23], id_mux_x5_2_output_x32[7]);
  nand nand_497 (out_10[24], nand_498_out, nand_498_out);
  nand nand_498 (nand_498_out, id_mux_x5_1_output_x32[24], id_mux_x5_2_output_x32[7]);
  nand nand_499 (out_10[25], nand_500_out, nand_500_out);
  nand nand_500 (nand_500_out, id_mux_x5_1_output_x32[25], id_mux_x5_2_output_x32[7]);
  nand nand_501 (out_10[26], nand_502_out, nand_502_out);
  nand nand_502 (nand_502_out, id_mux_x5_1_output_x32[26], id_mux_x5_2_output_x32[7]);
  nand nand_503 (out_10[27], nand_504_out, nand_504_out);
  nand nand_504 (nand_504_out, id_mux_x5_1_output_x32[27], id_mux_x5_2_output_x32[7]);
  nand nand_505 (out_10[28], nand_506_out, nand_506_out);
  nand nand_506 (nand_506_out, id_mux_x5_1_output_x32[28], id_mux_x5_2_output_x32[7]);
  nand nand_507 (out_10[29], nand_508_out, nand_508_out);
  nand nand_508 (nand_508_out, id_mux_x5_1_output_x32[29], id_mux_x5_2_output_x32[7]);
  nand nand_509 (out_10[30], nand_510_out, nand_510_out);
  nand nand_510 (nand_510_out, id_mux_x5_1_output_x32[30], id_mux_x5_2_output_x32[7]);
  nand nand_511 (out_10[31], nand_512_out, nand_512_out);
  nand nand_512 (nand_512_out, id_mux_x5_1_output_x32[31], id_mux_x5_2_output_x32[7]);
  nand nand_513 (out_11[0], nand_514_out, nand_514_out);
  nand nand_514 (nand_514_out, id_mux_x5_1_output_x32[0], id_mux_x5_2_output_x32[8]);
  nand nand_515 (out_11[1], nand_516_out, nand_516_out);
  nand nand_516 (nand_516_out, id_mux_x5_1_output_x32[1], id_mux_x5_2_output_x32[8]);
  nand nand_517 (out_11[2], nand_518_out, nand_518_out);
  nand nand_518 (nand_518_out, id_mux_x5_1_output_x32[2], id_mux_x5_2_output_x32[8]);
  nand nand_519 (out_11[3], nand_520_out, nand_520_out);
  nand nand_520 (nand_520_out, id_mux_x5_1_output_x32[3], id_mux_x5_2_output_x32[8]);
  nand nand_521 (out_11[4], nand_522_out, nand_522_out);
  nand nand_522 (nand_522_out, id_mux_x5_1_output_x32[4], id_mux_x5_2_output_x32[8]);
  nand nand_523 (out_11[5], nand_524_out, nand_524_out);
  nand nand_524 (nand_524_out, id_mux_x5_1_output_x32[5], id_mux_x5_2_output_x32[8]);
  nand nand_525 (out_11[6], nand_526_out, nand_526_out);
  nand nand_526 (nand_526_out, id_mux_x5_1_output_x32[6], id_mux_x5_2_output_x32[8]);
  nand nand_527 (out_11[7], nand_528_out, nand_528_out);
  nand nand_528 (nand_528_out, id_mux_x5_1_output_x32[7], id_mux_x5_2_output_x32[8]);
  nand nand_529 (out_11[8], nand_530_out, nand_530_out);
  nand nand_530 (nand_530_out, id_mux_x5_1_output_x32[8], id_mux_x5_2_output_x32[8]);
  nand nand_531 (out_11[9], nand_532_out, nand_532_out);
  nand nand_532 (nand_532_out, id_mux_x5_1_output_x32[9], id_mux_x5_2_output_x32[8]);
  nand nand_533 (out_11[10], nand_534_out, nand_534_out);
  nand nand_534 (nand_534_out, id_mux_x5_1_output_x32[10], id_mux_x5_2_output_x32[8]);
  nand nand_535 (out_11[11], nand_536_out, nand_536_out);
  nand nand_536 (nand_536_out, id_mux_x5_1_output_x32[11], id_mux_x5_2_output_x32[8]);
  nand nand_537 (out_11[12], nand_538_out, nand_538_out);
  nand nand_538 (nand_538_out, id_mux_x5_1_output_x32[12], id_mux_x5_2_output_x32[8]);
  nand nand_539 (out_11[13], nand_540_out, nand_540_out);
  nand nand_540 (nand_540_out, id_mux_x5_1_output_x32[13], id_mux_x5_2_output_x32[8]);
  nand nand_541 (out_11[14], nand_542_out, nand_542_out);
  nand nand_542 (nand_542_out, id_mux_x5_1_output_x32[14], id_mux_x5_2_output_x32[8]);
  nand nand_543 (out_11[15], nand_544_out, nand_544_out);
  nand nand_544 (nand_544_out, id_mux_x5_1_output_x32[15], id_mux_x5_2_output_x32[8]);
  nand nand_545 (out_11[16], nand_546_out, nand_546_out);
  nand nand_546 (nand_546_out, id_mux_x5_1_output_x32[16], id_mux_x5_2_output_x32[8]);
  nand nand_547 (out_11[17], nand_548_out, nand_548_out);
  nand nand_548 (nand_548_out, id_mux_x5_1_output_x32[17], id_mux_x5_2_output_x32[8]);
  nand nand_549 (out_11[18], nand_550_out, nand_550_out);
  nand nand_550 (nand_550_out, id_mux_x5_1_output_x32[18], id_mux_x5_2_output_x32[8]);
  nand nand_551 (out_11[19], nand_552_out, nand_552_out);
  nand nand_552 (nand_552_out, id_mux_x5_1_output_x32[19], id_mux_x5_2_output_x32[8]);
  nand nand_553 (out_11[20], nand_554_out, nand_554_out);
  nand nand_554 (nand_554_out, id_mux_x5_1_output_x32[20], id_mux_x5_2_output_x32[8]);
  nand nand_555 (out_11[21], nand_556_out, nand_556_out);
  nand nand_556 (nand_556_out, id_mux_x5_1_output_x32[21], id_mux_x5_2_output_x32[8]);
  nand nand_557 (out_11[22], nand_558_out, nand_558_out);
  nand nand_558 (nand_558_out, id_mux_x5_1_output_x32[22], id_mux_x5_2_output_x32[8]);
  nand nand_559 (out_11[23], nand_560_out, nand_560_out);
  nand nand_560 (nand_560_out, id_mux_x5_1_output_x32[23], id_mux_x5_2_output_x32[8]);
  nand nand_561 (out_11[24], nand_562_out, nand_562_out);
  nand nand_562 (nand_562_out, id_mux_x5_1_output_x32[24], id_mux_x5_2_output_x32[8]);
  nand nand_563 (out_11[25], nand_564_out, nand_564_out);
  nand nand_564 (nand_564_out, id_mux_x5_1_output_x32[25], id_mux_x5_2_output_x32[8]);
  nand nand_565 (out_11[26], nand_566_out, nand_566_out);
  nand nand_566 (nand_566_out, id_mux_x5_1_output_x32[26], id_mux_x5_2_output_x32[8]);
  nand nand_567 (out_11[27], nand_568_out, nand_568_out);
  nand nand_568 (nand_568_out, id_mux_x5_1_output_x32[27], id_mux_x5_2_output_x32[8]);
  nand nand_569 (out_11[28], nand_570_out, nand_570_out);
  nand nand_570 (nand_570_out, id_mux_x5_1_output_x32[28], id_mux_x5_2_output_x32[8]);
  nand nand_571 (out_11[29], nand_572_out, nand_572_out);
  nand nand_572 (nand_572_out, id_mux_x5_1_output_x32[29], id_mux_x5_2_output_x32[8]);
  nand nand_573 (out_11[30], nand_574_out, nand_574_out);
  nand nand_574 (nand_574_out, id_mux_x5_1_output_x32[30], id_mux_x5_2_output_x32[8]);
  nand nand_575 (out_11[31], nand_576_out, nand_576_out);
  nand nand_576 (nand_576_out, id_mux_x5_1_output_x32[31], id_mux_x5_2_output_x32[8]);
  nand nand_577 (out_12[0], nand_578_out, nand_578_out);
  nand nand_578 (nand_578_out, id_mux_x5_1_output_x32[0], id_mux_x5_2_output_x32[9]);
  nand nand_579 (out_12[1], nand_580_out, nand_580_out);
  nand nand_580 (nand_580_out, id_mux_x5_1_output_x32[1], id_mux_x5_2_output_x32[9]);
  nand nand_581 (out_12[2], nand_582_out, nand_582_out);
  nand nand_582 (nand_582_out, id_mux_x5_1_output_x32[2], id_mux_x5_2_output_x32[9]);
  nand nand_583 (out_12[3], nand_584_out, nand_584_out);
  nand nand_584 (nand_584_out, id_mux_x5_1_output_x32[3], id_mux_x5_2_output_x32[9]);
  nand nand_585 (out_12[4], nand_586_out, nand_586_out);
  nand nand_586 (nand_586_out, id_mux_x5_1_output_x32[4], id_mux_x5_2_output_x32[9]);
  nand nand_587 (out_12[5], nand_588_out, nand_588_out);
  nand nand_588 (nand_588_out, id_mux_x5_1_output_x32[5], id_mux_x5_2_output_x32[9]);
  nand nand_589 (out_12[6], nand_590_out, nand_590_out);
  nand nand_590 (nand_590_out, id_mux_x5_1_output_x32[6], id_mux_x5_2_output_x32[9]);
  nand nand_591 (out_12[7], nand_592_out, nand_592_out);
  nand nand_592 (nand_592_out, id_mux_x5_1_output_x32[7], id_mux_x5_2_output_x32[9]);
  nand nand_593 (out_12[8], nand_594_out, nand_594_out);
  nand nand_594 (nand_594_out, id_mux_x5_1_output_x32[8], id_mux_x5_2_output_x32[9]);
  nand nand_595 (out_12[9], nand_596_out, nand_596_out);
  nand nand_596 (nand_596_out, id_mux_x5_1_output_x32[9], id_mux_x5_2_output_x32[9]);
  nand nand_597 (out_12[10], nand_598_out, nand_598_out);
  nand nand_598 (nand_598_out, id_mux_x5_1_output_x32[10], id_mux_x5_2_output_x32[9]);
  nand nand_599 (out_12[11], nand_600_out, nand_600_out);
  nand nand_600 (nand_600_out, id_mux_x5_1_output_x32[11], id_mux_x5_2_output_x32[9]);
  nand nand_601 (out_12[12], nand_602_out, nand_602_out);
  nand nand_602 (nand_602_out, id_mux_x5_1_output_x32[12], id_mux_x5_2_output_x32[9]);
  nand nand_603 (out_12[13], nand_604_out, nand_604_out);
  nand nand_604 (nand_604_out, id_mux_x5_1_output_x32[13], id_mux_x5_2_output_x32[9]);
  nand nand_605 (out_12[14], nand_606_out, nand_606_out);
  nand nand_606 (nand_606_out, id_mux_x5_1_output_x32[14], id_mux_x5_2_output_x32[9]);
  nand nand_607 (out_12[15], nand_608_out, nand_608_out);
  nand nand_608 (nand_608_out, id_mux_x5_1_output_x32[15], id_mux_x5_2_output_x32[9]);
  nand nand_609 (out_12[16], nand_610_out, nand_610_out);
  nand nand_610 (nand_610_out, id_mux_x5_1_output_x32[16], id_mux_x5_2_output_x32[9]);
  nand nand_611 (out_12[17], nand_612_out, nand_612_out);
  nand nand_612 (nand_612_out, id_mux_x5_1_output_x32[17], id_mux_x5_2_output_x32[9]);
  nand nand_613 (out_12[18], nand_614_out, nand_614_out);
  nand nand_614 (nand_614_out, id_mux_x5_1_output_x32[18], id_mux_x5_2_output_x32[9]);
  nand nand_615 (out_12[19], nand_616_out, nand_616_out);
  nand nand_616 (nand_616_out, id_mux_x5_1_output_x32[19], id_mux_x5_2_output_x32[9]);
  nand nand_617 (out_12[20], nand_618_out, nand_618_out);
  nand nand_618 (nand_618_out, id_mux_x5_1_output_x32[20], id_mux_x5_2_output_x32[9]);
  nand nand_619 (out_12[21], nand_620_out, nand_620_out);
  nand nand_620 (nand_620_out, id_mux_x5_1_output_x32[21], id_mux_x5_2_output_x32[9]);
  nand nand_621 (out_12[22], nand_622_out, nand_622_out);
  nand nand_622 (nand_622_out, id_mux_x5_1_output_x32[22], id_mux_x5_2_output_x32[9]);
  nand nand_623 (out_12[23], nand_624_out, nand_624_out);
  nand nand_624 (nand_624_out, id_mux_x5_1_output_x32[23], id_mux_x5_2_output_x32[9]);
  nand nand_625 (out_12[24], nand_626_out, nand_626_out);
  nand nand_626 (nand_626_out, id_mux_x5_1_output_x32[24], id_mux_x5_2_output_x32[9]);
  nand nand_627 (out_12[25], nand_628_out, nand_628_out);
  nand nand_628 (nand_628_out, id_mux_x5_1_output_x32[25], id_mux_x5_2_output_x32[9]);
  nand nand_629 (out_12[26], nand_630_out, nand_630_out);
  nand nand_630 (nand_630_out, id_mux_x5_1_output_x32[26], id_mux_x5_2_output_x32[9]);
  nand nand_631 (out_12[27], nand_632_out, nand_632_out);
  nand nand_632 (nand_632_out, id_mux_x5_1_output_x32[27], id_mux_x5_2_output_x32[9]);
  nand nand_633 (out_12[28], nand_634_out, nand_634_out);
  nand nand_634 (nand_634_out, id_mux_x5_1_output_x32[28], id_mux_x5_2_output_x32[9]);
  nand nand_635 (out_12[29], nand_636_out, nand_636_out);
  nand nand_636 (nand_636_out, id_mux_x5_1_output_x32[29], id_mux_x5_2_output_x32[9]);
  nand nand_637 (out_12[30], nand_638_out, nand_638_out);
  nand nand_638 (nand_638_out, id_mux_x5_1_output_x32[30], id_mux_x5_2_output_x32[9]);
  nand nand_639 (out_12[31], nand_640_out, nand_640_out);
  nand nand_640 (nand_640_out, id_mux_x5_1_output_x32[31], id_mux_x5_2_output_x32[9]);
  nand nand_641 (out_13[0], nand_642_out, nand_642_out);
  nand nand_642 (nand_642_out, id_mux_x5_1_output_x32[0], id_mux_x5_2_output_x32[10]);
  nand nand_643 (out_13[1], nand_644_out, nand_644_out);
  nand nand_644 (nand_644_out, id_mux_x5_1_output_x32[1], id_mux_x5_2_output_x32[10]);
  nand nand_645 (out_13[2], nand_646_out, nand_646_out);
  nand nand_646 (nand_646_out, id_mux_x5_1_output_x32[2], id_mux_x5_2_output_x32[10]);
  nand nand_647 (out_13[3], nand_648_out, nand_648_out);
  nand nand_648 (nand_648_out, id_mux_x5_1_output_x32[3], id_mux_x5_2_output_x32[10]);
  nand nand_649 (out_13[4], nand_650_out, nand_650_out);
  nand nand_650 (nand_650_out, id_mux_x5_1_output_x32[4], id_mux_x5_2_output_x32[10]);
  nand nand_651 (out_13[5], nand_652_out, nand_652_out);
  nand nand_652 (nand_652_out, id_mux_x5_1_output_x32[5], id_mux_x5_2_output_x32[10]);
  nand nand_653 (out_13[6], nand_654_out, nand_654_out);
  nand nand_654 (nand_654_out, id_mux_x5_1_output_x32[6], id_mux_x5_2_output_x32[10]);
  nand nand_655 (out_13[7], nand_656_out, nand_656_out);
  nand nand_656 (nand_656_out, id_mux_x5_1_output_x32[7], id_mux_x5_2_output_x32[10]);
  nand nand_657 (out_13[8], nand_658_out, nand_658_out);
  nand nand_658 (nand_658_out, id_mux_x5_1_output_x32[8], id_mux_x5_2_output_x32[10]);
  nand nand_659 (out_13[9], nand_660_out, nand_660_out);
  nand nand_660 (nand_660_out, id_mux_x5_1_output_x32[9], id_mux_x5_2_output_x32[10]);
  nand nand_661 (out_13[10], nand_662_out, nand_662_out);
  nand nand_662 (nand_662_out, id_mux_x5_1_output_x32[10], id_mux_x5_2_output_x32[10]);
  nand nand_663 (out_13[11], nand_664_out, nand_664_out);
  nand nand_664 (nand_664_out, id_mux_x5_1_output_x32[11], id_mux_x5_2_output_x32[10]);
  nand nand_665 (out_13[12], nand_666_out, nand_666_out);
  nand nand_666 (nand_666_out, id_mux_x5_1_output_x32[12], id_mux_x5_2_output_x32[10]);
  nand nand_667 (out_13[13], nand_668_out, nand_668_out);
  nand nand_668 (nand_668_out, id_mux_x5_1_output_x32[13], id_mux_x5_2_output_x32[10]);
  nand nand_669 (out_13[14], nand_670_out, nand_670_out);
  nand nand_670 (nand_670_out, id_mux_x5_1_output_x32[14], id_mux_x5_2_output_x32[10]);
  nand nand_671 (out_13[15], nand_672_out, nand_672_out);
  nand nand_672 (nand_672_out, id_mux_x5_1_output_x32[15], id_mux_x5_2_output_x32[10]);
  nand nand_673 (out_13[16], nand_674_out, nand_674_out);
  nand nand_674 (nand_674_out, id_mux_x5_1_output_x32[16], id_mux_x5_2_output_x32[10]);
  nand nand_675 (out_13[17], nand_676_out, nand_676_out);
  nand nand_676 (nand_676_out, id_mux_x5_1_output_x32[17], id_mux_x5_2_output_x32[10]);
  nand nand_677 (out_13[18], nand_678_out, nand_678_out);
  nand nand_678 (nand_678_out, id_mux_x5_1_output_x32[18], id_mux_x5_2_output_x32[10]);
  nand nand_679 (out_13[19], nand_680_out, nand_680_out);
  nand nand_680 (nand_680_out, id_mux_x5_1_output_x32[19], id_mux_x5_2_output_x32[10]);
  nand nand_681 (out_13[20], nand_682_out, nand_682_out);
  nand nand_682 (nand_682_out, id_mux_x5_1_output_x32[20], id_mux_x5_2_output_x32[10]);
  nand nand_683 (out_13[21], nand_684_out, nand_684_out);
  nand nand_684 (nand_684_out, id_mux_x5_1_output_x32[21], id_mux_x5_2_output_x32[10]);
  nand nand_685 (out_13[22], nand_686_out, nand_686_out);
  nand nand_686 (nand_686_out, id_mux_x5_1_output_x32[22], id_mux_x5_2_output_x32[10]);
  nand nand_687 (out_13[23], nand_688_out, nand_688_out);
  nand nand_688 (nand_688_out, id_mux_x5_1_output_x32[23], id_mux_x5_2_output_x32[10]);
  nand nand_689 (out_13[24], nand_690_out, nand_690_out);
  nand nand_690 (nand_690_out, id_mux_x5_1_output_x32[24], id_mux_x5_2_output_x32[10]);
  nand nand_691 (out_13[25], nand_692_out, nand_692_out);
  nand nand_692 (nand_692_out, id_mux_x5_1_output_x32[25], id_mux_x5_2_output_x32[10]);
  nand nand_693 (out_13[26], nand_694_out, nand_694_out);
  nand nand_694 (nand_694_out, id_mux_x5_1_output_x32[26], id_mux_x5_2_output_x32[10]);
  nand nand_695 (out_13[27], nand_696_out, nand_696_out);
  nand nand_696 (nand_696_out, id_mux_x5_1_output_x32[27], id_mux_x5_2_output_x32[10]);
  nand nand_697 (out_13[28], nand_698_out, nand_698_out);
  nand nand_698 (nand_698_out, id_mux_x5_1_output_x32[28], id_mux_x5_2_output_x32[10]);
  nand nand_699 (out_13[29], nand_700_out, nand_700_out);
  nand nand_700 (nand_700_out, id_mux_x5_1_output_x32[29], id_mux_x5_2_output_x32[10]);
  nand nand_701 (out_13[30], nand_702_out, nand_702_out);
  nand nand_702 (nand_702_out, id_mux_x5_1_output_x32[30], id_mux_x5_2_output_x32[10]);
  nand nand_703 (out_13[31], nand_704_out, nand_704_out);
  nand nand_704 (nand_704_out, id_mux_x5_1_output_x32[31], id_mux_x5_2_output_x32[10]);
  nand nand_705 (out_14[0], nand_706_out, nand_706_out);
  nand nand_706 (nand_706_out, id_mux_x5_1_output_x32[0], id_mux_x5_2_output_x32[11]);
  nand nand_707 (out_14[1], nand_708_out, nand_708_out);
  nand nand_708 (nand_708_out, id_mux_x5_1_output_x32[1], id_mux_x5_2_output_x32[11]);
  nand nand_709 (out_14[2], nand_710_out, nand_710_out);
  nand nand_710 (nand_710_out, id_mux_x5_1_output_x32[2], id_mux_x5_2_output_x32[11]);
  nand nand_711 (out_14[3], nand_712_out, nand_712_out);
  nand nand_712 (nand_712_out, id_mux_x5_1_output_x32[3], id_mux_x5_2_output_x32[11]);
  nand nand_713 (out_14[4], nand_714_out, nand_714_out);
  nand nand_714 (nand_714_out, id_mux_x5_1_output_x32[4], id_mux_x5_2_output_x32[11]);
  nand nand_715 (out_14[5], nand_716_out, nand_716_out);
  nand nand_716 (nand_716_out, id_mux_x5_1_output_x32[5], id_mux_x5_2_output_x32[11]);
  nand nand_717 (out_14[6], nand_718_out, nand_718_out);
  nand nand_718 (nand_718_out, id_mux_x5_1_output_x32[6], id_mux_x5_2_output_x32[11]);
  nand nand_719 (out_14[7], nand_720_out, nand_720_out);
  nand nand_720 (nand_720_out, id_mux_x5_1_output_x32[7], id_mux_x5_2_output_x32[11]);
  nand nand_721 (out_14[8], nand_722_out, nand_722_out);
  nand nand_722 (nand_722_out, id_mux_x5_1_output_x32[8], id_mux_x5_2_output_x32[11]);
  nand nand_723 (out_14[9], nand_724_out, nand_724_out);
  nand nand_724 (nand_724_out, id_mux_x5_1_output_x32[9], id_mux_x5_2_output_x32[11]);
  nand nand_725 (out_14[10], nand_726_out, nand_726_out);
  nand nand_726 (nand_726_out, id_mux_x5_1_output_x32[10], id_mux_x5_2_output_x32[11]);
  nand nand_727 (out_14[11], nand_728_out, nand_728_out);
  nand nand_728 (nand_728_out, id_mux_x5_1_output_x32[11], id_mux_x5_2_output_x32[11]);
  nand nand_729 (out_14[12], nand_730_out, nand_730_out);
  nand nand_730 (nand_730_out, id_mux_x5_1_output_x32[12], id_mux_x5_2_output_x32[11]);
  nand nand_731 (out_14[13], nand_732_out, nand_732_out);
  nand nand_732 (nand_732_out, id_mux_x5_1_output_x32[13], id_mux_x5_2_output_x32[11]);
  nand nand_733 (out_14[14], nand_734_out, nand_734_out);
  nand nand_734 (nand_734_out, id_mux_x5_1_output_x32[14], id_mux_x5_2_output_x32[11]);
  nand nand_735 (out_14[15], nand_736_out, nand_736_out);
  nand nand_736 (nand_736_out, id_mux_x5_1_output_x32[15], id_mux_x5_2_output_x32[11]);
  nand nand_737 (out_14[16], nand_738_out, nand_738_out);
  nand nand_738 (nand_738_out, id_mux_x5_1_output_x32[16], id_mux_x5_2_output_x32[11]);
  nand nand_739 (out_14[17], nand_740_out, nand_740_out);
  nand nand_740 (nand_740_out, id_mux_x5_1_output_x32[17], id_mux_x5_2_output_x32[11]);
  nand nand_741 (out_14[18], nand_742_out, nand_742_out);
  nand nand_742 (nand_742_out, id_mux_x5_1_output_x32[18], id_mux_x5_2_output_x32[11]);
  nand nand_743 (out_14[19], nand_744_out, nand_744_out);
  nand nand_744 (nand_744_out, id_mux_x5_1_output_x32[19], id_mux_x5_2_output_x32[11]);
  nand nand_745 (out_14[20], nand_746_out, nand_746_out);
  nand nand_746 (nand_746_out, id_mux_x5_1_output_x32[20], id_mux_x5_2_output_x32[11]);
  nand nand_747 (out_14[21], nand_748_out, nand_748_out);
  nand nand_748 (nand_748_out, id_mux_x5_1_output_x32[21], id_mux_x5_2_output_x32[11]);
  nand nand_749 (out_14[22], nand_750_out, nand_750_out);
  nand nand_750 (nand_750_out, id_mux_x5_1_output_x32[22], id_mux_x5_2_output_x32[11]);
  nand nand_751 (out_14[23], nand_752_out, nand_752_out);
  nand nand_752 (nand_752_out, id_mux_x5_1_output_x32[23], id_mux_x5_2_output_x32[11]);
  nand nand_753 (out_14[24], nand_754_out, nand_754_out);
  nand nand_754 (nand_754_out, id_mux_x5_1_output_x32[24], id_mux_x5_2_output_x32[11]);
  nand nand_755 (out_14[25], nand_756_out, nand_756_out);
  nand nand_756 (nand_756_out, id_mux_x5_1_output_x32[25], id_mux_x5_2_output_x32[11]);
  nand nand_757 (out_14[26], nand_758_out, nand_758_out);
  nand nand_758 (nand_758_out, id_mux_x5_1_output_x32[26], id_mux_x5_2_output_x32[11]);
  nand nand_759 (out_14[27], nand_760_out, nand_760_out);
  nand nand_760 (nand_760_out, id_mux_x5_1_output_x32[27], id_mux_x5_2_output_x32[11]);
  nand nand_761 (out_14[28], nand_762_out, nand_762_out);
  nand nand_762 (nand_762_out, id_mux_x5_1_output_x32[28], id_mux_x5_2_output_x32[11]);
  nand nand_763 (out_14[29], nand_764_out, nand_764_out);
  nand nand_764 (nand_764_out, id_mux_x5_1_output_x32[29], id_mux_x5_2_output_x32[11]);
  nand nand_765 (out_14[30], nand_766_out, nand_766_out);
  nand nand_766 (nand_766_out, id_mux_x5_1_output_x32[30], id_mux_x5_2_output_x32[11]);
  nand nand_767 (out_14[31], nand_768_out, nand_768_out);
  nand nand_768 (nand_768_out, id_mux_x5_1_output_x32[31], id_mux_x5_2_output_x32[11]);
  nand nand_769 (out_15[0], nand_770_out, nand_770_out);
  nand nand_770 (nand_770_out, id_mux_x5_1_output_x32[0], id_mux_x5_2_output_x32[12]);
  nand nand_771 (out_15[1], nand_772_out, nand_772_out);
  nand nand_772 (nand_772_out, id_mux_x5_1_output_x32[1], id_mux_x5_2_output_x32[12]);
  nand nand_773 (out_15[2], nand_774_out, nand_774_out);
  nand nand_774 (nand_774_out, id_mux_x5_1_output_x32[2], id_mux_x5_2_output_x32[12]);
  nand nand_775 (out_15[3], nand_776_out, nand_776_out);
  nand nand_776 (nand_776_out, id_mux_x5_1_output_x32[3], id_mux_x5_2_output_x32[12]);
  nand nand_777 (out_15[4], nand_778_out, nand_778_out);
  nand nand_778 (nand_778_out, id_mux_x5_1_output_x32[4], id_mux_x5_2_output_x32[12]);
  nand nand_779 (out_15[5], nand_780_out, nand_780_out);
  nand nand_780 (nand_780_out, id_mux_x5_1_output_x32[5], id_mux_x5_2_output_x32[12]);
  nand nand_781 (out_15[6], nand_782_out, nand_782_out);
  nand nand_782 (nand_782_out, id_mux_x5_1_output_x32[6], id_mux_x5_2_output_x32[12]);
  nand nand_783 (out_15[7], nand_784_out, nand_784_out);
  nand nand_784 (nand_784_out, id_mux_x5_1_output_x32[7], id_mux_x5_2_output_x32[12]);
  nand nand_785 (out_15[8], nand_786_out, nand_786_out);
  nand nand_786 (nand_786_out, id_mux_x5_1_output_x32[8], id_mux_x5_2_output_x32[12]);
  nand nand_787 (out_15[9], nand_788_out, nand_788_out);
  nand nand_788 (nand_788_out, id_mux_x5_1_output_x32[9], id_mux_x5_2_output_x32[12]);
  nand nand_789 (out_15[10], nand_790_out, nand_790_out);
  nand nand_790 (nand_790_out, id_mux_x5_1_output_x32[10], id_mux_x5_2_output_x32[12]);
  nand nand_791 (out_15[11], nand_792_out, nand_792_out);
  nand nand_792 (nand_792_out, id_mux_x5_1_output_x32[11], id_mux_x5_2_output_x32[12]);
  nand nand_793 (out_15[12], nand_794_out, nand_794_out);
  nand nand_794 (nand_794_out, id_mux_x5_1_output_x32[12], id_mux_x5_2_output_x32[12]);
  nand nand_795 (out_15[13], nand_796_out, nand_796_out);
  nand nand_796 (nand_796_out, id_mux_x5_1_output_x32[13], id_mux_x5_2_output_x32[12]);
  nand nand_797 (out_15[14], nand_798_out, nand_798_out);
  nand nand_798 (nand_798_out, id_mux_x5_1_output_x32[14], id_mux_x5_2_output_x32[12]);
  nand nand_799 (out_15[15], nand_800_out, nand_800_out);
  nand nand_800 (nand_800_out, id_mux_x5_1_output_x32[15], id_mux_x5_2_output_x32[12]);
  nand nand_801 (out_15[16], nand_802_out, nand_802_out);
  nand nand_802 (nand_802_out, id_mux_x5_1_output_x32[16], id_mux_x5_2_output_x32[12]);
  nand nand_803 (out_15[17], nand_804_out, nand_804_out);
  nand nand_804 (nand_804_out, id_mux_x5_1_output_x32[17], id_mux_x5_2_output_x32[12]);
  nand nand_805 (out_15[18], nand_806_out, nand_806_out);
  nand nand_806 (nand_806_out, id_mux_x5_1_output_x32[18], id_mux_x5_2_output_x32[12]);
  nand nand_807 (out_15[19], nand_808_out, nand_808_out);
  nand nand_808 (nand_808_out, id_mux_x5_1_output_x32[19], id_mux_x5_2_output_x32[12]);
  nand nand_809 (out_15[20], nand_810_out, nand_810_out);
  nand nand_810 (nand_810_out, id_mux_x5_1_output_x32[20], id_mux_x5_2_output_x32[12]);
  nand nand_811 (out_15[21], nand_812_out, nand_812_out);
  nand nand_812 (nand_812_out, id_mux_x5_1_output_x32[21], id_mux_x5_2_output_x32[12]);
  nand nand_813 (out_15[22], nand_814_out, nand_814_out);
  nand nand_814 (nand_814_out, id_mux_x5_1_output_x32[22], id_mux_x5_2_output_x32[12]);
  nand nand_815 (out_15[23], nand_816_out, nand_816_out);
  nand nand_816 (nand_816_out, id_mux_x5_1_output_x32[23], id_mux_x5_2_output_x32[12]);
  nand nand_817 (out_15[24], nand_818_out, nand_818_out);
  nand nand_818 (nand_818_out, id_mux_x5_1_output_x32[24], id_mux_x5_2_output_x32[12]);
  nand nand_819 (out_15[25], nand_820_out, nand_820_out);
  nand nand_820 (nand_820_out, id_mux_x5_1_output_x32[25], id_mux_x5_2_output_x32[12]);
  nand nand_821 (out_15[26], nand_822_out, nand_822_out);
  nand nand_822 (nand_822_out, id_mux_x5_1_output_x32[26], id_mux_x5_2_output_x32[12]);
  nand nand_823 (out_15[27], nand_824_out, nand_824_out);
  nand nand_824 (nand_824_out, id_mux_x5_1_output_x32[27], id_mux_x5_2_output_x32[12]);
  nand nand_825 (out_15[28], nand_826_out, nand_826_out);
  nand nand_826 (nand_826_out, id_mux_x5_1_output_x32[28], id_mux_x5_2_output_x32[12]);
  nand nand_827 (out_15[29], nand_828_out, nand_828_out);
  nand nand_828 (nand_828_out, id_mux_x5_1_output_x32[29], id_mux_x5_2_output_x32[12]);
  nand nand_829 (out_15[30], nand_830_out, nand_830_out);
  nand nand_830 (nand_830_out, id_mux_x5_1_output_x32[30], id_mux_x5_2_output_x32[12]);
  nand nand_831 (out_15[31], nand_832_out, nand_832_out);
  nand nand_832 (nand_832_out, id_mux_x5_1_output_x32[31], id_mux_x5_2_output_x32[12]);
  nand nand_833 (out_16[0], nand_834_out, nand_834_out);
  nand nand_834 (nand_834_out, id_mux_x5_1_output_x32[0], id_mux_x5_2_output_x32[13]);
  nand nand_835 (out_16[1], nand_836_out, nand_836_out);
  nand nand_836 (nand_836_out, id_mux_x5_1_output_x32[1], id_mux_x5_2_output_x32[13]);
  nand nand_837 (out_16[2], nand_838_out, nand_838_out);
  nand nand_838 (nand_838_out, id_mux_x5_1_output_x32[2], id_mux_x5_2_output_x32[13]);
  nand nand_839 (out_16[3], nand_840_out, nand_840_out);
  nand nand_840 (nand_840_out, id_mux_x5_1_output_x32[3], id_mux_x5_2_output_x32[13]);
  nand nand_841 (out_16[4], nand_842_out, nand_842_out);
  nand nand_842 (nand_842_out, id_mux_x5_1_output_x32[4], id_mux_x5_2_output_x32[13]);
  nand nand_843 (out_16[5], nand_844_out, nand_844_out);
  nand nand_844 (nand_844_out, id_mux_x5_1_output_x32[5], id_mux_x5_2_output_x32[13]);
  nand nand_845 (out_16[6], nand_846_out, nand_846_out);
  nand nand_846 (nand_846_out, id_mux_x5_1_output_x32[6], id_mux_x5_2_output_x32[13]);
  nand nand_847 (out_16[7], nand_848_out, nand_848_out);
  nand nand_848 (nand_848_out, id_mux_x5_1_output_x32[7], id_mux_x5_2_output_x32[13]);
  nand nand_849 (out_16[8], nand_850_out, nand_850_out);
  nand nand_850 (nand_850_out, id_mux_x5_1_output_x32[8], id_mux_x5_2_output_x32[13]);
  nand nand_851 (out_16[9], nand_852_out, nand_852_out);
  nand nand_852 (nand_852_out, id_mux_x5_1_output_x32[9], id_mux_x5_2_output_x32[13]);
  nand nand_853 (out_16[10], nand_854_out, nand_854_out);
  nand nand_854 (nand_854_out, id_mux_x5_1_output_x32[10], id_mux_x5_2_output_x32[13]);
  nand nand_855 (out_16[11], nand_856_out, nand_856_out);
  nand nand_856 (nand_856_out, id_mux_x5_1_output_x32[11], id_mux_x5_2_output_x32[13]);
  nand nand_857 (out_16[12], nand_858_out, nand_858_out);
  nand nand_858 (nand_858_out, id_mux_x5_1_output_x32[12], id_mux_x5_2_output_x32[13]);
  nand nand_859 (out_16[13], nand_860_out, nand_860_out);
  nand nand_860 (nand_860_out, id_mux_x5_1_output_x32[13], id_mux_x5_2_output_x32[13]);
  nand nand_861 (out_16[14], nand_862_out, nand_862_out);
  nand nand_862 (nand_862_out, id_mux_x5_1_output_x32[14], id_mux_x5_2_output_x32[13]);
  nand nand_863 (out_16[15], nand_864_out, nand_864_out);
  nand nand_864 (nand_864_out, id_mux_x5_1_output_x32[15], id_mux_x5_2_output_x32[13]);
  nand nand_865 (out_16[16], nand_866_out, nand_866_out);
  nand nand_866 (nand_866_out, id_mux_x5_1_output_x32[16], id_mux_x5_2_output_x32[13]);
  nand nand_867 (out_16[17], nand_868_out, nand_868_out);
  nand nand_868 (nand_868_out, id_mux_x5_1_output_x32[17], id_mux_x5_2_output_x32[13]);
  nand nand_869 (out_16[18], nand_870_out, nand_870_out);
  nand nand_870 (nand_870_out, id_mux_x5_1_output_x32[18], id_mux_x5_2_output_x32[13]);
  nand nand_871 (out_16[19], nand_872_out, nand_872_out);
  nand nand_872 (nand_872_out, id_mux_x5_1_output_x32[19], id_mux_x5_2_output_x32[13]);
  nand nand_873 (out_16[20], nand_874_out, nand_874_out);
  nand nand_874 (nand_874_out, id_mux_x5_1_output_x32[20], id_mux_x5_2_output_x32[13]);
  nand nand_875 (out_16[21], nand_876_out, nand_876_out);
  nand nand_876 (nand_876_out, id_mux_x5_1_output_x32[21], id_mux_x5_2_output_x32[13]);
  nand nand_877 (out_16[22], nand_878_out, nand_878_out);
  nand nand_878 (nand_878_out, id_mux_x5_1_output_x32[22], id_mux_x5_2_output_x32[13]);
  nand nand_879 (out_16[23], nand_880_out, nand_880_out);
  nand nand_880 (nand_880_out, id_mux_x5_1_output_x32[23], id_mux_x5_2_output_x32[13]);
  nand nand_881 (out_16[24], nand_882_out, nand_882_out);
  nand nand_882 (nand_882_out, id_mux_x5_1_output_x32[24], id_mux_x5_2_output_x32[13]);
  nand nand_883 (out_16[25], nand_884_out, nand_884_out);
  nand nand_884 (nand_884_out, id_mux_x5_1_output_x32[25], id_mux_x5_2_output_x32[13]);
  nand nand_885 (out_16[26], nand_886_out, nand_886_out);
  nand nand_886 (nand_886_out, id_mux_x5_1_output_x32[26], id_mux_x5_2_output_x32[13]);
  nand nand_887 (out_16[27], nand_888_out, nand_888_out);
  nand nand_888 (nand_888_out, id_mux_x5_1_output_x32[27], id_mux_x5_2_output_x32[13]);
  nand nand_889 (out_16[28], nand_890_out, nand_890_out);
  nand nand_890 (nand_890_out, id_mux_x5_1_output_x32[28], id_mux_x5_2_output_x32[13]);
  nand nand_891 (out_16[29], nand_892_out, nand_892_out);
  nand nand_892 (nand_892_out, id_mux_x5_1_output_x32[29], id_mux_x5_2_output_x32[13]);
  nand nand_893 (out_16[30], nand_894_out, nand_894_out);
  nand nand_894 (nand_894_out, id_mux_x5_1_output_x32[30], id_mux_x5_2_output_x32[13]);
  nand nand_895 (out_16[31], nand_896_out, nand_896_out);
  nand nand_896 (nand_896_out, id_mux_x5_1_output_x32[31], id_mux_x5_2_output_x32[13]);
  nand nand_897 (out_17[0], nand_898_out, nand_898_out);
  nand nand_898 (nand_898_out, id_mux_x5_1_output_x32[0], id_mux_x5_2_output_x32[14]);
  nand nand_899 (out_17[1], nand_900_out, nand_900_out);
  nand nand_900 (nand_900_out, id_mux_x5_1_output_x32[1], id_mux_x5_2_output_x32[14]);
  nand nand_901 (out_17[2], nand_902_out, nand_902_out);
  nand nand_902 (nand_902_out, id_mux_x5_1_output_x32[2], id_mux_x5_2_output_x32[14]);
  nand nand_903 (out_17[3], nand_904_out, nand_904_out);
  nand nand_904 (nand_904_out, id_mux_x5_1_output_x32[3], id_mux_x5_2_output_x32[14]);
  nand nand_905 (out_17[4], nand_906_out, nand_906_out);
  nand nand_906 (nand_906_out, id_mux_x5_1_output_x32[4], id_mux_x5_2_output_x32[14]);
  nand nand_907 (out_17[5], nand_908_out, nand_908_out);
  nand nand_908 (nand_908_out, id_mux_x5_1_output_x32[5], id_mux_x5_2_output_x32[14]);
  nand nand_909 (out_17[6], nand_910_out, nand_910_out);
  nand nand_910 (nand_910_out, id_mux_x5_1_output_x32[6], id_mux_x5_2_output_x32[14]);
  nand nand_911 (out_17[7], nand_912_out, nand_912_out);
  nand nand_912 (nand_912_out, id_mux_x5_1_output_x32[7], id_mux_x5_2_output_x32[14]);
  nand nand_913 (out_17[8], nand_914_out, nand_914_out);
  nand nand_914 (nand_914_out, id_mux_x5_1_output_x32[8], id_mux_x5_2_output_x32[14]);
  nand nand_915 (out_17[9], nand_916_out, nand_916_out);
  nand nand_916 (nand_916_out, id_mux_x5_1_output_x32[9], id_mux_x5_2_output_x32[14]);
  nand nand_917 (out_17[10], nand_918_out, nand_918_out);
  nand nand_918 (nand_918_out, id_mux_x5_1_output_x32[10], id_mux_x5_2_output_x32[14]);
  nand nand_919 (out_17[11], nand_920_out, nand_920_out);
  nand nand_920 (nand_920_out, id_mux_x5_1_output_x32[11], id_mux_x5_2_output_x32[14]);
  nand nand_921 (out_17[12], nand_922_out, nand_922_out);
  nand nand_922 (nand_922_out, id_mux_x5_1_output_x32[12], id_mux_x5_2_output_x32[14]);
  nand nand_923 (out_17[13], nand_924_out, nand_924_out);
  nand nand_924 (nand_924_out, id_mux_x5_1_output_x32[13], id_mux_x5_2_output_x32[14]);
  nand nand_925 (out_17[14], nand_926_out, nand_926_out);
  nand nand_926 (nand_926_out, id_mux_x5_1_output_x32[14], id_mux_x5_2_output_x32[14]);
  nand nand_927 (out_17[15], nand_928_out, nand_928_out);
  nand nand_928 (nand_928_out, id_mux_x5_1_output_x32[15], id_mux_x5_2_output_x32[14]);
  nand nand_929 (out_17[16], nand_930_out, nand_930_out);
  nand nand_930 (nand_930_out, id_mux_x5_1_output_x32[16], id_mux_x5_2_output_x32[14]);
  nand nand_931 (out_17[17], nand_932_out, nand_932_out);
  nand nand_932 (nand_932_out, id_mux_x5_1_output_x32[17], id_mux_x5_2_output_x32[14]);
  nand nand_933 (out_17[18], nand_934_out, nand_934_out);
  nand nand_934 (nand_934_out, id_mux_x5_1_output_x32[18], id_mux_x5_2_output_x32[14]);
  nand nand_935 (out_17[19], nand_936_out, nand_936_out);
  nand nand_936 (nand_936_out, id_mux_x5_1_output_x32[19], id_mux_x5_2_output_x32[14]);
  nand nand_937 (out_17[20], nand_938_out, nand_938_out);
  nand nand_938 (nand_938_out, id_mux_x5_1_output_x32[20], id_mux_x5_2_output_x32[14]);
  nand nand_939 (out_17[21], nand_940_out, nand_940_out);
  nand nand_940 (nand_940_out, id_mux_x5_1_output_x32[21], id_mux_x5_2_output_x32[14]);
  nand nand_941 (out_17[22], nand_942_out, nand_942_out);
  nand nand_942 (nand_942_out, id_mux_x5_1_output_x32[22], id_mux_x5_2_output_x32[14]);
  nand nand_943 (out_17[23], nand_944_out, nand_944_out);
  nand nand_944 (nand_944_out, id_mux_x5_1_output_x32[23], id_mux_x5_2_output_x32[14]);
  nand nand_945 (out_17[24], nand_946_out, nand_946_out);
  nand nand_946 (nand_946_out, id_mux_x5_1_output_x32[24], id_mux_x5_2_output_x32[14]);
  nand nand_947 (out_17[25], nand_948_out, nand_948_out);
  nand nand_948 (nand_948_out, id_mux_x5_1_output_x32[25], id_mux_x5_2_output_x32[14]);
  nand nand_949 (out_17[26], nand_950_out, nand_950_out);
  nand nand_950 (nand_950_out, id_mux_x5_1_output_x32[26], id_mux_x5_2_output_x32[14]);
  nand nand_951 (out_17[27], nand_952_out, nand_952_out);
  nand nand_952 (nand_952_out, id_mux_x5_1_output_x32[27], id_mux_x5_2_output_x32[14]);
  nand nand_953 (out_17[28], nand_954_out, nand_954_out);
  nand nand_954 (nand_954_out, id_mux_x5_1_output_x32[28], id_mux_x5_2_output_x32[14]);
  nand nand_955 (out_17[29], nand_956_out, nand_956_out);
  nand nand_956 (nand_956_out, id_mux_x5_1_output_x32[29], id_mux_x5_2_output_x32[14]);
  nand nand_957 (out_17[30], nand_958_out, nand_958_out);
  nand nand_958 (nand_958_out, id_mux_x5_1_output_x32[30], id_mux_x5_2_output_x32[14]);
  nand nand_959 (out_17[31], nand_960_out, nand_960_out);
  nand nand_960 (nand_960_out, id_mux_x5_1_output_x32[31], id_mux_x5_2_output_x32[14]);
  nand nand_961 (out_18[0], nand_962_out, nand_962_out);
  nand nand_962 (nand_962_out, id_mux_x5_1_output_x32[0], id_mux_x5_2_output_x32[15]);
  nand nand_963 (out_18[1], nand_964_out, nand_964_out);
  nand nand_964 (nand_964_out, id_mux_x5_1_output_x32[1], id_mux_x5_2_output_x32[15]);
  nand nand_965 (out_18[2], nand_966_out, nand_966_out);
  nand nand_966 (nand_966_out, id_mux_x5_1_output_x32[2], id_mux_x5_2_output_x32[15]);
  nand nand_967 (out_18[3], nand_968_out, nand_968_out);
  nand nand_968 (nand_968_out, id_mux_x5_1_output_x32[3], id_mux_x5_2_output_x32[15]);
  nand nand_969 (out_18[4], nand_970_out, nand_970_out);
  nand nand_970 (nand_970_out, id_mux_x5_1_output_x32[4], id_mux_x5_2_output_x32[15]);
  nand nand_971 (out_18[5], nand_972_out, nand_972_out);
  nand nand_972 (nand_972_out, id_mux_x5_1_output_x32[5], id_mux_x5_2_output_x32[15]);
  nand nand_973 (out_18[6], nand_974_out, nand_974_out);
  nand nand_974 (nand_974_out, id_mux_x5_1_output_x32[6], id_mux_x5_2_output_x32[15]);
  nand nand_975 (out_18[7], nand_976_out, nand_976_out);
  nand nand_976 (nand_976_out, id_mux_x5_1_output_x32[7], id_mux_x5_2_output_x32[15]);
  nand nand_977 (out_18[8], nand_978_out, nand_978_out);
  nand nand_978 (nand_978_out, id_mux_x5_1_output_x32[8], id_mux_x5_2_output_x32[15]);
  nand nand_979 (out_18[9], nand_980_out, nand_980_out);
  nand nand_980 (nand_980_out, id_mux_x5_1_output_x32[9], id_mux_x5_2_output_x32[15]);
  nand nand_981 (out_18[10], nand_982_out, nand_982_out);
  nand nand_982 (nand_982_out, id_mux_x5_1_output_x32[10], id_mux_x5_2_output_x32[15]);
  nand nand_983 (out_18[11], nand_984_out, nand_984_out);
  nand nand_984 (nand_984_out, id_mux_x5_1_output_x32[11], id_mux_x5_2_output_x32[15]);
  nand nand_985 (out_18[12], nand_986_out, nand_986_out);
  nand nand_986 (nand_986_out, id_mux_x5_1_output_x32[12], id_mux_x5_2_output_x32[15]);
  nand nand_987 (out_18[13], nand_988_out, nand_988_out);
  nand nand_988 (nand_988_out, id_mux_x5_1_output_x32[13], id_mux_x5_2_output_x32[15]);
  nand nand_989 (out_18[14], nand_990_out, nand_990_out);
  nand nand_990 (nand_990_out, id_mux_x5_1_output_x32[14], id_mux_x5_2_output_x32[15]);
  nand nand_991 (out_18[15], nand_992_out, nand_992_out);
  nand nand_992 (nand_992_out, id_mux_x5_1_output_x32[15], id_mux_x5_2_output_x32[15]);
  nand nand_993 (out_18[16], nand_994_out, nand_994_out);
  nand nand_994 (nand_994_out, id_mux_x5_1_output_x32[16], id_mux_x5_2_output_x32[15]);
  nand nand_995 (out_18[17], nand_996_out, nand_996_out);
  nand nand_996 (nand_996_out, id_mux_x5_1_output_x32[17], id_mux_x5_2_output_x32[15]);
  nand nand_997 (out_18[18], nand_998_out, nand_998_out);
  nand nand_998 (nand_998_out, id_mux_x5_1_output_x32[18], id_mux_x5_2_output_x32[15]);
  nand nand_999 (out_18[19], nand_1000_out, nand_1000_out);
  nand nand_1000 (nand_1000_out, id_mux_x5_1_output_x32[19], id_mux_x5_2_output_x32[15]);
  nand nand_1001 (out_18[20], nand_1002_out, nand_1002_out);
  nand nand_1002 (nand_1002_out, id_mux_x5_1_output_x32[20], id_mux_x5_2_output_x32[15]);
  nand nand_1003 (out_18[21], nand_1004_out, nand_1004_out);
  nand nand_1004 (nand_1004_out, id_mux_x5_1_output_x32[21], id_mux_x5_2_output_x32[15]);
  nand nand_1005 (out_18[22], nand_1006_out, nand_1006_out);
  nand nand_1006 (nand_1006_out, id_mux_x5_1_output_x32[22], id_mux_x5_2_output_x32[15]);
  nand nand_1007 (out_18[23], nand_1008_out, nand_1008_out);
  nand nand_1008 (nand_1008_out, id_mux_x5_1_output_x32[23], id_mux_x5_2_output_x32[15]);
  nand nand_1009 (out_18[24], nand_1010_out, nand_1010_out);
  nand nand_1010 (nand_1010_out, id_mux_x5_1_output_x32[24], id_mux_x5_2_output_x32[15]);
  nand nand_1011 (out_18[25], nand_1012_out, nand_1012_out);
  nand nand_1012 (nand_1012_out, id_mux_x5_1_output_x32[25], id_mux_x5_2_output_x32[15]);
  nand nand_1013 (out_18[26], nand_1014_out, nand_1014_out);
  nand nand_1014 (nand_1014_out, id_mux_x5_1_output_x32[26], id_mux_x5_2_output_x32[15]);
  nand nand_1015 (out_18[27], nand_1016_out, nand_1016_out);
  nand nand_1016 (nand_1016_out, id_mux_x5_1_output_x32[27], id_mux_x5_2_output_x32[15]);
  nand nand_1017 (out_18[28], nand_1018_out, nand_1018_out);
  nand nand_1018 (nand_1018_out, id_mux_x5_1_output_x32[28], id_mux_x5_2_output_x32[15]);
  nand nand_1019 (out_18[29], nand_1020_out, nand_1020_out);
  nand nand_1020 (nand_1020_out, id_mux_x5_1_output_x32[29], id_mux_x5_2_output_x32[15]);
  nand nand_1021 (out_18[30], nand_1022_out, nand_1022_out);
  nand nand_1022 (nand_1022_out, id_mux_x5_1_output_x32[30], id_mux_x5_2_output_x32[15]);
  nand nand_1023 (out_18[31], nand_1024_out, nand_1024_out);
  nand nand_1024 (nand_1024_out, id_mux_x5_1_output_x32[31], id_mux_x5_2_output_x32[15]);
  nand nand_1025 (out_19[0], nand_1026_out, nand_1026_out);
  nand nand_1026 (nand_1026_out, id_mux_x5_1_output_x32[0], id_mux_x5_2_output_x32[16]);
  nand nand_1027 (out_19[1], nand_1028_out, nand_1028_out);
  nand nand_1028 (nand_1028_out, id_mux_x5_1_output_x32[1], id_mux_x5_2_output_x32[16]);
  nand nand_1029 (out_19[2], nand_1030_out, nand_1030_out);
  nand nand_1030 (nand_1030_out, id_mux_x5_1_output_x32[2], id_mux_x5_2_output_x32[16]);
  nand nand_1031 (out_19[3], nand_1032_out, nand_1032_out);
  nand nand_1032 (nand_1032_out, id_mux_x5_1_output_x32[3], id_mux_x5_2_output_x32[16]);
  nand nand_1033 (out_19[4], nand_1034_out, nand_1034_out);
  nand nand_1034 (nand_1034_out, id_mux_x5_1_output_x32[4], id_mux_x5_2_output_x32[16]);
  nand nand_1035 (out_19[5], nand_1036_out, nand_1036_out);
  nand nand_1036 (nand_1036_out, id_mux_x5_1_output_x32[5], id_mux_x5_2_output_x32[16]);
  nand nand_1037 (out_19[6], nand_1038_out, nand_1038_out);
  nand nand_1038 (nand_1038_out, id_mux_x5_1_output_x32[6], id_mux_x5_2_output_x32[16]);
  nand nand_1039 (out_19[7], nand_1040_out, nand_1040_out);
  nand nand_1040 (nand_1040_out, id_mux_x5_1_output_x32[7], id_mux_x5_2_output_x32[16]);
  nand nand_1041 (out_19[8], nand_1042_out, nand_1042_out);
  nand nand_1042 (nand_1042_out, id_mux_x5_1_output_x32[8], id_mux_x5_2_output_x32[16]);
  nand nand_1043 (out_19[9], nand_1044_out, nand_1044_out);
  nand nand_1044 (nand_1044_out, id_mux_x5_1_output_x32[9], id_mux_x5_2_output_x32[16]);
  nand nand_1045 (out_19[10], nand_1046_out, nand_1046_out);
  nand nand_1046 (nand_1046_out, id_mux_x5_1_output_x32[10], id_mux_x5_2_output_x32[16]);
  nand nand_1047 (out_19[11], nand_1048_out, nand_1048_out);
  nand nand_1048 (nand_1048_out, id_mux_x5_1_output_x32[11], id_mux_x5_2_output_x32[16]);
  nand nand_1049 (out_19[12], nand_1050_out, nand_1050_out);
  nand nand_1050 (nand_1050_out, id_mux_x5_1_output_x32[12], id_mux_x5_2_output_x32[16]);
  nand nand_1051 (out_19[13], nand_1052_out, nand_1052_out);
  nand nand_1052 (nand_1052_out, id_mux_x5_1_output_x32[13], id_mux_x5_2_output_x32[16]);
  nand nand_1053 (out_19[14], nand_1054_out, nand_1054_out);
  nand nand_1054 (nand_1054_out, id_mux_x5_1_output_x32[14], id_mux_x5_2_output_x32[16]);
  nand nand_1055 (out_19[15], nand_1056_out, nand_1056_out);
  nand nand_1056 (nand_1056_out, id_mux_x5_1_output_x32[15], id_mux_x5_2_output_x32[16]);
  nand nand_1057 (out_19[16], nand_1058_out, nand_1058_out);
  nand nand_1058 (nand_1058_out, id_mux_x5_1_output_x32[16], id_mux_x5_2_output_x32[16]);
  nand nand_1059 (out_19[17], nand_1060_out, nand_1060_out);
  nand nand_1060 (nand_1060_out, id_mux_x5_1_output_x32[17], id_mux_x5_2_output_x32[16]);
  nand nand_1061 (out_19[18], nand_1062_out, nand_1062_out);
  nand nand_1062 (nand_1062_out, id_mux_x5_1_output_x32[18], id_mux_x5_2_output_x32[16]);
  nand nand_1063 (out_19[19], nand_1064_out, nand_1064_out);
  nand nand_1064 (nand_1064_out, id_mux_x5_1_output_x32[19], id_mux_x5_2_output_x32[16]);
  nand nand_1065 (out_19[20], nand_1066_out, nand_1066_out);
  nand nand_1066 (nand_1066_out, id_mux_x5_1_output_x32[20], id_mux_x5_2_output_x32[16]);
  nand nand_1067 (out_19[21], nand_1068_out, nand_1068_out);
  nand nand_1068 (nand_1068_out, id_mux_x5_1_output_x32[21], id_mux_x5_2_output_x32[16]);
  nand nand_1069 (out_19[22], nand_1070_out, nand_1070_out);
  nand nand_1070 (nand_1070_out, id_mux_x5_1_output_x32[22], id_mux_x5_2_output_x32[16]);
  nand nand_1071 (out_19[23], nand_1072_out, nand_1072_out);
  nand nand_1072 (nand_1072_out, id_mux_x5_1_output_x32[23], id_mux_x5_2_output_x32[16]);
  nand nand_1073 (out_19[24], nand_1074_out, nand_1074_out);
  nand nand_1074 (nand_1074_out, id_mux_x5_1_output_x32[24], id_mux_x5_2_output_x32[16]);
  nand nand_1075 (out_19[25], nand_1076_out, nand_1076_out);
  nand nand_1076 (nand_1076_out, id_mux_x5_1_output_x32[25], id_mux_x5_2_output_x32[16]);
  nand nand_1077 (out_19[26], nand_1078_out, nand_1078_out);
  nand nand_1078 (nand_1078_out, id_mux_x5_1_output_x32[26], id_mux_x5_2_output_x32[16]);
  nand nand_1079 (out_19[27], nand_1080_out, nand_1080_out);
  nand nand_1080 (nand_1080_out, id_mux_x5_1_output_x32[27], id_mux_x5_2_output_x32[16]);
  nand nand_1081 (out_19[28], nand_1082_out, nand_1082_out);
  nand nand_1082 (nand_1082_out, id_mux_x5_1_output_x32[28], id_mux_x5_2_output_x32[16]);
  nand nand_1083 (out_19[29], nand_1084_out, nand_1084_out);
  nand nand_1084 (nand_1084_out, id_mux_x5_1_output_x32[29], id_mux_x5_2_output_x32[16]);
  nand nand_1085 (out_19[30], nand_1086_out, nand_1086_out);
  nand nand_1086 (nand_1086_out, id_mux_x5_1_output_x32[30], id_mux_x5_2_output_x32[16]);
  nand nand_1087 (out_19[31], nand_1088_out, nand_1088_out);
  nand nand_1088 (nand_1088_out, id_mux_x5_1_output_x32[31], id_mux_x5_2_output_x32[16]);
  nand nand_1089 (out_20[0], nand_1090_out, nand_1090_out);
  nand nand_1090 (nand_1090_out, id_mux_x5_1_output_x32[0], id_mux_x5_2_output_x32[17]);
  nand nand_1091 (out_20[1], nand_1092_out, nand_1092_out);
  nand nand_1092 (nand_1092_out, id_mux_x5_1_output_x32[1], id_mux_x5_2_output_x32[17]);
  nand nand_1093 (out_20[2], nand_1094_out, nand_1094_out);
  nand nand_1094 (nand_1094_out, id_mux_x5_1_output_x32[2], id_mux_x5_2_output_x32[17]);
  nand nand_1095 (out_20[3], nand_1096_out, nand_1096_out);
  nand nand_1096 (nand_1096_out, id_mux_x5_1_output_x32[3], id_mux_x5_2_output_x32[17]);
  nand nand_1097 (out_20[4], nand_1098_out, nand_1098_out);
  nand nand_1098 (nand_1098_out, id_mux_x5_1_output_x32[4], id_mux_x5_2_output_x32[17]);
  nand nand_1099 (out_20[5], nand_1100_out, nand_1100_out);
  nand nand_1100 (nand_1100_out, id_mux_x5_1_output_x32[5], id_mux_x5_2_output_x32[17]);
  nand nand_1101 (out_20[6], nand_1102_out, nand_1102_out);
  nand nand_1102 (nand_1102_out, id_mux_x5_1_output_x32[6], id_mux_x5_2_output_x32[17]);
  nand nand_1103 (out_20[7], nand_1104_out, nand_1104_out);
  nand nand_1104 (nand_1104_out, id_mux_x5_1_output_x32[7], id_mux_x5_2_output_x32[17]);
  nand nand_1105 (out_20[8], nand_1106_out, nand_1106_out);
  nand nand_1106 (nand_1106_out, id_mux_x5_1_output_x32[8], id_mux_x5_2_output_x32[17]);
  nand nand_1107 (out_20[9], nand_1108_out, nand_1108_out);
  nand nand_1108 (nand_1108_out, id_mux_x5_1_output_x32[9], id_mux_x5_2_output_x32[17]);
  nand nand_1109 (out_20[10], nand_1110_out, nand_1110_out);
  nand nand_1110 (nand_1110_out, id_mux_x5_1_output_x32[10], id_mux_x5_2_output_x32[17]);
  nand nand_1111 (out_20[11], nand_1112_out, nand_1112_out);
  nand nand_1112 (nand_1112_out, id_mux_x5_1_output_x32[11], id_mux_x5_2_output_x32[17]);
  nand nand_1113 (out_20[12], nand_1114_out, nand_1114_out);
  nand nand_1114 (nand_1114_out, id_mux_x5_1_output_x32[12], id_mux_x5_2_output_x32[17]);
  nand nand_1115 (out_20[13], nand_1116_out, nand_1116_out);
  nand nand_1116 (nand_1116_out, id_mux_x5_1_output_x32[13], id_mux_x5_2_output_x32[17]);
  nand nand_1117 (out_20[14], nand_1118_out, nand_1118_out);
  nand nand_1118 (nand_1118_out, id_mux_x5_1_output_x32[14], id_mux_x5_2_output_x32[17]);
  nand nand_1119 (out_20[15], nand_1120_out, nand_1120_out);
  nand nand_1120 (nand_1120_out, id_mux_x5_1_output_x32[15], id_mux_x5_2_output_x32[17]);
  nand nand_1121 (out_20[16], nand_1122_out, nand_1122_out);
  nand nand_1122 (nand_1122_out, id_mux_x5_1_output_x32[16], id_mux_x5_2_output_x32[17]);
  nand nand_1123 (out_20[17], nand_1124_out, nand_1124_out);
  nand nand_1124 (nand_1124_out, id_mux_x5_1_output_x32[17], id_mux_x5_2_output_x32[17]);
  nand nand_1125 (out_20[18], nand_1126_out, nand_1126_out);
  nand nand_1126 (nand_1126_out, id_mux_x5_1_output_x32[18], id_mux_x5_2_output_x32[17]);
  nand nand_1127 (out_20[19], nand_1128_out, nand_1128_out);
  nand nand_1128 (nand_1128_out, id_mux_x5_1_output_x32[19], id_mux_x5_2_output_x32[17]);
  nand nand_1129 (out_20[20], nand_1130_out, nand_1130_out);
  nand nand_1130 (nand_1130_out, id_mux_x5_1_output_x32[20], id_mux_x5_2_output_x32[17]);
  nand nand_1131 (out_20[21], nand_1132_out, nand_1132_out);
  nand nand_1132 (nand_1132_out, id_mux_x5_1_output_x32[21], id_mux_x5_2_output_x32[17]);
  nand nand_1133 (out_20[22], nand_1134_out, nand_1134_out);
  nand nand_1134 (nand_1134_out, id_mux_x5_1_output_x32[22], id_mux_x5_2_output_x32[17]);
  nand nand_1135 (out_20[23], nand_1136_out, nand_1136_out);
  nand nand_1136 (nand_1136_out, id_mux_x5_1_output_x32[23], id_mux_x5_2_output_x32[17]);
  nand nand_1137 (out_20[24], nand_1138_out, nand_1138_out);
  nand nand_1138 (nand_1138_out, id_mux_x5_1_output_x32[24], id_mux_x5_2_output_x32[17]);
  nand nand_1139 (out_20[25], nand_1140_out, nand_1140_out);
  nand nand_1140 (nand_1140_out, id_mux_x5_1_output_x32[25], id_mux_x5_2_output_x32[17]);
  nand nand_1141 (out_20[26], nand_1142_out, nand_1142_out);
  nand nand_1142 (nand_1142_out, id_mux_x5_1_output_x32[26], id_mux_x5_2_output_x32[17]);
  nand nand_1143 (out_20[27], nand_1144_out, nand_1144_out);
  nand nand_1144 (nand_1144_out, id_mux_x5_1_output_x32[27], id_mux_x5_2_output_x32[17]);
  nand nand_1145 (out_20[28], nand_1146_out, nand_1146_out);
  nand nand_1146 (nand_1146_out, id_mux_x5_1_output_x32[28], id_mux_x5_2_output_x32[17]);
  nand nand_1147 (out_20[29], nand_1148_out, nand_1148_out);
  nand nand_1148 (nand_1148_out, id_mux_x5_1_output_x32[29], id_mux_x5_2_output_x32[17]);
  nand nand_1149 (out_20[30], nand_1150_out, nand_1150_out);
  nand nand_1150 (nand_1150_out, id_mux_x5_1_output_x32[30], id_mux_x5_2_output_x32[17]);
  nand nand_1151 (out_20[31], nand_1152_out, nand_1152_out);
  nand nand_1152 (nand_1152_out, id_mux_x5_1_output_x32[31], id_mux_x5_2_output_x32[17]);
  nand nand_1153 (out_21[0], nand_1154_out, nand_1154_out);
  nand nand_1154 (nand_1154_out, id_mux_x5_1_output_x32[0], id_mux_x5_2_output_x32[18]);
  nand nand_1155 (out_21[1], nand_1156_out, nand_1156_out);
  nand nand_1156 (nand_1156_out, id_mux_x5_1_output_x32[1], id_mux_x5_2_output_x32[18]);
  nand nand_1157 (out_21[2], nand_1158_out, nand_1158_out);
  nand nand_1158 (nand_1158_out, id_mux_x5_1_output_x32[2], id_mux_x5_2_output_x32[18]);
  nand nand_1159 (out_21[3], nand_1160_out, nand_1160_out);
  nand nand_1160 (nand_1160_out, id_mux_x5_1_output_x32[3], id_mux_x5_2_output_x32[18]);
  nand nand_1161 (out_21[4], nand_1162_out, nand_1162_out);
  nand nand_1162 (nand_1162_out, id_mux_x5_1_output_x32[4], id_mux_x5_2_output_x32[18]);
  nand nand_1163 (out_21[5], nand_1164_out, nand_1164_out);
  nand nand_1164 (nand_1164_out, id_mux_x5_1_output_x32[5], id_mux_x5_2_output_x32[18]);
  nand nand_1165 (out_21[6], nand_1166_out, nand_1166_out);
  nand nand_1166 (nand_1166_out, id_mux_x5_1_output_x32[6], id_mux_x5_2_output_x32[18]);
  nand nand_1167 (out_21[7], nand_1168_out, nand_1168_out);
  nand nand_1168 (nand_1168_out, id_mux_x5_1_output_x32[7], id_mux_x5_2_output_x32[18]);
  nand nand_1169 (out_21[8], nand_1170_out, nand_1170_out);
  nand nand_1170 (nand_1170_out, id_mux_x5_1_output_x32[8], id_mux_x5_2_output_x32[18]);
  nand nand_1171 (out_21[9], nand_1172_out, nand_1172_out);
  nand nand_1172 (nand_1172_out, id_mux_x5_1_output_x32[9], id_mux_x5_2_output_x32[18]);
  nand nand_1173 (out_21[10], nand_1174_out, nand_1174_out);
  nand nand_1174 (nand_1174_out, id_mux_x5_1_output_x32[10], id_mux_x5_2_output_x32[18]);
  nand nand_1175 (out_21[11], nand_1176_out, nand_1176_out);
  nand nand_1176 (nand_1176_out, id_mux_x5_1_output_x32[11], id_mux_x5_2_output_x32[18]);
  nand nand_1177 (out_21[12], nand_1178_out, nand_1178_out);
  nand nand_1178 (nand_1178_out, id_mux_x5_1_output_x32[12], id_mux_x5_2_output_x32[18]);
  nand nand_1179 (out_21[13], nand_1180_out, nand_1180_out);
  nand nand_1180 (nand_1180_out, id_mux_x5_1_output_x32[13], id_mux_x5_2_output_x32[18]);
  nand nand_1181 (out_21[14], nand_1182_out, nand_1182_out);
  nand nand_1182 (nand_1182_out, id_mux_x5_1_output_x32[14], id_mux_x5_2_output_x32[18]);
  nand nand_1183 (out_21[15], nand_1184_out, nand_1184_out);
  nand nand_1184 (nand_1184_out, id_mux_x5_1_output_x32[15], id_mux_x5_2_output_x32[18]);
  nand nand_1185 (out_21[16], nand_1186_out, nand_1186_out);
  nand nand_1186 (nand_1186_out, id_mux_x5_1_output_x32[16], id_mux_x5_2_output_x32[18]);
  nand nand_1187 (out_21[17], nand_1188_out, nand_1188_out);
  nand nand_1188 (nand_1188_out, id_mux_x5_1_output_x32[17], id_mux_x5_2_output_x32[18]);
  nand nand_1189 (out_21[18], nand_1190_out, nand_1190_out);
  nand nand_1190 (nand_1190_out, id_mux_x5_1_output_x32[18], id_mux_x5_2_output_x32[18]);
  nand nand_1191 (out_21[19], nand_1192_out, nand_1192_out);
  nand nand_1192 (nand_1192_out, id_mux_x5_1_output_x32[19], id_mux_x5_2_output_x32[18]);
  nand nand_1193 (out_21[20], nand_1194_out, nand_1194_out);
  nand nand_1194 (nand_1194_out, id_mux_x5_1_output_x32[20], id_mux_x5_2_output_x32[18]);
  nand nand_1195 (out_21[21], nand_1196_out, nand_1196_out);
  nand nand_1196 (nand_1196_out, id_mux_x5_1_output_x32[21], id_mux_x5_2_output_x32[18]);
  nand nand_1197 (out_21[22], nand_1198_out, nand_1198_out);
  nand nand_1198 (nand_1198_out, id_mux_x5_1_output_x32[22], id_mux_x5_2_output_x32[18]);
  nand nand_1199 (out_21[23], nand_1200_out, nand_1200_out);
  nand nand_1200 (nand_1200_out, id_mux_x5_1_output_x32[23], id_mux_x5_2_output_x32[18]);
  nand nand_1201 (out_21[24], nand_1202_out, nand_1202_out);
  nand nand_1202 (nand_1202_out, id_mux_x5_1_output_x32[24], id_mux_x5_2_output_x32[18]);
  nand nand_1203 (out_21[25], nand_1204_out, nand_1204_out);
  nand nand_1204 (nand_1204_out, id_mux_x5_1_output_x32[25], id_mux_x5_2_output_x32[18]);
  nand nand_1205 (out_21[26], nand_1206_out, nand_1206_out);
  nand nand_1206 (nand_1206_out, id_mux_x5_1_output_x32[26], id_mux_x5_2_output_x32[18]);
  nand nand_1207 (out_21[27], nand_1208_out, nand_1208_out);
  nand nand_1208 (nand_1208_out, id_mux_x5_1_output_x32[27], id_mux_x5_2_output_x32[18]);
  nand nand_1209 (out_21[28], nand_1210_out, nand_1210_out);
  nand nand_1210 (nand_1210_out, id_mux_x5_1_output_x32[28], id_mux_x5_2_output_x32[18]);
  nand nand_1211 (out_21[29], nand_1212_out, nand_1212_out);
  nand nand_1212 (nand_1212_out, id_mux_x5_1_output_x32[29], id_mux_x5_2_output_x32[18]);
  nand nand_1213 (out_21[30], nand_1214_out, nand_1214_out);
  nand nand_1214 (nand_1214_out, id_mux_x5_1_output_x32[30], id_mux_x5_2_output_x32[18]);
  nand nand_1215 (out_21[31], nand_1216_out, nand_1216_out);
  nand nand_1216 (nand_1216_out, id_mux_x5_1_output_x32[31], id_mux_x5_2_output_x32[18]);
  nand nand_1217 (out_22[0], nand_1218_out, nand_1218_out);
  nand nand_1218 (nand_1218_out, id_mux_x5_1_output_x32[0], id_mux_x5_2_output_x32[19]);
  nand nand_1219 (out_22[1], nand_1220_out, nand_1220_out);
  nand nand_1220 (nand_1220_out, id_mux_x5_1_output_x32[1], id_mux_x5_2_output_x32[19]);
  nand nand_1221 (out_22[2], nand_1222_out, nand_1222_out);
  nand nand_1222 (nand_1222_out, id_mux_x5_1_output_x32[2], id_mux_x5_2_output_x32[19]);
  nand nand_1223 (out_22[3], nand_1224_out, nand_1224_out);
  nand nand_1224 (nand_1224_out, id_mux_x5_1_output_x32[3], id_mux_x5_2_output_x32[19]);
  nand nand_1225 (out_22[4], nand_1226_out, nand_1226_out);
  nand nand_1226 (nand_1226_out, id_mux_x5_1_output_x32[4], id_mux_x5_2_output_x32[19]);
  nand nand_1227 (out_22[5], nand_1228_out, nand_1228_out);
  nand nand_1228 (nand_1228_out, id_mux_x5_1_output_x32[5], id_mux_x5_2_output_x32[19]);
  nand nand_1229 (out_22[6], nand_1230_out, nand_1230_out);
  nand nand_1230 (nand_1230_out, id_mux_x5_1_output_x32[6], id_mux_x5_2_output_x32[19]);
  nand nand_1231 (out_22[7], nand_1232_out, nand_1232_out);
  nand nand_1232 (nand_1232_out, id_mux_x5_1_output_x32[7], id_mux_x5_2_output_x32[19]);
  nand nand_1233 (out_22[8], nand_1234_out, nand_1234_out);
  nand nand_1234 (nand_1234_out, id_mux_x5_1_output_x32[8], id_mux_x5_2_output_x32[19]);
  nand nand_1235 (out_22[9], nand_1236_out, nand_1236_out);
  nand nand_1236 (nand_1236_out, id_mux_x5_1_output_x32[9], id_mux_x5_2_output_x32[19]);
  nand nand_1237 (out_22[10], nand_1238_out, nand_1238_out);
  nand nand_1238 (nand_1238_out, id_mux_x5_1_output_x32[10], id_mux_x5_2_output_x32[19]);
  nand nand_1239 (out_22[11], nand_1240_out, nand_1240_out);
  nand nand_1240 (nand_1240_out, id_mux_x5_1_output_x32[11], id_mux_x5_2_output_x32[19]);
  nand nand_1241 (out_22[12], nand_1242_out, nand_1242_out);
  nand nand_1242 (nand_1242_out, id_mux_x5_1_output_x32[12], id_mux_x5_2_output_x32[19]);
  nand nand_1243 (out_22[13], nand_1244_out, nand_1244_out);
  nand nand_1244 (nand_1244_out, id_mux_x5_1_output_x32[13], id_mux_x5_2_output_x32[19]);
  nand nand_1245 (out_22[14], nand_1246_out, nand_1246_out);
  nand nand_1246 (nand_1246_out, id_mux_x5_1_output_x32[14], id_mux_x5_2_output_x32[19]);
  nand nand_1247 (out_22[15], nand_1248_out, nand_1248_out);
  nand nand_1248 (nand_1248_out, id_mux_x5_1_output_x32[15], id_mux_x5_2_output_x32[19]);
  nand nand_1249 (out_22[16], nand_1250_out, nand_1250_out);
  nand nand_1250 (nand_1250_out, id_mux_x5_1_output_x32[16], id_mux_x5_2_output_x32[19]);
  nand nand_1251 (out_22[17], nand_1252_out, nand_1252_out);
  nand nand_1252 (nand_1252_out, id_mux_x5_1_output_x32[17], id_mux_x5_2_output_x32[19]);
  nand nand_1253 (out_22[18], nand_1254_out, nand_1254_out);
  nand nand_1254 (nand_1254_out, id_mux_x5_1_output_x32[18], id_mux_x5_2_output_x32[19]);
  nand nand_1255 (out_22[19], nand_1256_out, nand_1256_out);
  nand nand_1256 (nand_1256_out, id_mux_x5_1_output_x32[19], id_mux_x5_2_output_x32[19]);
  nand nand_1257 (out_22[20], nand_1258_out, nand_1258_out);
  nand nand_1258 (nand_1258_out, id_mux_x5_1_output_x32[20], id_mux_x5_2_output_x32[19]);
  nand nand_1259 (out_22[21], nand_1260_out, nand_1260_out);
  nand nand_1260 (nand_1260_out, id_mux_x5_1_output_x32[21], id_mux_x5_2_output_x32[19]);
  nand nand_1261 (out_22[22], nand_1262_out, nand_1262_out);
  nand nand_1262 (nand_1262_out, id_mux_x5_1_output_x32[22], id_mux_x5_2_output_x32[19]);
  nand nand_1263 (out_22[23], nand_1264_out, nand_1264_out);
  nand nand_1264 (nand_1264_out, id_mux_x5_1_output_x32[23], id_mux_x5_2_output_x32[19]);
  nand nand_1265 (out_22[24], nand_1266_out, nand_1266_out);
  nand nand_1266 (nand_1266_out, id_mux_x5_1_output_x32[24], id_mux_x5_2_output_x32[19]);
  nand nand_1267 (out_22[25], nand_1268_out, nand_1268_out);
  nand nand_1268 (nand_1268_out, id_mux_x5_1_output_x32[25], id_mux_x5_2_output_x32[19]);
  nand nand_1269 (out_22[26], nand_1270_out, nand_1270_out);
  nand nand_1270 (nand_1270_out, id_mux_x5_1_output_x32[26], id_mux_x5_2_output_x32[19]);
  nand nand_1271 (out_22[27], nand_1272_out, nand_1272_out);
  nand nand_1272 (nand_1272_out, id_mux_x5_1_output_x32[27], id_mux_x5_2_output_x32[19]);
  nand nand_1273 (out_22[28], nand_1274_out, nand_1274_out);
  nand nand_1274 (nand_1274_out, id_mux_x5_1_output_x32[28], id_mux_x5_2_output_x32[19]);
  nand nand_1275 (out_22[29], nand_1276_out, nand_1276_out);
  nand nand_1276 (nand_1276_out, id_mux_x5_1_output_x32[29], id_mux_x5_2_output_x32[19]);
  nand nand_1277 (out_22[30], nand_1278_out, nand_1278_out);
  nand nand_1278 (nand_1278_out, id_mux_x5_1_output_x32[30], id_mux_x5_2_output_x32[19]);
  nand nand_1279 (out_22[31], nand_1280_out, nand_1280_out);
  nand nand_1280 (nand_1280_out, id_mux_x5_1_output_x32[31], id_mux_x5_2_output_x32[19]);
  nand nand_1281 (out_23[0], nand_1282_out, nand_1282_out);
  nand nand_1282 (nand_1282_out, id_mux_x5_1_output_x32[0], id_mux_x5_2_output_x32[20]);
  nand nand_1283 (out_23[1], nand_1284_out, nand_1284_out);
  nand nand_1284 (nand_1284_out, id_mux_x5_1_output_x32[1], id_mux_x5_2_output_x32[20]);
  nand nand_1285 (out_23[2], nand_1286_out, nand_1286_out);
  nand nand_1286 (nand_1286_out, id_mux_x5_1_output_x32[2], id_mux_x5_2_output_x32[20]);
  nand nand_1287 (out_23[3], nand_1288_out, nand_1288_out);
  nand nand_1288 (nand_1288_out, id_mux_x5_1_output_x32[3], id_mux_x5_2_output_x32[20]);
  nand nand_1289 (out_23[4], nand_1290_out, nand_1290_out);
  nand nand_1290 (nand_1290_out, id_mux_x5_1_output_x32[4], id_mux_x5_2_output_x32[20]);
  nand nand_1291 (out_23[5], nand_1292_out, nand_1292_out);
  nand nand_1292 (nand_1292_out, id_mux_x5_1_output_x32[5], id_mux_x5_2_output_x32[20]);
  nand nand_1293 (out_23[6], nand_1294_out, nand_1294_out);
  nand nand_1294 (nand_1294_out, id_mux_x5_1_output_x32[6], id_mux_x5_2_output_x32[20]);
  nand nand_1295 (out_23[7], nand_1296_out, nand_1296_out);
  nand nand_1296 (nand_1296_out, id_mux_x5_1_output_x32[7], id_mux_x5_2_output_x32[20]);
  nand nand_1297 (out_23[8], nand_1298_out, nand_1298_out);
  nand nand_1298 (nand_1298_out, id_mux_x5_1_output_x32[8], id_mux_x5_2_output_x32[20]);
  nand nand_1299 (out_23[9], nand_1300_out, nand_1300_out);
  nand nand_1300 (nand_1300_out, id_mux_x5_1_output_x32[9], id_mux_x5_2_output_x32[20]);
  nand nand_1301 (out_23[10], nand_1302_out, nand_1302_out);
  nand nand_1302 (nand_1302_out, id_mux_x5_1_output_x32[10], id_mux_x5_2_output_x32[20]);
  nand nand_1303 (out_23[11], nand_1304_out, nand_1304_out);
  nand nand_1304 (nand_1304_out, id_mux_x5_1_output_x32[11], id_mux_x5_2_output_x32[20]);
  nand nand_1305 (out_23[12], nand_1306_out, nand_1306_out);
  nand nand_1306 (nand_1306_out, id_mux_x5_1_output_x32[12], id_mux_x5_2_output_x32[20]);
  nand nand_1307 (out_23[13], nand_1308_out, nand_1308_out);
  nand nand_1308 (nand_1308_out, id_mux_x5_1_output_x32[13], id_mux_x5_2_output_x32[20]);
  nand nand_1309 (out_23[14], nand_1310_out, nand_1310_out);
  nand nand_1310 (nand_1310_out, id_mux_x5_1_output_x32[14], id_mux_x5_2_output_x32[20]);
  nand nand_1311 (out_23[15], nand_1312_out, nand_1312_out);
  nand nand_1312 (nand_1312_out, id_mux_x5_1_output_x32[15], id_mux_x5_2_output_x32[20]);
  nand nand_1313 (out_23[16], nand_1314_out, nand_1314_out);
  nand nand_1314 (nand_1314_out, id_mux_x5_1_output_x32[16], id_mux_x5_2_output_x32[20]);
  nand nand_1315 (out_23[17], nand_1316_out, nand_1316_out);
  nand nand_1316 (nand_1316_out, id_mux_x5_1_output_x32[17], id_mux_x5_2_output_x32[20]);
  nand nand_1317 (out_23[18], nand_1318_out, nand_1318_out);
  nand nand_1318 (nand_1318_out, id_mux_x5_1_output_x32[18], id_mux_x5_2_output_x32[20]);
  nand nand_1319 (out_23[19], nand_1320_out, nand_1320_out);
  nand nand_1320 (nand_1320_out, id_mux_x5_1_output_x32[19], id_mux_x5_2_output_x32[20]);
  nand nand_1321 (out_23[20], nand_1322_out, nand_1322_out);
  nand nand_1322 (nand_1322_out, id_mux_x5_1_output_x32[20], id_mux_x5_2_output_x32[20]);
  nand nand_1323 (out_23[21], nand_1324_out, nand_1324_out);
  nand nand_1324 (nand_1324_out, id_mux_x5_1_output_x32[21], id_mux_x5_2_output_x32[20]);
  nand nand_1325 (out_23[22], nand_1326_out, nand_1326_out);
  nand nand_1326 (nand_1326_out, id_mux_x5_1_output_x32[22], id_mux_x5_2_output_x32[20]);
  nand nand_1327 (out_23[23], nand_1328_out, nand_1328_out);
  nand nand_1328 (nand_1328_out, id_mux_x5_1_output_x32[23], id_mux_x5_2_output_x32[20]);
  nand nand_1329 (out_23[24], nand_1330_out, nand_1330_out);
  nand nand_1330 (nand_1330_out, id_mux_x5_1_output_x32[24], id_mux_x5_2_output_x32[20]);
  nand nand_1331 (out_23[25], nand_1332_out, nand_1332_out);
  nand nand_1332 (nand_1332_out, id_mux_x5_1_output_x32[25], id_mux_x5_2_output_x32[20]);
  nand nand_1333 (out_23[26], nand_1334_out, nand_1334_out);
  nand nand_1334 (nand_1334_out, id_mux_x5_1_output_x32[26], id_mux_x5_2_output_x32[20]);
  nand nand_1335 (out_23[27], nand_1336_out, nand_1336_out);
  nand nand_1336 (nand_1336_out, id_mux_x5_1_output_x32[27], id_mux_x5_2_output_x32[20]);
  nand nand_1337 (out_23[28], nand_1338_out, nand_1338_out);
  nand nand_1338 (nand_1338_out, id_mux_x5_1_output_x32[28], id_mux_x5_2_output_x32[20]);
  nand nand_1339 (out_23[29], nand_1340_out, nand_1340_out);
  nand nand_1340 (nand_1340_out, id_mux_x5_1_output_x32[29], id_mux_x5_2_output_x32[20]);
  nand nand_1341 (out_23[30], nand_1342_out, nand_1342_out);
  nand nand_1342 (nand_1342_out, id_mux_x5_1_output_x32[30], id_mux_x5_2_output_x32[20]);
  nand nand_1343 (out_23[31], nand_1344_out, nand_1344_out);
  nand nand_1344 (nand_1344_out, id_mux_x5_1_output_x32[31], id_mux_x5_2_output_x32[20]);
  nand nand_1345 (out_24[0], nand_1346_out, nand_1346_out);
  nand nand_1346 (nand_1346_out, id_mux_x5_1_output_x32[0], id_mux_x5_2_output_x32[21]);
  nand nand_1347 (out_24[1], nand_1348_out, nand_1348_out);
  nand nand_1348 (nand_1348_out, id_mux_x5_1_output_x32[1], id_mux_x5_2_output_x32[21]);
  nand nand_1349 (out_24[2], nand_1350_out, nand_1350_out);
  nand nand_1350 (nand_1350_out, id_mux_x5_1_output_x32[2], id_mux_x5_2_output_x32[21]);
  nand nand_1351 (out_24[3], nand_1352_out, nand_1352_out);
  nand nand_1352 (nand_1352_out, id_mux_x5_1_output_x32[3], id_mux_x5_2_output_x32[21]);
  nand nand_1353 (out_24[4], nand_1354_out, nand_1354_out);
  nand nand_1354 (nand_1354_out, id_mux_x5_1_output_x32[4], id_mux_x5_2_output_x32[21]);
  nand nand_1355 (out_24[5], nand_1356_out, nand_1356_out);
  nand nand_1356 (nand_1356_out, id_mux_x5_1_output_x32[5], id_mux_x5_2_output_x32[21]);
  nand nand_1357 (out_24[6], nand_1358_out, nand_1358_out);
  nand nand_1358 (nand_1358_out, id_mux_x5_1_output_x32[6], id_mux_x5_2_output_x32[21]);
  nand nand_1359 (out_24[7], nand_1360_out, nand_1360_out);
  nand nand_1360 (nand_1360_out, id_mux_x5_1_output_x32[7], id_mux_x5_2_output_x32[21]);
  nand nand_1361 (out_24[8], nand_1362_out, nand_1362_out);
  nand nand_1362 (nand_1362_out, id_mux_x5_1_output_x32[8], id_mux_x5_2_output_x32[21]);
  nand nand_1363 (out_24[9], nand_1364_out, nand_1364_out);
  nand nand_1364 (nand_1364_out, id_mux_x5_1_output_x32[9], id_mux_x5_2_output_x32[21]);
  nand nand_1365 (out_24[10], nand_1366_out, nand_1366_out);
  nand nand_1366 (nand_1366_out, id_mux_x5_1_output_x32[10], id_mux_x5_2_output_x32[21]);
  nand nand_1367 (out_24[11], nand_1368_out, nand_1368_out);
  nand nand_1368 (nand_1368_out, id_mux_x5_1_output_x32[11], id_mux_x5_2_output_x32[21]);
  nand nand_1369 (out_24[12], nand_1370_out, nand_1370_out);
  nand nand_1370 (nand_1370_out, id_mux_x5_1_output_x32[12], id_mux_x5_2_output_x32[21]);
  nand nand_1371 (out_24[13], nand_1372_out, nand_1372_out);
  nand nand_1372 (nand_1372_out, id_mux_x5_1_output_x32[13], id_mux_x5_2_output_x32[21]);
  nand nand_1373 (out_24[14], nand_1374_out, nand_1374_out);
  nand nand_1374 (nand_1374_out, id_mux_x5_1_output_x32[14], id_mux_x5_2_output_x32[21]);
  nand nand_1375 (out_24[15], nand_1376_out, nand_1376_out);
  nand nand_1376 (nand_1376_out, id_mux_x5_1_output_x32[15], id_mux_x5_2_output_x32[21]);
  nand nand_1377 (out_24[16], nand_1378_out, nand_1378_out);
  nand nand_1378 (nand_1378_out, id_mux_x5_1_output_x32[16], id_mux_x5_2_output_x32[21]);
  nand nand_1379 (out_24[17], nand_1380_out, nand_1380_out);
  nand nand_1380 (nand_1380_out, id_mux_x5_1_output_x32[17], id_mux_x5_2_output_x32[21]);
  nand nand_1381 (out_24[18], nand_1382_out, nand_1382_out);
  nand nand_1382 (nand_1382_out, id_mux_x5_1_output_x32[18], id_mux_x5_2_output_x32[21]);
  nand nand_1383 (out_24[19], nand_1384_out, nand_1384_out);
  nand nand_1384 (nand_1384_out, id_mux_x5_1_output_x32[19], id_mux_x5_2_output_x32[21]);
  nand nand_1385 (out_24[20], nand_1386_out, nand_1386_out);
  nand nand_1386 (nand_1386_out, id_mux_x5_1_output_x32[20], id_mux_x5_2_output_x32[21]);
  nand nand_1387 (out_24[21], nand_1388_out, nand_1388_out);
  nand nand_1388 (nand_1388_out, id_mux_x5_1_output_x32[21], id_mux_x5_2_output_x32[21]);
  nand nand_1389 (out_24[22], nand_1390_out, nand_1390_out);
  nand nand_1390 (nand_1390_out, id_mux_x5_1_output_x32[22], id_mux_x5_2_output_x32[21]);
  nand nand_1391 (out_24[23], nand_1392_out, nand_1392_out);
  nand nand_1392 (nand_1392_out, id_mux_x5_1_output_x32[23], id_mux_x5_2_output_x32[21]);
  nand nand_1393 (out_24[24], nand_1394_out, nand_1394_out);
  nand nand_1394 (nand_1394_out, id_mux_x5_1_output_x32[24], id_mux_x5_2_output_x32[21]);
  nand nand_1395 (out_24[25], nand_1396_out, nand_1396_out);
  nand nand_1396 (nand_1396_out, id_mux_x5_1_output_x32[25], id_mux_x5_2_output_x32[21]);
  nand nand_1397 (out_24[26], nand_1398_out, nand_1398_out);
  nand nand_1398 (nand_1398_out, id_mux_x5_1_output_x32[26], id_mux_x5_2_output_x32[21]);
  nand nand_1399 (out_24[27], nand_1400_out, nand_1400_out);
  nand nand_1400 (nand_1400_out, id_mux_x5_1_output_x32[27], id_mux_x5_2_output_x32[21]);
  nand nand_1401 (out_24[28], nand_1402_out, nand_1402_out);
  nand nand_1402 (nand_1402_out, id_mux_x5_1_output_x32[28], id_mux_x5_2_output_x32[21]);
  nand nand_1403 (out_24[29], nand_1404_out, nand_1404_out);
  nand nand_1404 (nand_1404_out, id_mux_x5_1_output_x32[29], id_mux_x5_2_output_x32[21]);
  nand nand_1405 (out_24[30], nand_1406_out, nand_1406_out);
  nand nand_1406 (nand_1406_out, id_mux_x5_1_output_x32[30], id_mux_x5_2_output_x32[21]);
  nand nand_1407 (out_24[31], nand_1408_out, nand_1408_out);
  nand nand_1408 (nand_1408_out, id_mux_x5_1_output_x32[31], id_mux_x5_2_output_x32[21]);
  nand nand_1409 (out_25[0], nand_1410_out, nand_1410_out);
  nand nand_1410 (nand_1410_out, id_mux_x5_1_output_x32[0], id_mux_x5_2_output_x32[22]);
  nand nand_1411 (out_25[1], nand_1412_out, nand_1412_out);
  nand nand_1412 (nand_1412_out, id_mux_x5_1_output_x32[1], id_mux_x5_2_output_x32[22]);
  nand nand_1413 (out_25[2], nand_1414_out, nand_1414_out);
  nand nand_1414 (nand_1414_out, id_mux_x5_1_output_x32[2], id_mux_x5_2_output_x32[22]);
  nand nand_1415 (out_25[3], nand_1416_out, nand_1416_out);
  nand nand_1416 (nand_1416_out, id_mux_x5_1_output_x32[3], id_mux_x5_2_output_x32[22]);
  nand nand_1417 (out_25[4], nand_1418_out, nand_1418_out);
  nand nand_1418 (nand_1418_out, id_mux_x5_1_output_x32[4], id_mux_x5_2_output_x32[22]);
  nand nand_1419 (out_25[5], nand_1420_out, nand_1420_out);
  nand nand_1420 (nand_1420_out, id_mux_x5_1_output_x32[5], id_mux_x5_2_output_x32[22]);
  nand nand_1421 (out_25[6], nand_1422_out, nand_1422_out);
  nand nand_1422 (nand_1422_out, id_mux_x5_1_output_x32[6], id_mux_x5_2_output_x32[22]);
  nand nand_1423 (out_25[7], nand_1424_out, nand_1424_out);
  nand nand_1424 (nand_1424_out, id_mux_x5_1_output_x32[7], id_mux_x5_2_output_x32[22]);
  nand nand_1425 (out_25[8], nand_1426_out, nand_1426_out);
  nand nand_1426 (nand_1426_out, id_mux_x5_1_output_x32[8], id_mux_x5_2_output_x32[22]);
  nand nand_1427 (out_25[9], nand_1428_out, nand_1428_out);
  nand nand_1428 (nand_1428_out, id_mux_x5_1_output_x32[9], id_mux_x5_2_output_x32[22]);
  nand nand_1429 (out_25[10], nand_1430_out, nand_1430_out);
  nand nand_1430 (nand_1430_out, id_mux_x5_1_output_x32[10], id_mux_x5_2_output_x32[22]);
  nand nand_1431 (out_25[11], nand_1432_out, nand_1432_out);
  nand nand_1432 (nand_1432_out, id_mux_x5_1_output_x32[11], id_mux_x5_2_output_x32[22]);
  nand nand_1433 (out_25[12], nand_1434_out, nand_1434_out);
  nand nand_1434 (nand_1434_out, id_mux_x5_1_output_x32[12], id_mux_x5_2_output_x32[22]);
  nand nand_1435 (out_25[13], nand_1436_out, nand_1436_out);
  nand nand_1436 (nand_1436_out, id_mux_x5_1_output_x32[13], id_mux_x5_2_output_x32[22]);
  nand nand_1437 (out_25[14], nand_1438_out, nand_1438_out);
  nand nand_1438 (nand_1438_out, id_mux_x5_1_output_x32[14], id_mux_x5_2_output_x32[22]);
  nand nand_1439 (out_25[15], nand_1440_out, nand_1440_out);
  nand nand_1440 (nand_1440_out, id_mux_x5_1_output_x32[15], id_mux_x5_2_output_x32[22]);
  nand nand_1441 (out_25[16], nand_1442_out, nand_1442_out);
  nand nand_1442 (nand_1442_out, id_mux_x5_1_output_x32[16], id_mux_x5_2_output_x32[22]);
  nand nand_1443 (out_25[17], nand_1444_out, nand_1444_out);
  nand nand_1444 (nand_1444_out, id_mux_x5_1_output_x32[17], id_mux_x5_2_output_x32[22]);
  nand nand_1445 (out_25[18], nand_1446_out, nand_1446_out);
  nand nand_1446 (nand_1446_out, id_mux_x5_1_output_x32[18], id_mux_x5_2_output_x32[22]);
  nand nand_1447 (out_25[19], nand_1448_out, nand_1448_out);
  nand nand_1448 (nand_1448_out, id_mux_x5_1_output_x32[19], id_mux_x5_2_output_x32[22]);
  nand nand_1449 (out_25[20], nand_1450_out, nand_1450_out);
  nand nand_1450 (nand_1450_out, id_mux_x5_1_output_x32[20], id_mux_x5_2_output_x32[22]);
  nand nand_1451 (out_25[21], nand_1452_out, nand_1452_out);
  nand nand_1452 (nand_1452_out, id_mux_x5_1_output_x32[21], id_mux_x5_2_output_x32[22]);
  nand nand_1453 (out_25[22], nand_1454_out, nand_1454_out);
  nand nand_1454 (nand_1454_out, id_mux_x5_1_output_x32[22], id_mux_x5_2_output_x32[22]);
  nand nand_1455 (out_25[23], nand_1456_out, nand_1456_out);
  nand nand_1456 (nand_1456_out, id_mux_x5_1_output_x32[23], id_mux_x5_2_output_x32[22]);
  nand nand_1457 (out_25[24], nand_1458_out, nand_1458_out);
  nand nand_1458 (nand_1458_out, id_mux_x5_1_output_x32[24], id_mux_x5_2_output_x32[22]);
  nand nand_1459 (out_25[25], nand_1460_out, nand_1460_out);
  nand nand_1460 (nand_1460_out, id_mux_x5_1_output_x32[25], id_mux_x5_2_output_x32[22]);
  nand nand_1461 (out_25[26], nand_1462_out, nand_1462_out);
  nand nand_1462 (nand_1462_out, id_mux_x5_1_output_x32[26], id_mux_x5_2_output_x32[22]);
  nand nand_1463 (out_25[27], nand_1464_out, nand_1464_out);
  nand nand_1464 (nand_1464_out, id_mux_x5_1_output_x32[27], id_mux_x5_2_output_x32[22]);
  nand nand_1465 (out_25[28], nand_1466_out, nand_1466_out);
  nand nand_1466 (nand_1466_out, id_mux_x5_1_output_x32[28], id_mux_x5_2_output_x32[22]);
  nand nand_1467 (out_25[29], nand_1468_out, nand_1468_out);
  nand nand_1468 (nand_1468_out, id_mux_x5_1_output_x32[29], id_mux_x5_2_output_x32[22]);
  nand nand_1469 (out_25[30], nand_1470_out, nand_1470_out);
  nand nand_1470 (nand_1470_out, id_mux_x5_1_output_x32[30], id_mux_x5_2_output_x32[22]);
  nand nand_1471 (out_25[31], nand_1472_out, nand_1472_out);
  nand nand_1472 (nand_1472_out, id_mux_x5_1_output_x32[31], id_mux_x5_2_output_x32[22]);
  nand nand_1473 (out_26[0], nand_1474_out, nand_1474_out);
  nand nand_1474 (nand_1474_out, id_mux_x5_1_output_x32[0], id_mux_x5_2_output_x32[23]);
  nand nand_1475 (out_26[1], nand_1476_out, nand_1476_out);
  nand nand_1476 (nand_1476_out, id_mux_x5_1_output_x32[1], id_mux_x5_2_output_x32[23]);
  nand nand_1477 (out_26[2], nand_1478_out, nand_1478_out);
  nand nand_1478 (nand_1478_out, id_mux_x5_1_output_x32[2], id_mux_x5_2_output_x32[23]);
  nand nand_1479 (out_26[3], nand_1480_out, nand_1480_out);
  nand nand_1480 (nand_1480_out, id_mux_x5_1_output_x32[3], id_mux_x5_2_output_x32[23]);
  nand nand_1481 (out_26[4], nand_1482_out, nand_1482_out);
  nand nand_1482 (nand_1482_out, id_mux_x5_1_output_x32[4], id_mux_x5_2_output_x32[23]);
  nand nand_1483 (out_26[5], nand_1484_out, nand_1484_out);
  nand nand_1484 (nand_1484_out, id_mux_x5_1_output_x32[5], id_mux_x5_2_output_x32[23]);
  nand nand_1485 (out_26[6], nand_1486_out, nand_1486_out);
  nand nand_1486 (nand_1486_out, id_mux_x5_1_output_x32[6], id_mux_x5_2_output_x32[23]);
  nand nand_1487 (out_26[7], nand_1488_out, nand_1488_out);
  nand nand_1488 (nand_1488_out, id_mux_x5_1_output_x32[7], id_mux_x5_2_output_x32[23]);
  nand nand_1489 (out_26[8], nand_1490_out, nand_1490_out);
  nand nand_1490 (nand_1490_out, id_mux_x5_1_output_x32[8], id_mux_x5_2_output_x32[23]);
  nand nand_1491 (out_26[9], nand_1492_out, nand_1492_out);
  nand nand_1492 (nand_1492_out, id_mux_x5_1_output_x32[9], id_mux_x5_2_output_x32[23]);
  nand nand_1493 (out_26[10], nand_1494_out, nand_1494_out);
  nand nand_1494 (nand_1494_out, id_mux_x5_1_output_x32[10], id_mux_x5_2_output_x32[23]);
  nand nand_1495 (out_26[11], nand_1496_out, nand_1496_out);
  nand nand_1496 (nand_1496_out, id_mux_x5_1_output_x32[11], id_mux_x5_2_output_x32[23]);
  nand nand_1497 (out_26[12], nand_1498_out, nand_1498_out);
  nand nand_1498 (nand_1498_out, id_mux_x5_1_output_x32[12], id_mux_x5_2_output_x32[23]);
  nand nand_1499 (out_26[13], nand_1500_out, nand_1500_out);
  nand nand_1500 (nand_1500_out, id_mux_x5_1_output_x32[13], id_mux_x5_2_output_x32[23]);
  nand nand_1501 (out_26[14], nand_1502_out, nand_1502_out);
  nand nand_1502 (nand_1502_out, id_mux_x5_1_output_x32[14], id_mux_x5_2_output_x32[23]);
  nand nand_1503 (out_26[15], nand_1504_out, nand_1504_out);
  nand nand_1504 (nand_1504_out, id_mux_x5_1_output_x32[15], id_mux_x5_2_output_x32[23]);
  nand nand_1505 (out_26[16], nand_1506_out, nand_1506_out);
  nand nand_1506 (nand_1506_out, id_mux_x5_1_output_x32[16], id_mux_x5_2_output_x32[23]);
  nand nand_1507 (out_26[17], nand_1508_out, nand_1508_out);
  nand nand_1508 (nand_1508_out, id_mux_x5_1_output_x32[17], id_mux_x5_2_output_x32[23]);
  nand nand_1509 (out_26[18], nand_1510_out, nand_1510_out);
  nand nand_1510 (nand_1510_out, id_mux_x5_1_output_x32[18], id_mux_x5_2_output_x32[23]);
  nand nand_1511 (out_26[19], nand_1512_out, nand_1512_out);
  nand nand_1512 (nand_1512_out, id_mux_x5_1_output_x32[19], id_mux_x5_2_output_x32[23]);
  nand nand_1513 (out_26[20], nand_1514_out, nand_1514_out);
  nand nand_1514 (nand_1514_out, id_mux_x5_1_output_x32[20], id_mux_x5_2_output_x32[23]);
  nand nand_1515 (out_26[21], nand_1516_out, nand_1516_out);
  nand nand_1516 (nand_1516_out, id_mux_x5_1_output_x32[21], id_mux_x5_2_output_x32[23]);
  nand nand_1517 (out_26[22], nand_1518_out, nand_1518_out);
  nand nand_1518 (nand_1518_out, id_mux_x5_1_output_x32[22], id_mux_x5_2_output_x32[23]);
  nand nand_1519 (out_26[23], nand_1520_out, nand_1520_out);
  nand nand_1520 (nand_1520_out, id_mux_x5_1_output_x32[23], id_mux_x5_2_output_x32[23]);
  nand nand_1521 (out_26[24], nand_1522_out, nand_1522_out);
  nand nand_1522 (nand_1522_out, id_mux_x5_1_output_x32[24], id_mux_x5_2_output_x32[23]);
  nand nand_1523 (out_26[25], nand_1524_out, nand_1524_out);
  nand nand_1524 (nand_1524_out, id_mux_x5_1_output_x32[25], id_mux_x5_2_output_x32[23]);
  nand nand_1525 (out_26[26], nand_1526_out, nand_1526_out);
  nand nand_1526 (nand_1526_out, id_mux_x5_1_output_x32[26], id_mux_x5_2_output_x32[23]);
  nand nand_1527 (out_26[27], nand_1528_out, nand_1528_out);
  nand nand_1528 (nand_1528_out, id_mux_x5_1_output_x32[27], id_mux_x5_2_output_x32[23]);
  nand nand_1529 (out_26[28], nand_1530_out, nand_1530_out);
  nand nand_1530 (nand_1530_out, id_mux_x5_1_output_x32[28], id_mux_x5_2_output_x32[23]);
  nand nand_1531 (out_26[29], nand_1532_out, nand_1532_out);
  nand nand_1532 (nand_1532_out, id_mux_x5_1_output_x32[29], id_mux_x5_2_output_x32[23]);
  nand nand_1533 (out_26[30], nand_1534_out, nand_1534_out);
  nand nand_1534 (nand_1534_out, id_mux_x5_1_output_x32[30], id_mux_x5_2_output_x32[23]);
  nand nand_1535 (out_26[31], nand_1536_out, nand_1536_out);
  nand nand_1536 (nand_1536_out, id_mux_x5_1_output_x32[31], id_mux_x5_2_output_x32[23]);
  nand nand_1537 (out_27[0], nand_1538_out, nand_1538_out);
  nand nand_1538 (nand_1538_out, id_mux_x5_1_output_x32[0], id_mux_x5_2_output_x32[24]);
  nand nand_1539 (out_27[1], nand_1540_out, nand_1540_out);
  nand nand_1540 (nand_1540_out, id_mux_x5_1_output_x32[1], id_mux_x5_2_output_x32[24]);
  nand nand_1541 (out_27[2], nand_1542_out, nand_1542_out);
  nand nand_1542 (nand_1542_out, id_mux_x5_1_output_x32[2], id_mux_x5_2_output_x32[24]);
  nand nand_1543 (out_27[3], nand_1544_out, nand_1544_out);
  nand nand_1544 (nand_1544_out, id_mux_x5_1_output_x32[3], id_mux_x5_2_output_x32[24]);
  nand nand_1545 (out_27[4], nand_1546_out, nand_1546_out);
  nand nand_1546 (nand_1546_out, id_mux_x5_1_output_x32[4], id_mux_x5_2_output_x32[24]);
  nand nand_1547 (out_27[5], nand_1548_out, nand_1548_out);
  nand nand_1548 (nand_1548_out, id_mux_x5_1_output_x32[5], id_mux_x5_2_output_x32[24]);
  nand nand_1549 (out_27[6], nand_1550_out, nand_1550_out);
  nand nand_1550 (nand_1550_out, id_mux_x5_1_output_x32[6], id_mux_x5_2_output_x32[24]);
  nand nand_1551 (out_27[7], nand_1552_out, nand_1552_out);
  nand nand_1552 (nand_1552_out, id_mux_x5_1_output_x32[7], id_mux_x5_2_output_x32[24]);
  nand nand_1553 (out_27[8], nand_1554_out, nand_1554_out);
  nand nand_1554 (nand_1554_out, id_mux_x5_1_output_x32[8], id_mux_x5_2_output_x32[24]);
  nand nand_1555 (out_27[9], nand_1556_out, nand_1556_out);
  nand nand_1556 (nand_1556_out, id_mux_x5_1_output_x32[9], id_mux_x5_2_output_x32[24]);
  nand nand_1557 (out_27[10], nand_1558_out, nand_1558_out);
  nand nand_1558 (nand_1558_out, id_mux_x5_1_output_x32[10], id_mux_x5_2_output_x32[24]);
  nand nand_1559 (out_27[11], nand_1560_out, nand_1560_out);
  nand nand_1560 (nand_1560_out, id_mux_x5_1_output_x32[11], id_mux_x5_2_output_x32[24]);
  nand nand_1561 (out_27[12], nand_1562_out, nand_1562_out);
  nand nand_1562 (nand_1562_out, id_mux_x5_1_output_x32[12], id_mux_x5_2_output_x32[24]);
  nand nand_1563 (out_27[13], nand_1564_out, nand_1564_out);
  nand nand_1564 (nand_1564_out, id_mux_x5_1_output_x32[13], id_mux_x5_2_output_x32[24]);
  nand nand_1565 (out_27[14], nand_1566_out, nand_1566_out);
  nand nand_1566 (nand_1566_out, id_mux_x5_1_output_x32[14], id_mux_x5_2_output_x32[24]);
  nand nand_1567 (out_27[15], nand_1568_out, nand_1568_out);
  nand nand_1568 (nand_1568_out, id_mux_x5_1_output_x32[15], id_mux_x5_2_output_x32[24]);
  nand nand_1569 (out_27[16], nand_1570_out, nand_1570_out);
  nand nand_1570 (nand_1570_out, id_mux_x5_1_output_x32[16], id_mux_x5_2_output_x32[24]);
  nand nand_1571 (out_27[17], nand_1572_out, nand_1572_out);
  nand nand_1572 (nand_1572_out, id_mux_x5_1_output_x32[17], id_mux_x5_2_output_x32[24]);
  nand nand_1573 (out_27[18], nand_1574_out, nand_1574_out);
  nand nand_1574 (nand_1574_out, id_mux_x5_1_output_x32[18], id_mux_x5_2_output_x32[24]);
  nand nand_1575 (out_27[19], nand_1576_out, nand_1576_out);
  nand nand_1576 (nand_1576_out, id_mux_x5_1_output_x32[19], id_mux_x5_2_output_x32[24]);
  nand nand_1577 (out_27[20], nand_1578_out, nand_1578_out);
  nand nand_1578 (nand_1578_out, id_mux_x5_1_output_x32[20], id_mux_x5_2_output_x32[24]);
  nand nand_1579 (out_27[21], nand_1580_out, nand_1580_out);
  nand nand_1580 (nand_1580_out, id_mux_x5_1_output_x32[21], id_mux_x5_2_output_x32[24]);
  nand nand_1581 (out_27[22], nand_1582_out, nand_1582_out);
  nand nand_1582 (nand_1582_out, id_mux_x5_1_output_x32[22], id_mux_x5_2_output_x32[24]);
  nand nand_1583 (out_27[23], nand_1584_out, nand_1584_out);
  nand nand_1584 (nand_1584_out, id_mux_x5_1_output_x32[23], id_mux_x5_2_output_x32[24]);
  nand nand_1585 (out_27[24], nand_1586_out, nand_1586_out);
  nand nand_1586 (nand_1586_out, id_mux_x5_1_output_x32[24], id_mux_x5_2_output_x32[24]);
  nand nand_1587 (out_27[25], nand_1588_out, nand_1588_out);
  nand nand_1588 (nand_1588_out, id_mux_x5_1_output_x32[25], id_mux_x5_2_output_x32[24]);
  nand nand_1589 (out_27[26], nand_1590_out, nand_1590_out);
  nand nand_1590 (nand_1590_out, id_mux_x5_1_output_x32[26], id_mux_x5_2_output_x32[24]);
  nand nand_1591 (out_27[27], nand_1592_out, nand_1592_out);
  nand nand_1592 (nand_1592_out, id_mux_x5_1_output_x32[27], id_mux_x5_2_output_x32[24]);
  nand nand_1593 (out_27[28], nand_1594_out, nand_1594_out);
  nand nand_1594 (nand_1594_out, id_mux_x5_1_output_x32[28], id_mux_x5_2_output_x32[24]);
  nand nand_1595 (out_27[29], nand_1596_out, nand_1596_out);
  nand nand_1596 (nand_1596_out, id_mux_x5_1_output_x32[29], id_mux_x5_2_output_x32[24]);
  nand nand_1597 (out_27[30], nand_1598_out, nand_1598_out);
  nand nand_1598 (nand_1598_out, id_mux_x5_1_output_x32[30], id_mux_x5_2_output_x32[24]);
  nand nand_1599 (out_27[31], nand_1600_out, nand_1600_out);
  nand nand_1600 (nand_1600_out, id_mux_x5_1_output_x32[31], id_mux_x5_2_output_x32[24]);
  nand nand_1601 (out_28[0], nand_1602_out, nand_1602_out);
  nand nand_1602 (nand_1602_out, id_mux_x5_1_output_x32[0], id_mux_x5_2_output_x32[25]);
  nand nand_1603 (out_28[1], nand_1604_out, nand_1604_out);
  nand nand_1604 (nand_1604_out, id_mux_x5_1_output_x32[1], id_mux_x5_2_output_x32[25]);
  nand nand_1605 (out_28[2], nand_1606_out, nand_1606_out);
  nand nand_1606 (nand_1606_out, id_mux_x5_1_output_x32[2], id_mux_x5_2_output_x32[25]);
  nand nand_1607 (out_28[3], nand_1608_out, nand_1608_out);
  nand nand_1608 (nand_1608_out, id_mux_x5_1_output_x32[3], id_mux_x5_2_output_x32[25]);
  nand nand_1609 (out_28[4], nand_1610_out, nand_1610_out);
  nand nand_1610 (nand_1610_out, id_mux_x5_1_output_x32[4], id_mux_x5_2_output_x32[25]);
  nand nand_1611 (out_28[5], nand_1612_out, nand_1612_out);
  nand nand_1612 (nand_1612_out, id_mux_x5_1_output_x32[5], id_mux_x5_2_output_x32[25]);
  nand nand_1613 (out_28[6], nand_1614_out, nand_1614_out);
  nand nand_1614 (nand_1614_out, id_mux_x5_1_output_x32[6], id_mux_x5_2_output_x32[25]);
  nand nand_1615 (out_28[7], nand_1616_out, nand_1616_out);
  nand nand_1616 (nand_1616_out, id_mux_x5_1_output_x32[7], id_mux_x5_2_output_x32[25]);
  nand nand_1617 (out_28[8], nand_1618_out, nand_1618_out);
  nand nand_1618 (nand_1618_out, id_mux_x5_1_output_x32[8], id_mux_x5_2_output_x32[25]);
  nand nand_1619 (out_28[9], nand_1620_out, nand_1620_out);
  nand nand_1620 (nand_1620_out, id_mux_x5_1_output_x32[9], id_mux_x5_2_output_x32[25]);
  nand nand_1621 (out_28[10], nand_1622_out, nand_1622_out);
  nand nand_1622 (nand_1622_out, id_mux_x5_1_output_x32[10], id_mux_x5_2_output_x32[25]);
  nand nand_1623 (out_28[11], nand_1624_out, nand_1624_out);
  nand nand_1624 (nand_1624_out, id_mux_x5_1_output_x32[11], id_mux_x5_2_output_x32[25]);
  nand nand_1625 (out_28[12], nand_1626_out, nand_1626_out);
  nand nand_1626 (nand_1626_out, id_mux_x5_1_output_x32[12], id_mux_x5_2_output_x32[25]);
  nand nand_1627 (out_28[13], nand_1628_out, nand_1628_out);
  nand nand_1628 (nand_1628_out, id_mux_x5_1_output_x32[13], id_mux_x5_2_output_x32[25]);
  nand nand_1629 (out_28[14], nand_1630_out, nand_1630_out);
  nand nand_1630 (nand_1630_out, id_mux_x5_1_output_x32[14], id_mux_x5_2_output_x32[25]);
  nand nand_1631 (out_28[15], nand_1632_out, nand_1632_out);
  nand nand_1632 (nand_1632_out, id_mux_x5_1_output_x32[15], id_mux_x5_2_output_x32[25]);
  nand nand_1633 (out_28[16], nand_1634_out, nand_1634_out);
  nand nand_1634 (nand_1634_out, id_mux_x5_1_output_x32[16], id_mux_x5_2_output_x32[25]);
  nand nand_1635 (out_28[17], nand_1636_out, nand_1636_out);
  nand nand_1636 (nand_1636_out, id_mux_x5_1_output_x32[17], id_mux_x5_2_output_x32[25]);
  nand nand_1637 (out_28[18], nand_1638_out, nand_1638_out);
  nand nand_1638 (nand_1638_out, id_mux_x5_1_output_x32[18], id_mux_x5_2_output_x32[25]);
  nand nand_1639 (out_28[19], nand_1640_out, nand_1640_out);
  nand nand_1640 (nand_1640_out, id_mux_x5_1_output_x32[19], id_mux_x5_2_output_x32[25]);
  nand nand_1641 (out_28[20], nand_1642_out, nand_1642_out);
  nand nand_1642 (nand_1642_out, id_mux_x5_1_output_x32[20], id_mux_x5_2_output_x32[25]);
  nand nand_1643 (out_28[21], nand_1644_out, nand_1644_out);
  nand nand_1644 (nand_1644_out, id_mux_x5_1_output_x32[21], id_mux_x5_2_output_x32[25]);
  nand nand_1645 (out_28[22], nand_1646_out, nand_1646_out);
  nand nand_1646 (nand_1646_out, id_mux_x5_1_output_x32[22], id_mux_x5_2_output_x32[25]);
  nand nand_1647 (out_28[23], nand_1648_out, nand_1648_out);
  nand nand_1648 (nand_1648_out, id_mux_x5_1_output_x32[23], id_mux_x5_2_output_x32[25]);
  nand nand_1649 (out_28[24], nand_1650_out, nand_1650_out);
  nand nand_1650 (nand_1650_out, id_mux_x5_1_output_x32[24], id_mux_x5_2_output_x32[25]);
  nand nand_1651 (out_28[25], nand_1652_out, nand_1652_out);
  nand nand_1652 (nand_1652_out, id_mux_x5_1_output_x32[25], id_mux_x5_2_output_x32[25]);
  nand nand_1653 (out_28[26], nand_1654_out, nand_1654_out);
  nand nand_1654 (nand_1654_out, id_mux_x5_1_output_x32[26], id_mux_x5_2_output_x32[25]);
  nand nand_1655 (out_28[27], nand_1656_out, nand_1656_out);
  nand nand_1656 (nand_1656_out, id_mux_x5_1_output_x32[27], id_mux_x5_2_output_x32[25]);
  nand nand_1657 (out_28[28], nand_1658_out, nand_1658_out);
  nand nand_1658 (nand_1658_out, id_mux_x5_1_output_x32[28], id_mux_x5_2_output_x32[25]);
  nand nand_1659 (out_28[29], nand_1660_out, nand_1660_out);
  nand nand_1660 (nand_1660_out, id_mux_x5_1_output_x32[29], id_mux_x5_2_output_x32[25]);
  nand nand_1661 (out_28[30], nand_1662_out, nand_1662_out);
  nand nand_1662 (nand_1662_out, id_mux_x5_1_output_x32[30], id_mux_x5_2_output_x32[25]);
  nand nand_1663 (out_28[31], nand_1664_out, nand_1664_out);
  nand nand_1664 (nand_1664_out, id_mux_x5_1_output_x32[31], id_mux_x5_2_output_x32[25]);
  nand nand_1665 (out_29[0], nand_1666_out, nand_1666_out);
  nand nand_1666 (nand_1666_out, id_mux_x5_1_output_x32[0], id_mux_x5_2_output_x32[26]);
  nand nand_1667 (out_29[1], nand_1668_out, nand_1668_out);
  nand nand_1668 (nand_1668_out, id_mux_x5_1_output_x32[1], id_mux_x5_2_output_x32[26]);
  nand nand_1669 (out_29[2], nand_1670_out, nand_1670_out);
  nand nand_1670 (nand_1670_out, id_mux_x5_1_output_x32[2], id_mux_x5_2_output_x32[26]);
  nand nand_1671 (out_29[3], nand_1672_out, nand_1672_out);
  nand nand_1672 (nand_1672_out, id_mux_x5_1_output_x32[3], id_mux_x5_2_output_x32[26]);
  nand nand_1673 (out_29[4], nand_1674_out, nand_1674_out);
  nand nand_1674 (nand_1674_out, id_mux_x5_1_output_x32[4], id_mux_x5_2_output_x32[26]);
  nand nand_1675 (out_29[5], nand_1676_out, nand_1676_out);
  nand nand_1676 (nand_1676_out, id_mux_x5_1_output_x32[5], id_mux_x5_2_output_x32[26]);
  nand nand_1677 (out_29[6], nand_1678_out, nand_1678_out);
  nand nand_1678 (nand_1678_out, id_mux_x5_1_output_x32[6], id_mux_x5_2_output_x32[26]);
  nand nand_1679 (out_29[7], nand_1680_out, nand_1680_out);
  nand nand_1680 (nand_1680_out, id_mux_x5_1_output_x32[7], id_mux_x5_2_output_x32[26]);
  nand nand_1681 (out_29[8], nand_1682_out, nand_1682_out);
  nand nand_1682 (nand_1682_out, id_mux_x5_1_output_x32[8], id_mux_x5_2_output_x32[26]);
  nand nand_1683 (out_29[9], nand_1684_out, nand_1684_out);
  nand nand_1684 (nand_1684_out, id_mux_x5_1_output_x32[9], id_mux_x5_2_output_x32[26]);
  nand nand_1685 (out_29[10], nand_1686_out, nand_1686_out);
  nand nand_1686 (nand_1686_out, id_mux_x5_1_output_x32[10], id_mux_x5_2_output_x32[26]);
  nand nand_1687 (out_29[11], nand_1688_out, nand_1688_out);
  nand nand_1688 (nand_1688_out, id_mux_x5_1_output_x32[11], id_mux_x5_2_output_x32[26]);
  nand nand_1689 (out_29[12], nand_1690_out, nand_1690_out);
  nand nand_1690 (nand_1690_out, id_mux_x5_1_output_x32[12], id_mux_x5_2_output_x32[26]);
  nand nand_1691 (out_29[13], nand_1692_out, nand_1692_out);
  nand nand_1692 (nand_1692_out, id_mux_x5_1_output_x32[13], id_mux_x5_2_output_x32[26]);
  nand nand_1693 (out_29[14], nand_1694_out, nand_1694_out);
  nand nand_1694 (nand_1694_out, id_mux_x5_1_output_x32[14], id_mux_x5_2_output_x32[26]);
  nand nand_1695 (out_29[15], nand_1696_out, nand_1696_out);
  nand nand_1696 (nand_1696_out, id_mux_x5_1_output_x32[15], id_mux_x5_2_output_x32[26]);
  nand nand_1697 (out_29[16], nand_1698_out, nand_1698_out);
  nand nand_1698 (nand_1698_out, id_mux_x5_1_output_x32[16], id_mux_x5_2_output_x32[26]);
  nand nand_1699 (out_29[17], nand_1700_out, nand_1700_out);
  nand nand_1700 (nand_1700_out, id_mux_x5_1_output_x32[17], id_mux_x5_2_output_x32[26]);
  nand nand_1701 (out_29[18], nand_1702_out, nand_1702_out);
  nand nand_1702 (nand_1702_out, id_mux_x5_1_output_x32[18], id_mux_x5_2_output_x32[26]);
  nand nand_1703 (out_29[19], nand_1704_out, nand_1704_out);
  nand nand_1704 (nand_1704_out, id_mux_x5_1_output_x32[19], id_mux_x5_2_output_x32[26]);
  nand nand_1705 (out_29[20], nand_1706_out, nand_1706_out);
  nand nand_1706 (nand_1706_out, id_mux_x5_1_output_x32[20], id_mux_x5_2_output_x32[26]);
  nand nand_1707 (out_29[21], nand_1708_out, nand_1708_out);
  nand nand_1708 (nand_1708_out, id_mux_x5_1_output_x32[21], id_mux_x5_2_output_x32[26]);
  nand nand_1709 (out_29[22], nand_1710_out, nand_1710_out);
  nand nand_1710 (nand_1710_out, id_mux_x5_1_output_x32[22], id_mux_x5_2_output_x32[26]);
  nand nand_1711 (out_29[23], nand_1712_out, nand_1712_out);
  nand nand_1712 (nand_1712_out, id_mux_x5_1_output_x32[23], id_mux_x5_2_output_x32[26]);
  nand nand_1713 (out_29[24], nand_1714_out, nand_1714_out);
  nand nand_1714 (nand_1714_out, id_mux_x5_1_output_x32[24], id_mux_x5_2_output_x32[26]);
  nand nand_1715 (out_29[25], nand_1716_out, nand_1716_out);
  nand nand_1716 (nand_1716_out, id_mux_x5_1_output_x32[25], id_mux_x5_2_output_x32[26]);
  nand nand_1717 (out_29[26], nand_1718_out, nand_1718_out);
  nand nand_1718 (nand_1718_out, id_mux_x5_1_output_x32[26], id_mux_x5_2_output_x32[26]);
  nand nand_1719 (out_29[27], nand_1720_out, nand_1720_out);
  nand nand_1720 (nand_1720_out, id_mux_x5_1_output_x32[27], id_mux_x5_2_output_x32[26]);
  nand nand_1721 (out_29[28], nand_1722_out, nand_1722_out);
  nand nand_1722 (nand_1722_out, id_mux_x5_1_output_x32[28], id_mux_x5_2_output_x32[26]);
  nand nand_1723 (out_29[29], nand_1724_out, nand_1724_out);
  nand nand_1724 (nand_1724_out, id_mux_x5_1_output_x32[29], id_mux_x5_2_output_x32[26]);
  nand nand_1725 (out_29[30], nand_1726_out, nand_1726_out);
  nand nand_1726 (nand_1726_out, id_mux_x5_1_output_x32[30], id_mux_x5_2_output_x32[26]);
  nand nand_1727 (out_29[31], nand_1728_out, nand_1728_out);
  nand nand_1728 (nand_1728_out, id_mux_x5_1_output_x32[31], id_mux_x5_2_output_x32[26]);
  nand nand_1729 (out_30[0], nand_1730_out, nand_1730_out);
  nand nand_1730 (nand_1730_out, id_mux_x5_1_output_x32[0], id_mux_x5_2_output_x32[27]);
  nand nand_1731 (out_30[1], nand_1732_out, nand_1732_out);
  nand nand_1732 (nand_1732_out, id_mux_x5_1_output_x32[1], id_mux_x5_2_output_x32[27]);
  nand nand_1733 (out_30[2], nand_1734_out, nand_1734_out);
  nand nand_1734 (nand_1734_out, id_mux_x5_1_output_x32[2], id_mux_x5_2_output_x32[27]);
  nand nand_1735 (out_30[3], nand_1736_out, nand_1736_out);
  nand nand_1736 (nand_1736_out, id_mux_x5_1_output_x32[3], id_mux_x5_2_output_x32[27]);
  nand nand_1737 (out_30[4], nand_1738_out, nand_1738_out);
  nand nand_1738 (nand_1738_out, id_mux_x5_1_output_x32[4], id_mux_x5_2_output_x32[27]);
  nand nand_1739 (out_30[5], nand_1740_out, nand_1740_out);
  nand nand_1740 (nand_1740_out, id_mux_x5_1_output_x32[5], id_mux_x5_2_output_x32[27]);
  nand nand_1741 (out_30[6], nand_1742_out, nand_1742_out);
  nand nand_1742 (nand_1742_out, id_mux_x5_1_output_x32[6], id_mux_x5_2_output_x32[27]);
  nand nand_1743 (out_30[7], nand_1744_out, nand_1744_out);
  nand nand_1744 (nand_1744_out, id_mux_x5_1_output_x32[7], id_mux_x5_2_output_x32[27]);
  nand nand_1745 (out_30[8], nand_1746_out, nand_1746_out);
  nand nand_1746 (nand_1746_out, id_mux_x5_1_output_x32[8], id_mux_x5_2_output_x32[27]);
  nand nand_1747 (out_30[9], nand_1748_out, nand_1748_out);
  nand nand_1748 (nand_1748_out, id_mux_x5_1_output_x32[9], id_mux_x5_2_output_x32[27]);
  nand nand_1749 (out_30[10], nand_1750_out, nand_1750_out);
  nand nand_1750 (nand_1750_out, id_mux_x5_1_output_x32[10], id_mux_x5_2_output_x32[27]);
  nand nand_1751 (out_30[11], nand_1752_out, nand_1752_out);
  nand nand_1752 (nand_1752_out, id_mux_x5_1_output_x32[11], id_mux_x5_2_output_x32[27]);
  nand nand_1753 (out_30[12], nand_1754_out, nand_1754_out);
  nand nand_1754 (nand_1754_out, id_mux_x5_1_output_x32[12], id_mux_x5_2_output_x32[27]);
  nand nand_1755 (out_30[13], nand_1756_out, nand_1756_out);
  nand nand_1756 (nand_1756_out, id_mux_x5_1_output_x32[13], id_mux_x5_2_output_x32[27]);
  nand nand_1757 (out_30[14], nand_1758_out, nand_1758_out);
  nand nand_1758 (nand_1758_out, id_mux_x5_1_output_x32[14], id_mux_x5_2_output_x32[27]);
  nand nand_1759 (out_30[15], nand_1760_out, nand_1760_out);
  nand nand_1760 (nand_1760_out, id_mux_x5_1_output_x32[15], id_mux_x5_2_output_x32[27]);
  nand nand_1761 (out_30[16], nand_1762_out, nand_1762_out);
  nand nand_1762 (nand_1762_out, id_mux_x5_1_output_x32[16], id_mux_x5_2_output_x32[27]);
  nand nand_1763 (out_30[17], nand_1764_out, nand_1764_out);
  nand nand_1764 (nand_1764_out, id_mux_x5_1_output_x32[17], id_mux_x5_2_output_x32[27]);
  nand nand_1765 (out_30[18], nand_1766_out, nand_1766_out);
  nand nand_1766 (nand_1766_out, id_mux_x5_1_output_x32[18], id_mux_x5_2_output_x32[27]);
  nand nand_1767 (out_30[19], nand_1768_out, nand_1768_out);
  nand nand_1768 (nand_1768_out, id_mux_x5_1_output_x32[19], id_mux_x5_2_output_x32[27]);
  nand nand_1769 (out_30[20], nand_1770_out, nand_1770_out);
  nand nand_1770 (nand_1770_out, id_mux_x5_1_output_x32[20], id_mux_x5_2_output_x32[27]);
  nand nand_1771 (out_30[21], nand_1772_out, nand_1772_out);
  nand nand_1772 (nand_1772_out, id_mux_x5_1_output_x32[21], id_mux_x5_2_output_x32[27]);
  nand nand_1773 (out_30[22], nand_1774_out, nand_1774_out);
  nand nand_1774 (nand_1774_out, id_mux_x5_1_output_x32[22], id_mux_x5_2_output_x32[27]);
  nand nand_1775 (out_30[23], nand_1776_out, nand_1776_out);
  nand nand_1776 (nand_1776_out, id_mux_x5_1_output_x32[23], id_mux_x5_2_output_x32[27]);
  nand nand_1777 (out_30[24], nand_1778_out, nand_1778_out);
  nand nand_1778 (nand_1778_out, id_mux_x5_1_output_x32[24], id_mux_x5_2_output_x32[27]);
  nand nand_1779 (out_30[25], nand_1780_out, nand_1780_out);
  nand nand_1780 (nand_1780_out, id_mux_x5_1_output_x32[25], id_mux_x5_2_output_x32[27]);
  nand nand_1781 (out_30[26], nand_1782_out, nand_1782_out);
  nand nand_1782 (nand_1782_out, id_mux_x5_1_output_x32[26], id_mux_x5_2_output_x32[27]);
  nand nand_1783 (out_30[27], nand_1784_out, nand_1784_out);
  nand nand_1784 (nand_1784_out, id_mux_x5_1_output_x32[27], id_mux_x5_2_output_x32[27]);
  nand nand_1785 (out_30[28], nand_1786_out, nand_1786_out);
  nand nand_1786 (nand_1786_out, id_mux_x5_1_output_x32[28], id_mux_x5_2_output_x32[27]);
  nand nand_1787 (out_30[29], nand_1788_out, nand_1788_out);
  nand nand_1788 (nand_1788_out, id_mux_x5_1_output_x32[29], id_mux_x5_2_output_x32[27]);
  nand nand_1789 (out_30[30], nand_1790_out, nand_1790_out);
  nand nand_1790 (nand_1790_out, id_mux_x5_1_output_x32[30], id_mux_x5_2_output_x32[27]);
  nand nand_1791 (out_30[31], nand_1792_out, nand_1792_out);
  nand nand_1792 (nand_1792_out, id_mux_x5_1_output_x32[31], id_mux_x5_2_output_x32[27]);
  nand nand_1793 (out_31[0], nand_1794_out, nand_1794_out);
  nand nand_1794 (nand_1794_out, id_mux_x5_1_output_x32[0], id_mux_x5_2_output_x32[28]);
  nand nand_1795 (out_31[1], nand_1796_out, nand_1796_out);
  nand nand_1796 (nand_1796_out, id_mux_x5_1_output_x32[1], id_mux_x5_2_output_x32[28]);
  nand nand_1797 (out_31[2], nand_1798_out, nand_1798_out);
  nand nand_1798 (nand_1798_out, id_mux_x5_1_output_x32[2], id_mux_x5_2_output_x32[28]);
  nand nand_1799 (out_31[3], nand_1800_out, nand_1800_out);
  nand nand_1800 (nand_1800_out, id_mux_x5_1_output_x32[3], id_mux_x5_2_output_x32[28]);
  nand nand_1801 (out_31[4], nand_1802_out, nand_1802_out);
  nand nand_1802 (nand_1802_out, id_mux_x5_1_output_x32[4], id_mux_x5_2_output_x32[28]);
  nand nand_1803 (out_31[5], nand_1804_out, nand_1804_out);
  nand nand_1804 (nand_1804_out, id_mux_x5_1_output_x32[5], id_mux_x5_2_output_x32[28]);
  nand nand_1805 (out_31[6], nand_1806_out, nand_1806_out);
  nand nand_1806 (nand_1806_out, id_mux_x5_1_output_x32[6], id_mux_x5_2_output_x32[28]);
  nand nand_1807 (out_31[7], nand_1808_out, nand_1808_out);
  nand nand_1808 (nand_1808_out, id_mux_x5_1_output_x32[7], id_mux_x5_2_output_x32[28]);
  nand nand_1809 (out_31[8], nand_1810_out, nand_1810_out);
  nand nand_1810 (nand_1810_out, id_mux_x5_1_output_x32[8], id_mux_x5_2_output_x32[28]);
  nand nand_1811 (out_31[9], nand_1812_out, nand_1812_out);
  nand nand_1812 (nand_1812_out, id_mux_x5_1_output_x32[9], id_mux_x5_2_output_x32[28]);
  nand nand_1813 (out_31[10], nand_1814_out, nand_1814_out);
  nand nand_1814 (nand_1814_out, id_mux_x5_1_output_x32[10], id_mux_x5_2_output_x32[28]);
  nand nand_1815 (out_31[11], nand_1816_out, nand_1816_out);
  nand nand_1816 (nand_1816_out, id_mux_x5_1_output_x32[11], id_mux_x5_2_output_x32[28]);
  nand nand_1817 (out_31[12], nand_1818_out, nand_1818_out);
  nand nand_1818 (nand_1818_out, id_mux_x5_1_output_x32[12], id_mux_x5_2_output_x32[28]);
  nand nand_1819 (out_31[13], nand_1820_out, nand_1820_out);
  nand nand_1820 (nand_1820_out, id_mux_x5_1_output_x32[13], id_mux_x5_2_output_x32[28]);
  nand nand_1821 (out_31[14], nand_1822_out, nand_1822_out);
  nand nand_1822 (nand_1822_out, id_mux_x5_1_output_x32[14], id_mux_x5_2_output_x32[28]);
  nand nand_1823 (out_31[15], nand_1824_out, nand_1824_out);
  nand nand_1824 (nand_1824_out, id_mux_x5_1_output_x32[15], id_mux_x5_2_output_x32[28]);
  nand nand_1825 (out_31[16], nand_1826_out, nand_1826_out);
  nand nand_1826 (nand_1826_out, id_mux_x5_1_output_x32[16], id_mux_x5_2_output_x32[28]);
  nand nand_1827 (out_31[17], nand_1828_out, nand_1828_out);
  nand nand_1828 (nand_1828_out, id_mux_x5_1_output_x32[17], id_mux_x5_2_output_x32[28]);
  nand nand_1829 (out_31[18], nand_1830_out, nand_1830_out);
  nand nand_1830 (nand_1830_out, id_mux_x5_1_output_x32[18], id_mux_x5_2_output_x32[28]);
  nand nand_1831 (out_31[19], nand_1832_out, nand_1832_out);
  nand nand_1832 (nand_1832_out, id_mux_x5_1_output_x32[19], id_mux_x5_2_output_x32[28]);
  nand nand_1833 (out_31[20], nand_1834_out, nand_1834_out);
  nand nand_1834 (nand_1834_out, id_mux_x5_1_output_x32[20], id_mux_x5_2_output_x32[28]);
  nand nand_1835 (out_31[21], nand_1836_out, nand_1836_out);
  nand nand_1836 (nand_1836_out, id_mux_x5_1_output_x32[21], id_mux_x5_2_output_x32[28]);
  nand nand_1837 (out_31[22], nand_1838_out, nand_1838_out);
  nand nand_1838 (nand_1838_out, id_mux_x5_1_output_x32[22], id_mux_x5_2_output_x32[28]);
  nand nand_1839 (out_31[23], nand_1840_out, nand_1840_out);
  nand nand_1840 (nand_1840_out, id_mux_x5_1_output_x32[23], id_mux_x5_2_output_x32[28]);
  nand nand_1841 (out_31[24], nand_1842_out, nand_1842_out);
  nand nand_1842 (nand_1842_out, id_mux_x5_1_output_x32[24], id_mux_x5_2_output_x32[28]);
  nand nand_1843 (out_31[25], nand_1844_out, nand_1844_out);
  nand nand_1844 (nand_1844_out, id_mux_x5_1_output_x32[25], id_mux_x5_2_output_x32[28]);
  nand nand_1845 (out_31[26], nand_1846_out, nand_1846_out);
  nand nand_1846 (nand_1846_out, id_mux_x5_1_output_x32[26], id_mux_x5_2_output_x32[28]);
  nand nand_1847 (out_31[27], nand_1848_out, nand_1848_out);
  nand nand_1848 (nand_1848_out, id_mux_x5_1_output_x32[27], id_mux_x5_2_output_x32[28]);
  nand nand_1849 (out_31[28], nand_1850_out, nand_1850_out);
  nand nand_1850 (nand_1850_out, id_mux_x5_1_output_x32[28], id_mux_x5_2_output_x32[28]);
  nand nand_1851 (out_31[29], nand_1852_out, nand_1852_out);
  nand nand_1852 (nand_1852_out, id_mux_x5_1_output_x32[29], id_mux_x5_2_output_x32[28]);
  nand nand_1853 (out_31[30], nand_1854_out, nand_1854_out);
  nand nand_1854 (nand_1854_out, id_mux_x5_1_output_x32[30], id_mux_x5_2_output_x32[28]);
  nand nand_1855 (out_31[31], nand_1856_out, nand_1856_out);
  nand nand_1856 (nand_1856_out, id_mux_x5_1_output_x32[31], id_mux_x5_2_output_x32[28]);
  nand nand_1857 (out_32[0], nand_1858_out, nand_1858_out);
  nand nand_1858 (nand_1858_out, id_mux_x5_1_output_x32[0], id_mux_x5_2_output_x32[29]);
  nand nand_1859 (out_32[1], nand_1860_out, nand_1860_out);
  nand nand_1860 (nand_1860_out, id_mux_x5_1_output_x32[1], id_mux_x5_2_output_x32[29]);
  nand nand_1861 (out_32[2], nand_1862_out, nand_1862_out);
  nand nand_1862 (nand_1862_out, id_mux_x5_1_output_x32[2], id_mux_x5_2_output_x32[29]);
  nand nand_1863 (out_32[3], nand_1864_out, nand_1864_out);
  nand nand_1864 (nand_1864_out, id_mux_x5_1_output_x32[3], id_mux_x5_2_output_x32[29]);
  nand nand_1865 (out_32[4], nand_1866_out, nand_1866_out);
  nand nand_1866 (nand_1866_out, id_mux_x5_1_output_x32[4], id_mux_x5_2_output_x32[29]);
  nand nand_1867 (out_32[5], nand_1868_out, nand_1868_out);
  nand nand_1868 (nand_1868_out, id_mux_x5_1_output_x32[5], id_mux_x5_2_output_x32[29]);
  nand nand_1869 (out_32[6], nand_1870_out, nand_1870_out);
  nand nand_1870 (nand_1870_out, id_mux_x5_1_output_x32[6], id_mux_x5_2_output_x32[29]);
  nand nand_1871 (out_32[7], nand_1872_out, nand_1872_out);
  nand nand_1872 (nand_1872_out, id_mux_x5_1_output_x32[7], id_mux_x5_2_output_x32[29]);
  nand nand_1873 (out_32[8], nand_1874_out, nand_1874_out);
  nand nand_1874 (nand_1874_out, id_mux_x5_1_output_x32[8], id_mux_x5_2_output_x32[29]);
  nand nand_1875 (out_32[9], nand_1876_out, nand_1876_out);
  nand nand_1876 (nand_1876_out, id_mux_x5_1_output_x32[9], id_mux_x5_2_output_x32[29]);
  nand nand_1877 (out_32[10], nand_1878_out, nand_1878_out);
  nand nand_1878 (nand_1878_out, id_mux_x5_1_output_x32[10], id_mux_x5_2_output_x32[29]);
  nand nand_1879 (out_32[11], nand_1880_out, nand_1880_out);
  nand nand_1880 (nand_1880_out, id_mux_x5_1_output_x32[11], id_mux_x5_2_output_x32[29]);
  nand nand_1881 (out_32[12], nand_1882_out, nand_1882_out);
  nand nand_1882 (nand_1882_out, id_mux_x5_1_output_x32[12], id_mux_x5_2_output_x32[29]);
  nand nand_1883 (out_32[13], nand_1884_out, nand_1884_out);
  nand nand_1884 (nand_1884_out, id_mux_x5_1_output_x32[13], id_mux_x5_2_output_x32[29]);
  nand nand_1885 (out_32[14], nand_1886_out, nand_1886_out);
  nand nand_1886 (nand_1886_out, id_mux_x5_1_output_x32[14], id_mux_x5_2_output_x32[29]);
  nand nand_1887 (out_32[15], nand_1888_out, nand_1888_out);
  nand nand_1888 (nand_1888_out, id_mux_x5_1_output_x32[15], id_mux_x5_2_output_x32[29]);
  nand nand_1889 (out_32[16], nand_1890_out, nand_1890_out);
  nand nand_1890 (nand_1890_out, id_mux_x5_1_output_x32[16], id_mux_x5_2_output_x32[29]);
  nand nand_1891 (out_32[17], nand_1892_out, nand_1892_out);
  nand nand_1892 (nand_1892_out, id_mux_x5_1_output_x32[17], id_mux_x5_2_output_x32[29]);
  nand nand_1893 (out_32[18], nand_1894_out, nand_1894_out);
  nand nand_1894 (nand_1894_out, id_mux_x5_1_output_x32[18], id_mux_x5_2_output_x32[29]);
  nand nand_1895 (out_32[19], nand_1896_out, nand_1896_out);
  nand nand_1896 (nand_1896_out, id_mux_x5_1_output_x32[19], id_mux_x5_2_output_x32[29]);
  nand nand_1897 (out_32[20], nand_1898_out, nand_1898_out);
  nand nand_1898 (nand_1898_out, id_mux_x5_1_output_x32[20], id_mux_x5_2_output_x32[29]);
  nand nand_1899 (out_32[21], nand_1900_out, nand_1900_out);
  nand nand_1900 (nand_1900_out, id_mux_x5_1_output_x32[21], id_mux_x5_2_output_x32[29]);
  nand nand_1901 (out_32[22], nand_1902_out, nand_1902_out);
  nand nand_1902 (nand_1902_out, id_mux_x5_1_output_x32[22], id_mux_x5_2_output_x32[29]);
  nand nand_1903 (out_32[23], nand_1904_out, nand_1904_out);
  nand nand_1904 (nand_1904_out, id_mux_x5_1_output_x32[23], id_mux_x5_2_output_x32[29]);
  nand nand_1905 (out_32[24], nand_1906_out, nand_1906_out);
  nand nand_1906 (nand_1906_out, id_mux_x5_1_output_x32[24], id_mux_x5_2_output_x32[29]);
  nand nand_1907 (out_32[25], nand_1908_out, nand_1908_out);
  nand nand_1908 (nand_1908_out, id_mux_x5_1_output_x32[25], id_mux_x5_2_output_x32[29]);
  nand nand_1909 (out_32[26], nand_1910_out, nand_1910_out);
  nand nand_1910 (nand_1910_out, id_mux_x5_1_output_x32[26], id_mux_x5_2_output_x32[29]);
  nand nand_1911 (out_32[27], nand_1912_out, nand_1912_out);
  nand nand_1912 (nand_1912_out, id_mux_x5_1_output_x32[27], id_mux_x5_2_output_x32[29]);
  nand nand_1913 (out_32[28], nand_1914_out, nand_1914_out);
  nand nand_1914 (nand_1914_out, id_mux_x5_1_output_x32[28], id_mux_x5_2_output_x32[29]);
  nand nand_1915 (out_32[29], nand_1916_out, nand_1916_out);
  nand nand_1916 (nand_1916_out, id_mux_x5_1_output_x32[29], id_mux_x5_2_output_x32[29]);
  nand nand_1917 (out_32[30], nand_1918_out, nand_1918_out);
  nand nand_1918 (nand_1918_out, id_mux_x5_1_output_x32[30], id_mux_x5_2_output_x32[29]);
  nand nand_1919 (out_32[31], nand_1920_out, nand_1920_out);
  nand nand_1920 (nand_1920_out, id_mux_x5_1_output_x32[31], id_mux_x5_2_output_x32[29]);
  nand nand_1921 (out_33[0], nand_1922_out, nand_1922_out);
  nand nand_1922 (nand_1922_out, id_mux_x5_1_output_x32[0], id_mux_x5_2_output_x32[30]);
  nand nand_1923 (out_33[1], nand_1924_out, nand_1924_out);
  nand nand_1924 (nand_1924_out, id_mux_x5_1_output_x32[1], id_mux_x5_2_output_x32[30]);
  nand nand_1925 (out_33[2], nand_1926_out, nand_1926_out);
  nand nand_1926 (nand_1926_out, id_mux_x5_1_output_x32[2], id_mux_x5_2_output_x32[30]);
  nand nand_1927 (out_33[3], nand_1928_out, nand_1928_out);
  nand nand_1928 (nand_1928_out, id_mux_x5_1_output_x32[3], id_mux_x5_2_output_x32[30]);
  nand nand_1929 (out_33[4], nand_1930_out, nand_1930_out);
  nand nand_1930 (nand_1930_out, id_mux_x5_1_output_x32[4], id_mux_x5_2_output_x32[30]);
  nand nand_1931 (out_33[5], nand_1932_out, nand_1932_out);
  nand nand_1932 (nand_1932_out, id_mux_x5_1_output_x32[5], id_mux_x5_2_output_x32[30]);
  nand nand_1933 (out_33[6], nand_1934_out, nand_1934_out);
  nand nand_1934 (nand_1934_out, id_mux_x5_1_output_x32[6], id_mux_x5_2_output_x32[30]);
  nand nand_1935 (out_33[7], nand_1936_out, nand_1936_out);
  nand nand_1936 (nand_1936_out, id_mux_x5_1_output_x32[7], id_mux_x5_2_output_x32[30]);
  nand nand_1937 (out_33[8], nand_1938_out, nand_1938_out);
  nand nand_1938 (nand_1938_out, id_mux_x5_1_output_x32[8], id_mux_x5_2_output_x32[30]);
  nand nand_1939 (out_33[9], nand_1940_out, nand_1940_out);
  nand nand_1940 (nand_1940_out, id_mux_x5_1_output_x32[9], id_mux_x5_2_output_x32[30]);
  nand nand_1941 (out_33[10], nand_1942_out, nand_1942_out);
  nand nand_1942 (nand_1942_out, id_mux_x5_1_output_x32[10], id_mux_x5_2_output_x32[30]);
  nand nand_1943 (out_33[11], nand_1944_out, nand_1944_out);
  nand nand_1944 (nand_1944_out, id_mux_x5_1_output_x32[11], id_mux_x5_2_output_x32[30]);
  nand nand_1945 (out_33[12], nand_1946_out, nand_1946_out);
  nand nand_1946 (nand_1946_out, id_mux_x5_1_output_x32[12], id_mux_x5_2_output_x32[30]);
  nand nand_1947 (out_33[13], nand_1948_out, nand_1948_out);
  nand nand_1948 (nand_1948_out, id_mux_x5_1_output_x32[13], id_mux_x5_2_output_x32[30]);
  nand nand_1949 (out_33[14], nand_1950_out, nand_1950_out);
  nand nand_1950 (nand_1950_out, id_mux_x5_1_output_x32[14], id_mux_x5_2_output_x32[30]);
  nand nand_1951 (out_33[15], nand_1952_out, nand_1952_out);
  nand nand_1952 (nand_1952_out, id_mux_x5_1_output_x32[15], id_mux_x5_2_output_x32[30]);
  nand nand_1953 (out_33[16], nand_1954_out, nand_1954_out);
  nand nand_1954 (nand_1954_out, id_mux_x5_1_output_x32[16], id_mux_x5_2_output_x32[30]);
  nand nand_1955 (out_33[17], nand_1956_out, nand_1956_out);
  nand nand_1956 (nand_1956_out, id_mux_x5_1_output_x32[17], id_mux_x5_2_output_x32[30]);
  nand nand_1957 (out_33[18], nand_1958_out, nand_1958_out);
  nand nand_1958 (nand_1958_out, id_mux_x5_1_output_x32[18], id_mux_x5_2_output_x32[30]);
  nand nand_1959 (out_33[19], nand_1960_out, nand_1960_out);
  nand nand_1960 (nand_1960_out, id_mux_x5_1_output_x32[19], id_mux_x5_2_output_x32[30]);
  nand nand_1961 (out_33[20], nand_1962_out, nand_1962_out);
  nand nand_1962 (nand_1962_out, id_mux_x5_1_output_x32[20], id_mux_x5_2_output_x32[30]);
  nand nand_1963 (out_33[21], nand_1964_out, nand_1964_out);
  nand nand_1964 (nand_1964_out, id_mux_x5_1_output_x32[21], id_mux_x5_2_output_x32[30]);
  nand nand_1965 (out_33[22], nand_1966_out, nand_1966_out);
  nand nand_1966 (nand_1966_out, id_mux_x5_1_output_x32[22], id_mux_x5_2_output_x32[30]);
  nand nand_1967 (out_33[23], nand_1968_out, nand_1968_out);
  nand nand_1968 (nand_1968_out, id_mux_x5_1_output_x32[23], id_mux_x5_2_output_x32[30]);
  nand nand_1969 (out_33[24], nand_1970_out, nand_1970_out);
  nand nand_1970 (nand_1970_out, id_mux_x5_1_output_x32[24], id_mux_x5_2_output_x32[30]);
  nand nand_1971 (out_33[25], nand_1972_out, nand_1972_out);
  nand nand_1972 (nand_1972_out, id_mux_x5_1_output_x32[25], id_mux_x5_2_output_x32[30]);
  nand nand_1973 (out_33[26], nand_1974_out, nand_1974_out);
  nand nand_1974 (nand_1974_out, id_mux_x5_1_output_x32[26], id_mux_x5_2_output_x32[30]);
  nand nand_1975 (out_33[27], nand_1976_out, nand_1976_out);
  nand nand_1976 (nand_1976_out, id_mux_x5_1_output_x32[27], id_mux_x5_2_output_x32[30]);
  nand nand_1977 (out_33[28], nand_1978_out, nand_1978_out);
  nand nand_1978 (nand_1978_out, id_mux_x5_1_output_x32[28], id_mux_x5_2_output_x32[30]);
  nand nand_1979 (out_33[29], nand_1980_out, nand_1980_out);
  nand nand_1980 (nand_1980_out, id_mux_x5_1_output_x32[29], id_mux_x5_2_output_x32[30]);
  nand nand_1981 (out_33[30], nand_1982_out, nand_1982_out);
  nand nand_1982 (nand_1982_out, id_mux_x5_1_output_x32[30], id_mux_x5_2_output_x32[30]);
  nand nand_1983 (out_33[31], nand_1984_out, nand_1984_out);
  nand nand_1984 (nand_1984_out, id_mux_x5_1_output_x32[31], id_mux_x5_2_output_x32[30]);
  nand nand_1985 (out_34[0], nand_1986_out, nand_1986_out);
  nand nand_1986 (nand_1986_out, id_mux_x5_1_output_x32[0], id_mux_x5_2_output_x32[31]);
  nand nand_1987 (out_34[1], nand_1988_out, nand_1988_out);
  nand nand_1988 (nand_1988_out, id_mux_x5_1_output_x32[1], id_mux_x5_2_output_x32[31]);
  nand nand_1989 (out_34[2], nand_1990_out, nand_1990_out);
  nand nand_1990 (nand_1990_out, id_mux_x5_1_output_x32[2], id_mux_x5_2_output_x32[31]);
  nand nand_1991 (out_34[3], nand_1992_out, nand_1992_out);
  nand nand_1992 (nand_1992_out, id_mux_x5_1_output_x32[3], id_mux_x5_2_output_x32[31]);
  nand nand_1993 (out_34[4], nand_1994_out, nand_1994_out);
  nand nand_1994 (nand_1994_out, id_mux_x5_1_output_x32[4], id_mux_x5_2_output_x32[31]);
  nand nand_1995 (out_34[5], nand_1996_out, nand_1996_out);
  nand nand_1996 (nand_1996_out, id_mux_x5_1_output_x32[5], id_mux_x5_2_output_x32[31]);
  nand nand_1997 (out_34[6], nand_1998_out, nand_1998_out);
  nand nand_1998 (nand_1998_out, id_mux_x5_1_output_x32[6], id_mux_x5_2_output_x32[31]);
  nand nand_1999 (out_34[7], nand_2000_out, nand_2000_out);
  nand nand_2000 (nand_2000_out, id_mux_x5_1_output_x32[7], id_mux_x5_2_output_x32[31]);
  nand nand_2001 (out_34[8], nand_2002_out, nand_2002_out);
  nand nand_2002 (nand_2002_out, id_mux_x5_1_output_x32[8], id_mux_x5_2_output_x32[31]);
  nand nand_2003 (out_34[9], nand_2004_out, nand_2004_out);
  nand nand_2004 (nand_2004_out, id_mux_x5_1_output_x32[9], id_mux_x5_2_output_x32[31]);
  nand nand_2005 (out_34[10], nand_2006_out, nand_2006_out);
  nand nand_2006 (nand_2006_out, id_mux_x5_1_output_x32[10], id_mux_x5_2_output_x32[31]);
  nand nand_2007 (out_34[11], nand_2008_out, nand_2008_out);
  nand nand_2008 (nand_2008_out, id_mux_x5_1_output_x32[11], id_mux_x5_2_output_x32[31]);
  nand nand_2009 (out_34[12], nand_2010_out, nand_2010_out);
  nand nand_2010 (nand_2010_out, id_mux_x5_1_output_x32[12], id_mux_x5_2_output_x32[31]);
  nand nand_2011 (out_34[13], nand_2012_out, nand_2012_out);
  nand nand_2012 (nand_2012_out, id_mux_x5_1_output_x32[13], id_mux_x5_2_output_x32[31]);
  nand nand_2013 (out_34[14], nand_2014_out, nand_2014_out);
  nand nand_2014 (nand_2014_out, id_mux_x5_1_output_x32[14], id_mux_x5_2_output_x32[31]);
  nand nand_2015 (out_34[15], nand_2016_out, nand_2016_out);
  nand nand_2016 (nand_2016_out, id_mux_x5_1_output_x32[15], id_mux_x5_2_output_x32[31]);
  nand nand_2017 (out_34[16], nand_2018_out, nand_2018_out);
  nand nand_2018 (nand_2018_out, id_mux_x5_1_output_x32[16], id_mux_x5_2_output_x32[31]);
  nand nand_2019 (out_34[17], nand_2020_out, nand_2020_out);
  nand nand_2020 (nand_2020_out, id_mux_x5_1_output_x32[17], id_mux_x5_2_output_x32[31]);
  nand nand_2021 (out_34[18], nand_2022_out, nand_2022_out);
  nand nand_2022 (nand_2022_out, id_mux_x5_1_output_x32[18], id_mux_x5_2_output_x32[31]);
  nand nand_2023 (out_34[19], nand_2024_out, nand_2024_out);
  nand nand_2024 (nand_2024_out, id_mux_x5_1_output_x32[19], id_mux_x5_2_output_x32[31]);
  nand nand_2025 (out_34[20], nand_2026_out, nand_2026_out);
  nand nand_2026 (nand_2026_out, id_mux_x5_1_output_x32[20], id_mux_x5_2_output_x32[31]);
  nand nand_2027 (out_34[21], nand_2028_out, nand_2028_out);
  nand nand_2028 (nand_2028_out, id_mux_x5_1_output_x32[21], id_mux_x5_2_output_x32[31]);
  nand nand_2029 (out_34[22], nand_2030_out, nand_2030_out);
  nand nand_2030 (nand_2030_out, id_mux_x5_1_output_x32[22], id_mux_x5_2_output_x32[31]);
  nand nand_2031 (out_34[23], nand_2032_out, nand_2032_out);
  nand nand_2032 (nand_2032_out, id_mux_x5_1_output_x32[23], id_mux_x5_2_output_x32[31]);
  nand nand_2033 (out_34[24], nand_2034_out, nand_2034_out);
  nand nand_2034 (nand_2034_out, id_mux_x5_1_output_x32[24], id_mux_x5_2_output_x32[31]);
  nand nand_2035 (out_34[25], nand_2036_out, nand_2036_out);
  nand nand_2036 (nand_2036_out, id_mux_x5_1_output_x32[25], id_mux_x5_2_output_x32[31]);
  nand nand_2037 (out_34[26], nand_2038_out, nand_2038_out);
  nand nand_2038 (nand_2038_out, id_mux_x5_1_output_x32[26], id_mux_x5_2_output_x32[31]);
  nand nand_2039 (out_34[27], nand_2040_out, nand_2040_out);
  nand nand_2040 (nand_2040_out, id_mux_x5_1_output_x32[27], id_mux_x5_2_output_x32[31]);
  nand nand_2041 (out_34[28], nand_2042_out, nand_2042_out);
  nand nand_2042 (nand_2042_out, id_mux_x5_1_output_x32[28], id_mux_x5_2_output_x32[31]);
  nand nand_2043 (out_34[29], nand_2044_out, nand_2044_out);
  nand nand_2044 (nand_2044_out, id_mux_x5_1_output_x32[29], id_mux_x5_2_output_x32[31]);
  nand nand_2045 (out_34[30], nand_2046_out, nand_2046_out);
  nand nand_2046 (nand_2046_out, id_mux_x5_1_output_x32[30], id_mux_x5_2_output_x32[31]);
  nand nand_2047 (out_34[31], nand_2048_out, nand_2048_out);
  nand nand_2048 (nand_2048_out, id_mux_x5_1_output_x32[31], id_mux_x5_2_output_x32[31]);
endmodule

module USE_CPU_MATRIX (
  input  in_1,
  input  [7:0] in_2,
  input  [7:0] in_3,
  input  [7:0] in_4,
  input  [7:0] in_5,
  input  [7:0] in_6,
  input  [7:0] in_7,
  input  [7:0] in_8,
  input  [7:0] in_9
);

  wire button_1_out, clock_1_out;
  wire [7:0] m_all_cpu_m_1_port_output_0, m_all_cpu_m_1_port_output_1, rom_1_data;
  wire [15:0] m_all_cpu_m_1_rom_address;
  wire [31:0] matrixled_controller_32x32_1_out_3, matrixled_controller_32x32_1_out_4,
       matrixled_controller_32x32_1_out_5, matrixled_controller_32x32_1_out_6,
       matrixled_controller_32x32_1_out_7, matrixled_controller_32x32_1_out_8,
       matrixled_controller_32x32_1_out_9, matrixled_controller_32x32_1_out_10,
       matrixled_controller_32x32_1_out_11, matrixled_controller_32x32_1_out_12,
       matrixled_controller_32x32_1_out_13, matrixled_controller_32x32_1_out_14,
       matrixled_controller_32x32_1_out_15, matrixled_controller_32x32_1_out_16,
       matrixled_controller_32x32_1_out_17, matrixled_controller_32x32_1_out_18,
       matrixled_controller_32x32_1_out_19, matrixled_controller_32x32_1_out_20,
       matrixled_controller_32x32_1_out_21, matrixled_controller_32x32_1_out_22,
       matrixled_controller_32x32_1_out_23;

  ROM #(.addrWidth(16)) rom_1 (.addr(m_all_cpu_m_1_rom_address), .data(rom_1_data));
  Button button_1 (.out(button_1_out));
  Clock clock_1 (.out(clock_1_out));
  M_ALL_CPU_M m_all_cpu_m_1 (
    .ROM_Data(rom_1_data), .RST(button_1_out), .CLK(clock_1_out), .IDReset(in_1), .Port_Input_0(in_2),
    .Port_Input_1(in_3), .Port_Input_2(in_4), .Port_Input_3(in_5), .Port_Input_4(in_6), .Port_Input_5(in_7),
    .Port_Input_6(in_8), .Port_Input_7(in_9), .Port_Output_0(m_all_cpu_m_1_port_output_0),
    .Port_Output_1(m_all_cpu_m_1_port_output_1), .ROM_Address(m_all_cpu_m_1_rom_address));  // open: Port_Output_2, Port_Output_3, Port_Output_4, Port_Output_5, Port_Output_6, Port_Output_7
  DotMatrix #(.matrixcols(21), .matrixrows(32)) dotmatrix_1 (
    .col0(matrixled_controller_32x32_1_out_3), .col1(matrixled_controller_32x32_1_out_4),
    .col2(matrixled_controller_32x32_1_out_5), .col3(matrixled_controller_32x32_1_out_6),
    .col4(matrixled_controller_32x32_1_out_7), .col5(matrixled_controller_32x32_1_out_8),
    .col6(matrixled_controller_32x32_1_out_9), .col7(matrixled_controller_32x32_1_out_10),
    .col8(matrixled_controller_32x32_1_out_11), .col9(matrixled_controller_32x32_1_out_12),
    .col10(matrixled_controller_32x32_1_out_13), .col11(matrixled_controller_32x32_1_out_14),
    .col12(matrixled_controller_32x32_1_out_15), .col13(matrixled_controller_32x32_1_out_16),
    .col14(matrixled_controller_32x32_1_out_17), .col15(matrixled_controller_32x32_1_out_18),
    .col16(matrixled_controller_32x32_1_out_19), .col17(matrixled_controller_32x32_1_out_20),
    .col18(matrixled_controller_32x32_1_out_21), .col19(matrixled_controller_32x32_1_out_22),
    .col20(matrixled_controller_32x32_1_out_23));
  MatrixLED_Controller_32x32 matrixled_controller_32x32_1 (
    .INPUT_Y(m_all_cpu_m_1_port_output_0), .INPUT_X(m_all_cpu_m_1_port_output_1),
    .out_3(matrixled_controller_32x32_1_out_3), .out_4(matrixled_controller_32x32_1_out_4),
    .out_5(matrixled_controller_32x32_1_out_5), .out_6(matrixled_controller_32x32_1_out_6),
    .out_7(matrixled_controller_32x32_1_out_7), .out_8(matrixled_controller_32x32_1_out_8),
    .out_9(matrixled_controller_32x32_1_out_9), .out_10(matrixled_controller_32x32_1_out_10),
    .out_11(matrixled_controller_32x32_1_out_11), .out_12(matrixled_controller_32x32_1_out_12),
    .out_13(matrixled_controller_32x32_1_out_13), .out_14(matrixled_controller_32x32_1_out_14),
    .out_15(matrixled_controller_32x32_1_out_15), .out_16(matrixled_controller_32x32_1_out_16),
    .out_17(matrixled_controller_32x32_1_out_17), .out_18(matrixled_controller_32x32_1_out_18),
    .out_19(matrixled_controller_32x32_1_out_19), .out_20(matrixled_controller_32x32_1_out_20),
    .out_21(matrixled_controller_32x32_1_out_21), .out_22(matrixled_controller_32x32_1_out_22),
    .out_23(matrixled_controller_32x32_1_out_23));  // open: out_24, out_25, out_26, out_27, out_28, out_29, out_30, out_31, out_32, out_33, out_34

  // Notes on the sheet:
  //   ２，IDResetを1にします
  //   ４，IDResetを0にします
  //   contents of rom_1 (hex, n*v repeats v):
  //   0 a 0 1 6 1 1 a 2 0 6 3 1 c 0 0 c 1 2 2 0 5 1 20 7 0 4 1f 24 42 0 40 2 0 4 0 24 42 0 4c 2 2 5 3 20 7
  //   2 4 14 24 42 0 46 2 2 4 0 24 42 0 52 40 0 d 6 1 ff 40 0 20 6 3 ff 40 0 35 6 1 1 40 0 28 6 3 1 40 0
  //   3d
  //   CPUのリセット方法
  //   ３，CLKを1パルスだけ入力します
  //   5, クロックを有効にします
  //   １，CLKとIDResetが0の状態でRSTを押します
  //   X,Y = 0,0 は左下です
  //   マトリックスLED内で跳ね返り続ける点を描画します
  //   初期座標を入力ポートの0,1で指定できます
  //   入力ポート0がX座標，1がY座標です
  //   (10進数)
  //   プログラムの関係上，Xは0~19，はY0~30の間で指定してください
  //   (10進数)
endmodule
